// Logisim project box.circ as structural Verilog: 1 circuit, main circuit main
module main (
);

  wire alu_1_equal, and_4_out, and_6_out, and_8_out, and_9_out, CLK, comparator_1_eq, comparator_2_eq,
       counter_2_carry, counter_3_carry, counter_4_carry, d_ff_1_qn, dhex, displaying, Go, halt, INT,
       intgen_1_intg, irc, irs, MemWrite, Mode, MovDown, MovLeft, MovRight, MovUp, music_1_en, not_1_out,
       not_2_out, not_3_out, not_4_out, not_5_out, not_6_out, or_1_out, or_2_out, or_3_out, or_4_out,
       or_5_out, or_6_out, or_7_out, or_8_out, or_9_out, or_11_out, over, Play, register_2_q, RegWrite,
       Replay, RST, START, Uret, \单周期硬布线控制器_1_alu_src , \单周期硬布线控制器_1_beq , \单周期硬布线控制器_1_bne ,
       \单周期硬布线控制器_1_ecall , \单周期硬布线控制器_1_jal , \单周期硬布线控制器_1_jalr , \单周期硬布线控制器_1_memtoreg ,
       \单周期硬布线控制器_1_s_type ;
  wire [1:0] regch_1_x0, register_4_q;
  wire [1:1] or_10_out;
  wire [2:0] counter_1_q, intgen_1_intx, multiplexer_9_out, pcch_1_x0, t1, t2;
  wire [3:0] multiplexer_11_out, multiplexer_12_out, x1, x2, y1, y2, \单周期硬布线控制器_1_alu_op ;
  wire [4:0] multiplexer_3_out, multiplexer_4_out;
  wire [6:0] counter_2_q, keyboard_1_data, LCDX, LCDY, multiplexer_13_out, multiplexer_14_out;
  wire [7:0] VOL;
  wire [13:0] \music_1_频率 ;
  wire [15:0] counter_3_q, counter_4_q, LCDRGB, multiplexer_10_out;
  wire [31:0] adder_1_out, adder_2_out, adder_3_out, alu_1_result, and_5_out, bit_extender_1_out,
       bit_extender_2_out, bit_extender_3_out, bit_extender_4_out, ecallA, ecallV, INTAddr, IR, LedData,
       multiplexer_1_out, multiplexer_2_out, multiplexer_5_out, multiplexer_6_out, PC, ram_1_data, RDin,
       register_3_q, shifter_1_out, shifter_2_out, UretAddr;
  wire [31:16] rom_2_data;
  wire [31:22] controlled_buffer_1_out;

  Button button_1 (.out(RST));
  Button \u_继续运行  (.out(Go));
  or or_1 (or_1_out, not_1_out, Go);
  not not_1 (not_1_out, halt);
  Multiplexer #(.select(2), .width(32), .disabled("Z"), .enable("false")) multiplexer_1 (
    .in0(multiplexer_2_out), .in1(INTAddr), .in2(UretAddr), .out(multiplexer_1_out), .sel({Uret, INT}));  // open: in3
  Comparator #(.width(32), .mode("twosComplement")) comparator_1 (
    .a(ecallV), .b(32'h22), .eq(comparator_1_eq));  // open: gt, lt
  Comparator #(.width(32), .mode("twosComplement")) comparator_2 (
    .a(ecallV), .b(32'h2c), .eq(comparator_2_eq));  // open: gt, lt
  Register #(.width(32), .trigger("rising"), .Select("low")) u_PC (
    .D(multiplexer_1_out), .en(or_1_out), .Q(PC), .clk(CLK), .clr(RST), .cs(1'b0), .preset(1'b0));
  Clock #(.highDuration(1), .lowDuration(1)) clock_1 (.out(CLK));
  Register #(.width(32), .trigger("rising"), .Select("low")) register_1 (
    .D(ecallA), .en(dhex), .Q(LedData), .clk(CLK), .clr(RST), .cs(1'b0), .preset(1'b0));
  and and_1 (halt, ~comparator_1_eq, ~comparator_2_eq, \单周期硬布线控制器_1_ecall );  // AND_Gate
  and and_2 (dhex, comparator_1_eq, \单周期硬布线控制器_1_ecall );
  and and_3 (over, \单周期硬布线控制器_1_ecall , comparator_2_eq);
  Button button_2 (.out(START));
  ROM #(.addrWidth(10), .dataWidth(32), .Select("high")) rom_1 (.addr(PC[11:2]), .data(IR), .sel(1'b1));
  and and_4 (and_4_out, \单周期硬布线控制器_1_beq , alu_1_equal);
  \单周期硬布线控制器  \u_单周期硬布线控制器_1  (
    .Funct({IR[30], IR[25], IR[14:12]}), .OP(IR[6:2]), .ALU_OP(\单周期硬布线控制器_1_alu_op ),
    .MemToReg(\单周期硬布线控制器_1_memtoreg ), .MemWrite(MemWrite), .ALU_SRC(\单周期硬布线控制器_1_alu_src ),
    .RegWrite(RegWrite), .ecall(\单周期硬布线控制器_1_ecall ), .S_type(\单周期硬布线控制器_1_s_type ),
    .Jalr(\单周期硬布线控制器_1_jalr ), .Beq(\单周期硬布线控制器_1_beq ), .JAL(\单周期硬布线控制器_1_jal ), .Bne(\单周期硬布线控制器_1_bne ),
    .IR21(IR[21]), .uret(Uret), .irs(irs), .irc(irc));
  assign bit_extender_1_out = {{20{IR[31]}}, IR[31:20]};  // Bit_Extender bit_extender_1
  assign bit_extender_2_out = {{20{IR[31]}}, {IR[31:25], IR[11:7]}};  // Bit_Extender bit_extender_2
  assign and_5_out = alu_1_result & 32'hfffffffe;  // AND_Gate and_5, 32 bits wide
  assign bit_extender_3_out = {{20{IR[31]}}, {IR[31], IR[7], IR[30:25], IR[11:8]}};  // Bit_Extender bit_extender_3
  assign bit_extender_4_out = {{12{IR[31]}}, {IR[31], IR[19:12], IR[20], IR[30:21]}};  // Bit_Extender bit_extender_4
  and and_6 (and_6_out, \单周期硬布线控制器_1_bne , not_2_out);
  Adder #(.width(32)) adder_1 (.a(32'h4), .b(PC), .out(adder_1_out));  // open: cin, cout
  Shifter #(.width(32), .shift("ll")) shifter_1 (.in(bit_extender_3_out), .\dist (5'b00001), .out(shifter_1_out));
  Adder #(.width(32)) adder_2 (.a(shifter_1_out), .b(PC), .out(adder_2_out));  // open: cin, cout
  Shifter #(.width(32), .shift("ll")) shifter_2 (.in(bit_extender_4_out), .\dist (5'b00001), .out(shifter_2_out));
  Adder #(.width(32)) adder_3 (.a(shifter_2_out), .b(PC), .out(adder_3_out));  // open: cin, cout
  Keyboard #(.Char_bit_width(7), .buflen(32), .trigger("rising")) keyboard_1 (
    .clk(CLK), .re(1'b1), .clr(START), .data(keyboard_1_data));  // open: avail
  \键盘解析  \u_键盘解析_1  (
    .in_1(CLK), .in_2(START), .\缓冲区最前端的ASCII码 (keyboard_1_data), .UP_W(MovUp), .DOWN_S(MovDown),
    .LEFT_A(MovLeft), .RIGHT_D(MovRight));
  pcCh pcch_1 (
    .jalr(\单周期硬布线控制器_1_jalr ), .beq(and_4_out), .bne(and_6_out), .jal(\单周期硬布线控制器_1_jal ), .X0(pcch_1_x0[0]),
    .X1(pcch_1_x0[1]), .X2(pcch_1_x0[2]));
  Multiplexer #(.select(3), .width(32), .disabled("Z"), .enable("false")) multiplexer_2 (
    .in0(adder_1_out), .in1(and_5_out), .in2(adder_2_out), .in3(adder_3_out), .out(multiplexer_2_out),
    .sel(pcch_1_x0));  // open: in4, in5, in6, in7
  Multiplexer #(.select(1), .width(5), .disabled("Z"), .enable("false")) multiplexer_3 (
    .in0(IR[19:15]), .in1(5'b01010), .out(multiplexer_3_out), .sel(\单周期硬布线控制器_1_ecall ));
  Multiplexer #(.select(1), .width(5), .disabled("Z"), .enable("false")) multiplexer_4 (
    .in0(IR[24:20]), .in1(5'b10001), .out(multiplexer_4_out), .sel(\单周期硬布线控制器_1_ecall ));
  RegCh regch_1 (
    .m2r(\单周期硬布线控制器_1_memtoreg ), .jal(\单周期硬布线控制器_1_jal ), .jalr(\单周期硬布线控制器_1_jalr ), .x0(regch_1_x0[0]),
    .x1(regch_1_x0[1]));
  Regifile regifile_1 (
    .Din(RDin), .Clk(CLK), .R1(ecallA), .R2(ecallV), .WE(RegWrite), .W_num(IR[11:7]),
    .R1_num(multiplexer_3_out), .R2_num(multiplexer_4_out));
  not not_2 (not_2_out, alu_1_equal);
  Multiplexer #(.select(1), .width(32), .disabled("Z"), .enable("false")) multiplexer_5 (
    .in0(ecallV), .in1(multiplexer_6_out), .out(multiplexer_5_out), .sel(\单周期硬布线控制器_1_alu_src ));
  Multiplexer #(.select(1), .width(32), .disabled("Z"), .enable("false")) multiplexer_6 (
    .in0(bit_extender_1_out), .in1(bit_extender_2_out), .out(multiplexer_6_out), .sel(\单周期硬布线控制器_1_s_type ));
  // LCD_Video lcd_video_1: pin names not known; wires that end beside it: START, CLK, displaying, LCDX, LCDY, LCDRGB
  // Probe on \单周期硬布线控制器_1_alu_op 
  ALU alu_1 (
    .X(ecallA), .Y(multiplexer_5_out), .AluOP(\单周期硬布线控制器_1_alu_op ), .Equal(alu_1_equal),
    .Result(alu_1_result));  // open: Result_2, out_4, out_6
  or or_2 (or_2_out, INT, START, Uret);
  intGen intgen_1 (
    .clk(CLK), .ints1(MovLeft), .ints2(MovRight), .ints3(MovUp), .rst(INT), .intX(intgen_1_intx),
    .intG(intgen_1_intg), .ints4(MovDown), .ints5(START));  // open: ints6
  // DipSwitch #(.NSwitches(2)) dipswitch_1: pin names not known; wires that end beside it: Play, Mode
  Button \u_重放  (.out(Replay));
  Slider #(.width(8), .Direction("left_to_right"), .value('h24)) \u_音量  (.out(VOL));
  Register #(.width(32), .trigger("rising"), .Select("low")) EPC (
    .D(multiplexer_2_out), .en(INT), .Q(UretAddr), .clk(CLK));  // open: clr
  D_Flip_Flop #(.trigger("rising"), .Pre_Clr_Positions("LEGACY"), .NegatePresetClear("false"), .enable("true"), .NewFFLayout("false")) d_ff_1 (
    .clk(CLK), .D(d_ff_1_qn), .Qn(d_ff_1_qn), .en(or_2_out));  // open: Q, preset, reset
  RAM #(.addrWidth(10), .dataWidth(32), .bus("separate"), .Select("high")) ram_1 (
    .addr(alu_1_result[11:2]), .din(ecallV), .data(ram_1_data), .str(MemWrite), .clk(CLK),
    .ld(\单周期硬布线控制器_1_memtoreg ), .clr(RST));  // open: sel
  and and_7 (INT, d_ff_1_qn, ~displaying, intgen_1_intg);  // AND_Gate
  Multiplexer #(.select(2), .width(32), .disabled("Z"), .enable("false")) multiplexer_7 (
    .in0(alu_1_result), .in1(ram_1_data), .in2(adder_1_out), .out(RDin), .sel(regch_1_x0));  // open: in3
  // Probe on intgen_1_intx
  Multiplexer #(.select(3), .width(32), .disabled("Z"), .enable("false")) multiplexer_8 (
    .in1(32'h354), .in2(32'h368), .in3(32'h340), .in4(32'h32c), .in5(32'h1c), .out(INTAddr),
    .sel(intgen_1_intx));  // open: in0, in6, in7
  or or_3 (or_3_out, over, and_9_out);
  and and_8 (and_8_out, ~register_4_q[0], START);  // AND_Gate
  and and_9 (and_9_out, ~displaying, register_2_q);  // AND_Gate
  not not_3 (not_3_out, register_2_q);
  Register #(.width(1), .trigger("rising"), .Select("low")) register_2 (
    .D(not_3_out), .en(or_3_out), .Q(register_2_q), .clk(CLK));  // open: clr
  not not_4 (not_4_out, displaying);
  or or_4 (or_4_out, dhex, counter_2_carry);
  not not_5 (not_5_out, register_4_q[0]);
  or or_5 (or_5_out, and_8_out, counter_3_carry);
  not not_6 (not_6_out, register_4_q[1]);
  or or_6 (or_6_out, and_9_out, counter_4_carry);
  or or_7 (or_7_out, START, Replay);
  assign {controlled_buffer_1_out, t2, x2, y2, t1, x1, y1} = counter_1_q[0] ? LedData : 32'bz;  // Controlled_Buffer controlled_buffer_1
  assign {controlled_buffer_1_out, t2, x2, y2, t1, x1, y1} = counter_1_q[1] ? register_3_q : 32'bz;  // Controlled_Buffer controlled_buffer_2
  Register #(.width(32), .trigger("rising"), .Select("low")) register_3 (
    .D(LedData), .en(not_4_out), .Q(register_3_q), .clk(CLK));  // open: clr
  or or_8 (or_8_out, counter_1_q[0], counter_1_q[1]);
  Counter #(.width(3), .max('h7), .ongoal("wrap"), .trigger("rising"), .behavior("new")) counter_1 (
    .D(3'b000), .count(or_4_out), .Q(counter_1_q), .clk(CLK), .down(counter_2_carry));  // open: load, carry, clr, preset
  Register #(.width(1), .trigger("rising"), .Select("low")) register_4 (
    .D(not_5_out), .en(or_5_out), .Q(register_4_q[0]), .clk(CLK));  // open: clr
  Register #(.width(1), .trigger("rising"), .Select("low")) register_5 (
    .D(not_6_out), .en(or_6_out), .Q(register_4_q[1]), .clk(CLK));  // open: clr
  music music_1 (
    .CLK(CLK), .RST(or_7_out), .Play(Play), .\频率 (\music_1_频率 ), .EN(music_1_en), .Mode(Mode), .Success(over));
  Register #(.width(1), .trigger("rising"), .Select("low")) register_6 (
    .D(or_9_out), .Q(displaying), .clk(CLK));  // open: en, clr
  or or_9 (or_9_out, or_8_out, or_10_out[1]);
  Counter #(.width(7), .max('h7f), .ongoal("wrap"), .trigger("rising"), .behavior("new")) counter_2 (
    .count(or_8_out), .Q(counter_2_q), .carry(counter_2_carry), .clk(CLK));  // open: load, D, clr, preset, down
  Counter #(.width(16), .max('ha7f), .ongoal("wrap"), .trigger("rising"), .behavior("new")) counter_3 (
    .load(START), .D(16'h180), .count(register_4_q[0]), .Q(counter_3_q), .carry(counter_3_carry), .clk(CLK));  // open: clr, preset, down
  or or_10 (or_10_out[1], register_4_q[0], register_4_q[1]);
  or or_11 (or_11_out, register_4_q[1], and_9_out);
  Counter #(.width(16), .max('h1c00), .ongoal("wrap"), .trigger("rising"), .behavior("new")) counter_4 (
    .load(and_9_out), .D(16'ha80), .count(or_11_out), .Q(counter_4_q), .carry(counter_4_carry), .clk(CLK));  // open: clr, preset, down
  // Buzzer #(.freq_measure("Hz"), .vol_width(8)) buzzer_1: pin names not known; wires that end beside it: \music_1_频率 , music_1_en, VOL
  Multiplexer #(.select(1), .width(3), .disabled("Z"), .enable("false")) multiplexer_9 (
    .in0(t1), .in1(t2), .out(multiplexer_9_out), .sel(counter_2_q[6]));
  Multiplexer #(.select(2), .width(16), .disabled("Z"), .enable("false")) multiplexer_10 (
    .in0({{7{1'b0}}, multiplexer_9_out, counter_2_q[5:0]}), .in1(counter_3_q), .in2(counter_4_q),
    .out(multiplexer_10_out), .sel(register_4_q));  // open: in3
  ROM #(.addrWidth(16), .dataWidth(32), .Select("low")) rom_2 (.addr(multiplexer_10_out), .data({rom_2_data, LCDRGB}));
  Multiplexer #(.select(2), .width(4), .disabled("Z"), .enable("false")) multiplexer_11 (
    .in0(x1), .in1(x2), .in2(rom_2_data[22:19]), .in3(rom_2_data[22:19]), .out(multiplexer_11_out),
    .sel({or_10_out[1], counter_2_q[6]}));
  Multiplexer #(.select(2), .width(4), .disabled("Z"), .enable("false")) multiplexer_12 (
    .in0(y1), .in1(y2), .in2(rom_2_data[29:26]), .in3(rom_2_data[29:26]), .out(multiplexer_12_out),
    .sel({or_10_out[1], counter_2_q[6]}));
  Multiplexer #(.select(1), .width(7), .disabled("Z"), .enable("false")) multiplexer_13 (
    .in0(7'b0101000), .in1({7{1'b0}}), .out(multiplexer_13_out), .sel(or_11_out));
  Multiplexer #(.select(1), .width(7), .disabled("Z"), .enable("false")) multiplexer_14 (
    .in0(7'b0010100), .in1({7{1'b0}}), .out(multiplexer_14_out), .sel(or_11_out));
  Adder #(.width(7)) adder_4 (
    .a(multiplexer_13_out), .b({multiplexer_11_out, rom_2_data[18:16]}), .out(LCDX));  // open: cin, cout
  Adder #(.width(7)) adder_5 (
    .a(multiplexer_14_out), .b({multiplexer_12_out, rom_2_data[25:23]}), .out(LCDY));  // open: cin, cout
  // Probe on LCDRGB
  // Probe on {multiplexer_11_out, rom_2_data[18:16]}
  // Probe on {multiplexer_12_out, rom_2_data[25:23]}

  // Other names for the same wires on the sheet: MDin[31:0] = ecallV

  // Notes on the sheet:
  //   指令存储器
  //   rs1
  //   rs2
  //   指令字
  //   contents of rom_1 (hex, n*v repeats v):
  //   40006f 5*13 fedff06f 100413 500493 100a93 e93 100993 13ea023 4e8e93 100993 13ea023 4e8e93 100993
  //   13ea023 4e8e93 100993 13ea023 4e8e93 100993 13ea023 4e8e93 100993 13ea023 4e8e93 100993 13ea023
  //   4e8e93 100993 13ea023 4e8e93 100993 13ea023 4e8e93 200993 13ea023 4e8e93 200993 13ea023 4e8e93
  //   400993 13ea023 4e8e93 200993 13ea023 4e8e93 100993 13ea023 4e8e93 100993 13ea023 4e8e93 100993
  //   13ea023 4e8e93 100993 13ea023 4e8e93 200993 13ea023 4e8e93 300993 13ea023 4e8e93 993 13ea023 4e8e93
  //   993 13ea023 4e8e93 100993 13ea023 4e8e93 100993 13ea023 4e8e93 100993 13ea023 4e8e93 100993 13ea023
  //   4e8e93 100993 13ea023 4e8e93 993 13ea023 4e8e93 300993 13ea023 4e8e93 993 13ea023 4e8e93 100993
  //   13ea023 4e8e93 100993 13ea023 4e8e93 100993 13ea023 4e8e93 100993 13ea023 4e8e93 100993 13ea023
  //   4e8e93 300993 13ea023 4e8e93 993 13ea023 4e8e93 993 13ea023 4e8e93 100993 13ea023 4e8e93 100993
  //   13ea023 4e8e93 100993 13ea023 4e8e93 100993 13ea023 4e8e93 993 13ea023 4e8e93 300993 13ea023 4e8e93
  //   993 13ea023 4e8e93 100993 13ea023 4e8e93 100993 13ea023 4e8e93 100993 13ea023 4e8e93 100993 13ea023
  //   4e8e93 100993 13ea023 4e8e93 100993 13ea023 4e8e93 993 13ea023 4e8e93 993 13ea023 4e8e93 100993
  //   13ea023 4e8e93 993 13ea023 4e8e93 100993 13ea023 4e8e93 100993 13ea023 4e8e93 993 13ea023 4e8e93
  //   100993 13ea023 4e8e93 100993 13ea023 4e8e93 100993 13ea023 4e8e93 100993 13ea023 4e8e93 993 13ea023
  //   4e8e93 100993 13ea023 4e8e93 100993 13ea023 4e8e93 40293 148313 28393 130e13 400006f 40293 fff48313
  //   28393 fff30e13 2c0006f fff40293 48313 fff28393 30e13 180006f 140293 48313 128393 30e13 40006f e93
  //   229f13 1ee8eb3 531693 de8eb3 ea983 f93 33f8263 100f93 73f8263 200f93 73f8063 300f93 b3f8063 400f93
  //   1f3f8c63 30513 429f13 1e50533 500f13 8f1f13 1e50533 b49f13 1e50533 f41f13 1e50533 1391f13 1e50533
  //   2200893 73 28413 30493 913 200073 200073 30513 429f13 1e50533 500f13 8f1f13 1e50533 b49f13 1e50533
  //   f41f13 1e50533 1391f13 1e50533 2200893 73 28413 30493 200913 200073 f93 239f13 1ef8fb3 5e1693 df8fb3
  //   faa03 200693 1468863 693 b468463 200073 e0513 439f13 1e50533 400f13 8f1f13 1e50533 b31f13 1e50533
  //   f29f13 1e50533 f13 13f1f13 1e50533 2200893 73 400f13 1efa023 f13 1eea023 30513 429f13 1e50533 500f13
  //   8f1f13 1e50533 b49f13 1e50533 f41f13 1e50533 1391f13 1e50533 2200893 73 28413 30493 913 1a8a93
  //   500f13 1fea8a63 200073 e0513 439f13 1e50533 300f13 8f1f13 1e50533 b31f13 1e50533 f29f13 1e50533 f13
  //   13f1f13 1e50533 2200893 73 300f13 1efa023 f13 1eea023 30513 429f13 1e50533 500f13 8f1f13 1e50533
  //   b49f13 1e50533 f41f13 1e50533 1391f13 1e50533 2200893 73 28413 30493 913 200073 f93 239f13 1ef8fb3
  //   5e1693 df8fb3 faa03 200693 1468863 693 9468e63 200073 e0513 439f13 1e50533 400f13 8f1f13 1e50533
  //   b31f13 1e50533 f29f13 1e50533 200f13 13f1f13 1e50533 2200893 73 400f13 1efa023 200f13 1eea023 30513
  //   429f13 1e50533 500f13 8f1f13 1e50533 b49f13 1e50533 f41f13 1e50533 1391f13 1e50533 2200893 73 28413
  //   30493 200913 200073 e0513 339f13 1e50533 300f13 8f1f13 1e50533 b31f13 1e50533 f29f13 1e50533 200f13
  //   13f1f13 1e50533 2200893 73 300f13 1efa023 200f13 1eea023 30513 429f13 1e50533 500f13 8f1f13 1e50533
  //   b49f13 1e50533 f41f13 1e50533 1391f13 1e50533 2200893 73 28413 30493 200913 fffa8a93 200073 2c00893
  //   73
  //   rd
  //   immI
  //   immS
  //   immB
  //   immJ
  //   Beq
  //   Bne
  //   MemToReg
  //   MemWrite
  //   AluOP
  //   AluSrcB
  //   RegWrite
  //   S_type
  //   点击键盘，WSAD控制上下左右
  //   声音开关
  //   模式选择
  //   背景音乐
  //   歌曲播放
  //   数据存储器
  //   重置需要RST,CRTL+R会导致蜂鸣器杂音
  //   contents of rom_2 (hex, n*v repeats v):
  //   0 10000 20000 30000 40000 50000 60000 70000 800000 810000 820000 830000 840000 850000 860000 870000
  //   1000000 1010000 1020000 1030000 1040000 1050000 1060000 1070000 1800000 1810000 1820000 1830000
  //   1840000 1850000 1860000 1870000 2000000 2010000 2020000 2030000 2040000 2050000 2060000 2070000
  //   2800000 2810000 2820000 2830000 2840000 2850000 2860000 2870000 3000000 3010000 3020000 3030000
  //   3040000 3050000 3060000 3070000 3800000 3810000 3820000 3830000 3840000 3850000 3860000 3870000 0
  //   10000 20000 30000 40000 50000 60000 70000 800000 810000 820000 830000 840000 850000 860000 870000
  //   1000000 1010000 1020000 1030000 1040000 1050000 1060000 1070000 1800000 1810000 1820000 1830000
  //   1840000 1850000 1860000 1870000 2000000 2010000 2020000 2030000 2040000 2050000 2060000 2070000
  //   2800000 2810000 2820000 2830000 2840000 2850000 2860000 2870000 3000000 3010000 3020000 3030000
  //   3040000 3050000 3060000 3070000 3800000 3810000 3820000 3830000 3840000 3850000 3860000 3870000 7ee0
  //   17ee0 27ee0 37ee0 47ee0 57ee0 67ee0 77ae4 807ee0 817ee0 827ee1 837b08 847ae5 857ee0 867ee0 877f03
  //   1007ee0 1017ee1 1027b93 1037f95 1047bb7 1057b2a 1067ee0 1077ee3 1807ee0 1817f27 1827f95 1837ec0
  //   1847f27 1857fb5 1867ee0 1877ee3 2007ee0 2017f04 2027bb7 2037b07 2047b4f 2057f92 2067ee0 2077f03
  //   2807ee0 2817ee0 2827f49 2837f95 2847f92 2857f02 2867ee0 2877f03 3007ee0 3017ee0 3027ee0 3037ee0
  //   3047ee0 3057ee0 3067ee0 3077ee3 3807f05 3817f04 3827f04 3837f04 3847f04 3857f04 3867f04 3877b2a 55e8
  //   159e8 255e8 355e8 455e8 555c8 659e8 759e8 8059e9 815e0a 8255e9 8351a7 844da7 8555e8 865e09 875a09
  //   10055e8 1015e09 1025e09 10355e8 10455e8 1055e09 1065e09 10759e9 18055c8 18151c8 1825a09 1835e09
  //   1845e09 1855e09 18651c8 18755c8 20055c8 20151a7 20259e9 2035e09 2045e0a 2055a09 20651a7 20755c8
  //   28055e8 28159e9 2825e09 2835a09 2845a09 2855e09 2865a09 28755e8 30059e9 3015e09 3025a09 30351c8
  //   30451a7 30559e9 3065e0a 3075a09 38059e8 3815a09 38255e8 38355c8 38455c8 38555c8 3865a09 38759e8 3ea5
  //   13ea4 23e84 33ea4 43e84 53e84 63ea4 742c5 803ea4 8142e3 823e84 833a44 843a44 853e83 8642e4 873ea4
  //   1003ea4 10142e3 10242e3 1033a84 1043ea4 10542e3 1063ec3 1073ea4 1803a84 1813a64 1823ec4 18342e4
  //   18442e4 1853ec4 1863a64 1873a84 2003a84 2013a44 2023ea4 2034303 20442e4 2053ea4 2063644 2073e84
  //   2803e84 2813ec4 2824303 2833ea4 2843ec4 2854303 2863ea4 2873e84 3003ea4 30142e4 3023ea3 3033a44
  //   3043a44 3053ea4 30642e4 3073ea4 3803aa4 3813ea4 3823e84 3833a84 3843a84 3853e84 3863ea4 3873ea4 0
  //   10000 20000 30000 40000 50000 60000 70000 800000 810420 8245a0 8365c4 8465e3 854180 860420 870000
  //   1000000 10155e0 1027f20 1037a44 1047a44 1057f20 1064dc0 1070000 1801880 1817ee0 1827f00 1837a24
  //   1847a44 1857f00 1867ac0 1871060 2001ca0 2017ee0 2027f00 2037a24 2047a44 2057f00 2067ee0 2071480
  //   2800420 2816660 2827f20 2837a24 2847a44 2857f20 2866240 2870400 3000000 3011480 3026260 3037624
  //   3047624 3055e40 3061060 3070000 3800000 3810000 3820000 3831861 3841861 3850000 3860000 3870000 56f7
  //   156f8 25718 35718 45718 55718 656f8 75b17 8056f7 815718 8256f7 8352f7 8456f7 8556f8 865718 875718
  //   10056f7 1015718 10252d6 1034ed6 10452d6 10556f7 1065718 1075718 18056f7 1815718 18252d6 18352d6
  //   18452d6 18556f7 1865718 1875718 20056f7 2015718 20256f7 20356f7 2045af7 2055b18 20656f8 2075718
  //   28056f7 2815718 2825718 2835718 2845f39 2855f39 28656f8 2875718 30056f7 3015718 3025718 3035718
  //   3045b18 3055b18 30656f8 3075718 38056f7 3815718 3825718 3835718 38456f7 38556f7 3865718 3875718
  //   856f7 956f8 a5718 b5718 c5718 d5718 e56f8 f5b17 8856f7 895718 8a56f7 8b52f7 8c56f7 8d56f8 8e5718
  //   8f5718 10856f7 1095718 10a52d6 10b4ed6 10c52d6 10d56f7 10e5718 10f5718 18856f7 1895718 18a52d6
  //   18b52d6 18c52d6 18d56f7 18e5718 18f5718 20856f7 2095718 20a56f7 20b56f7 20c5af7 20d5b18 20e56f8
  //   20f5718 28856f7 2895718 28a5718 28b5718 28c5f39 28d5f39 28e56f8 28f5718 30856f7 3095718 30a5718
  //   30b5718 30c5b18 30d5b18 30e56f8 30f5718 38856f7 3895718 38a5718 38b5718 38c56f7 38d56f7 38e5718
  //   38f5718 1056f7 1156f8 125718 135718 145718 155718 1656f8 175b17 9056f7 915718 9256f7 9352f7 9456f7
  //   9556f8 965718 975718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
endmodule
