// Logisim project cpu21-riscv.circ as structural Verilog
module \单周期RISC_V  (
  input  IR1,
  input  IR2,
  input  IR3,
  output RegWrite,
  output MemWrite,
  output [31:0] PC,
  output [31:0] IR,
  output [31:0] RDin,
  output [31:0] MDin,
  output [31:0] LedData
);

  wire alu_1_equal, and_3_out, and_4_out, CLK, clock_2_out, comparator_1_eq, comparator_2_eq,
       comparator_2_lt, d_ff_1_q, dhex, Go, halt, IR1_t, IR2_t, IR3_t, IRA, IRB, IRC, nand_1_out, not_1_out,
       not_2_out, not_3_out, not_4_out, or_1_out, or_2_out, RST, W1, W2, W3, \单周期硬布线控制器_1_alu_src ,
       \单周期硬布线控制器_1_beq , \单周期硬布线控制器_1_bne , \单周期硬布线控制器_1_ecall , \单周期硬布线控制器_1_jal , \单周期硬布线控制器_1_jalr ,
       \单周期硬布线控制器_1_memtoreg , \单周期硬布线控制器_1_s_type ;
  wire [1:0] regch_1_x0;
  wire [2:0] pcch_1_x0;
  wire [3:0] \单周期硬布线控制器_1_alu_op ;
  wire [4:0] multiplexer_2_out, multiplexer_3_out;
  wire [9:0] alu_1_result_2;
  wire [12:0] CNT_num;
  wire [15:0] \总周期数 ;
  wire [31:0] adder_1_out, adder_2_out, adder_3_out, alu_1_result, and_5_out, bit_extender_1_out,
       bit_extender_2_out, bit_extender_3_out, bit_extender_4_out, ecallA, multiplexer_1_out,
       multiplexer_4_out, multiplexer_5_out, ram_1_data, shifter_1_out, shifter_2_out;

  Clock #(.highDuration(1), .lowDuration(1)) clock_1 ();  // open: out
  Button _1 (.out(IRA));
  Button _2 (.out(IRB));
  Button _3 (.out(IRC));
  Button \u_继续运行  (.out(Go));
  LED #(.active("true")) led_1 (.in(W1));
  LED #(.active("true")) led_2 (.in(W2));
  LED #(.active("true")) led_3 (.in(W3));
  Button RESET (.out(RST));
  Comparator #(.width(32), .mode("twosComplement")) comparator_1 (
    .a(MDin), .b(32'h22), .eq(comparator_1_eq));  // open: gt, lt
  or or_1 (or_1_out, not_1_out, Go);
  not not_1 (not_1_out, halt);
  Hex_Digit_Display hex_digit_display_1 (.value(LedData[31:28]));  // open: dp
  not not_2 (not_2_out, comparator_1_eq);
  Register #(.width(32), .trigger("falling"), .Select("low")) u_PC (
    .D(multiplexer_1_out), .en(or_1_out), .Q(PC), .clk(CLK), .clr(RST), .cs(1'b0), .preset(1'b0));
  Hex_Digit_Display hex_digit_display_2 (.value(LedData[23:20]));  // open: dp
  Hex_Digit_Display hex_digit_display_3 (.value(LedData[27:24]));  // open: dp
  Register #(.width(32), .trigger("rising"), .Select("low")) register_1 (
    .D(ecallA), .en(dhex), .Q(LedData), .clk(CLK), .clr(RST), .cs(1'b0), .preset(1'b0));
  and and_1 (halt, not_2_out, \单周期硬布线控制器_1_ecall );
  and and_2 (dhex, comparator_1_eq, \单周期硬布线控制器_1_ecall );
  Hex_Digit_Display hex_digit_display_4 (.value(LedData[19:16]));  // open: dp
  Hex_Digit_Display hex_digit_display_5 (.value(LedData[15:12]));  // open: dp
  or or_2 (or_2_out, not_3_out, Go);
  not not_3 (not_3_out, halt);
  // RiscV_Probe riscv_probe_1: pin names not known; wires that end beside it: IR, IR[19:15]
  Hex_Digit_Display hex_digit_display_6 (.value(LedData[11:8]));  // open: dp
  Hex_Digit_Display hex_digit_display_7 (.value(LedData[7:4]));  // open: dp
  // Probe on \总周期数 
  Counter #(.width(16), .max('hffff), .ongoal("wrap"), .trigger("rising"), .behavior("new")) counter_1 (
    .count(or_2_out), .Q(\总周期数 ), .clk(CLK));  // open: load, D, carry, clr, preset, down
  ROM #(.addrWidth(10), .dataWidth(32), .Select("high")) rom_1 (.addr(PC[11:2]), .data(IR), .sel(1'b1));
  Hex_Digit_Display hex_digit_display_8 (.value(LedData[3:0]));  // open: dp
  \单周期硬布线控制器  \u_单周期硬布线控制器_1  (
    .Funct({IR[30], IR[25], IR[14:12]}), .OP(IR[6:2]), .ALU_OP(\单周期硬布线控制器_1_alu_op ),
    .MemToReg(\单周期硬布线控制器_1_memtoreg ), .MemWrite(MemWrite), .ALU_SRC(\单周期硬布线控制器_1_alu_src ),
    .RegWrite(RegWrite), .ecall(\单周期硬布线控制器_1_ecall ), .S_type(\单周期硬布线控制器_1_s_type ),
    .Jalr(\单周期硬布线控制器_1_jalr ), .Beq(\单周期硬布线控制器_1_beq ), .JAL(\单周期硬布线控制器_1_jal ), .Bne(\单周期硬布线控制器_1_bne ),
    .IR21(IR[21]));  // open: uret, irs, irc
  assign bit_extender_1_out = {{20{IR[31]}}, IR[31:20]};  // Bit_Extender bit_extender_1
  assign bit_extender_2_out = {{20{IR[31]}}, {IR[31:25], IR[11:7]}};  // Bit_Extender bit_extender_2
  assign bit_extender_3_out = {{20{IR[31]}}, {IR[31], IR[7], IR[30:25], IR[11:8]}};  // Bit_Extender bit_extender_3
  assign bit_extender_4_out = {{12{IR[31]}}, {IR[31], IR[19:12], IR[20], IR[30:21]}};  // Bit_Extender bit_extender_4
  or or_3 (IR1_t, IR1, IRA);
  and and_3 (and_3_out, \单周期硬布线控制器_1_beq , alu_1_equal);
  and and_4 (and_4_out, \单周期硬布线控制器_1_bne , not_4_out);
  assign and_5_out = {alu_1_result[31:12], alu_1_result_2, alu_1_result[1:0]} & 32'hfffffffe;  // AND_Gate and_5, 32 bits wide
  Shifter #(.width(32), .shift("ll")) shifter_1 (.in(bit_extender_3_out), .\dist (5'b00001), .out(shifter_1_out));
  Shifter #(.width(32), .shift("ll")) shifter_2 (.in(bit_extender_4_out), .\dist (5'b00001), .out(shifter_2_out));
  or or_4 (IR2_t, IR2, IRB);
  pcCh pcch_1 (
    .jalr(\单周期硬布线控制器_1_jalr ), .beq(and_3_out), .bne(and_4_out), .jal(\单周期硬布线控制器_1_jal ), .X0(pcch_1_x0[0]),
    .X1(pcch_1_x0[1]), .X2(pcch_1_x0[2]));
  Adder #(.width(32)) adder_1 (.a(32'h4), .b(PC), .out(adder_1_out));  // open: cin, cout
  Multiplexer #(.select(3), .width(32), .disabled("Z"), .enable("false")) multiplexer_1 (
    .in0(adder_1_out), .in1(and_5_out), .in2(adder_2_out), .in3(adder_3_out), .out(multiplexer_1_out),
    .sel(pcch_1_x0));  // open: in4, in5, in6, in7
  Adder #(.width(32)) adder_2 (.a(shifter_1_out), .b(PC), .out(adder_2_out));  // open: cin, cout
  Adder #(.width(32)) adder_3 (.a(shifter_2_out), .b(PC), .out(adder_3_out));  // open: cin, cout
  Multiplexer #(.select(1), .width(5), .disabled("Z"), .enable("false")) multiplexer_2 (
    .in0(IR[19:15]), .in1(5'b01010), .out(multiplexer_2_out), .sel(\单周期硬布线控制器_1_ecall ));
  Multiplexer #(.select(1), .width(5), .disabled("Z"), .enable("false")) multiplexer_3 (
    .in0(IR[24:20]), .in1(5'b10001), .out(multiplexer_3_out), .sel(\单周期硬布线控制器_1_ecall ));
  or or_5 (IR3_t, IR3, IRC);
  RegCh regch_1 (
    .m2r(\单周期硬布线控制器_1_memtoreg ), .jal(\单周期硬布线控制器_1_jal ), .jalr(\单周期硬布线控制器_1_jalr ), .x0(regch_1_x0[0]),
    .x1(regch_1_x0[1]));
  Regifile regifile_1 (
    .Din(RDin), .Clk(CLK), .R1(ecallA), .R2(MDin), .WE(RegWrite), .W_num(IR[11:7]),
    .R1_num(multiplexer_2_out), .R2_num(multiplexer_3_out));
  Multiplexer #(.select(1), .width(32), .disabled("Z"), .enable("false")) multiplexer_4 (
    .in0(bit_extender_1_out), .in1(bit_extender_2_out), .out(multiplexer_4_out), .sel(\单周期硬布线控制器_1_s_type ));
  not not_4 (not_4_out, alu_1_equal);
  Multiplexer #(.select(1), .width(32), .disabled("Z"), .enable("false")) multiplexer_5 (
    .in0(MDin), .in1(multiplexer_4_out), .out(multiplexer_5_out), .sel(\单周期硬布线控制器_1_alu_src ));
  // Probe on \单周期硬布线控制器_1_alu_op 
  ALU alu_1 (
    .X(ecallA), .Y(multiplexer_5_out), .AluOP(\单周期硬布线控制器_1_alu_op ), .Equal(alu_1_equal),
    .Result({alu_1_result[31:12], alu_1_result_2, alu_1_result[1:0]}));  // open: Result_2, out_4, out_6
  RAM #(.addrWidth(10), .dataWidth(32), .bus("separate"), .Select("high")) ram_1 (
    .addr(alu_1_result_2), .din(MDin), .data(ram_1_data), .str(MemWrite), .clk(CLK),
    .ld(\单周期硬布线控制器_1_memtoreg ), .clr(RST));  // open: sel
  D_Flip_Flop #(.trigger("high"), .Pre_Clr_Positions("LEGACY"), .NegatePresetClear("false"), .enable("true"), .NewFFLayout("false")) d_ff_1 (.Q(d_ff_1_q));  // open: clk, D, Qn, preset, en, reset
  // Probe on 13'hc
  Multiplexer #(.select(2), .width(32), .disabled("Z"), .enable("false")) multiplexer_6 (
    .in0({alu_1_result[31:12], alu_1_result_2, alu_1_result[1:0]}), .in1(ram_1_data), .in2(adder_1_out),
    .out(RDin), .sel(regch_1_x0));  // open: in3
  Comparator #(.width(13), .mode("twosComplement")) comparator_2 (
    .a(CNT_num), .b(13'hc), .eq(comparator_2_eq), .lt(comparator_2_lt));  // open: gt
  Clock #(.highDuration(1), .lowDuration(1)) clock_2 (.out(clock_2_out));
  Counter #(.width(13), .max('h1fff), .ongoal("stay"), .trigger("rising"), .behavior("old")) counter_2 (
    .count(comparator_2_lt), .Q(CNT_num), .clk(clock_2_out));  // open: load, D, carry, clr, preset
  nand nand_1 (nand_1_out, d_ff_1_q, comparator_2_eq);
  assign CLK = nand_1_out ? clock_2_out : 1'bz;  // Controlled_Buffer controlled_buffer_1
  Pull_Resistor #(.pull(1)) pull_resistor_1 (.node(CLK));

  // Other names for the same wires on the sheet: ecallV[31:0] = MDin

  // Notes on the sheet:
  //   中断源
  //   中断等待指示
  //   总复位信号应将除ROM以外所有存储组件全部清零
  //   数码管输出
  //   指令存储器
  //   数码管输出应该用寄存器锁存，否则显示数据只能一闪而过
  //   指令字
  //   contents of rom_1 (hex, n*v repeats v):
  //   100493 100006f 100493 200913 300993 100006f 100493 200913 300993 100006f 100493 200913 300993
  //   100006f 100493 200913 300993 29c000ef 100413 100493 1f49493 900533 2200893 73 24d493 48463 fedff06f
  //   900533 2200893 73 100493 249493 900533 2200893 73 48463 fedff06f 100493 1f49493 900533 2200893 73
  //   4034d493 900533 2200893 73 4044d493 900533 2200893 73 4044d493 900533 2200893 73 4044d493 900533
  //   2200893 73 4044d493 900533 2200893 73 4044d493 900533 2200893 73 4044d493 900533 2200893 73 4044d493
  //   900533 2200893 73 100413 1f41993 41f9d993 433 c00913 300b13 140413 f47413 800293 100313 499993
  //   89e9b3 1300533 2200893 73 406282b3 fe0294e3 140413 f00f93 1f47433 1c41413 800293 100313 49d993
  //   89e9b3 1300533 2200893 73 406282b3 fe0294e3 1c45413 406b0b33 b0463 f95ff06f 2b3 fff2c293 829293
  //   ff2e293 500533 2200893 73 fff00413 493 84a023 140413 448493 84a023 140413 448493 84a023 140413
  //   448493 84a023 140413 448493 84a023 140413 448493 84a023 140413 448493 84a023 140413 448493 84a023
  //   140413 448493 84a023 140413 448493 84a023 140413 448493 84a023 140413 448493 84a023 140413 448493
  //   84a023 140413 448493 84a023 140413 448493 84a023 140413 448493 84a023 140413 448493 140413 433
  //   3c00493 42983 4aa03 149a2b3 28663 134a023 1442023 ffc48493 fe9412e3 800533 2200893 73 440413 3c00493
  //   fc9416e3 a00893 73 413 140413 800533 2200893 73 240413 800533 2200893 73 340413 800533 2200893 73
  //   440413 800533 2200893 73 540413 800533 2200893 73 640413 800533 2200893 73 740413 800533 2200893 73
  //   840413 800533 2200893 2200893 73 8067
  //   rs1
  //   rs2
  //   rd
  //   immI
  //   immS
  //   immB
  //   immJ
  //   Beq
  //   Bne
  //   MemToReg
  //   MemWrite
  //   AluOP
  //   AluSrcB
  //   RegWrite
  //   S_type
  //   为方便自动评测，需要输出PC，IR，寄存器堆写如数据RDin
  //   RAM写使能MemWrite、RAM写入数据MDin等信号
  //   数据存储器
  //   控制位
  //   暂停节拍，不能为0
  //   戳工具置1进入计数暂停模式，ctrl+k时钟自动运行到对应节拍暂停
  //   ctrl+k关闭时钟连续运行，将控制位置零，进入单步调试模式调试
  //   用这个时钟源需要去掉电路中的其他时钟源
  //   可计数暂停的时钟源
endmodule

// 单周期硬布线控制器
module \单周期硬布线控制器  (
  input  [4:0] OP,
  input  [4:0] Funct,
  input  IR21,
  output [3:0] ALU_OP,
  output MemToReg,
  output MemWrite,
  output ALU_SRC,
  output RegWrite,
  output ecall,
  output S_type,
  output Beq,
  output Bne,
  output Jalr,
  output JAL,
  output uret,
  output irs,
  output irc
);

  \运算控制器自动生成  \u_运算控制器自动生成_1  (
    .OP2(OP[0]), .OP3(OP[1]), .OP4(OP[2]), .OP5(OP[3]), .OP6(OP[4]), .F12(Funct[0]), .F13(Funct[1]),
    .F14(Funct[2]), .F25(Funct[3]), .F30(Funct[4]), .S0(ALU_OP[0]), .S1(ALU_OP[1]), .S2(ALU_OP[2]),
    .S3(ALU_OP[3]));
  \控制信号自动生成  \u_控制信号自动生成_1  (
    .OP2(OP[0]), .OP3(OP[1]), .MemToReg(MemToReg), .OP4(OP[2]), .OP5(OP[3]), .OP6(OP[4]), .F12(Funct[0]),
    .MemWrite(MemWrite), .F13(Funct[1]), .F14(Funct[2]), .F25(Funct[3]), .F30(Funct[4]), .ALU_SRC(ALU_SRC),
    .RegWrite(RegWrite), .ecall(ecall), .S_Type(S_type), .BEQ(Beq), .BNE(Bne), .JALR(Jalr), .JAL(JAL),
    .uret(uret), .irs(irs), .irc(irc), .IR21(IR21));

  // Other names for the same wires on the sheet: OP_CODE[4:0] = OP

  // Notes on the sheet:
  //   运算器控制器，根据指令生成运算器功能选择信号
  //   控制信号生成，产生数据通路需要的其他控制信号
endmodule

// 运算器控制器
module \运算控制器自动生成  (
  input  OP2,
  input  OP3,
  input  OP4,
  input  OP5,
  input  OP6,
  input  F12,
  input  F13,
  input  F14,
  input  F25,
  input  F30,
  output S0,
  output S1,
  output S2,
  output S3
);

  wire and_1_out, and_2_out, and_3_out, and_4_out, and_5_out, and_6_out, and_7_out, and_8_out, and_9_out,
       and_10_out, and_11_out, and_12_out, and_13_out, and_14_out, and_15_out, and_16_out, and_17_out,
       and_18_out, and_19_out, and_20_out, and_21_out, and_22_out, and_23_out, and_24_out, and_25_out,
       and_26_out, and_27_out, and_28_out, and_29_out, and_30_out, and_31_out, and_32_out, and_33_out,
       and_34_out, not_1_out, not_2_out, not_3_out, not_4_out, not_5_out, not_6_out, not_7_out, not_8_out,
       not_9_out, not_10_out, not_11_out, not_12_out, not_13_out, not_14_out, not_15_out, not_16_out,
       not_17_out, not_18_out, not_19_out, not_20_out, not_21_out, not_22_out, not_23_out, not_24_out,
       not_25_out, not_26_out, not_27_out, not_28_out, not_29_out, not_30_out, not_31_out, not_32_out,
       not_33_out, not_34_out, not_35_out, not_36_out, not_37_out, not_38_out, not_39_out, not_40_out,
       not_41_out, not_42_out, not_43_out, not_44_out, not_45_out, not_46_out, not_47_out, not_48_out,
       not_49_out, not_50_out, not_51_out, not_52_out, not_53_out, not_54_out, not_55_out, not_56_out,
       not_57_out, not_58_out, not_59_out, not_60_out, not_61_out, not_62_out, not_63_out, not_64_out,
       not_65_out, not_66_out, not_67_out, not_68_out, not_69_out, not_70_out, not_71_out, not_72_out,
       not_73_out, not_74_out, not_75_out, not_76_out, not_77_out, not_78_out, not_79_out, not_80_out,
       not_81_out, not_82_out, not_83_out, not_84_out, not_85_out, not_86_out, not_87_out, not_88_out,
       not_89_out, not_90_out, not_91_out, not_92_out, not_93_out, not_94_out, not_95_out, not_96_out,
       not_97_out, not_98_out, not_99_out, not_100_out, not_101_out, not_102_out, not_103_out, not_104_out,
       not_105_out, not_106_out, not_107_out, not_108_out, not_109_out, not_110_out, not_111_out,
       not_112_out, not_113_out, not_114_out, not_115_out, not_116_out, not_117_out, not_118_out,
       not_119_out, not_120_out, not_121_out, not_122_out, not_123_out, not_124_out, not_125_out,
       not_126_out, not_127_out, not_128_out, not_129_out, not_130_out, not_131_out, not_132_out,
       not_133_out, not_134_out, not_135_out, not_136_out, not_137_out, not_138_out, not_139_out,
       not_140_out, not_141_out, not_142_out, not_143_out, not_144_out, not_145_out, not_146_out,
       not_147_out, not_148_out, not_149_out, not_150_out, not_151_out, not_152_out, not_153_out,
       not_154_out, not_155_out, not_156_out, not_157_out, not_158_out, not_159_out, not_160_out,
       not_161_out, not_162_out, not_163_out, not_164_out, not_165_out, not_166_out, not_167_out,
       not_168_out, not_169_out, not_170_out, not_171_out, not_172_out, not_173_out, not_174_out,
       not_175_out, not_176_out, not_177_out, not_178_out, not_179_out, not_180_out, not_181_out,
       not_182_out, not_183_out, not_184_out, not_185_out, not_186_out, not_187_out, not_188_out,
       not_189_out, not_190_out, not_191_out, not_192_out, not_193_out, not_194_out, not_195_out,
       not_196_out, not_197_out, not_198_out, not_199_out, not_200_out, not_201_out, not_202_out,
       not_203_out, not_204_out, not_205_out, not_206_out;

  not not_1 (not_1_out, F30);
  not not_2 (not_2_out, F25);
  not not_3 (not_3_out, F14);
  not not_4 (not_4_out, F13);
  not not_5 (not_5_out, F12);
  not not_6 (not_6_out, OP6);
  not not_7 (not_7_out, OP3);
  not not_8 (not_8_out, OP2);
  not not_9 (not_9_out, F30);
  not not_10 (not_10_out, F25);
  not not_11 (not_11_out, OP6);
  not not_12 (not_12_out, OP3);
  not not_13 (not_13_out, OP2);
  not not_14 (not_14_out, F30);
  not not_15 (not_15_out, F25);
  not not_16 (not_16_out, F14);
  not not_17 (not_17_out, F12);
  not not_18 (not_18_out, OP6);
  not not_19 (not_19_out, OP3);
  not not_20 (not_20_out, OP2);
  not not_21 (not_21_out, F14);
  not not_22 (not_22_out, F13);
  not not_23 (not_23_out, F12);
  not not_24 (not_24_out, OP6);
  not not_25 (not_25_out, OP5);
  not not_26 (not_26_out, OP3);
  not not_27 (not_27_out, OP2);
  not not_28 (not_28_out, OP6);
  not not_29 (not_29_out, OP5);
  not not_30 (not_30_out, OP3);
  not not_31 (not_31_out, OP2);
  not not_32 (not_32_out, F13);
  not not_33 (not_33_out, F12);
  not not_34 (not_34_out, OP6);
  not not_35 (not_35_out, OP5);
  not not_36 (not_36_out, OP3);
  not not_37 (not_37_out, OP2);
  not not_38 (not_38_out, F14);
  not not_39 (not_39_out, F12);
  not not_40 (not_40_out, OP6);
  not not_41 (not_41_out, OP5);
  not not_42 (not_42_out, OP3);
  not not_43 (not_43_out, OP2);
  not not_44 (not_44_out, F25);
  not not_45 (not_45_out, F13);
  not not_46 (not_46_out, OP6);
  not not_47 (not_47_out, OP5);
  not not_48 (not_48_out, OP3);
  not not_49 (not_49_out, OP2);
  not not_50 (not_50_out, F14);
  not not_51 (not_51_out, F12);
  not not_52 (not_52_out, OP6);
  not not_53 (not_53_out, OP5);
  not not_54 (not_54_out, OP4);
  not not_55 (not_55_out, OP3);
  not not_56 (not_56_out, OP2);
  not not_57 (not_57_out, F14);
  not not_58 (not_58_out, F12);
  not not_59 (not_59_out, OP6);
  not not_60 (not_60_out, OP4);
  not not_61 (not_61_out, OP3);
  not not_62 (not_62_out, OP2);
  not not_63 (not_63_out, F25);
  not not_64 (not_64_out, F14);
  not not_65 (not_65_out, F13);
  not not_66 (not_66_out, F12);
  not not_67 (not_67_out, OP6);
  not not_68 (not_68_out, OP3);
  not not_69 (not_69_out, OP2);
  not not_70 (not_70_out, F30);
  not not_71 (not_71_out, F25);
  not not_72 (not_72_out, OP6);
  not not_73 (not_73_out, OP3);
  not not_74 (not_74_out, OP2);
  not not_75 (not_75_out, F30);
  not not_76 (not_76_out, F25);
  not not_77 (not_77_out, F14);
  not not_78 (not_78_out, F12);
  not not_79 (not_79_out, OP6);
  not not_80 (not_80_out, OP3);
  not not_81 (not_81_out, OP2);
  not not_82 (not_82_out, OP6);
  not not_83 (not_83_out, OP5);
  not not_84 (not_84_out, OP3);
  not not_85 (not_85_out, OP2);
  not not_86 (not_86_out, F14);
  not not_87 (not_87_out, F12);
  not not_88 (not_88_out, OP6);
  not not_89 (not_89_out, OP5);
  not not_90 (not_90_out, OP3);
  not not_91 (not_91_out, OP2);
  not not_92 (not_92_out, F30);
  not not_93 (not_93_out, F25);
  not not_94 (not_94_out, F13);
  not not_95 (not_95_out, OP6);
  not not_96 (not_96_out, OP5);
  not not_97 (not_97_out, OP3);
  not not_98 (not_98_out, OP2);
  not not_99 (not_99_out, F14);
  not not_100 (not_100_out, F13);
  not not_101 (not_101_out, F12);
  not not_102 (not_102_out, OP4);
  not not_103 (not_103_out, OP3);
  not not_104 (not_104_out, OP2);
  not not_105 (not_105_out, F14);
  not not_106 (not_106_out, F13);
  not not_107 (not_107_out, OP4);
  not not_108 (not_108_out, OP3);
  not not_109 (not_109_out, OP2);
  not not_110 (not_110_out, F30);
  not not_111 (not_111_out, F25);
  not not_112 (not_112_out, F14);
  not not_113 (not_113_out, F13);
  not not_114 (not_114_out, F12);
  not not_115 (not_115_out, OP6);
  not not_116 (not_116_out, OP3);
  not not_117 (not_117_out, OP2);
  not not_118 (not_118_out, F25);
  not not_119 (not_119_out, F14);
  not not_120 (not_120_out, F13);
  not not_121 (not_121_out, F12);
  not not_122 (not_122_out, OP6);
  not not_123 (not_123_out, OP3);
  not not_124 (not_124_out, OP2);
  not not_125 (not_125_out, F30);
  not not_126 (not_126_out, F25);
  not not_127 (not_127_out, OP6);
  not not_128 (not_128_out, OP3);
  not not_129 (not_129_out, OP2);
  not not_130 (not_130_out, F30);
  not not_131 (not_131_out, F25);
  not not_132 (not_132_out, F14);
  not not_133 (not_133_out, OP6);
  not not_134 (not_134_out, OP3);
  not not_135 (not_135_out, OP2);
  not not_136 (not_136_out, F14);
  not not_137 (not_137_out, F13);
  not not_138 (not_138_out, F12);
  not not_139 (not_139_out, OP6);
  not not_140 (not_140_out, OP5);
  not not_141 (not_141_out, OP3);
  not not_142 (not_142_out, OP2);
  not not_143 (not_143_out, OP6);
  not not_144 (not_144_out, OP5);
  not not_145 (not_145_out, OP3);
  not not_146 (not_146_out, OP2);
  not not_147 (not_147_out, F14);
  not not_148 (not_148_out, F12);
  not not_149 (not_149_out, OP6);
  not not_150 (not_150_out, OP5);
  not not_151 (not_151_out, OP4);
  not not_152 (not_152_out, OP3);
  not not_153 (not_153_out, OP2);
  not not_154 (not_154_out, F14);
  not not_155 (not_155_out, F12);
  not not_156 (not_156_out, OP6);
  not not_157 (not_157_out, OP4);
  not not_158 (not_158_out, OP3);
  not not_159 (not_159_out, OP2);
  not not_160 (not_160_out, F14);
  not not_161 (not_161_out, F13);
  not not_162 (not_162_out, F12);
  not not_163 (not_163_out, OP4);
  not not_164 (not_164_out, OP3);
  not not_165 (not_165_out, OP2);
  not not_166 (not_166_out, F14);
  not not_167 (not_167_out, F13);
  not not_168 (not_168_out, OP4);
  not not_169 (not_169_out, OP3);
  not not_170 (not_170_out, OP2);
  not not_171 (not_171_out, F30);
  not not_172 (not_172_out, F25);
  not not_173 (not_173_out, F12);
  not not_174 (not_174_out, OP6);
  not not_175 (not_175_out, OP3);
  not not_176 (not_176_out, OP2);
  not not_177 (not_177_out, F30);
  not not_178 (not_178_out, F25);
  not not_179 (not_179_out, F14);
  not not_180 (not_180_out, F12);
  not not_181 (not_181_out, OP6);
  not not_182 (not_182_out, OP3);
  not not_183 (not_183_out, OP2);
  not not_184 (not_184_out, F30);
  not not_185 (not_185_out, F25);
  not not_186 (not_186_out, F14);
  not not_187 (not_187_out, OP6);
  not not_188 (not_188_out, OP3);
  not not_189 (not_189_out, OP2);
  not not_190 (not_190_out, F12);
  not not_191 (not_191_out, OP6);
  not not_192 (not_192_out, OP5);
  not not_193 (not_193_out, OP3);
  not not_194 (not_194_out, OP2);
  not not_195 (not_195_out, F13);
  not not_196 (not_196_out, F12);
  not not_197 (not_197_out, OP6);
  not not_198 (not_198_out, OP5);
  not not_199 (not_199_out, OP3);
  not not_200 (not_200_out, OP2);
  not not_201 (not_201_out, F14);
  not not_202 (not_202_out, F12);
  not not_203 (not_203_out, OP6);
  not not_204 (not_204_out, OP5);
  not not_205 (not_205_out, OP3);
  not not_206 (not_206_out, OP2);
  and and_1 (and_1_out, not_1_out, not_2_out, not_3_out, not_4_out, not_5_out, not_6_out, OP5, OP4, not_7_out, not_8_out);
  and and_2 (and_2_out, not_9_out, not_10_out, F14, F13, F12, not_11_out, OP5, OP4, not_12_out, not_13_out);
  and and_3 (and_3_out, not_14_out, not_15_out, not_16_out, F13, not_17_out, not_18_out, OP5, OP4, not_19_out, not_20_out);
  and and_4 (and_4_out, not_21_out, not_22_out, not_23_out, not_24_out, not_25_out, OP4, not_26_out, not_27_out);
  and and_5 (and_5_out, F14, F13, F12, not_28_out, not_29_out, OP4, not_30_out, not_31_out);
  and and_6 (and_6_out, F14, not_32_out, not_33_out, not_34_out, not_35_out, OP4, not_36_out, not_37_out);
  and and_7 (and_7_out, not_38_out, F13, not_39_out, not_40_out, not_41_out, OP4, not_42_out, not_43_out);
  and and_8 (and_8_out, F30, not_44_out, F14, not_45_out, F12, not_46_out, not_47_out, OP4, not_48_out, not_49_out);
  and and_9 (and_9_out, not_50_out, F13, not_51_out, not_52_out, not_53_out, not_54_out, not_55_out, not_56_out);
  and and_10 (and_10_out, not_57_out, F13, not_58_out, not_59_out, OP5, not_60_out, not_61_out, not_62_out);
  and and_11 (and_11_out, F30, not_63_out, not_64_out, not_65_out, not_66_out, not_67_out, OP5, OP4, not_68_out, not_69_out);
  and and_12 (and_12_out, not_70_out, not_71_out, F14, F13, F12, not_72_out, OP5, OP4, not_73_out, not_74_out);
  and and_13 (and_13_out, not_75_out, not_76_out, not_77_out, F13, not_78_out, not_79_out, OP5, OP4, not_80_out, not_81_out);
  and and_14 (and_14_out, F14, F13, F12, not_82_out, not_83_out, OP4, not_84_out, not_85_out);
  and and_15 (and_15_out, not_86_out, F13, not_87_out, not_88_out, not_89_out, OP4, not_90_out, not_91_out);
  and and_16 (and_16_out, not_92_out, not_93_out, F14, not_94_out, F12, not_95_out, not_96_out, OP4, not_97_out, not_98_out);
  and and_17 (and_17_out, not_99_out, not_100_out, not_101_out, OP6, OP5, not_102_out, not_103_out, not_104_out);
  and and_18 (and_18_out, not_105_out, not_106_out, F12, OP6, OP5, not_107_out, not_108_out, not_109_out);
  and and_19 (and_19_out, not_110_out, not_111_out, not_112_out, not_113_out, not_114_out, not_115_out, OP5, OP4, not_116_out, not_117_out);
  and and_20 (and_20_out, F30, not_118_out, not_119_out, not_120_out, not_121_out, not_122_out, OP5, OP4, not_123_out, not_124_out);
  and and_21 (and_21_out, not_125_out, not_126_out, F14, F13, F12, not_127_out, OP5, OP4, not_128_out, not_129_out);
  and and_22 (and_22_out, not_130_out, not_131_out, not_132_out, F13, F12, not_133_out, OP5, OP4, not_134_out, not_135_out);
  and and_23 (and_23_out, not_136_out, not_137_out, not_138_out, not_139_out, not_140_out, OP4, not_141_out, not_142_out);
  and and_24 (and_24_out, F14, F13, F12, not_143_out, not_144_out, OP4, not_145_out, not_146_out);
  and and_25 (and_25_out, not_147_out, F13, not_148_out, not_149_out, not_150_out, not_151_out, not_152_out, not_153_out);
  and and_26 (and_26_out, not_154_out, F13, not_155_out, not_156_out, OP5, not_157_out, not_158_out, not_159_out);
  and and_27 (and_27_out, not_160_out, not_161_out, not_162_out, OP6, OP5, not_163_out, not_164_out, not_165_out);
  and and_28 (and_28_out, not_166_out, not_167_out, F12, OP6, OP5, not_168_out, not_169_out, not_170_out);
  and and_29 (and_29_out, not_171_out, not_172_out, F14, F13, not_173_out, not_174_out, OP5, OP4, not_175_out, not_176_out);
  and and_30 (and_30_out, not_177_out, not_178_out, not_179_out, F13, not_180_out, not_181_out, OP5, OP4, not_182_out, not_183_out);
  and and_31 (and_31_out, not_184_out, not_185_out, not_186_out, F13, F12, not_187_out, OP5, OP4, not_188_out, not_189_out);
  and and_32 (and_32_out, F14, F13, not_190_out, not_191_out, not_192_out, OP4, not_193_out, not_194_out);
  and and_33 (and_33_out, F14, not_195_out, not_196_out, not_197_out, not_198_out, OP4, not_199_out, not_200_out);
  and and_34 (and_34_out, not_201_out, F13, not_202_out, not_203_out, not_204_out, OP4, not_205_out, not_206_out);
  or or_1 (S0, and_1_out, and_2_out, and_3_out, and_4_out, and_5_out, and_6_out, and_7_out, and_8_out, and_9_out, and_10_out);
  or or_2 (S1, and_11_out, and_12_out, and_13_out, and_14_out, and_15_out, and_16_out, and_17_out, and_18_out);
  or or_3 (S2, and_19_out, and_20_out, and_21_out, and_22_out, and_23_out, and_24_out, and_25_out, and_26_out, and_27_out, and_28_out);
  or or_4 (S3, and_29_out, and_30_out, and_31_out, and_32_out, and_33_out, and_34_out);
endmodule

// 控制信号生成
module \控制信号自动生成  (
  input  OP2,
  input  OP3,
  input  OP4,
  input  OP5,
  input  OP6,
  input  F12,
  input  F13,
  input  F14,
  input  F25,
  input  F30,
  input  IR21,
  output MemToReg,
  output MemWrite,
  output ALU_SRC,
  output RegWrite,
  output ecall,
  output S_Type,
  output BEQ,
  output BNE,
  output JALR,
  output JAL,
  output uret,
  output irs,
  output irc
);

  wire and_3_out, and_4_out, and_5_out, and_6_out, and_7_out, and_8_out, and_9_out, and_10_out, and_11_out,
       and_12_out, and_13_out, and_14_out, and_15_out, and_16_out, and_17_out, and_18_out, and_19_out,
       and_20_out, and_21_out, and_22_out, and_23_out, and_24_out, and_25_out, and_26_out, and_27_out,
       and_28_out, and_29_out, not_1_out, not_2_out, not_3_out, not_4_out, not_5_out, not_6_out, not_7_out,
       not_8_out, not_9_out, not_10_out, not_11_out, not_12_out, not_13_out, not_14_out, not_15_out,
       not_16_out, not_17_out, not_18_out, not_19_out, not_20_out, not_21_out, not_22_out, not_23_out,
       not_24_out, not_25_out, not_26_out, not_27_out, not_28_out, not_29_out, not_30_out, not_31_out,
       not_32_out, not_33_out, not_34_out, not_35_out, not_36_out, not_37_out, not_38_out, not_39_out,
       not_40_out, not_41_out, not_42_out, not_43_out, not_44_out, not_45_out, not_46_out, not_47_out,
       not_48_out, not_49_out, not_50_out, not_51_out, not_52_out, not_53_out, not_54_out, not_55_out,
       not_56_out, not_57_out, not_58_out, not_59_out, not_60_out, not_61_out, not_62_out, not_63_out,
       not_64_out, not_65_out, not_66_out, not_67_out, not_68_out, not_69_out, not_70_out, not_71_out,
       not_72_out, not_73_out, not_74_out, not_75_out, not_76_out, not_77_out, not_78_out, not_79_out,
       not_80_out, not_81_out, not_82_out, not_83_out, not_84_out, not_85_out, not_86_out, not_87_out,
       not_88_out, not_89_out, not_90_out, not_91_out, not_92_out, not_93_out, not_94_out, not_95_out,
       not_96_out, not_97_out, not_98_out, not_99_out, not_100_out, not_101_out, not_102_out, not_103_out,
       not_104_out, not_105_out, not_106_out, not_107_out, not_108_out, not_109_out, not_110_out,
       not_111_out, not_112_out, not_113_out, not_114_out, not_115_out, not_116_out, not_117_out,
       not_118_out, not_119_out, not_120_out, not_121_out, not_122_out, not_123_out, not_124_out,
       not_125_out, not_126_out, not_127_out, not_128_out, not_129_out, not_130_out, not_131_out,
       not_132_out, not_133_out, not_134_out, not_135_out, not_136_out, not_137_out, not_138_out,
       not_139_out, not_140_out, not_141_out, not_142_out, not_143_out, not_144_out, not_145_out,
       not_146_out, not_147_out, not_148_out, not_149_out, not_150_out, not_151_out, not_152_out,
       not_153_out, not_154_out, not_155_out, not_156_out, not_157_out, not_158_out, not_159_out,
       not_160_out, not_161_out, not_162_out, not_163_out, not_164_out, not_165_out, not_166_out,
       not_167_out, not_168_out, not_169_out, not_170_out, not_171_out, not_172_out, not_173_out,
       not_174_out, not_175_out, not_176_out, not_177_out, not_178_out, not_179_out, not_180_out,
       not_181_out, not_182_out, not_183_out, not_184_out, not_185_out, not_186_out, not_187_out,
       not_188_out, not_189_out, not_190_out, not_191_out, not_192_out, not_193_out, not_194_out,
       not_195_out, not_196_out, not_197_out, not_198_out, not_199_out, not_200_out, not_201_out,
       not_202_out, not_203_out, not_204_out, not_205_out, not_206_out, not_207_out, not_208_out,
       not_209_out, not_210_out, not_211_out, not_212_out, not_213_out, not_214_out, not_215_out,
       not_216_out, not_217_out, not_218_out, not_219_out;

  not not_1 (not_1_out, F14);
  not not_2 (not_2_out, F12);
  not not_3 (not_3_out, OP6);
  not not_4 (not_4_out, OP5);
  not not_5 (not_5_out, OP4);
  not not_6 (not_6_out, OP3);
  not not_7 (not_7_out, OP2);
  not not_8 (not_8_out, OP2);
  not not_9 (not_9_out, OP3);
  not not_10 (not_10_out, OP4);
  not not_11 (not_11_out, OP6);
  not not_12 (not_12_out, F12);
  not not_13 (not_13_out, F14);
  not not_14 (not_14_out, F14);
  not not_15 (not_15_out, F13);
  not not_16 (not_16_out, F12);
  not not_17 (not_17_out, OP6);
  not not_18 (not_18_out, OP5);
  not not_19 (not_19_out, OP3);
  not not_20 (not_20_out, OP2);
  not not_21 (not_21_out, OP6);
  not not_22 (not_22_out, OP5);
  not not_23 (not_23_out, OP3);
  not not_24 (not_24_out, OP2);
  not not_25 (not_25_out, F12);
  not not_26 (not_26_out, OP6);
  not not_27 (not_27_out, OP5);
  not not_28 (not_28_out, OP3);
  not not_29 (not_29_out, OP2);
  not not_30 (not_30_out, F13);
  not not_31 (not_31_out, F12);
  not not_32 (not_32_out, OP6);
  not not_33 (not_33_out, OP5);
  not not_34 (not_34_out, OP3);
  not not_35 (not_35_out, OP2);
  not not_36 (not_36_out, F14);
  not not_37 (not_37_out, F12);
  not not_38 (not_38_out, OP6);
  not not_39 (not_39_out, OP5);
  not not_40 (not_40_out, OP3);
  not not_41 (not_41_out, OP2);
  not not_42 (not_42_out, F30);
  not not_43 (not_43_out, F25);
  not not_44 (not_44_out, F14);
  not not_45 (not_45_out, F13);
  not not_46 (not_46_out, OP6);
  not not_47 (not_47_out, OP5);
  not not_48 (not_48_out, OP3);
  not not_49 (not_49_out, OP2);
  not not_50 (not_50_out, F30);
  not not_51 (not_51_out, F25);
  not not_52 (not_52_out, F13);
  not not_53 (not_53_out, OP6);
  not not_54 (not_54_out, OP5);
  not not_55 (not_55_out, OP3);
  not not_56 (not_56_out, OP2);
  not not_57 (not_57_out, F25);
  not not_58 (not_58_out, F13);
  not not_59 (not_59_out, OP6);
  not not_60 (not_60_out, OP5);
  not not_61 (not_61_out, OP3);
  not not_62 (not_62_out, OP2);
  not not_63 (not_63_out, F14);
  not not_64 (not_64_out, F12);
  not not_65 (not_65_out, OP6);
  not not_66 (not_66_out, OP5);
  not not_67 (not_67_out, OP4);
  not not_68 (not_68_out, OP3);
  not not_69 (not_69_out, OP2);
  not not_70 (not_70_out, F14);
  not not_71 (not_71_out, F12);
  not not_72 (not_72_out, OP6);
  not not_73 (not_73_out, OP4);
  not not_74 (not_74_out, OP3);
  not not_75 (not_75_out, OP2);
  not not_76 (not_76_out, F30);
  not not_77 (not_77_out, F25);
  not not_78 (not_78_out, F14);
  not not_79 (not_79_out, F13);
  not not_80 (not_80_out, F12);
  not not_81 (not_81_out, OP6);
  not not_82 (not_82_out, OP3);
  not not_83 (not_83_out, OP2);
  not not_84 (not_84_out, F25);
  not not_85 (not_85_out, F14);
  not not_86 (not_86_out, F13);
  not not_87 (not_87_out, F12);
  not not_88 (not_88_out, OP6);
  not not_89 (not_89_out, OP3);
  not not_90 (not_90_out, OP2);
  not not_91 (not_91_out, F30);
  not not_92 (not_92_out, F25);
  not not_93 (not_93_out, OP6);
  not not_94 (not_94_out, OP3);
  not not_95 (not_95_out, OP2);
  not not_96 (not_96_out, F30);
  not not_97 (not_97_out, F25);
  not not_98 (not_98_out, F12);
  not not_99 (not_99_out, OP6);
  not not_100 (not_100_out, OP3);
  not not_101 (not_101_out, OP2);
  not not_102 (not_102_out, F30);
  not not_103 (not_103_out, F25);
  not not_104 (not_104_out, F14);
  not not_105 (not_105_out, F12);
  not not_106 (not_106_out, OP6);
  not not_107 (not_107_out, OP3);
  not not_108 (not_108_out, OP2);
  not not_109 (not_109_out, F30);
  not not_110 (not_110_out, F25);
  not not_111 (not_111_out, F14);
  not not_112 (not_112_out, OP6);
  not not_113 (not_113_out, OP3);
  not not_114 (not_114_out, OP2);
  not not_115 (not_115_out, F14);
  not not_116 (not_116_out, F13);
  not not_117 (not_117_out, F12);
  not not_118 (not_118_out, OP6);
  not not_119 (not_119_out, OP5);
  not not_120 (not_120_out, OP3);
  not not_121 (not_121_out, OP2);
  not not_122 (not_122_out, OP6);
  not not_123 (not_123_out, OP5);
  not not_124 (not_124_out, OP3);
  not not_125 (not_125_out, OP2);
  not not_126 (not_126_out, F12);
  not not_127 (not_127_out, OP6);
  not not_128 (not_128_out, OP5);
  not not_129 (not_129_out, OP3);
  not not_130 (not_130_out, OP2);
  not not_131 (not_131_out, F13);
  not not_132 (not_132_out, F12);
  not not_133 (not_133_out, OP6);
  not not_134 (not_134_out, OP5);
  not not_135 (not_135_out, OP3);
  not not_136 (not_136_out, OP2);
  not not_137 (not_137_out, F14);
  not not_138 (not_138_out, F12);
  not not_139 (not_139_out, OP6);
  not not_140 (not_140_out, OP5);
  not not_141 (not_141_out, OP3);
  not not_142 (not_142_out, OP2);
  not not_143 (not_143_out, F30);
  not not_144 (not_144_out, F25);
  not not_145 (not_145_out, F14);
  not not_146 (not_146_out, F13);
  not not_147 (not_147_out, OP6);
  not not_148 (not_148_out, OP5);
  not not_149 (not_149_out, OP3);
  not not_150 (not_150_out, OP2);
  not not_151 (not_151_out, F30);
  not not_152 (not_152_out, F25);
  not not_153 (not_153_out, F13);
  not not_154 (not_154_out, OP6);
  not not_155 (not_155_out, OP5);
  not not_156 (not_156_out, OP3);
  not not_157 (not_157_out, OP2);
  not not_158 (not_158_out, F25);
  not not_159 (not_159_out, F13);
  not not_160 (not_160_out, OP6);
  not not_161 (not_161_out, OP5);
  not not_162 (not_162_out, OP3);
  not not_163 (not_163_out, OP2);
  not not_164 (not_164_out, F14);
  not not_165 (not_165_out, F12);
  not not_166 (not_166_out, OP6);
  not not_167 (not_167_out, OP5);
  not not_168 (not_168_out, OP4);
  not not_169 (not_169_out, OP3);
  not not_170 (not_170_out, OP2);
  not not_171 (not_171_out, OP4);
  not not_172 (not_172_out, F14);
  not not_173 (not_173_out, F13);
  not not_174 (not_174_out, F12);
  not not_175 (not_175_out, OP4);
  not not_176 (not_176_out, OP3);
  not not_177 (not_177_out, F30);
  not not_178 (not_178_out, F25);
  not not_179 (not_179_out, F14);
  not not_180 (not_180_out, F13);
  not not_181 (not_181_out, F12);
  not not_182 (not_182_out, IR21);
  not not_183 (not_183_out, OP3);
  not not_184 (not_184_out, OP2);
  not not_185 (not_185_out, OP2);
  not not_186 (not_186_out, OP3);
  not not_187 (not_187_out, OP4);
  not not_188 (not_188_out, OP6);
  not not_189 (not_189_out, F12);
  not not_190 (not_190_out, F14);
  not not_191 (not_191_out, F14);
  not not_192 (not_192_out, F13);
  not not_193 (not_193_out, F12);
  not not_194 (not_194_out, OP4);
  not not_195 (not_195_out, OP3);
  not not_196 (not_196_out, OP2);
  not not_197 (not_197_out, F14);
  not not_198 (not_198_out, F13);
  not not_199 (not_199_out, OP4);
  not not_200 (not_200_out, OP3);
  not not_201 (not_201_out, OP2);
  not not_202 (not_202_out, F14);
  not not_203 (not_203_out, F13);
  not not_204 (not_204_out, F12);
  not not_205 (not_205_out, OP4);
  not not_206 (not_206_out, OP3);
  not not_207 (not_207_out, OP4);
  not not_208 (not_208_out, F30);
  not not_209 (not_209_out, F25);
  not not_210 (not_210_out, F14);
  not not_211 (not_211_out, F13);
  not not_212 (not_212_out, F12);
  not not_213 (not_213_out, OP3);
  not not_214 (not_214_out, OP2);
  not not_215 (not_215_out, F12);
  not not_216 (not_216_out, OP3);
  not not_217 (not_217_out, OP2);
  not not_218 (not_218_out, OP3);
  not not_219 (not_219_out, OP2);
  and and_1 (MemToReg, not_1_out, F13, not_2_out, not_3_out, not_4_out, not_5_out, not_6_out, not_7_out);
  and and_2 (MemWrite, not_8_out, not_9_out, not_10_out, OP5, not_11_out, not_12_out, F13, not_13_out);
  and and_3 (and_3_out, not_14_out, not_15_out, not_16_out, not_17_out, not_18_out, OP4, not_19_out, not_20_out);
  and and_4 (and_4_out, F14, F13, F12, not_21_out, not_22_out, OP4, not_23_out, not_24_out);
  and and_5 (and_5_out, F14, F13, not_25_out, not_26_out, not_27_out, OP4, not_28_out, not_29_out);
  and and_6 (and_6_out, F14, not_30_out, not_31_out, not_32_out, not_33_out, OP4, not_34_out, not_35_out);
  and and_7 (and_7_out, not_36_out, F13, not_37_out, not_38_out, not_39_out, OP4, not_40_out, not_41_out);
  and and_8 (and_8_out, not_42_out, not_43_out, not_44_out, not_45_out, F12, not_46_out, not_47_out, OP4, not_48_out, not_49_out);
  and and_9 (and_9_out, not_50_out, not_51_out, F14, not_52_out, F12, not_53_out, not_54_out, OP4, not_55_out, not_56_out);
  and and_10 (and_10_out, F30, not_57_out, F14, not_58_out, F12, not_59_out, not_60_out, OP4, not_61_out, not_62_out);
  and and_11 (and_11_out, not_63_out, F13, not_64_out, not_65_out, not_66_out, not_67_out, not_68_out, not_69_out);
  and and_12 (and_12_out, not_70_out, F13, not_71_out, not_72_out, OP5, not_73_out, not_74_out, not_75_out);
  and and_13 (and_13_out, not_76_out, not_77_out, not_78_out, not_79_out, not_80_out, not_81_out, OP5, OP4, not_82_out, not_83_out);
  and and_14 (and_14_out, F30, not_84_out, not_85_out, not_86_out, not_87_out, not_88_out, OP5, OP4, not_89_out, not_90_out);
  and and_15 (and_15_out, not_91_out, not_92_out, F14, F13, F12, not_93_out, OP5, OP4, not_94_out, not_95_out);
  and and_16 (and_16_out, not_96_out, not_97_out, F14, F13, not_98_out, not_99_out, OP5, OP4, not_100_out, not_101_out);
  and and_17 (and_17_out, not_102_out, not_103_out, not_104_out, F13, not_105_out, not_106_out, OP5, OP4, not_107_out, not_108_out);
  and and_18 (and_18_out, not_109_out, not_110_out, not_111_out, F13, F12, not_112_out, OP5, OP4, not_113_out, not_114_out);
  and and_19 (and_19_out, not_115_out, not_116_out, not_117_out, not_118_out, not_119_out, OP4, not_120_out, not_121_out);
  and and_20 (and_20_out, F14, F13, F12, not_122_out, not_123_out, OP4, not_124_out, not_125_out);
  and and_21 (and_21_out, F14, F13, not_126_out, not_127_out, not_128_out, OP4, not_129_out, not_130_out);
  and and_22 (and_22_out, F14, not_131_out, not_132_out, not_133_out, not_134_out, OP4, not_135_out, not_136_out);
  and and_23 (and_23_out, not_137_out, F13, not_138_out, not_139_out, not_140_out, OP4, not_141_out, not_142_out);
  and and_24 (and_24_out, not_143_out, not_144_out, not_145_out, not_146_out, F12, not_147_out, not_148_out, OP4, not_149_out, not_150_out);
  and and_25 (and_25_out, not_151_out, not_152_out, F14, not_153_out, F12, not_154_out, not_155_out, OP4, not_156_out, not_157_out);
  and and_26 (and_26_out, F30, not_158_out, F14, not_159_out, F12, not_160_out, not_161_out, OP4, not_162_out, not_163_out);
  and and_27 (and_27_out, not_164_out, F13, not_165_out, not_166_out, not_167_out, not_168_out, not_169_out, not_170_out);
  and and_28 (and_28_out, OP6, OP5, not_171_out, OP3, OP2);
  and and_29 (and_29_out, not_172_out, not_173_out, not_174_out, OP6, OP5, not_175_out, not_176_out, OP2);
  and and_30 (ecall, not_177_out, not_178_out, not_179_out, not_180_out, not_181_out, not_182_out, OP6, OP5, OP4, not_183_out, not_184_out);
  and and_31 (S_Type, not_185_out, not_186_out, not_187_out, OP5, not_188_out, not_189_out, F13, not_190_out);
  and and_32 (BEQ, not_191_out, not_192_out, not_193_out, OP6, OP5, not_194_out, not_195_out, not_196_out);
  and and_33 (BNE, not_197_out, not_198_out, F12, OP6, OP5, not_199_out, not_200_out, not_201_out);
  and and_34 (JALR, not_202_out, not_203_out, not_204_out, OP6, OP5, not_205_out, not_206_out, OP2);
  and and_35 (JAL, OP6, OP5, not_207_out, OP3, OP2);
  and and_36 (uret, not_208_out, not_209_out, not_210_out, not_211_out, not_212_out, IR21, OP6, OP5, OP4, not_213_out, not_214_out);
  and and_37 (irs, F14, F13, not_215_out, OP6, OP5, OP4, not_216_out, not_217_out);
  and and_38 (irc, F14, F13, F12, OP6, OP5, OP4, not_218_out, not_219_out);
  or or_1 (ALU_SRC, and_3_out, and_4_out, and_5_out, and_6_out, and_7_out, and_8_out, and_9_out, and_10_out, and_11_out, and_12_out);
  or or_2 (RegWrite, and_13_out, and_14_out, and_15_out, and_16_out, and_17_out, and_18_out, and_19_out, and_20_out, and_21_out, and_22_out, and_23_out, and_24_out, and_25_out, and_26_out, and_27_out, and_28_out, and_29_out);
endmodule

// ALU
module ALU (
  input  [31:0] X,
  input  [31:0] Y,
  input  [3:0] AluOP,
  output out_4,
  output Equal,
  output out_6,
  output [31:0] Result,
  output [31:0] Result_2
);

  wire [0:0] comparator_1_lt, comparator_2_lt;
  wire [31:0] adder_1_out, AND_out, divider_1_out, divider_1_rem, multiplier_1_cout, multiplier_1_out,
       NOR_out, OR_out, shifter_1_out, shifter_2_out, shifter_3_out, subtractor_1_out, XOR_out;

  assign AND_out = X & Y;  // AND_Gate AND, 32 bits wide
  assign OR_out = X | Y;  // OR_Gate OR, 32 bits wide
  Shifter #(.width(32), .shift("ll")) shifter_1 (.in(X), .\dist (Y[4:0]), .out(shifter_1_out));
  Shifter #(.width(32), .shift("ar")) shifter_2 (.in(X), .\dist (Y[4:0]), .out(shifter_2_out));
  Shifter #(.width(32), .shift("lr")) shifter_3 (.in(X), .\dist (Y[4:0]), .out(shifter_3_out));
  Multiplier #(.width(32)) multiplier_1 (.a(X), .b(Y), .out(multiplier_1_out), .cout(multiplier_1_cout));  // open: cin
  Divider #(.width(32)) divider_1 (.a(X), .b(Y), .out(divider_1_out), .rem(divider_1_rem));  // open: upper
  Adder #(.width(32)) adder_1 (.a(X), .b(Y), .out(adder_1_out));  // open: cin, cout
  Subtractor #(.width(32)) subtractor_1 (.a(X), .b(Y), .out(subtractor_1_out));  // open: bin, bout
  assign XOR_out = X ^ Y;  // XOR_Gate XOR, 32 bits wide
  assign NOR_out = ~(X | Y);  // NOR_Gate NOR, 32 bits wide
  Comparator #(.width(32), .mode("twosComplement")) comparator_1 (
    .a(X), .b(Y), .eq(Equal), .lt(comparator_1_lt[0]));  // open: gt
  Comparator #(.width(32), .mode("unsigned")) comparator_2 (.a(X), .b(Y), .lt(comparator_2_lt[0]));  // open: gt, eq
  Multiplexer #(.select(4), .width(32), .disabled("Z"), .enable("false")) multiplexer_1 (
    .in0(shifter_1_out), .in1(shifter_2_out), .in2(shifter_3_out), .in3(multiplier_1_out),
    .in4(divider_1_out), .in5(adder_1_out), .in6(subtractor_1_out), .in7(AND_out), .in8(OR_out),
    .in9(XOR_out), .in10(NOR_out), .in11({{31{1'b0}}, comparator_1_lt[0]}),
    .in12({{31{1'b0}}, comparator_2_lt[0]}), .in13({32{1'b0}}), .in14({32{1'b0}}), .in15({32{1'b0}}),
    .out(Result), .sel(AluOP));
  Multiplexer #(.select(4), .width(32), .disabled("Z"), .enable("false")) multiplexer_2 (
    .in0({32{1'b0}}), .in1({32{1'b0}}), .in2({32{1'b0}}), .in3(multiplier_1_cout), .in4(divider_1_rem),
    .in5({32{1'b0}}), .in6({32{1'b0}}), .in7({32{1'b0}}), .in8({32{1'b0}}), .in9({32{1'b0}}),
    .in10({32{1'b0}}), .in11({32{1'b0}}), .in12({32{1'b0}}), .in13({32{1'b0}}), .in14({32{1'b0}}),
    .in15({32{1'b0}}), .out(Result_2), .sel(AluOP));
  Multiplexer #(.select(4), .width(1), .disabled("Z"), .enable("false")) multiplexer_3 (
    .in0(1'b0), .in1(1'b0), .in2(1'b0), .in3(1'b0), .in4(1'b0), .in5(1'b0), .in6(1'b0), .in7(1'b0),
    .in8(1'b0), .in9(1'b0), .in10(1'b0), .in11(comparator_1_lt[0]), .in12(comparator_2_lt[0]), .in13(1'b0),
    .in14(1'b0), .in15(1'b0), .out(out_6), .sel(AluOP));
  not not_1 (out_4, out_6);

  // Other names for the same wires on the sheet: Result2[31:0] = Result_2; S[3:0] = AluOP; tunnel = out_6;
  //   tunnel_t = out_4

  // Notes on the sheet:
  //   不要改变此引脚区域内容，也不要改变ALU封装形式
  //   输入引脚
  //   输出引脚
endmodule

module Regifile (
  input  [31:0] Din,
  input  Clk,
  input  WE,
  input  [4:0] R1_num,
  input  [4:0] W_num,
  input  [4:0] R2_num,
  output [31:0] R1,
  output [31:0] R2
);

  // RegisterFile registerfile_1: pin names not known; wires that end beside it: Din, Clk, WE, W_num, R1_num, R2_num, R1, R2
endmodule

module \理想流水线  (
  output RegWrite,
  output MemWrite,
  output [31:0] IF_PC,
  output [31:0] ID_PC,
  output [31:0] EX_PC,
  output [31:0] M_PC,
  output [31:0] WB_PC,
  output [31:0] RDin,
  output [31:0] MDin,
  output [31:0] LedData
);

  wire CLK, clock_1_out, clock_2_out, comparator_1_eq, comparator_1_lt, comparator_2_eq, d_ff_1_q, dhex, EN,
       ex_mem_1_p11, ex_mem_1_p16, ex_mem_1_p17, ex_mem_1_p19, Go, halt, id_ex_1_ecall_2, id_ex_1_mem_2,
       id_ex_1_rw_2, id_ex_1_wb_2, IR1, IR2, IR3, mem_wb_1_ecall_2, mem_wb_1_rw_2, nand_1_out, not_1_out,
       not_2_out, RST, W1, W2, W3, \单周期硬布线控制器_1_alu_src , \单周期硬布线控制器_1_ecall , \单周期硬布线控制器_1_memtoreg ,
       \单周期硬布线控制器_1_memwrite , \单周期硬布线控制器_1_regwrite , \单周期硬布线控制器_1_s_type ;
  wire [3:0] id_ex_1_aluop_2, \单周期硬布线控制器_1_alu_op ;
  wire [4:0] ex_mem_1_p24, id_ex_1_rd_2, multiplexer_1_out, multiplexer_2_out, RD;
  wire [12:0] CNT_num;
  wire [15:0] \LoadUse次数 , \总周期数 , \插入气泡数 , \无条件分支数 , \条件分支成功数 ;
  wire [31:0] adder_1_out, alu_1_result, bit_extender_1_out, bit_extender_2_out, ecallA, ecallV, EX_IR,
       ex_mem_1_p22, id_ex_1_imm_2, id_ex_1_r1_2, id_ex_1_r2_2, ID_IR, IF_IR, MEM_IR, mem_wb_1_alu_2,
       mem_wb_1_m_2, multiplexer_3_out, multiplexer_4_out, ram_1_data, WB_IR;

  Button \u_总复位  (.out(RST));
  Button _1 (.out(IR1));
  Button _2 (.out(IR2));
  Button _3 (.out(IR3));
  // Probe on \总周期数 
  // Probe on \总周期数 
  not not_1 (not_1_out, halt);
  Button \u_继续运行  (.out(Go));
  LED #(.active("true")) led_1 (.in(W1));
  LED #(.active("true")) led_2 (.in(W2));
  LED #(.active("true")) led_3 (.in(W3));
  Register #(.width(32), .trigger("rising"), .Select("low")) PC (
    .D(adder_1_out), .en(EN), .Q(IF_PC), .clk(CLK), .clr(RST), .cs(1'b0), .preset(1'b0));
  or or_1 (EN, not_1_out, Go);
  Hex_Digit_Display hex_digit_display_1 (.value(LedData[31:28]));  // open: dp
  // Probe on IF_PC[19:0]
  // RiscV_Probe riscv_probe_1: pin names not known; wires that end beside it: IF_IR
  Hex_Digit_Display hex_digit_display_2 (.value(LedData[23:20]));  // open: dp
  Hex_Digit_Display hex_digit_display_3 (.value(LedData[27:24]));  // open: dp
  // Probe on ID_PC[19:0]
  // RiscV_Probe riscv_probe_2: pin names not known; wires that end beside it: ID_IR
  Adder #(.width(32)) adder_1 (.a(IF_PC), .b(32'h4), .out(adder_1_out));  // open: cin, cout
  Hex_Digit_Display hex_digit_display_4 (.value(LedData[15:12]));  // open: dp
  Hex_Digit_Display hex_digit_display_5 (.value(LedData[19:16]));  // open: dp
  ROM #(.addrWidth(10), .dataWidth(32), .Select("high")) rom_1 (.addr(IF_PC[11:2]), .data(IF_IR));
  Hex_Digit_Display hex_digit_display_6 (.value(LedData[11:8]));  // open: dp
  Hex_Digit_Display hex_digit_display_7 (.value(LedData[7:4]));  // open: dp
  Clock #(.highDuration(1), .lowDuration(1)) clock_1 (.out(clock_1_out));
  // Probe on EX_PC[19:0]
  // RiscV_Probe riscv_probe_3: pin names not known; wires that end beside it: clock_1_out, EX_IR, CLK
  IF_ID if_id_1 (.IR(IF_IR), .PC(IF_PC), .ID_IR(ID_IR), .ID_PC(ID_PC), .EN(EN), .CLK(CLK), .RST(RST), .NOP(1'b0));
  Hex_Digit_Display hex_digit_display_8 (.value(LedData[3:0]));  // open: dp
  // Probe on \总周期数 
  // Probe on M_PC[19:0]
  // RiscV_Probe riscv_probe_4: pin names not known; wires that end beside it: MEM_IR
  \单周期硬布线控制器  \u_单周期硬布线控制器_1  (
    .Funct({ID_IR[30], ID_IR[25], ID_IR[14:12]}), .OP(ID_IR[6:2]), .ALU_OP(\单周期硬布线控制器_1_alu_op ),
    .MemToReg(\单周期硬布线控制器_1_memtoreg ), .MemWrite(\单周期硬布线控制器_1_memwrite ), .ALU_SRC(\单周期硬布线控制器_1_alu_src ),
    .RegWrite(\单周期硬布线控制器_1_regwrite ), .ecall(\单周期硬布线控制器_1_ecall ), .S_type(\单周期硬布线控制器_1_s_type ));  // open: Jalr, Beq, JAL, Bne, IR21, uret, irs, irc
  assign bit_extender_1_out = {{20{ID_IR[31]}}, ID_IR[31:20]};  // Bit_Extender bit_extender_1
  assign bit_extender_2_out = {{20{ID_IR[31]}}, {ID_IR[31:25], ID_IR[11:7]}};  // Bit_Extender bit_extender_2
  // Probe on \总周期数 
  // Probe on \无条件分支数 
  // Probe on \条件分支成功数 
  // Probe on \插入气泡数 
  // Probe on \LoadUse次数 
  Multiplexer #(.select(1), .width(5), .disabled("Z"), .enable("false")) multiplexer_1 (
    .in0(ID_IR[19:15]), .in1(5'b01010), .out(multiplexer_1_out), .sel(\单周期硬布线控制器_1_ecall ));
  Multiplexer #(.select(1), .width(5), .disabled("Z"), .enable("false")) multiplexer_2 (
    .in0(ID_IR[24:20]), .in1(5'b10001), .out(multiplexer_2_out), .sel(\单周期硬布线控制器_1_ecall ));
  // Probe on IF_PC[11:0]
  // Probe on WB_PC[19:0]
  // RiscV_Probe riscv_probe_5: pin names not known; wires that end beside it: WB_IR
  // Probe on ID_PC[11:0]
  // Probe on EX_PC[11:0]
  Regifile regifile_1 (
    .Din(RDin), .Clk(CLK), .R1(ecallA), .R2(ecallV), .WE(RegWrite), .W_num(RD), .R1_num(multiplexer_1_out),
    .R2_num(multiplexer_2_out));
  Multiplexer #(.select(1), .width(32), .disabled("Z"), .enable("false")) multiplexer_3 (
    .in0(bit_extender_1_out), .in1(bit_extender_2_out), .out(multiplexer_3_out), .sel(\单周期硬布线控制器_1_s_type ));
  // Probe on M_PC[11:0]
  D_Flip_Flop #(.trigger("high"), .Pre_Clr_Positions("LEGACY"), .NegatePresetClear("false"), .enable("true"), .NewFFLayout("false")) d_ff_1 (.Q(d_ff_1_q));  // open: clk, D, Qn, preset, en, reset
  // Probe on 13'hc
  Multiplexer #(.select(1), .width(32), .disabled("Z"), .enable("false")) multiplexer_4 (
    .in0(ecallV), .in1(multiplexer_3_out), .out(multiplexer_4_out), .sel(\单周期硬布线控制器_1_alu_src ));
  // Probe on WB_PC[11:0]
  Comparator #(.width(13), .mode("twosComplement")) comparator_1 (
    .a(CNT_num), .b(13'hc), .eq(comparator_1_eq), .lt(comparator_1_lt));  // open: gt
  Clock #(.highDuration(1), .lowDuration(1)) clock_2 (.out(clock_2_out));
  ID_EX id_ex_1 (
    .WB(\单周期硬布线控制器_1_memtoreg ), .Mem(\单周期硬布线控制器_1_memwrite ), .ALUop(\单周期硬布线控制器_1_alu_op ), .IR(ID_IR),
    .PC(ID_PC), .WB_2(id_ex_1_wb_2), .Mem_2(id_ex_1_mem_2), .ALUop_2(id_ex_1_aluop_2), .EX_IR(EX_IR),
    .EX_PC(EX_PC), .EN(EN), .RST(RST), .CLK(CLK), .R1(ecallA), .R1_2(id_ex_1_r1_2), .IMM(multiplexer_4_out),
    .IMM_2(id_ex_1_imm_2), .RW(\单周期硬布线控制器_1_regwrite ), .RW_2(id_ex_1_rw_2), .R2(ecallV),
    .R2_2(id_ex_1_r2_2), .RD(ID_IR[11:7]), .RD_2(id_ex_1_rd_2), .ecall(\单周期硬布线控制器_1_ecall ),
    .ecall_2(id_ex_1_ecall_2), .NOP(1'b0));  // open: jal, jal_2, jalr, jalr_2, beq, beq_2, bne, bne_2, AluS, AluS_2, rs1Ch, rs1Ch_2, rs2Ch, rs2Ch_2
  nand nand_1 (nand_1_out, d_ff_1_q, comparator_1_eq);
  Counter #(.width(13), .max('h1fff), .ongoal("stay"), .trigger("rising"), .behavior("old")) counter_1 (
    .count(comparator_1_lt), .Q(CNT_num), .clk(clock_2_out));  // open: load, D, carry, clr, preset
  ALU alu_1 (
    .X(id_ex_1_r1_2), .Y(id_ex_1_imm_2), .AluOP(id_ex_1_aluop_2), .Result(alu_1_result));  // open: Equal, Result_2, out_4, out_6
  assign CLK = nand_1_out ? clock_2_out : 1'bz;  // Controlled_Buffer controlled_buffer_1
  Pull_Resistor #(.pull(1)) pull_resistor_1 (.node(CLK));
  // EX_MEM ex_mem_1: pin names not known; wires that end beside it: id_ex_1_wb_2, id_ex_1_rw_2, id_ex_1_mem_2, id_ex_1_ecall_2, EX_IR, EX_PC, alu_1_result, id_ex_1_r2_2, id_ex_1_rd_2, 1'b0, ex_mem_1_p11, ex_mem_1_p11, EN, RST, CLK, ex_mem_1_p16, ex_mem_1_p17, MemWrite, ex_mem_1_p19, MEM_IR, M_PC, ex_mem_1_p22, MDin, ex_mem_1_p24
  RAM #(.addrWidth(10), .dataWidth(32), .bus("separate"), .Select("high")) ram_1 (
    .addr(ex_mem_1_p22[11:2]), .din(MDin), .data(ram_1_data), .str(MemWrite), .clk(CLK), .ld(ex_mem_1_p17));  // open: sel, clr
  MEM_WB mem_wb_1 (
    .WB(ex_mem_1_p16), .IR(MEM_IR), .PC(M_PC), .ALU(ex_mem_1_p22), .M(ram_1_data), .WB_2(RegWrite),
    .IR_2(WB_IR), .PC_2(WB_PC), .ALU_2(mem_wb_1_alu_2), .M_2(mem_wb_1_m_2), .EN(EN), .RST(RST), .CLK(CLK),
    .RW(ex_mem_1_p17), .RW_2(mem_wb_1_rw_2), .RD(ex_mem_1_p24), .RD_2(RD), .ecall(ex_mem_1_p19),
    .ecall_2(mem_wb_1_ecall_2), .NOP(1'b0));  // open: R1, R1_2, R2, R2_2
  Multiplexer #(.select(1), .width(32), .disabled("Z"), .enable("false")) multiplexer_5 (
    .in0(mem_wb_1_alu_2), .in1(mem_wb_1_m_2), .out(RDin), .sel(mem_wb_1_rw_2));
  Comparator #(.width(32), .mode("twosComplement")) comparator_2 (
    .a(ecallV), .b(32'h22), .eq(comparator_2_eq));  // open: gt, lt
  not not_2 (not_2_out, comparator_2_eq);
  Register #(.width(32), .trigger("rising"), .Select("low")) register_1 (
    .D(ecallA), .en(dhex), .Q(LedData), .clk(CLK), .clr(RST), .cs(1'b0), .preset(1'b0));
  and and_1 (halt, not_2_out, mem_wb_1_ecall_2);
  and and_2 (dhex, comparator_2_eq, mem_wb_1_ecall_2);

  // Other names for the same wires on the sheet: MEM_PC[31:0] = M_PC

  // Notes on the sheet:
  //   中断源
  //   时空图监测，可删除
  //   中断等待指示
  //   数码管输出
  //   contents of rom_1 (hex, n*v repeats v):
  //   413 493 913 993 46413 14e493 296913 39e993 842023 942223 1242423 1342623 a00893 493 913 993 73
  //   rs1
  //   rs2
  //   rd
  //   immI
  //   immS
  //   控制位
  //   流水调试日志用
  //   暂停节拍，不能为0
  //   戳工具置1进入计数暂停模式，ctrl+k时钟自动运行到对应节拍暂停
  //   ctrl+k关闭时钟连续运行，将控制位置零，进入单步调试模式调试
  //   用这个时钟源需要去掉电路中的其他时钟源
  //   可计数暂停的时钟源
  //   为方便自动评测，需要输出流水线各段保存的PC值，注意是PC不是PC+4，另外ID段寄存器写入信息，Mem段内存写入信息也要输出
endmodule

module \气泡流水线  (
  output RegWrite,
  output MemWrite,
  output [31:0] IF_PC,
  output [31:0] ID_PC,
  output [31:0] EX_PC,
  output [31:0] M_PC,
  output [31:0] WB_PC,
  output [31:0] RDin,
  output [31:0] MDin,
  output [31:0] LedData
);

  wire alu_1_equal, and_1_out, and_2_out, and_3_out, and_4_out, and_5_out, CLK, clock_1_out, clock_2_out,
       comparator_1_eq, comparator_1_lt, comparator_2_eq, d_ff_1_q, dhex, EN, ex_mem_1_ecall_2,
       ex_mem_1_rw_2, ex_mem_1_wb_2, Go, halt, id_ex_1_alus_2, id_ex_1_beq_2, id_ex_1_bne_2, id_ex_1_ecall_2,
       id_ex_1_jal_2, id_ex_1_jalr_2, id_ex_1_mem_2, id_ex_1_rw_2, id_ex_1_wb_2, IR1, IR2, IR3, JMP,
       mem_wb_1_ecall_2, mem_wb_1_wb_2, nand_1_out, ncf, nor_1_out, not_1_out, not_2_out, or_2_out, or_4_out,
       regconf_1_conf, regconf_2_conf, RST, W1, W2, W3, \单周期硬布线控制器_1_alu_src , \单周期硬布线控制器_1_beq ,
       \单周期硬布线控制器_1_bne , \单周期硬布线控制器_1_ecall , \单周期硬布线控制器_1_jal , \单周期硬布线控制器_1_jalr , \单周期硬布线控制器_1_memtoreg ,
       \单周期硬布线控制器_1_memwrite , \单周期硬布线控制器_1_regwrite , \单周期硬布线控制器_1_s_type ;
  wire [1:0] immch_1_x0;
  wire [3:0] id_ex_1_aluop_2, \单周期硬布线控制器_1_alu_op ;
  wire [4:0] ex_mem_1_rd_2, id_ex_1_rd_2, RD, rs1, rs2;
  wire [12:0] CNT_num;
  wire [15:0] \LoadUse次数 , \总周期数 , \插入气泡数 , \无条件分支数 , \条件分支成功数 ;
  wire [31:0] adder_1_out, adder_2_out, adder_3_out, alu_1_result, and_6_out, bit_extender_1_out,
       bit_extender_2_out, bit_extender_3_out, bit_extender_4_out, ecallA, ecallV, EX_IR, ex_mem_1_alu_2,
       ex_mem_1_r1_2, id_ex_1_imm_2, id_ex_1_r1_2, id_ex_1_r2_2, ID_IR, IF_IR, MEM_IR, mem_wb_1_alu_2,
       mem_wb_1_m_2, multiplexer_1_out, multiplexer_4_out, multiplexer_5_out, multiplexer_6_out,
       multiplexer_7_out, ram_1_data, regifile_1_r1, regifile_1_r2, shifter_1_out, shifter_2_out, WB_IR;

  Button \u_总复位  (.out(RST));
  Button _1 (.out(IR1));
  Button _2 (.out(IR2));
  Button _3 (.out(IR3));
  // Probe on \总周期数 
  // Probe on \总周期数 
  Multiplexer #(.select(1), .width(32), .disabled("Z"), .enable("false")) multiplexer_1 (
    .in0(adder_1_out), .in1(multiplexer_6_out), .out(multiplexer_1_out), .sel(JMP));
  Button \u_继续运行  (.out(Go));
  LED #(.active("true")) led_1 (.in(W1));
  LED #(.active("true")) led_2 (.in(W2));
  LED #(.active("true")) led_3 (.in(W3));
  Register #(.width(32), .trigger("rising"), .Select("low")) PC (
    .D(multiplexer_1_out), .en(and_1_out), .Q(IF_PC), .clk(CLK), .clr(RST), .cs(1'b0), .preset(1'b0));
  and and_1 (and_1_out, ncf, EN);
  Hex_Digit_Display hex_digit_display_1 (.value(LedData[31:28]));  // open: dp
  // Probe on IF_PC[19:0]
  // RiscV_Probe riscv_probe_1: pin names not known; wires that end beside it: IF_IR
  not not_1 (not_1_out, halt);
  Hex_Digit_Display hex_digit_display_2 (.value(LedData[23:20]));  // open: dp
  Hex_Digit_Display hex_digit_display_3 (.value(LedData[27:24]));  // open: dp
  // Probe on ID_PC[19:0]
  // RiscV_Probe riscv_probe_2: pin names not known; wires that end beside it: ID_IR
  or or_1 (EN, not_1_out, Go);
  Adder #(.width(32)) adder_1 (.a(IF_PC), .b(32'h4), .out(adder_1_out));  // open: cin, cout
  Hex_Digit_Display hex_digit_display_4 (.value(LedData[19:16]));  // open: dp
  Hex_Digit_Display hex_digit_display_5 (.value(LedData[15:12]));  // open: dp
  ROM #(.addrWidth(10), .dataWidth(32), .Select("high")) rom_1 (.addr(IF_PC[11:2]), .data(IF_IR));
  and and_2 (and_2_out, ncf, EN);
  Hex_Digit_Display hex_digit_display_6 (.value(LedData[7:4]));  // open: dp
  Hex_Digit_Display hex_digit_display_7 (.value(LedData[11:8]));  // open: dp
  Clock #(.highDuration(1), .lowDuration(1)) clock_1 (.out(clock_1_out));
  // Probe on EX_PC[19:0]
  // RiscV_Probe riscv_probe_3: pin names not known; wires that end beside it: clock_1_out, EX_IR, CLK
  IF_ID if_id_1 (.IR(IF_IR), .PC(IF_PC), .ID_IR(ID_IR), .ID_PC(ID_PC), .EN(and_2_out), .CLK(CLK), .RST(RST), .NOP(JMP));
  Hex_Digit_Display hex_digit_display_8 (.value(LedData[3:0]));  // open: dp
  // Probe on \总周期数 
  // Probe on M_PC[19:0]
  // RiscV_Probe riscv_probe_4: pin names not known; wires that end beside it: MEM_IR
  \单周期硬布线控制器  \u_单周期硬布线控制器_1  (
    .Funct({ID_IR[30], ID_IR[25], ID_IR[14:12]}), .OP(ID_IR[6:2]), .ALU_OP(\单周期硬布线控制器_1_alu_op ),
    .MemToReg(\单周期硬布线控制器_1_memtoreg ), .MemWrite(\单周期硬布线控制器_1_memwrite ), .ALU_SRC(\单周期硬布线控制器_1_alu_src ),
    .RegWrite(\单周期硬布线控制器_1_regwrite ), .ecall(\单周期硬布线控制器_1_ecall ), .S_type(\单周期硬布线控制器_1_s_type ),
    .Jalr(\单周期硬布线控制器_1_jalr ), .Beq(\单周期硬布线控制器_1_beq ), .JAL(\单周期硬布线控制器_1_jal ), .Bne(\单周期硬布线控制器_1_bne ));  // open: IR21, uret, irs, irc
  assign bit_extender_1_out = {{20{ID_IR[31]}}, ID_IR[31:20]};  // Bit_Extender bit_extender_1
  assign bit_extender_2_out = {{20{ID_IR[31]}}, {ID_IR[31:25], ID_IR[11:7]}};  // Bit_Extender bit_extender_2
  assign bit_extender_3_out = {{20{ID_IR[31]}}, {ID_IR[31], ID_IR[7], ID_IR[30:25], ID_IR[11:8]}};  // Bit_Extender bit_extender_3
  assign bit_extender_4_out = {{12{ID_IR[31]}}, {ID_IR[31], ID_IR[19:12], ID_IR[20], ID_IR[30:21]}};  // Bit_Extender bit_extender_4
  // Probe on \总周期数 
  // Probe on \无条件分支数 
  // Probe on \条件分支成功数 
  // Probe on \插入气泡数 
  // Probe on \LoadUse次数 
  Multiplexer #(.select(1), .width(5), .disabled("Z"), .enable("false")) multiplexer_2 (
    .in0(ID_IR[19:15]), .in1(5'b01010), .out(rs1), .sel(\单周期硬布线控制器_1_ecall ));
  Multiplexer #(.select(1), .width(5), .disabled("Z"), .enable("false")) multiplexer_3 (
    .in0(ID_IR[24:20]), .in1(5'b10001), .out(rs2), .sel(\单周期硬布线控制器_1_ecall ));
  Shifter #(.width(32), .shift("ll")) shifter_1 (.in(bit_extender_3_out), .\dist (5'b00001), .out(shifter_1_out));
  Shifter #(.width(32), .shift("ll")) shifter_2 (.in(bit_extender_4_out), .\dist (5'b00001), .out(shifter_2_out));
  // Probe on IF_PC[11:0]
  // Probe on WB_PC[19:0]
  // RiscV_Probe riscv_probe_5: pin names not known; wires that end beside it: WB_IR
  // Probe on ID_PC[11:0]
  // Probe on EX_PC[11:0]
  IMMch immch_1 (
    .jal(\单周期硬布线控制器_1_jal ), .beq(\单周期硬布线控制器_1_beq ), .bne(\单周期硬布线控制器_1_bne ), .st(\单周期硬布线控制器_1_s_type ),
    .X1(immch_1_x0[1]), .X0(immch_1_x0[0]));
  Regifile regifile_1 (
    .Din(RDin), .Clk(CLK), .R1(regifile_1_r1), .R2(regifile_1_r2), .WE(RegWrite), .W_num(RD), .R1_num(rs1),
    .R2_num(rs2));
  Multiplexer #(.select(2), .width(32), .disabled("Z"), .enable("false")) multiplexer_4 (
    .in0(bit_extender_1_out), .in1(bit_extender_2_out), .in2(shifter_1_out), .in3(shifter_2_out),
    .out(multiplexer_4_out), .sel(immch_1_x0));
  // Probe on M_PC[11:0]
  D_Flip_Flop #(.trigger("high"), .Pre_Clr_Positions("LEGACY"), .NegatePresetClear("false"), .enable("true"), .NewFFLayout("false")) d_ff_1 (.Q(d_ff_1_q));  // open: clk, D, Qn, preset, en, reset
  // Probe on 13'hc
  or or_2 (or_2_out, ~and_3_out, JMP);  // OR_Gate
  and and_3 (and_3_out, ncf, EN);
  // Probe on WB_PC[11:0]
  Comparator #(.width(13), .mode("twosComplement")) comparator_1 (
    .a(CNT_num), .b(13'hc), .eq(comparator_1_eq), .lt(comparator_1_lt));  // open: gt
  Clock #(.highDuration(1), .lowDuration(1)) clock_2 (.out(clock_2_out));
  ID_EX id_ex_1 (
    .WB(\单周期硬布线控制器_1_memtoreg ), .Mem(\单周期硬布线控制器_1_memwrite ), .ALUop(\单周期硬布线控制器_1_alu_op ), .IR(ID_IR),
    .PC(ID_PC), .WB_2(id_ex_1_wb_2), .Mem_2(id_ex_1_mem_2), .ALUop_2(id_ex_1_aluop_2), .EX_IR(EX_IR),
    .EX_PC(EX_PC), .EN(EN), .RST(RST), .CLK(CLK), .R1(regifile_1_r1), .R1_2(id_ex_1_r1_2),
    .IMM(multiplexer_4_out), .IMM_2(id_ex_1_imm_2), .RW(\单周期硬布线控制器_1_regwrite ), .RW_2(id_ex_1_rw_2),
    .R2(regifile_1_r2), .R2_2(id_ex_1_r2_2), .RD(ID_IR[11:7]), .RD_2(id_ex_1_rd_2), .jal(\单周期硬布线控制器_1_jal ),
    .jal_2(id_ex_1_jal_2), .jalr(\单周期硬布线控制器_1_jalr ), .jalr_2(id_ex_1_jalr_2), .beq(\单周期硬布线控制器_1_beq ),
    .beq_2(id_ex_1_beq_2), .bne(\单周期硬布线控制器_1_bne ), .bne_2(id_ex_1_bne_2), .ecall(\单周期硬布线控制器_1_ecall ),
    .ecall_2(id_ex_1_ecall_2), .NOP(or_2_out), .AluS(\单周期硬布线控制器_1_alu_src ), .AluS_2(id_ex_1_alus_2));  // open: rs1Ch, rs1Ch_2, rs2Ch, rs2Ch_2
  nand nand_1 (nand_1_out, d_ff_1_q, comparator_1_eq);
  Counter #(.width(13), .max('h1fff), .ongoal("stay"), .trigger("rising"), .behavior("old")) counter_1 (
    .count(comparator_1_lt), .Q(CNT_num), .clk(clock_2_out));  // open: load, D, carry, clr, preset
  and and_4 (and_4_out, id_ex_1_beq_2, alu_1_equal);
  and and_5 (and_5_out, id_ex_1_bne_2, ~alu_1_equal);  // AND_Gate
  Multiplexer #(.select(1), .width(32), .disabled("Z"), .enable("false")) multiplexer_5 (
    .in0(id_ex_1_r2_2), .in1(id_ex_1_imm_2), .out(multiplexer_5_out), .sel(id_ex_1_alus_2));
  Adder #(.width(32)) adder_2 (.a(EX_PC), .b(id_ex_1_imm_2), .out(adder_2_out));  // open: cin, cout
  assign and_6_out = alu_1_result & 32'hfffffffe;  // AND_Gate and_6, 32 bits wide
  Adder #(.width(32)) adder_3 (.a(EX_PC), .b(32'h4), .out(adder_3_out));  // open: cin, cout
  assign CLK = nand_1_out ? clock_2_out : 1'bz;  // Controlled_Buffer controlled_buffer_1
  or or_3 (JMP, id_ex_1_jal_2, id_ex_1_jalr_2, and_4_out, and_5_out);
  or or_4 (or_4_out, id_ex_1_jal_2, id_ex_1_jalr_2);
  ALU alu_1 (
    .X(id_ex_1_r1_2), .Y(multiplexer_5_out), .AluOP(id_ex_1_aluop_2), .Equal(alu_1_equal),
    .Result(alu_1_result));  // open: Result_2, out_4, out_6
  RegConf regconf_1 (
    .RegWt(id_ex_1_rw_2), .RD(id_ex_1_rd_2), .rs1(rs1), .rs2(rs2), .Conf(regconf_1_conf),
    .AluS(\单周期硬布线控制器_1_alu_src ));
  Multiplexer #(.select(1), .width(32), .disabled("Z"), .enable("false")) multiplexer_6 (
    .in0(adder_2_out), .in1(and_6_out), .out(multiplexer_6_out), .sel(id_ex_1_jalr_2));
  Pull_Resistor #(.pull(1)) pull_resistor_1 (.node(CLK));
  Multiplexer #(.select(1), .width(32), .disabled("Z"), .enable("false")) multiplexer_7 (
    .in0(alu_1_result), .in1(adder_3_out), .out(multiplexer_7_out), .sel(or_4_out));
  // Probe on adder_3_out
  EX_MEM ex_mem_1 (
    .WB(id_ex_1_wb_2), .Mem(id_ex_1_mem_2), .IR(EX_IR), .PC(EX_PC), .WB_2(ex_mem_1_wb_2), .Mem_2(MemWrite),
    .IR_2(MEM_IR), .PC_2(M_PC), .EN(EN), .RST(RST), .CLK(CLK), .ALU(multiplexer_7_out),
    .ALU_2(ex_mem_1_alu_2), .R2(id_ex_1_r2_2), .R2_2(MDin), .RW(id_ex_1_rw_2), .RW_2(ex_mem_1_rw_2),
    .RD(id_ex_1_rd_2), .RD_2(ex_mem_1_rd_2), .ecall(id_ex_1_ecall_2), .ecall_2(ex_mem_1_ecall_2), .NOP(1'b0),
    .R1(id_ex_1_r1_2), .R1_2(ex_mem_1_r1_2));
  RegConf regconf_2 (
    .RegWt(ex_mem_1_rw_2), .RD(ex_mem_1_rd_2), .rs1(rs1), .rs2(rs2), .Conf(regconf_2_conf),
    .AluS(\单周期硬布线控制器_1_alu_src ));
  nor nor_1 (nor_1_out, regconf_2_conf, regconf_1_conf);
  or or_5 (ncf, nor_1_out, JMP);
  RAM #(.addrWidth(10), .dataWidth(32), .bus("separate"), .Select("high")) ram_1 (
    .addr(ex_mem_1_alu_2[11:2]), .din(MDin), .data(ram_1_data), .str(MemWrite), .clk(CLK), .ld(ex_mem_1_rw_2));  // open: sel, clr
  Register #(.width(32), .trigger("rising"), .Select("low")) register_1 (
    .D(ecallA), .en(dhex), .Q(LedData), .clk(CLK), .clr(RST), .cs(1'b0), .preset(1'b0));
  Comparator #(.width(32), .mode("twosComplement")) comparator_2 (
    .a(ecallV), .b(32'h22), .eq(comparator_2_eq));  // open: gt, lt
  MEM_WB mem_wb_1 (
    .WB(ex_mem_1_wb_2), .IR(MEM_IR), .PC(M_PC), .ALU(ex_mem_1_alu_2), .M(ram_1_data), .WB_2(mem_wb_1_wb_2),
    .IR_2(WB_IR), .PC_2(WB_PC), .ALU_2(mem_wb_1_alu_2), .M_2(mem_wb_1_m_2), .EN(EN), .RST(RST), .CLK(CLK),
    .RW(ex_mem_1_rw_2), .RW_2(RegWrite), .RD(ex_mem_1_rd_2), .RD_2(RD), .ecall(ex_mem_1_ecall_2),
    .ecall_2(mem_wb_1_ecall_2), .NOP(1'b0), .R1(ex_mem_1_r1_2), .R1_2(ecallA), .R2(MDin), .R2_2(ecallV));
  Multiplexer #(.select(1), .width(32), .disabled("Z"), .enable("false")) multiplexer_8 (
    .in0(mem_wb_1_alu_2), .in1(mem_wb_1_m_2), .out(RDin), .sel(mem_wb_1_wb_2));
  // Probe on RDin
  not not_2 (not_2_out, comparator_2_eq);
  and and_7 (halt, not_2_out, mem_wb_1_ecall_2);
  and and_8 (dhex, comparator_2_eq, mem_wb_1_ecall_2);

  // Other names for the same wires on the sheet: MEM_PC[31:0] = M_PC

  // Notes on the sheet:
  //   中断源
  //   时空图监测，可删除
  //   中断等待指示
  //   数码管输出
  //   contents of rom_1 (hex, n*v repeats v):
  //   100493 100006f 100493 200913 300993 100006f 100493 200913 300993 100006f 100493 200913 300993
  //   100006f 100493 200913 300993 29c000ef 100413 100493 1f49493 900533 2200893 73 24d493 48463 fedff06f
  //   900533 2200893 73 100493 249493 900533 2200893 73 48463 fedff06f 100493 1f49493 900533 2200893 73
  //   4034d493 900533 2200893 73 4044d493 900533 2200893 73 4044d493 900533 2200893 73 4044d493 900533
  //   2200893 73 4044d493 900533 2200893 73 4044d493 900533 2200893 73 4044d493 900533 2200893 73 4044d493
  //   900533 2200893 73 100413 1f41993 41f9d993 433 c00913 300b13 140413 f47413 800293 100313 499993
  //   89e9b3 1300533 2200893 73 406282b3 fe0294e3 140413 f00f93 1f47433 1c41413 800293 100313 49d993
  //   89e9b3 1300533 2200893 73 406282b3 fe0294e3 1c45413 406b0b33 b0463 f95ff06f 2b3 fff2c293 829293
  //   ff2e293 500533 2200893 73 fff00413 493 84a023 140413 448493 84a023 140413 448493 84a023 140413
  //   448493 84a023 140413 448493 84a023 140413 448493 84a023 140413 448493 84a023 140413 448493 84a023
  //   140413 448493 84a023 140413 448493 84a023 140413 448493 84a023 140413 448493 84a023 140413 448493
  //   84a023 140413 448493 84a023 140413 448493 84a023 140413 448493 84a023 140413 448493 140413 433
  //   3c00493 42983 4aa03 149a2b3 28663 134a023 1442023 ffc48493 fe9412e3 800533 2200893 73 440413 3c00493
  //   fc9416e3 a00893 73 413 140413 800533 2200893 73 240413 800533 2200893 73 340413 800533 2200893 73
  //   440413 800533 2200893 73 540413 800533 2200893 73 640413 800533 2200893 73 740413 800533 2200893 73
  //   840413 800533 2200893 2200893 73 8067
  //   rs1
  //   rs2
  //   rd
  //   immI
  //   immS
  //   immB
  //   immJ
  //   控制位
  //   流水调试日志用
  //   暂停节拍，不能为0
  //   可计数暂停的时钟源
  //   为方便自动评测，需要输出流水线各段保存的PC值，注意是PC不是PC+4，另外ID段寄存器写入信息，Mem段内存写入信息也要输出
  //   戳工具置1进入计数暂停模式，ctrl+k时钟自动运行到对应节拍暂停
  //   ctrl+k关闭时钟连续运行，将控制位置零，进入单步调试模式调试
endmodule

module \重定向流水线  (
  output RegWrite,
  output MemWrite,
  output [31:0] IF_PC,
  output [31:0] ID_PC,
  output [31:0] EX_PC,
  output [31:0] M_PC,
  output [31:0] WB_PC,
  output [31:0] RDin,
  output [31:0] MDin,
  output [31:0] LedData
);

  wire alu_1_equal, and_1_out, and_2_out, and_3_out, and_4_out, and_5_out, CLK, clock_1_out, clock_2_out,
       comparator_1_eq, comparator_1_lt, comparator_2_eq, d_ff_1_q, dhex, EN, ex_mem_1_ecall_2,
       ex_mem_1_rw_2, ex_mem_1_wb_2, Go, halt, id_ex_1_alus_2, id_ex_1_beq_2, id_ex_1_bne_2, id_ex_1_ecall_2,
       id_ex_1_jal_2, id_ex_1_jalr_2, id_ex_1_mem_2, id_ex_1_rw_2, id_ex_1_wb_2, IR1, IR2, IR3, JMP, ldu,
       mem_wb_1_ecall_2, mem_wb_1_wb_2, nand_1_out, not_1_out, not_2_out, or_2_out, or_4_out, RST, W1, W2,
       W3, \单周期硬布线控制器_1_alu_src , \单周期硬布线控制器_1_beq , \单周期硬布线控制器_1_bne , \单周期硬布线控制器_1_ecall ,
       \单周期硬布线控制器_1_jal , \单周期硬布线控制器_1_jalr , \单周期硬布线控制器_1_memtoreg , \单周期硬布线控制器_1_memwrite ,
       \单周期硬布线控制器_1_regwrite , \单周期硬布线控制器_1_s_type ;
  wire [1:0] id_ex_1_rs1ch_2, id_ex_1_rs2ch_2, immch_1_x0, rs1Ch, rs2Ch;
  wire [3:0] id_ex_1_aluop_2, \单周期硬布线控制器_1_alu_op ;
  wire [4:0] ex_mem_1_rd_2, id_ex_1_rd_2, RD, rs1, rs2;
  wire [12:0] CNT_num;
  wire [15:0] \LoadUse次数 , \总周期数 , \插入气泡数 , \无条件分支数 , \条件分支成功数 ;
  wire [31:0] adder_1_out, adder_2_out, adder_3_out, alu_1_result, and_6_out, bit_extender_1_out,
       bit_extender_2_out, bit_extender_3_out, bit_extender_4_out, ecallA, ecallV, EX_IR, ex_mem_1_alu_2,
       ex_mem_1_r1_2, id_ex_1_imm_2, id_ex_1_r1_2, id_ex_1_r2_2, ID_IR, IF_IR, MEM_IR, mem_wb_1_alu_2,
       mem_wb_1_m_2, multiplexer_1_out, multiplexer_4_out, multiplexer_5_out, multiplexer_6_out,
       multiplexer_7_out, multiplexer_8_out, multiplexer_9_out, ram_1_data, regifile_1_r1, regifile_1_r2,
       shifter_1_out, shifter_2_out, WB_IR;

  Button \u_总复位  (.out(RST));
  Button _1 (.out(IR1));
  Button _2 (.out(IR2));
  Button _3 (.out(IR3));
  // Probe on \总周期数 
  // Probe on \总周期数 
  Counter #(.width(16), .max('hffff), .ongoal("wrap"), .trigger("rising"), .behavior("new")) counter_1 (
    .count(EN), .Q(\总周期数 ), .clk(CLK));  // open: load, D, carry, clr, preset, down
  Multiplexer #(.select(1), .width(32), .disabled("Z"), .enable("false")) multiplexer_1 (
    .in0(adder_1_out), .in1(multiplexer_9_out), .out(multiplexer_1_out), .sel(JMP));
  Button \u_继续运行  (.out(Go));
  LED #(.active("true")) led_1 (.in(W1));
  LED #(.active("true")) led_2 (.in(W2));
  LED #(.active("true")) led_3 (.in(W3));
  Register #(.width(32), .trigger("rising"), .Select("low")) PC (
    .D(multiplexer_1_out), .en(and_1_out), .Q(IF_PC), .clk(CLK), .clr(RST), .cs(1'b0), .preset(1'b0));
  and and_1 (and_1_out, EN, ~ldu);  // AND_Gate
  Hex_Digit_Display hex_digit_display_1 (.value(LedData[31:28]));  // open: dp
  // Probe on IF_PC[19:0]
  // RiscV_Probe riscv_probe_1: pin names not known; wires that end beside it: IF_IR
  not not_1 (not_1_out, halt);
  Hex_Digit_Display hex_digit_display_2 (.value(LedData[23:20]));  // open: dp
  Hex_Digit_Display hex_digit_display_3 (.value(LedData[27:24]));  // open: dp
  // Probe on ID_PC[19:0]
  // RiscV_Probe riscv_probe_2: pin names not known; wires that end beside it: ID_IR
  or or_1 (EN, not_1_out, Go);
  Adder #(.width(32)) adder_1 (.a(IF_PC), .b(32'h4), .out(adder_1_out));  // open: cin, cout
  Hex_Digit_Display hex_digit_display_4 (.value(LedData[19:16]));  // open: dp
  Hex_Digit_Display hex_digit_display_5 (.value(LedData[15:12]));  // open: dp
  ROM #(.addrWidth(10), .dataWidth(32), .Select("high")) rom_1 (.addr(IF_PC[11:2]), .data(IF_IR));
  and and_2 (and_2_out, EN, ~ldu);  // AND_Gate
  Hex_Digit_Display hex_digit_display_6 (.value(LedData[7:4]));  // open: dp
  Hex_Digit_Display hex_digit_display_7 (.value(LedData[11:8]));  // open: dp
  Clock #(.highDuration(1), .lowDuration(1)) clock_1 (.out(clock_1_out));
  // Probe on EX_PC[19:0]
  // RiscV_Probe riscv_probe_3: pin names not known; wires that end beside it: clock_1_out, EX_IR, CLK
  IF_ID if_id_1 (.IR(IF_IR), .PC(IF_PC), .ID_IR(ID_IR), .ID_PC(ID_PC), .EN(and_2_out), .CLK(CLK), .RST(RST), .NOP(JMP));
  Hex_Digit_Display hex_digit_display_8 (.value(LedData[3:0]));  // open: dp
  // Probe on \总周期数 
  // Probe on M_PC[19:0]
  // RiscV_Probe riscv_probe_4: pin names not known; wires that end beside it: MEM_IR
  \单周期硬布线控制器  \u_单周期硬布线控制器_1  (
    .Funct({ID_IR[30], ID_IR[25], ID_IR[14:12]}), .OP(ID_IR[6:2]), .ALU_OP(\单周期硬布线控制器_1_alu_op ),
    .MemToReg(\单周期硬布线控制器_1_memtoreg ), .MemWrite(\单周期硬布线控制器_1_memwrite ), .ALU_SRC(\单周期硬布线控制器_1_alu_src ),
    .RegWrite(\单周期硬布线控制器_1_regwrite ), .ecall(\单周期硬布线控制器_1_ecall ), .S_type(\单周期硬布线控制器_1_s_type ),
    .Jalr(\单周期硬布线控制器_1_jalr ), .Beq(\单周期硬布线控制器_1_beq ), .JAL(\单周期硬布线控制器_1_jal ), .Bne(\单周期硬布线控制器_1_bne ),
    .IR21(ID_IR[21]));  // open: uret, irs, irc
  assign bit_extender_1_out = {{20{ID_IR[31]}}, ID_IR[31:20]};  // Bit_Extender bit_extender_1
  assign bit_extender_2_out = {{20{ID_IR[31]}}, {ID_IR[31:25], ID_IR[11:7]}};  // Bit_Extender bit_extender_2
  assign bit_extender_3_out = {{20{ID_IR[31]}}, {ID_IR[31], ID_IR[7], ID_IR[30:25], ID_IR[11:8]}};  // Bit_Extender bit_extender_3
  assign bit_extender_4_out = {{12{ID_IR[31]}}, {ID_IR[31], ID_IR[19:12], ID_IR[20], ID_IR[30:21]}};  // Bit_Extender bit_extender_4
  // Probe on \总周期数 
  // Probe on \无条件分支数 
  // Probe on \条件分支成功数 
  // Probe on \插入气泡数 
  // Probe on \LoadUse次数 
  Multiplexer #(.select(1), .width(5), .disabled("Z"), .enable("false")) multiplexer_2 (
    .in0(ID_IR[19:15]), .in1(5'b01010), .out(rs1), .sel(\单周期硬布线控制器_1_ecall ));
  Multiplexer #(.select(1), .width(5), .disabled("Z"), .enable("false")) multiplexer_3 (
    .in0(ID_IR[24:20]), .in1(5'b10001), .out(rs2), .sel(\单周期硬布线控制器_1_ecall ));
  Shifter #(.width(32), .shift("ll")) shifter_1 (.in(bit_extender_3_out), .\dist (5'b00001), .out(shifter_1_out));
  Shifter #(.width(32), .shift("ll")) shifter_2 (.in(bit_extender_4_out), .\dist (5'b00001), .out(shifter_2_out));
  // Probe on IF_PC[11:0]
  // Probe on WB_PC[19:0]
  // RiscV_Probe riscv_probe_5: pin names not known; wires that end beside it: WB_IR
  and and_3 (and_3_out, ~\单周期硬布线控制器_1_s_type , \单周期硬布线控制器_1_alu_src );  // AND_Gate
  // Probe on EX_PC[11:0]
  // Probe on ID_PC[11:0]
  IMMch immch_1 (
    .jal(\单周期硬布线控制器_1_jal ), .beq(\单周期硬布线控制器_1_beq ), .bne(\单周期硬布线控制器_1_bne ), .st(\单周期硬布线控制器_1_s_type ),
    .X1(immch_1_x0[1]), .X0(immch_1_x0[0]));
  Regifile regifile_1 (
    .Din(RDin), .Clk(CLK), .R1(regifile_1_r1), .R2(regifile_1_r2), .WE(RegWrite), .W_num(RD), .R1_num(rs1),
    .R2_num(rs2));
  Multiplexer #(.select(2), .width(32), .disabled("Z"), .enable("false")) multiplexer_4 (
    .in0(bit_extender_1_out), .in1(bit_extender_2_out), .in2(shifter_1_out), .in3(shifter_2_out),
    .out(multiplexer_4_out), .sel(immch_1_x0));
  // Probe on M_PC[11:0]
  D_Flip_Flop #(.trigger("high"), .Pre_Clr_Positions("LEGACY"), .NegatePresetClear("false"), .enable("true"), .NewFFLayout("false")) d_ff_1 (.Q(d_ff_1_q));  // open: clk, D, Qn, preset, en, reset
  // Probe on 13'hc
  or or_2 (or_2_out, JMP, ldu);
  // Probe on WB_PC[11:0]
  Comparator #(.width(13), .mode("twosComplement")) comparator_1 (
    .a(CNT_num), .b(13'hc), .eq(comparator_1_eq), .lt(comparator_1_lt));  // open: gt
  Clock #(.highDuration(1), .lowDuration(1)) clock_2 (.out(clock_2_out));
  ID_EX id_ex_1 (
    .WB(\单周期硬布线控制器_1_memtoreg ), .Mem(\单周期硬布线控制器_1_memwrite ), .ALUop(\单周期硬布线控制器_1_alu_op ), .IR(ID_IR),
    .PC(ID_PC), .WB_2(id_ex_1_wb_2), .Mem_2(id_ex_1_mem_2), .ALUop_2(id_ex_1_aluop_2), .EX_IR(EX_IR),
    .EX_PC(EX_PC), .EN(EN), .RST(RST), .CLK(CLK), .R1(regifile_1_r1), .R1_2(id_ex_1_r1_2),
    .IMM(multiplexer_4_out), .IMM_2(id_ex_1_imm_2), .RW(\单周期硬布线控制器_1_regwrite ), .RW_2(id_ex_1_rw_2),
    .R2(regifile_1_r2), .R2_2(id_ex_1_r2_2), .RD(ID_IR[11:7]), .RD_2(id_ex_1_rd_2), .jal(\单周期硬布线控制器_1_jal ),
    .jal_2(id_ex_1_jal_2), .jalr(\单周期硬布线控制器_1_jalr ), .jalr_2(id_ex_1_jalr_2), .beq(\单周期硬布线控制器_1_beq ),
    .beq_2(id_ex_1_beq_2), .bne(\单周期硬布线控制器_1_bne ), .bne_2(id_ex_1_bne_2), .ecall(\单周期硬布线控制器_1_ecall ),
    .ecall_2(id_ex_1_ecall_2), .NOP(or_2_out), .AluS(\单周期硬布线控制器_1_alu_src ), .AluS_2(id_ex_1_alus_2),
    .rs1Ch(rs1Ch), .rs1Ch_2(id_ex_1_rs1ch_2), .rs2Ch(rs2Ch), .rs2Ch_2(id_ex_1_rs2ch_2));
  // Probe on RDin
  nand nand_1 (nand_1_out, d_ff_1_q, comparator_1_eq);
  Counter #(.width(13), .max('h1fff), .ongoal("stay"), .trigger("rising"), .behavior("old")) counter_2 (
    .count(comparator_1_lt), .Q(CNT_num), .clk(clock_2_out));  // open: load, D, carry, clr, preset
  and and_4 (and_4_out, id_ex_1_beq_2, alu_1_equal);
  and and_5 (and_5_out, id_ex_1_bne_2, ~alu_1_equal);  // AND_Gate
  Multiplexer #(.select(2), .width(32), .disabled("Z"), .enable("false")) multiplexer_5 (
    .in0(id_ex_1_r1_2), .in1(ex_mem_1_alu_2), .in2(RDin), .in3(ex_mem_1_alu_2), .out(multiplexer_5_out),
    .sel(id_ex_1_rs1ch_2));
  Multiplexer #(.select(2), .width(32), .disabled("Z"), .enable("false")) multiplexer_6 (
    .in0(id_ex_1_r2_2), .in1(ex_mem_1_alu_2), .in2(RDin), .in3(ex_mem_1_alu_2), .out(multiplexer_6_out),
    .sel(id_ex_1_rs2ch_2));
  assign CLK = nand_1_out ? clock_2_out : 1'bz;  // Controlled_Buffer controlled_buffer_1
  or or_3 (JMP, id_ex_1_jal_2, id_ex_1_jalr_2, and_4_out, and_5_out);
  or or_4 (or_4_out, id_ex_1_jal_2, id_ex_1_jalr_2);
  Multiplexer #(.select(1), .width(32), .disabled("Z"), .enable("false")) multiplexer_7 (
    .in0(multiplexer_6_out), .in1(id_ex_1_imm_2), .out(multiplexer_7_out), .sel(id_ex_1_alus_2));
  // Probe on id_ex_1_rs1ch_2
  // Probe on id_ex_1_rs2ch_2
  Pull_Resistor #(.pull(1)) pull_resistor_1 (.node(CLK));
  ALU alu_1 (
    .X(multiplexer_5_out), .Y(multiplexer_7_out), .AluOP(id_ex_1_aluop_2), .Equal(alu_1_equal),
    .Result(alu_1_result));  // open: Result_2, out_4, out_6
  Adder #(.width(32)) adder_2 (.a(EX_PC), .b(id_ex_1_imm_2), .out(adder_2_out));  // open: cin, cout
  assign and_6_out = alu_1_result & 32'hfffffffe;  // AND_Gate and_6, 32 bits wide
  Adder #(.width(32)) adder_3 (.a(EX_PC), .b(32'h4), .out(adder_3_out));  // open: cin, cout
  Multiplexer #(.select(1), .width(32), .disabled("Z"), .enable("false")) multiplexer_8 (
    .in0(alu_1_result), .in1(adder_3_out), .out(multiplexer_8_out), .sel(or_4_out));
  Redirect redirect_1 (
    .Rw(id_ex_1_rw_2), .rs1(rs1), .rs2(rs2), .rd(id_ex_1_rd_2), .x1(rs1Ch[0]), .x2(rs2Ch[0]),
    .m2r(id_ex_1_wb_2), .ldu(ldu), .AluS(and_3_out));
  Multiplexer #(.select(1), .width(32), .disabled("Z"), .enable("false")) multiplexer_9 (
    .in0(adder_2_out), .in1(and_6_out), .out(multiplexer_9_out), .sel(id_ex_1_jalr_2));
  EX_MEM ex_mem_1 (
    .WB(id_ex_1_wb_2), .Mem(id_ex_1_mem_2), .IR(EX_IR), .PC(EX_PC), .WB_2(ex_mem_1_wb_2), .Mem_2(MemWrite),
    .IR_2(MEM_IR), .PC_2(M_PC), .EN(EN), .RST(RST), .CLK(CLK), .ALU(multiplexer_8_out),
    .ALU_2(ex_mem_1_alu_2), .R2(multiplexer_6_out), .R2_2(MDin), .RW(id_ex_1_rw_2), .RW_2(ex_mem_1_rw_2),
    .RD(id_ex_1_rd_2), .RD_2(ex_mem_1_rd_2), .ecall(id_ex_1_ecall_2), .ecall_2(ex_mem_1_ecall_2), .NOP(1'b0),
    .R1(multiplexer_5_out), .R1_2(ex_mem_1_r1_2));
  RAM #(.addrWidth(10), .dataWidth(32), .bus("separate"), .Select("high")) ram_1 (
    .addr(ex_mem_1_alu_2[11:2]), .din(MDin), .data(ram_1_data), .str(MemWrite), .clk(CLK), .ld(ex_mem_1_wb_2));  // open: sel, clr
  Redirect redirect_2 (
    .Rw(ex_mem_1_rw_2), .rs1(rs1), .rs2(rs2), .rd(ex_mem_1_rd_2), .x1(rs1Ch[1]), .x2(rs2Ch[1]), .m2r(1'b0),
    .AluS(and_3_out));  // open: ldu
  Register #(.width(32), .trigger("rising"), .Select("low")) register_1 (
    .D(ecallA), .en(dhex), .Q(LedData), .clk(CLK), .clr(RST), .cs(1'b0), .preset(1'b0));
  Comparator #(.width(32), .mode("twosComplement")) comparator_2 (
    .a(ecallV), .b(32'h22), .eq(comparator_2_eq));  // open: gt, lt
  MEM_WB mem_wb_1 (
    .WB(ex_mem_1_wb_2), .IR(MEM_IR), .PC(M_PC), .ALU(ex_mem_1_alu_2), .M(ram_1_data), .WB_2(mem_wb_1_wb_2),
    .IR_2(WB_IR), .PC_2(WB_PC), .ALU_2(mem_wb_1_alu_2), .M_2(mem_wb_1_m_2), .EN(EN), .RST(RST), .CLK(CLK),
    .RW(ex_mem_1_rw_2), .RW_2(RegWrite), .RD(ex_mem_1_rd_2), .RD_2(RD), .ecall(ex_mem_1_ecall_2),
    .ecall_2(mem_wb_1_ecall_2), .NOP(1'b0), .R1(ex_mem_1_r1_2), .R1_2(ecallA), .R2(MDin), .R2_2(ecallV));
  Multiplexer #(.select(1), .width(32), .disabled("Z"), .enable("false")) multiplexer_10 (
    .in0(mem_wb_1_alu_2), .in1(mem_wb_1_m_2), .out(RDin), .sel(mem_wb_1_wb_2));
  not not_2 (not_2_out, comparator_2_eq);
  and and_7 (halt, not_2_out, mem_wb_1_ecall_2);
  and and_8 (dhex, comparator_2_eq, mem_wb_1_ecall_2);

  // Other names for the same wires on the sheet: MEM_PC[31:0] = M_PC

  // Notes on the sheet:
  //   中断源
  //   时空图监测，可删除
  //   中断等待指示
  //   数码管输出
  //   contents of rom_1 (hex, n*v repeats v):
  //   100493 100006f 100493 200913 300993 100006f 100493 200913 300993 100006f 100493 200913 300993
  //   100006f 100493 200913 300993 3d0000ef 100413 100493 1f49493 900533 2200893 73 24d493 48463 fedff06f
  //   900533 2200893 73 100493 249493 900533 2200893 73 48463 fedff06f 100493 1f49493 900533 2200893 73
  //   4034d493 900533 2200893 73 4044d493 900533 2200893 73 4044d493 900533 2200893 73 4044d493 900533
  //   2200893 73 4044d493 900533 2200893 73 4044d493 900533 2200893 73 4044d493 900533 2200893 73 4044d493
  //   900533 2200893 73 100413 1f41993 41f9d993 433 c00913 300b13 140413 f47413 800293 100313 499993
  //   89e9b3 1300533 2200893 73 406282b3 fe0294e3 140413 f00f93 1f47433 1c41413 800293 100313 49d993
  //   89e9b3 1300533 2200893 73 406282b3 fe0294e3 1c45413 406b0b33 b0463 f95ff06f 2b3 fff2c293 829293
  //   ff2e293 500533 2200893 73 fff00413 493 84a023 140413 448493 84a023 140413 448493 84a023 140413
  //   448493 84a023 140413 448493 84a023 140413 448493 84a023 140413 448493 84a023 140413 448493 84a023
  //   140413 448493 84a023 140413 448493 84a023 140413 448493 84a023 140413 448493 84a023 140413 448493
  //   84a023 140413 448493 84a023 140413 448493 84a023 140413 448493 84a023 140413 448493 140413 433
  //   3c00493 42983 4aa03 149a2b3 28663 134a023 1442023 ffc48493 fe9412e3 800533 2200893 73 440413 3c00493
  //   fc9416e3 a00893 73 100293 300313 800493 849493 7648493 1449493 900533 2200893 73 800e13 4054d4b3
  //   4064d4b3 900533 2200893 73 fffe0e13 fe0e14e3 a00893 73 fff00293 7700493 849493 7748493 900533
  //   2200893 73 1000e13 54c4b3 900533 2200893 73 fffe0e13 fe0e16e3 a00893 73 313 1000e13 8400493 849493
  //   8348493 400913 891913 490913 849493 8248493 849493 8148493 891913 490913 891913 490913 932023
  //   12484b3 430313 fffe0e13 fe0e18e3 2000e13 313 31483 900533 2200893 73 230313 fffe0e13 fe0e14e3 a00893
  //   73 f00493 900533 2200893 73 fff48493 fe04d8e3 a00893 73 a00893 73 413 140413 800533 2200893 73
  //   240413 800533 2200893 73 340413 800533 2200893 73 440413 800533 2200893 73 540413 800533 2200893 73
  //   640413 800533 2200893 73 740413 800533 2200893 73 840413 800533 2200893 2200893 73 8067
  //   rs1
  //   rs2
  //   rd
  //   immI
  //   immS
  //   immB
  //   immJ
  //   控制位
  //   流水调试日志用
  //   暂停节拍，不能为0
  //   戳工具置1进入计数暂停模式，ctrl+k时钟自动运行到对应节拍暂停
  //   ctrl+k关闭时钟连续运行，将控制位置零，进入单步调试模式调试
  //   可计数暂停的时钟源
  //   为方便自动评测，需要输出流水线各段保存的PC值，注意是PC不是PC+4，另外ID段寄存器写入信息，Mem段内存写入信息也要输出
endmodule

module \中断按键参考电路  (
  input  \同步清零信号 ,
  output \与中断屏蔽位与 
);

  wire \_1号中断_out , and_1_out, clock_1_out, d_ff_1_q, or_1_out, or_2_out;

  Clock #(.highDuration(1), .lowDuration(1)) clock_1 (.out(clock_1_out));
  Button \_1号中断  (.out(\_1号中断_out ));
  or or_1 (or_1_out, \与中断屏蔽位与 , d_ff_1_q);
  LED #(.active("true")) \_1号中断等待指示灯  (.in(or_1_out));
  D_Flip_Flop #(.trigger("rising"), .Pre_Clr_Positions("LEGACY"), .NegatePresetClear("false"), .enable("true"), .NewFFLayout("false")) d_ff_1 (
    .clk(\_1号中断_out ), .D(1'b1), .Q(d_ff_1_q), .reset(\与中断屏蔽位与 ));  // open: Qn, preset, en
  or or_2 (or_2_out, d_ff_1_q, \与中断屏蔽位与 );
  and and_1 (and_1_out, or_2_out, ~\同步清零信号 );  // AND_Gate
  D_Flip_Flop #(.trigger("rising"), .Pre_Clr_Positions("LEGACY"), .NegatePresetClear("false"), .enable("true"), .NewFFLayout("false")) IR1 (
    .clk(clock_1_out), .D(and_1_out), .Q(\与中断屏蔽位与 ));  // open: Qn, preset, en, reset

  // Notes on the sheet:
  //   中断信号采样参考电路
  //   Reset 
endmodule

module \封装正确性测试  (
);

  wire IR1, IR2, IR3, MemW, RegW;
  wire [31:0] EX_PC, ID_PC, IF_PC, IR, LED, MDin, MDinr, MEM_PC, PC, RDin, RDinr, WB_PC;

  \单周期RISC_V  \u_单周期risc_v_1  (
    .IR1(IR1), .IR2(IR2), .IR3(IR3), .RegWrite(RegW), .MemWrite(MemW), .PC(PC), .IR(IR), .RDin(RDin),
    .MDin(MDin), .LedData(LED));
  \气泡流水线  \u_气泡流水线_1  (
    .RegWrite(RegW), .MemWrite(MemW), .IF_PC(IF_PC), .ID_PC(ID_PC), .EX_PC(EX_PC), .M_PC(MEM_PC),
    .WB_PC(WB_PC), .RDin(RDinr), .MDin(MDinr), .LedData(LED));
  \单周期_单级中断  \u_单周期_单级中断_1  ();
  \理想流水线  \u_理想流水线_1  (
    .RegWrite(RegW), .MemWrite(MemW), .IF_PC(IF_PC), .ID_PC(ID_PC), .EX_PC(EX_PC), .M_PC(MEM_PC),
    .WB_PC(WB_PC), .RDin(RDinr), .MDin(MDinr), .LedData(LED));
  \重定向流水线  \u_重定向流水线_1  (
    .RegWrite(RegW), .MemWrite(MemW), .IF_PC(IF_PC), .ID_PC(ID_PC), .EX_PC(EX_PC), .M_PC(MEM_PC),
    .WB_PC(WB_PC), .RDin(RDinr), .MDin(MDinr), .LedData(LED));
  \单周期_多级中断  \u_单周期_多级中断_1  ();

  // Notes on the sheet:
  //   单周期封装测试
  //   气泡流水封装测试
  //   单周期+单级中断封装测试
  //   请检查上面封装有无位宽不匹配，引脚标签是否和连接的标签相对应，否则无法在educoder平台上正确测试
  //   理想流水封装测试
  //   重定向流水封装测试
  //   单周期+多级中断封装测试
endmodule

module pcCh (
  input  jalr,
  input  beq,
  input  bne,
  input  jal,
  output X0,
  output X1,
  output X2
);

  or or_1 (X0, jalr, jal);
  or or_2 (X1, beq, jal, bne);

  assign X2 = 1'b0;
endmodule

module RegCh (
  input  m2r,
  input  jal,
  input  jalr,
  output x0,
  output x1
);

  or or_1 (x1, jal, jalr);

  assign x0 = m2r;
endmodule

module try (
  input  [2:0] in_1,
  input  [3:0] in_2,
  input  [3:0] in_3
);

  wire clock_1_out, comparator_1_lt;
  wire [6:0] adder_1_out, adder_2_out;
  wire [14:0] counter_1_q;
  wire [31:0] rom_1_data;

  Comparator #(.width(15), .mode("unsigned")) comparator_1 (
    .a(counter_1_q), .b({{6{1'b0}}, in_1, {6{1'b1}}}), .lt(comparator_1_lt));  // open: gt, eq
  Counter #(.width(15), .max('h7fff), .ongoal("wrap"), .trigger("rising"), .behavior("new")) counter_1 (
    .D({{6{1'b0}}, in_1, {6{1'b0}}}), .count(comparator_1_lt), .Q(counter_1_q), .clk(clock_1_out));  // open: load, carry, clr, preset, down
  ROM #(.addrWidth(15), .dataWidth(32), .Select("low")) rom_1 (.addr(counter_1_q), .data(rom_1_data));
  Clock #(.highDuration(1), .lowDuration(1)) clock_1 (.out(clock_1_out));
  Adder #(.width(7)) adder_1 (.a(rom_1_data[22:16]), .b({in_2, 3'b000}), .out(adder_1_out));  // open: cin, cout
  Adder #(.width(7)) adder_2 (.a(rom_1_data[29:23]), .b({in_3, 3'b000}), .out(adder_2_out));  // open: cin, cout
  // LCD_Video lcd_video_1: pin names not known; wires that end beside it: 1'b0, clock_1_out, comparator_1_lt, adder_1_out, adder_2_out, rom_1_data[15:0]

  // Notes on the sheet:
  //   contents of rom_1 (hex, n*v repeats v):
  //   0 10000 20000 30000 40000 50000 60000 70000 800000 810420 8245a0 8365c4 8465e3 854180 860420 870000
  //   1000000 10155e0 1027f20 1037a44 1047a44 1057f20 1064dc0 1070000 1801880 1817ee0 1827f00 1837a24
  //   1847a44 1857f00 1867ac0 1871060 2001ca0 2017ee0 2027f00 2037a24 2047a44 2057f00 2067ee0 2071480
  //   2800420 2816660 2827f20 2837a24 2847a44 2857f20 2866240 2870400 3000000 3011480 3026260 3037624
  //   3047624 3055e40 3061060 3070000 3800000 3810000 3820000 3831861 3841861 3850000 3860000 3870000 55e8
  //   159e8 255e8 355e8 455e8 555c8 659e8 759e8 8059e9 815e0a 8255e9 8351a7 844da7 8555e8 865e09 875a09
  //   10055e8 1015e09 1025e09 10355e8 10455e8 1055e09 1065e09 10759e9 18055c8 18151c8 1825a09 1835e09
  //   1845e09 1855e09 18651c8 18755c8 20055c8 20151a7 20259e9 2035e09 2045e0a 2055a09 20651a7 20755c8
  //   28055e8 28159e9 2825e09 2835a09 2845a09 2855e09 2865a09 28755e8 30059e9 3015e09 3025a09 30351c8
  //   30451a7 30559e9 3065e0a 3075a09 38059e8 3815a09 38255e8 38355c8 38455c8 38555c8 3865a09 38759e8 3ea5
  //   13ea4 23e84 33ea4 43e84 53e84 63ea4 742c5 803ea4 8142e3 823e84 833a44 843a44 853e83 8642e4 873ea4
  //   1003ea4 10142e3 10242e3 1033a84 1043ea4 10542e3 1063ec3 1073ea4 1803a84 1813a64 1823ec4 18342e4
  //   18442e4 1853ec4 1863a64 1873a84 2003a84 2013a44 2023ea4 2034303 20442e4 2053ea4 2063644 2073e84
  //   2803e84 2813ec4 2824303 2833ea4 2843ec4 2854303 2863ea4 2873e84 3003ea4 30142e4 3023ea3 3033a44
  //   3043a44 3053ea4 30642e4 3073ea4 3803aa4 3813ea4 3823e84 3833a84 3843a84 3853e84 3863ea4 3873ea4 7ee0
  //   17ee0 27ee0 37ee0 47ee0 57ee0 67ee0 77ae4 807ee0 817ee0 827ee1 837b08 847ae5 857ee0 867ee0 877f03
  //   1007ee0 1017ee1 1027b93 1037f95 1047bb7 1057b2a 1067ee0 1077ee3 1807ee0 1817f27 1827f95 1837ec0
  //   1847f27 1857fb5 1867ee0 1877ee3 2007ee0 2017f04 2027bb7 2037b07 2047b4f 2057f92 2067ee0 2077f03
  //   2807ee0 2817ee0 2827f49 2837f95 2847f92 2857f02 2867ee0 2877f03 3007ee0 3017ee0 3027ee0 3037ee0
  //   3047ee0 3057ee0 3067ee0 3077ee3 3807f05 3817f04 3827f04 3837f04 3847f04 3857f04 3867f04 3877b2a
endmodule

module IF_ID (
  input  NOP,
  input  [31:0] IR,
  input  [31:0] PC,
  input  EN,
  input  CLK,
  input  RST,
  output [31:0] ID_IR,
  output [31:0] ID_PC
);

  wire [31:0] multiplexer_1_out, multiplexer_2_out;

  Multiplexer #(.select(1), .width(32), .disabled("Z"), .enable("false")) multiplexer_1 (
    .in0(IR), .in1({32{1'b0}}), .out(multiplexer_1_out), .sel(NOP));
  Multiplexer #(.select(1), .width(32), .disabled("Z"), .enable("false")) multiplexer_2 (
    .in0(PC), .in1({32{1'b0}}), .out(multiplexer_2_out), .sel(NOP));
  Register #(.width(32), .trigger("rising"), .Select("low")) u_IR (
    .D(multiplexer_1_out), .en(EN), .Q(ID_IR), .clk(CLK), .clr(RST));
  Register #(.width(32), .trigger("rising"), .Select("low")) u_PC (
    .D(multiplexer_2_out), .en(EN), .Q(ID_PC), .clk(CLK), .clr(RST));
endmodule

module ID_EX (
  input  NOP,
  input  AluS,
  input  [3:0] ALUop,
  input  jal,
  input  jalr,
  input  [31:0] IR,
  input  beq,
  input  [31:0] PC,
  input  bne,
  input  [31:0] R1,
  input  RW,
  input  [31:0] IMM,
  input  WB,
  input  [31:0] R2,
  input  Mem,
  input  [1:0] rs1Ch,
  input  [4:0] RD,
  input  ecall,
  input  [1:0] rs2Ch,
  input  EN,
  input  RST,
  input  CLK,
  output AluS_2,
  output [3:0] ALUop_2,
  output jal_2,
  output jalr_2,
  output [31:0] EX_IR,
  output beq_2,
  output [31:0] EX_PC,
  output bne_2,
  output [31:0] R1_2,
  output RW_2,
  output [31:0] IMM_2,
  output WB_2,
  output [31:0] R2_2,
  output Mem_2,
  output [1:0] rs1Ch_2,
  output [4:0] RD_2,
  output ecall_2,
  output [1:0] rs2Ch_2
);

  wire multiplexer_8_out, multiplexer_9_out, multiplexer_10_out, multiplexer_11_out, multiplexer_12_out,
       multiplexer_13_out, multiplexer_14_out, multiplexer_15_out, multiplexer_16_out;
  wire [1:0] multiplexer_17_out, multiplexer_18_out;
  wire [3:0] multiplexer_1_out;
  wire [4:0] multiplexer_7_out;
  wire [31:0] multiplexer_2_out, multiplexer_3_out, multiplexer_4_out, multiplexer_5_out, multiplexer_6_out;

  Multiplexer #(.select(1), .width(4), .disabled("Z"), .enable("false")) multiplexer_1 (
    .in0(ALUop), .in1(4'b0000), .out(multiplexer_1_out), .sel(NOP));
  Multiplexer #(.select(1), .width(32), .disabled("Z"), .enable("false")) multiplexer_2 (
    .in0(IR), .in1({32{1'b0}}), .out(multiplexer_2_out), .sel(NOP));
  Multiplexer #(.select(1), .width(32), .disabled("Z"), .enable("false")) multiplexer_3 (
    .in0(PC), .in1({32{1'b0}}), .out(multiplexer_3_out), .sel(NOP));
  Multiplexer #(.select(1), .width(32), .disabled("Z"), .enable("false")) multiplexer_4 (
    .in0(R1), .in1({32{1'b0}}), .out(multiplexer_4_out), .sel(NOP));
  Multiplexer #(.select(1), .width(32), .disabled("Z"), .enable("false")) multiplexer_5 (
    .in0(IMM), .in1({32{1'b0}}), .out(multiplexer_5_out), .sel(NOP));
  Multiplexer #(.select(1), .width(32), .disabled("Z"), .enable("false")) multiplexer_6 (
    .in0(R2), .in1({32{1'b0}}), .out(multiplexer_6_out), .sel(NOP));
  Multiplexer #(.select(1), .width(5), .disabled("Z"), .enable("false")) multiplexer_7 (
    .in0(RD), .in1({5{1'b0}}), .out(multiplexer_7_out), .sel(NOP));
  Register #(.width(4), .trigger("rising"), .Select("low")) u_ALUs (
    .D(multiplexer_1_out), .en(EN), .Q(ALUop_2), .clk(CLK), .clr(RST));
  Register #(.width(32), .trigger("rising"), .Select("low")) u_IR (
    .D(multiplexer_2_out), .en(EN), .Q(EX_IR), .clk(CLK), .clr(RST));
  Register #(.width(32), .trigger("rising"), .Select("low")) u_PC (
    .D(multiplexer_3_out), .en(EN), .Q(EX_PC), .clk(CLK), .clr(RST));
  Register #(.width(32), .trigger("rising"), .Select("low")) IR_2 (
    .D(multiplexer_4_out), .en(EN), .Q(R1_2), .clk(CLK), .clr(RST));
  Register #(.width(32), .trigger("rising"), .Select("low")) PC_2 (
    .D(multiplexer_5_out), .en(EN), .Q(IMM_2), .clk(CLK), .clr(RST));
  Register #(.width(32), .trigger("rising"), .Select("low")) PC_3 (
    .D(multiplexer_6_out), .en(EN), .Q(R2_2), .clk(CLK), .clr(RST));
  Register #(.width(5), .trigger("rising"), .Select("low")) PC_4 (
    .D(multiplexer_7_out), .en(EN), .Q(RD_2), .clk(CLK), .clr(RST));
  Multiplexer #(.select(1), .width(1), .disabled("Z"), .enable("false")) multiplexer_8 (
    .in0(AluS), .in1(1'b0), .out(multiplexer_8_out), .sel(NOP));
  Multiplexer #(.select(1), .width(1), .disabled("Z"), .enable("false")) multiplexer_9 (
    .in0(jal), .in1(1'b0), .out(multiplexer_9_out), .sel(NOP));
  Multiplexer #(.select(1), .width(1), .disabled("Z"), .enable("false")) multiplexer_10 (
    .in0(jalr), .in1(1'b0), .out(multiplexer_10_out), .sel(NOP));
  Multiplexer #(.select(1), .width(1), .disabled("Z"), .enable("false")) multiplexer_11 (
    .in0(beq), .in1(1'b0), .out(multiplexer_11_out), .sel(NOP));
  Multiplexer #(.select(1), .width(1), .disabled("Z"), .enable("false")) multiplexer_12 (
    .in0(bne), .in1(1'b0), .out(multiplexer_12_out), .sel(NOP));
  Multiplexer #(.select(1), .width(1), .disabled("Z"), .enable("false")) multiplexer_13 (
    .in0(RW), .in1(1'b0), .out(multiplexer_13_out), .sel(NOP));
  Multiplexer #(.select(1), .width(1), .disabled("Z"), .enable("false")) multiplexer_14 (
    .in0(WB), .in1(1'b0), .out(multiplexer_14_out), .sel(NOP));
  Multiplexer #(.select(1), .width(1), .disabled("Z"), .enable("false")) multiplexer_15 (
    .in0(Mem), .in1(1'b0), .out(multiplexer_15_out), .sel(NOP));
  Multiplexer #(.select(1), .width(1), .disabled("Z"), .enable("false")) multiplexer_16 (
    .in0(ecall), .in1(1'b0), .out(multiplexer_16_out), .sel(NOP));
  Register #(.width(1), .trigger("rising"), .Select("low")) u_AluS_2 (
    .D(multiplexer_8_out), .en(EN), .Q(AluS_2), .clk(CLK), .clr(RST));
  Register #(.width(1), .trigger("rising"), .Select("low")) u_jal (
    .D(multiplexer_9_out), .en(EN), .Q(jal_2), .clk(CLK), .clr(RST));
  Register #(.width(1), .trigger("rising"), .Select("low")) u_jalr (
    .D(multiplexer_10_out), .en(EN), .Q(jalr_2), .clk(CLK), .clr(RST));
  Register #(.width(1), .trigger("rising"), .Select("low")) u_beq (
    .D(multiplexer_11_out), .en(EN), .Q(beq_2), .clk(CLK), .clr(RST));
  Register #(.width(1), .trigger("rising"), .Select("low")) u_bne (
    .D(multiplexer_12_out), .en(EN), .Q(bne_2), .clk(CLK), .clr(RST));
  Register #(.width(1), .trigger("rising"), .Select("low")) u_RW (
    .D(multiplexer_13_out), .en(EN), .Q(RW_2), .clk(CLK), .clr(RST));
  Register #(.width(1), .trigger("rising"), .Select("low")) u_WB (
    .D(multiplexer_14_out), .en(EN), .Q(WB_2), .clk(CLK), .clr(RST));
  Register #(.width(1), .trigger("rising"), .Select("low")) u_Mem (
    .D(multiplexer_15_out), .en(EN), .Q(Mem_2), .clk(CLK), .clr(RST));
  Register #(.width(1), .trigger("rising"), .Select("low")) u_ecall (
    .D(multiplexer_16_out), .en(EN), .Q(ecall_2), .clk(CLK), .clr(RST));
  Multiplexer #(.select(1), .width(2), .disabled("Z"), .enable("false")) multiplexer_17 (
    .in0(rs1Ch), .in1(2'b00), .out(multiplexer_17_out), .sel(NOP));
  Multiplexer #(.select(1), .width(2), .disabled("Z"), .enable("false")) multiplexer_18 (
    .in0(rs2Ch), .in1(2'b00), .out(multiplexer_18_out), .sel(NOP));
  Register #(.width(2), .trigger("rising"), .Select("low")) u_rs1Ch (
    .D(multiplexer_17_out), .en(EN), .Q(rs1Ch_2), .clk(CLK), .clr(RST));
  Register #(.width(2), .trigger("rising"), .Select("low")) u_rs2Ch (
    .D(multiplexer_18_out), .en(EN), .Q(rs2Ch_2), .clk(CLK), .clr(RST));
endmodule
module EX_MEM (
  input  NOP,
  input  RW,
  input  WB,
  input  Mem,
  input  ecall,
  input  [31:0] IR,
  input  [31:0] PC,
  input  [31:0] ALU,
  input  [31:0] R1,
  input  [31:0] R2,
  input  [4:0] RD,
  input  EN,
  input  RST,
  input  CLK,
  output RW_2,
  output WB_2,
  output Mem_2,
  output ecall_2,
  output [31:0] IR_2,
  output [31:0] PC_2,
  output [31:0] ALU_2,
  output [31:0] R1_2,
  output [31:0] R2_2,
  output [4:0] RD_2
);

  wire multiplexer_1_out, multiplexer_2_out, multiplexer_3_out, multiplexer_4_out;
  wire [4:0] multiplexer_10_out;
  wire [31:0] multiplexer_5_out, multiplexer_6_out, multiplexer_7_out, multiplexer_8_out, multiplexer_9_out;

  Multiplexer #(.select(1), .width(1), .disabled("Z"), .enable("false")) multiplexer_1 (
    .in0(RW), .in1(1'b0), .out(multiplexer_1_out), .sel(NOP));
  Multiplexer #(.select(1), .width(1), .disabled("Z"), .enable("false")) multiplexer_2 (
    .in0(WB), .in1(1'b0), .out(multiplexer_2_out), .sel(NOP));
  Multiplexer #(.select(1), .width(1), .disabled("Z"), .enable("false")) multiplexer_3 (
    .in0(Mem), .in1(1'b0), .out(multiplexer_3_out), .sel(NOP));
  Multiplexer #(.select(1), .width(1), .disabled("Z"), .enable("false")) multiplexer_4 (
    .in0(ecall), .in1(1'b0), .out(multiplexer_4_out), .sel(NOP));
  Multiplexer #(.select(1), .width(32), .disabled("Z"), .enable("false")) multiplexer_5 (
    .in0(IR), .in1({32{1'b0}}), .out(multiplexer_5_out), .sel(NOP));
  Multiplexer #(.select(1), .width(32), .disabled("Z"), .enable("false")) multiplexer_6 (
    .in0(PC), .in1({32{1'b0}}), .out(multiplexer_6_out), .sel(NOP));
  Multiplexer #(.select(1), .width(32), .disabled("Z"), .enable("false")) multiplexer_7 (
    .in0(ALU), .in1({32{1'b0}}), .out(multiplexer_7_out), .sel(NOP));
  Multiplexer #(.select(1), .width(32), .disabled("Z"), .enable("false")) multiplexer_8 (
    .in0(R1), .in1({32{1'b0}}), .out(multiplexer_8_out), .sel(NOP));
  Multiplexer #(.select(1), .width(32), .disabled("Z"), .enable("false")) multiplexer_9 (
    .in0(R2), .in1({32{1'b0}}), .out(multiplexer_9_out), .sel(NOP));
  Multiplexer #(.select(1), .width(5), .disabled("Z"), .enable("false")) multiplexer_10 (
    .in0(RD), .in1({5{1'b0}}), .out(multiplexer_10_out), .sel(NOP));
  Register #(.width(1), .trigger("rising"), .Select("low")) u_RW (
    .D(multiplexer_1_out), .en(EN), .Q(RW_2), .clk(CLK), .clr(RST));
  Register #(.width(1), .trigger("rising"), .Select("low")) u_WB (
    .D(multiplexer_2_out), .en(EN), .Q(WB_2), .clk(CLK), .clr(RST));
  Register #(.width(1), .trigger("rising"), .Select("low")) u_Mem (
    .D(multiplexer_3_out), .en(EN), .Q(Mem_2), .clk(CLK), .clr(RST));
  Register #(.width(1), .trigger("rising"), .Select("low")) u_Mem_2 (
    .D(multiplexer_4_out), .en(EN), .Q(ecall_2), .clk(CLK), .clr(RST));
  Register #(.width(32), .trigger("rising"), .Select("low")) u_IR (
    .D(multiplexer_5_out), .en(EN), .Q(IR_2), .clk(CLK), .clr(RST));
  Register #(.width(32), .trigger("rising"), .Select("low")) u_PC (
    .D(multiplexer_6_out), .en(EN), .Q(PC_2), .clk(CLK), .clr(RST));
  Register #(.width(32), .trigger("rising"), .Select("low")) u_ALU (
    .D(multiplexer_7_out), .en(EN), .Q(ALU_2), .clk(CLK), .clr(RST));
  Register #(.width(32), .trigger("rising"), .Select("low")) u_R1 (
    .D(multiplexer_8_out), .en(EN), .Q(R1_2), .clk(CLK), .clr(RST));
  Register #(.width(32), .trigger("rising"), .Select("low")) u_R2 (
    .D(multiplexer_9_out), .en(EN), .Q(R2_2), .clk(CLK), .clr(RST));
  Register #(.width(5), .trigger("rising"), .Select("low")) u_PC_2 (
    .D(multiplexer_10_out), .en(EN), .Q(RD_2), .clk(CLK), .clr(RST));
endmodule

module MEM_WB (
  input  NOP,
  input  RW,
  input  WB,
  input  ecall,
  input  [31:0] IR,
  input  [31:0] PC,
  input  [31:0] ALU,
  input  [31:0] M,
  input  [31:0] R1,
  input  [31:0] R2,
  input  [4:0] RD,
  input  EN,
  input  RST,
  input  CLK,
  output RW_2,
  output WB_2,
  output ecall_2,
  output [31:0] IR_2,
  output [31:0] PC_2,
  output [31:0] ALU_2,
  output [31:0] M_2,
  output [31:0] R1_2,
  output [31:0] R2_2,
  output [4:0] RD_2
);

  wire multiplexer_1_out, multiplexer_2_out, multiplexer_3_out;
  wire [4:0] multiplexer_10_out;
  wire [31:0] multiplexer_4_out, multiplexer_5_out, multiplexer_6_out, multiplexer_7_out, multiplexer_8_out,
       multiplexer_9_out;

  Multiplexer #(.select(1), .width(1), .disabled("Z"), .enable("false")) multiplexer_1 (
    .in0(RW), .in1(1'b0), .out(multiplexer_1_out), .sel(NOP));
  Multiplexer #(.select(1), .width(1), .disabled("Z"), .enable("false")) multiplexer_2 (
    .in0(WB), .in1(1'b0), .out(multiplexer_2_out), .sel(NOP));
  Multiplexer #(.select(1), .width(1), .disabled("Z"), .enable("false")) multiplexer_3 (
    .in0(ecall), .in1(1'b0), .out(multiplexer_3_out), .sel(NOP));
  Multiplexer #(.select(1), .width(32), .disabled("Z"), .enable("false")) multiplexer_4 (
    .in0(IR), .in1({32{1'b0}}), .out(multiplexer_4_out), .sel(NOP));
  Multiplexer #(.select(1), .width(32), .disabled("Z"), .enable("false")) multiplexer_5 (
    .in0(PC), .in1({32{1'b0}}), .out(multiplexer_5_out), .sel(NOP));
  Multiplexer #(.select(1), .width(32), .disabled("Z"), .enable("false")) multiplexer_6 (
    .in0(ALU), .in1({32{1'b0}}), .out(multiplexer_6_out), .sel(NOP));
  Multiplexer #(.select(1), .width(32), .disabled("Z"), .enable("false")) multiplexer_7 (
    .in0(M), .in1({32{1'b0}}), .out(multiplexer_7_out), .sel(NOP));
  Multiplexer #(.select(1), .width(32), .disabled("Z"), .enable("false")) multiplexer_8 (
    .in0(R1), .in1({32{1'b0}}), .out(multiplexer_8_out), .sel(NOP));
  Multiplexer #(.select(1), .width(32), .disabled("Z"), .enable("false")) multiplexer_9 (
    .in0(R2), .in1({32{1'b0}}), .out(multiplexer_9_out), .sel(NOP));
  Multiplexer #(.select(1), .width(5), .disabled("Z"), .enable("false")) multiplexer_10 (
    .in0(RD), .in1({5{1'b0}}), .out(multiplexer_10_out), .sel(NOP));
  Register #(.width(1), .trigger("rising"), .Select("low")) u_RW (
    .D(multiplexer_1_out), .en(EN), .Q(RW_2), .clk(CLK), .clr(RST));
  Register #(.width(1), .trigger("rising"), .Select("low")) u_WB (
    .D(multiplexer_2_out), .en(EN), .Q(WB_2), .clk(CLK), .clr(RST));
  Register #(.width(1), .trigger("rising"), .Select("low")) u_ecall (
    .D(multiplexer_3_out), .en(EN), .Q(ecall_2), .clk(CLK), .clr(RST));
  Register #(.width(32), .trigger("rising"), .Select("low")) u_IR (
    .D(multiplexer_4_out), .en(EN), .Q(IR_2), .clk(CLK), .clr(RST));
  Register #(.width(32), .trigger("rising"), .Select("low")) u_PC (
    .D(multiplexer_5_out), .en(EN), .Q(PC_2), .clk(CLK), .clr(RST));
  Register #(.width(32), .trigger("rising"), .Select("low")) u_ALU (
    .D(multiplexer_6_out), .en(EN), .Q(ALU_2), .clk(CLK), .clr(RST));
  Register #(.width(32), .trigger("rising"), .Select("low")) u_M (
    .D(multiplexer_7_out), .en(EN), .Q(M_2), .clk(CLK), .clr(RST));
  Register #(.width(32), .trigger("rising"), .Select("low")) u_M_2 (
    .D(multiplexer_8_out), .en(EN), .Q(R1_2), .clk(CLK), .clr(RST));
  Register #(.width(32), .trigger("rising"), .Select("low")) M_3 (
    .D(multiplexer_9_out), .en(EN), .Q(R2_2), .clk(CLK), .clr(RST));
  Register #(.width(5), .trigger("rising"), .Select("low")) u_PC_2 (
    .D(multiplexer_10_out), .en(EN), .Q(RD_2), .clk(CLK), .clr(RST));
endmodule

module IMMch (
  input  jal,
  input  beq,
  input  bne,
  input  st,
  output X1,
  output X0
);

  or or_1 (X1, beq, jal, bne);
  or or_2 (X0, jal, st);
endmodule

module RegConf (
  input  RegWt,
  input  [4:0] RD,
  input  [4:0] rs1,
  input  [4:0] rs2,
  input  AluS,
  output Conf
);

  wire and_1_out, comparator_1_eq, comparator_2_eq, comparator_3_eq, or_1_out;

  Comparator #(.width(5), .mode("twosComplement")) comparator_1 (
    .a({5{1'b0}}), .b(RD), .eq(comparator_1_eq));  // open: gt, lt
  Comparator #(.width(5), .mode("twosComplement")) comparator_2 (
    .a(RD), .b(rs1), .eq(comparator_2_eq));  // open: gt, lt
  Comparator #(.width(5), .mode("twosComplement")) comparator_3 (
    .a(RD), .b(rs2), .eq(comparator_3_eq));  // open: gt, lt
  or or_1 (or_1_out, comparator_2_eq, and_1_out);
  and and_1 (and_1_out, comparator_3_eq, ~AluS);  // AND_Gate
  and and_2 (Conf, RegWt, ~comparator_1_eq, or_1_out);  // AND_Gate
endmodule

module Redirect (
  input  m2r,
  input  Rw,
  input  [4:0] rs1,
  input  [4:0] rs2,
  input  [4:0] rd,
  input  AluS,
  output ldu,
  output x1,
  output x2
);

  wire and_1_out, comparator_1_eq, comparator_2_eq, not_1_out, or_1_out;

  not not_1 (not_1_out, AluS);
  Comparator #(.width(5), .mode("twosComplement")) comparator_1 (
    .a(rs1), .b(rd), .eq(comparator_1_eq));  // open: gt, lt
  Comparator #(.width(5), .mode("twosComplement")) comparator_2 (
    .a(rs2), .b(rd), .eq(comparator_2_eq));  // open: gt, lt
  and and_1 (and_1_out, comparator_2_eq, not_1_out);
  or or_1 (or_1_out, comparator_1_eq, and_1_out);
  and and_2 (x1, Rw, comparator_1_eq);
  and and_3 (x2, Rw, and_1_out);
  and and_4 (ldu, m2r, or_1_out);
endmodule

module intGen (
  input  clk,
  input  ints1,
  input  ints2,
  input  ints3,
  input  ints4,
  input  ints5,
  input  ints6,
  input  rst,
  output [2:0] intX,
  output intG
);

  wire and_1_out, and_2_out, and_3_out, and_4_out, and_5_out, and_6_out, d_ff_1_q, d_ff_2_q, d_ff_3_q,
       d_ff_4_q, d_ff_5_q, d_ff_6_q, decoder_1_out1, decoder_1_out2, decoder_1_out3, decoder_1_out4,
       decoder_1_out5, decoder_1_out6, int1, int2, int3, int4, int5, int6, or_1_out, or_2_out, or_3_out,
       or_4_out, or_5_out, or_6_out;

  Decoder #(.select(3), .tristate("false"), .disabled(0), .enable("true")) decoder_1 (
    .out1(decoder_1_out1), .out2(decoder_1_out2), .out3(decoder_1_out3), .out4(decoder_1_out4),
    .out5(decoder_1_out5), .out6(decoder_1_out6), .sel(intX), .en(rst));  // open: out0, out7
  Priority_Encoder #(.select(3), .disabled("Z")) priority_encoder_1 (
    .in0(1'b0), .in1(int1), .in2(int2), .in3(int3), .in4(int4), .in5(int5), .in6(int6), .out(intX), .gs(intG));  // open: in7, en_out, en_in
  D_Flip_Flop #(.trigger("rising"), .Pre_Clr_Positions("LEGACY"), .NegatePresetClear("false"), .enable("true"), .NewFFLayout("false")) d_ff_1 (
    .clk(ints1), .D(1'b1), .Q(d_ff_1_q), .reset(int1));  // open: Qn, preset, en
  D_Flip_Flop #(.trigger("rising"), .Pre_Clr_Positions("LEGACY"), .NegatePresetClear("false"), .enable("true"), .NewFFLayout("false")) d_ff_2 (
    .clk(ints2), .D(1'b1), .Q(d_ff_2_q), .reset(int2));  // open: Qn, preset, en
  D_Flip_Flop #(.trigger("rising"), .Pre_Clr_Positions("LEGACY"), .NegatePresetClear("false"), .enable("true"), .NewFFLayout("false")) d_ff_3 (
    .clk(ints3), .D(1'b1), .Q(d_ff_3_q), .reset(int3));  // open: Qn, preset, en
  D_Flip_Flop #(.trigger("rising"), .Pre_Clr_Positions("LEGACY"), .NegatePresetClear("false"), .enable("true"), .NewFFLayout("false")) d_ff_4 (
    .clk(ints4), .D(1'b1), .Q(d_ff_4_q), .reset(int4));  // open: Qn, preset, en
  D_Flip_Flop #(.trigger("rising"), .Pre_Clr_Positions("LEGACY"), .NegatePresetClear("false"), .enable("true"), .NewFFLayout("false")) d_ff_5 (
    .clk(ints5), .D(1'b1), .Q(d_ff_5_q), .reset(int5));  // open: Qn, preset, en
  D_Flip_Flop #(.trigger("rising"), .Pre_Clr_Positions("LEGACY"), .NegatePresetClear("false"), .enable("true"), .NewFFLayout("false")) d_ff_6 (
    .clk(ints6), .D(1'b1), .Q(d_ff_6_q), .reset(int6));  // open: Qn, preset, en
  or or_1 (or_1_out, d_ff_1_q, int1);
  or or_2 (or_2_out, d_ff_2_q, int2);
  or or_3 (or_3_out, d_ff_3_q, int3);
  or or_4 (or_4_out, d_ff_4_q, int4);
  or or_5 (or_5_out, d_ff_5_q, int5);
  or or_6 (or_6_out, d_ff_6_q, int6);
  and and_1 (and_1_out, or_1_out, ~decoder_1_out1);  // AND_Gate
  and and_2 (and_2_out, or_2_out, ~decoder_1_out2);  // AND_Gate
  and and_3 (and_3_out, or_3_out, ~decoder_1_out3);  // AND_Gate
  and and_4 (and_4_out, or_4_out, ~decoder_1_out4);  // AND_Gate
  and and_5 (and_5_out, or_5_out, ~decoder_1_out5);  // AND_Gate
  and and_6 (and_6_out, or_6_out, ~decoder_1_out6);  // AND_Gate
  D_Flip_Flop #(.trigger("rising"), .Pre_Clr_Positions("LEGACY"), .NegatePresetClear("false"), .enable("true"), .NewFFLayout("false")) IR1 (
    .clk(clk), .D(and_1_out), .Q(int1));  // open: Qn, preset, en, reset
  D_Flip_Flop #(.trigger("rising"), .Pre_Clr_Positions("LEGACY"), .NegatePresetClear("false"), .enable("true"), .NewFFLayout("false")) IR2 (
    .clk(clk), .D(and_2_out), .Q(int2));  // open: Qn, preset, en, reset
  D_Flip_Flop #(.trigger("rising"), .Pre_Clr_Positions("LEGACY"), .NegatePresetClear("false"), .enable("true"), .NewFFLayout("false")) IR3 (
    .clk(clk), .D(and_3_out), .Q(int3));  // open: Qn, preset, en, reset
  D_Flip_Flop #(.trigger("rising"), .Pre_Clr_Positions("LEGACY"), .NegatePresetClear("false"), .enable("true"), .NewFFLayout("false")) IR4 (
    .clk(clk), .D(and_4_out), .Q(int4));  // open: Qn, preset, en, reset
  D_Flip_Flop #(.trigger("rising"), .Pre_Clr_Positions("LEGACY"), .NegatePresetClear("false"), .enable("true"), .NewFFLayout("false")) IR5 (
    .clk(clk), .D(and_5_out), .Q(int5));  // open: Qn, preset, en, reset
  D_Flip_Flop #(.trigger("rising"), .Pre_Clr_Positions("LEGACY"), .NegatePresetClear("false"), .enable("true"), .NewFFLayout("false")) IR6 (
    .clk(clk), .D(and_6_out), .Q(int6));  // open: Qn, preset, en, reset

  // Notes on the sheet:
  //   Reset 
  //   Reset 
  //   Reset 
  //   Reset 
  //   Reset 
  //   Reset 
endmodule

module EPCstack (
  input  [1:0] PriIN,
  input  [31:0] PC,
  input  INT,
  input  Uret,
  input  RST,
  input  CLK,
  output [1:0] PriOUT,
  output [31:0] EPC
);

  wire decoder_1_out0, decoder_1_out1, decoder_1_out2, or_1_out;
  wire [1:0] counter_1_q, register_1_q, register_3_q, register_5_q;
  wire [31:0] register_2_q, register_4_q, register_6_q;

  Decoder #(.select(2), .tristate("false"), .disabled(0), .enable("false")) decoder_1 (
    .out0(decoder_1_out0), .out1(decoder_1_out1), .out2(decoder_1_out2), .sel(counter_1_q));  // open: out3
  Register #(.width(2), .trigger("rising"), .Select("low")) register_1 (
    .D(PriIN), .en(decoder_1_out0), .Q(register_1_q), .clk(CLK), .clr(RST));
  Register #(.width(32), .trigger("rising"), .Select("low")) register_2 (
    .D(PC), .en(decoder_1_out0), .Q(register_2_q), .clk(CLK), .clr(RST));
  or or_1 (or_1_out, INT, Uret);
  Counter #(.width(2), .max('h3), .ongoal("wrap"), .trigger("rising"), .behavior("new")) counter_1 (
    .count(or_1_out), .Q(counter_1_q), .clk(CLK), .clr(RST), .down(Uret));  // open: load, D, carry, preset
  Register #(.width(2), .trigger("rising"), .Select("low")) register_3 (
    .D(PriIN), .en(decoder_1_out1), .Q(register_3_q), .clk(CLK), .clr(RST));
  Register #(.width(32), .trigger("rising"), .Select("low")) register_4 (
    .D(PC), .en(decoder_1_out1), .Q(register_4_q), .clk(CLK), .clr(RST));
  Register #(.width(2), .trigger("rising"), .Select("low")) register_5 (
    .D(PriIN), .en(decoder_1_out2), .Q(register_5_q), .clk(CLK), .clr(RST));
  Register #(.width(32), .trigger("rising"), .Select("low")) register_6 (
    .D(PC), .en(decoder_1_out2), .Q(register_6_q), .clk(CLK), .clr(RST));
  Multiplexer #(.select(2), .width(2), .disabled("Z"), .enable("false")) multiplexer_1 (
    .in0(2'b00), .in1(register_1_q), .in2(register_3_q), .in3(register_5_q), .out(PriOUT), .sel(counter_1_q));
  Multiplexer #(.select(2), .width(32), .disabled("Z"), .enable("false")) multiplexer_2 (
    .in0(register_2_q), .in1(register_2_q), .in2(register_4_q), .in3(register_6_q), .out(EPC),
    .sel(counter_1_q));
endmodule

module BOX (
);

  wire alu_1_equal, and_3_out, and_5_out, CLK, comparator_1_eq, counter_1_carry, counter_2_carry, d_ff_1_qn,
       dhex, displaying, Go, halt, INT, intgen_1_intg, irc, irs, MemWrite, MovDown, MovLeft, MovRight, MovUp,
       not_1_out, not_2_out, not_3_out, not_4_out, not_5_out, or_1_out, or_2_out, or_3_out, or_5_out,
       register_2_q, RegWrite, RST, START, Uret, \单周期硬布线控制器_1_alu_src , \单周期硬布线控制器_1_beq , \单周期硬布线控制器_1_bne ,
       \单周期硬布线控制器_1_ecall , \单周期硬布线控制器_1_jal , \单周期硬布线控制器_1_jalr , \单周期硬布线控制器_1_memtoreg ,
       \单周期硬布线控制器_1_s_type ;
  wire [1:0] counter_1_q_2, regch_1_x0;
  wire [2:0] intgen_1_intx, multiplexer_5_out, pcch_1_x0;
  wire [3:0] multiplexer_9_out, multiplexer_10_out, rom_2_data_2, rom_2_data_3, \单周期硬布线控制器_1_alu_op ;
  wire [4:0] multiplexer_3_out, multiplexer_4_out;
  wire [5:0] counter_1_q;
  wire [15:0] counter_2_q, multiplexer_8_out;
  wire [31:0] adder_1_out, adder_2_out, adder_3_out, alu_1_result, and_4_out, bit_extender_1_out,
       bit_extender_2_out, bit_extender_3_out, bit_extender_4_out, ecallA, ecallV, INTAddr, IR, LedData,
       multiplexer_1_out, multiplexer_2_out, multiplexer_6_out, multiplexer_7_out, PC, ram_1_data, RDin,
       rom_2_data, shifter_1_out, shifter_2_out, UretAddr;

  Clock #(.highDuration(1), .lowDuration(1)) clock_1 (.out(CLK));
  Button RESET (.out(RST));
  Button \u_继续运行  (.out(Go));
  or or_1 (or_1_out, not_1_out, Go);
  not not_1 (not_1_out, halt);
  Multiplexer #(.select(2), .width(32), .disabled("Z"), .enable("false")) multiplexer_1 (
    .in0(multiplexer_2_out), .in1(INTAddr), .in2(UretAddr), .out(multiplexer_1_out), .sel({Uret, INT}));  // open: in3
  Comparator #(.width(32), .mode("twosComplement")) comparator_1 (
    .a(ecallV), .b(32'h22), .eq(comparator_1_eq));  // open: gt, lt
  Register #(.width(32), .trigger("rising"), .Select("low")) u_PC (
    .D(multiplexer_1_out), .en(or_1_out), .Q(PC), .clk(CLK), .clr(RST), .cs(1'b0), .preset(1'b0));
  Register #(.width(32), .trigger("rising"), .Select("low")) register_1 (
    .D(ecallA), .en(dhex), .Q(LedData), .clk(CLK), .clr(RST), .cs(1'b0), .preset(1'b0));
  Button button_1 (.out(START));
  not not_2 (not_2_out, comparator_1_eq);
  and and_1 (halt, not_2_out, \单周期硬布线控制器_1_ecall );
  and and_2 (dhex, comparator_1_eq, \单周期硬布线控制器_1_ecall );
  ROM #(.addrWidth(10), .dataWidth(32), .Select("high")) rom_1 (.addr(PC[11:2]), .data(IR), .sel(1'b1));
  Button button_2 (.out(MovUp));
  Button button_3 (.out(MovLeft));
  Button button_4 (.out(MovDown));
  and and_3 (and_3_out, \单周期硬布线控制器_1_beq , alu_1_equal);
  \单周期硬布线控制器  \u_单周期硬布线控制器_1  (
    .Funct({IR[30], IR[25], IR[14:12]}), .OP(IR[6:2]), .ALU_OP(\单周期硬布线控制器_1_alu_op ),
    .MemToReg(\单周期硬布线控制器_1_memtoreg ), .MemWrite(MemWrite), .ALU_SRC(\单周期硬布线控制器_1_alu_src ),
    .RegWrite(RegWrite), .ecall(\单周期硬布线控制器_1_ecall ), .S_type(\单周期硬布线控制器_1_s_type ),
    .Jalr(\单周期硬布线控制器_1_jalr ), .Beq(\单周期硬布线控制器_1_beq ), .JAL(\单周期硬布线控制器_1_jal ), .Bne(\单周期硬布线控制器_1_bne ),
    .IR21(IR[21]), .uret(Uret), .irs(irs), .irc(irc));
  assign bit_extender_1_out = {{20{IR[31]}}, IR[31:20]};  // Bit_Extender bit_extender_1
  assign bit_extender_2_out = {{20{IR[31]}}, {IR[31:25], IR[11:7]}};  // Bit_Extender bit_extender_2
  assign and_4_out = alu_1_result & 32'hfffffffe;  // AND_Gate and_4, 32 bits wide
  assign bit_extender_3_out = {{20{IR[31]}}, {IR[31], IR[7], IR[30:25], IR[11:8]}};  // Bit_Extender bit_extender_3
  assign bit_extender_4_out = {{12{IR[31]}}, {IR[31], IR[19:12], IR[20], IR[30:21]}};  // Bit_Extender bit_extender_4
  Button button_5 (.out(MovRight));
  and and_5 (and_5_out, \单周期硬布线控制器_1_bne , not_5_out);
  Adder #(.width(32)) adder_1 (.a(32'h4), .b(PC), .out(adder_1_out));  // open: cin, cout
  Shifter #(.width(32), .shift("ll")) shifter_1 (.in(bit_extender_3_out), .\dist (5'b00001), .out(shifter_1_out));
  Adder #(.width(32)) adder_2 (.a(shifter_1_out), .b(PC), .out(adder_2_out));  // open: cin, cout
  Shifter #(.width(32), .shift("ll")) shifter_2 (.in(bit_extender_4_out), .\dist (5'b00001), .out(shifter_2_out));
  Adder #(.width(32)) adder_3 (.a(shifter_2_out), .b(PC), .out(adder_3_out));  // open: cin, cout
  // Probe on LedData
  or or_2 (or_2_out, dhex, counter_1_carry);
  or or_3 (or_3_out, START, counter_2_carry);
  pcCh pcch_1 (
    .jalr(\单周期硬布线控制器_1_jalr ), .beq(and_3_out), .bne(and_5_out), .jal(\单周期硬布线控制器_1_jal ), .X0(pcch_1_x0[0]),
    .X1(pcch_1_x0[1]), .X2(pcch_1_x0[2]));
  Multiplexer #(.select(3), .width(32), .disabled("Z"), .enable("false")) multiplexer_2 (
    .in0(adder_1_out), .in1(and_4_out), .in2(adder_2_out), .in3(adder_3_out), .out(multiplexer_2_out),
    .sel(pcch_1_x0));  // open: in4, in5, in6, in7
  not not_3 (not_3_out, register_2_q);
  Register #(.width(1), .trigger("rising"), .Select("low")) register_2 (
    .D(not_3_out), .en(or_2_out), .Q(register_2_q), .clk(CLK));  // open: clr
  Register #(.width(1), .trigger("rising"), .Select("low")) register_3 (
    .D(not_4_out), .en(or_3_out), .Q(counter_1_q_2[1]), .clk(CLK));  // open: clr
  not not_4 (not_4_out, counter_1_q_2[1]);
  Multiplexer #(.select(1), .width(5), .disabled("Z"), .enable("false")) multiplexer_3 (
    .in0(IR[19:15]), .in1(5'b01010), .out(multiplexer_3_out), .sel(\单周期硬布线控制器_1_ecall ));
  Multiplexer #(.select(1), .width(5), .disabled("Z"), .enable("false")) multiplexer_4 (
    .in0(IR[24:20]), .in1(5'b10001), .out(multiplexer_4_out), .sel(\单周期硬布线控制器_1_ecall ));
  Counter #(.width(7), .max('h7f), .ongoal("wrap"), .trigger("rising"), .behavior("new")) counter_1 (
    .count(register_2_q), .Q({counter_1_q_2[0], counter_1_q}), .carry(counter_1_carry), .clk(CLK));  // open: load, D, clr, preset, down
  Counter #(.width(16), .max('ha7f), .ongoal("wrap"), .trigger("rising"), .behavior("new")) counter_2 (
    .load(START), .D(16'h180), .count(counter_1_q_2[1]), .Q(counter_2_q), .carry(counter_2_carry), .clk(CLK));  // open: clr, preset, down
  RegCh regch_1 (
    .m2r(\单周期硬布线控制器_1_memtoreg ), .jal(\单周期硬布线控制器_1_jal ), .jalr(\单周期硬布线控制器_1_jalr ), .x0(regch_1_x0[0]),
    .x1(regch_1_x0[1]));
  Regifile regifile_1 (
    .Din(RDin), .Clk(CLK), .R1(ecallA), .R2(ecallV), .WE(RegWrite), .W_num(IR[11:7]),
    .R1_num(multiplexer_3_out), .R2_num(multiplexer_4_out));
  or or_4 (displaying, register_2_q, counter_1_q_2[1]);
  Multiplexer #(.select(1), .width(3), .disabled("Z"), .enable("false")) multiplexer_5 (
    .in0(LedData[10:8]), .in1(LedData[21:19]), .out(multiplexer_5_out), .sel(counter_1_q_2[0]));
  // Probe on multiplexer_5_out
  not not_5 (not_5_out, alu_1_equal);
  Multiplexer #(.select(1), .width(32), .disabled("Z"), .enable("false")) multiplexer_6 (
    .in0(ecallV), .in1(multiplexer_7_out), .out(multiplexer_6_out), .sel(\单周期硬布线控制器_1_alu_src ));
  Multiplexer #(.select(1), .width(32), .disabled("Z"), .enable("false")) multiplexer_7 (
    .in0(bit_extender_1_out), .in1(bit_extender_2_out), .out(multiplexer_7_out), .sel(\单周期硬布线控制器_1_s_type ));
  // Probe on \单周期硬布线控制器_1_alu_op 
  ALU alu_1 (
    .X(ecallA), .Y(multiplexer_6_out), .AluOP(\单周期硬布线控制器_1_alu_op ), .Equal(alu_1_equal),
    .Result(alu_1_result));  // open: Result_2, out_4, out_6
  Multiplexer #(.select(1), .width(16), .disabled("Z"), .enable("false")) multiplexer_8 (
    .in0({{7{1'b0}}, multiplexer_5_out, counter_1_q}), .in1(counter_2_q), .out(multiplexer_8_out),
    .sel(counter_1_q_2[1]));
  or or_5 (or_5_out, INT, Uret);
  intGen intgen_1 (
    .clk(CLK), .ints1(MovLeft), .ints2(MovRight), .ints3(MovUp), .rst(INT), .intX(intgen_1_intx),
    .intG(intgen_1_intg), .ints4(MovDown), .ints5(START));  // open: ints6
  ROM #(.addrWidth(16), .dataWidth(32), .Select("low")) rom_2 (
    .addr(multiplexer_8_out),
    .data({rom_2_data[31:30], rom_2_data_3, rom_2_data[25:23], rom_2_data_2, rom_2_data[18:0]}));
  Multiplexer #(.select(2), .width(4), .disabled("Z"), .enable("false")) multiplexer_9 (
    .in0(LedData[7:4]), .in1(LedData[18:15]), .in2(rom_2_data_2), .in3(rom_2_data_2),
    .out(multiplexer_9_out), .sel(counter_1_q_2));
  Multiplexer #(.select(2), .width(4), .disabled("Z"), .enable("false")) multiplexer_10 (
    .in0(LedData[3:0]), .in1(LedData[14:11]), .in2(rom_2_data_3), .in3(rom_2_data_3),
    .out(multiplexer_10_out), .sel(counter_1_q_2));
  Register #(.width(32), .trigger("rising"), .Select("low")) EPC (
    .D(multiplexer_2_out), .en(INT), .Q(UretAddr), .clk(CLK));  // open: clr
  D_Flip_Flop #(.trigger("rising"), .Pre_Clr_Positions("LEGACY"), .NegatePresetClear("false"), .enable("true"), .NewFFLayout("false")) d_ff_1 (
    .clk(CLK), .D(d_ff_1_qn), .Qn(d_ff_1_qn), .en(or_5_out));  // open: Q, preset, reset
  RAM #(.addrWidth(10), .dataWidth(32), .bus("separate"), .Select("high")) ram_1 (
    .addr(alu_1_result[11:2]), .din(ecallV), .data(ram_1_data), .str(MemWrite), .clk(CLK),
    .ld(\单周期硬布线控制器_1_memtoreg ), .clr(RST));  // open: sel
  and and_6 (INT, d_ff_1_qn, ~displaying, intgen_1_intg);  // AND_Gate
  Multiplexer #(.select(2), .width(32), .disabled("Z"), .enable("false")) multiplexer_11 (
    .in0(alu_1_result), .in1(ram_1_data), .in2(adder_1_out), .out(RDin), .sel(regch_1_x0));  // open: in3
  // LCD_Video lcd_video_1: pin names not known; wires that end beside it: CLK, displaying, {multiplexer_9_out, rom_2_data[18:16]}, {multiplexer_10_out, rom_2_data[25:23]}, rom_2_data[15:0]
  // Probe on rom_2_data[15:0]
  // Probe on {multiplexer_9_out, rom_2_data[18:16]}
  // Probe on {multiplexer_10_out, rom_2_data[25:23]}
  Multiplexer #(.select(3), .width(32), .disabled("Z"), .enable("false")) multiplexer_12 (
    .in1(32'h350), .in2(32'h364), .in3(32'h33c), .in4(32'h328), .in5(32'h18), .out(INTAddr),
    .sel(intgen_1_intx));  // open: in0, in6, in7

  // Other names for the same wires on the sheet: MDin[31:0] = ecallV; y1[3:0] = LedData[3:0]; x1[3:0] = LedData[7:4];
  //   t1[2:0] = LedData[10:8]; y2[3:0] = LedData[14:11]; x2[3:0] = LedData[18:15]; t2[2:0] = LedData[21:19]

  // Notes on the sheet:
  //   指令存储器
  //   rs1
  //   rs2
  //   指令字
  //   contents of rom_1 (hex, n*v repeats v):
  //   40006f 4*13 ff1ff06f 100413 500493 e93 100993 13ea023 4e8e93 100993 13ea023 4e8e93 100993 13ea023
  //   4e8e93 100993 13ea023 4e8e93 100993 13ea023 4e8e93 100993 13ea023 4e8e93 100993 13ea023 4e8e93
  //   100993 13ea023 4e8e93 100993 13ea023 4e8e93 200993 13ea023 4e8e93 200993 13ea023 4e8e93 400993
  //   13ea023 4e8e93 200993 13ea023 4e8e93 100993 13ea023 4e8e93 100993 13ea023 4e8e93 100993 13ea023
  //   4e8e93 100993 13ea023 4e8e93 200993 13ea023 4e8e93 300993 13ea023 4e8e93 993 13ea023 4e8e93 993
  //   13ea023 4e8e93 100993 13ea023 4e8e93 100993 13ea023 4e8e93 100993 13ea023 4e8e93 100993 13ea023
  //   4e8e93 100993 13ea023 4e8e93 993 13ea023 4e8e93 300993 13ea023 4e8e93 993 13ea023 4e8e93 100993
  //   13ea023 4e8e93 100993 13ea023 4e8e93 100993 13ea023 4e8e93 100993 13ea023 4e8e93 100993 13ea023
  //   4e8e93 300993 13ea023 4e8e93 993 13ea023 4e8e93 993 13ea023 4e8e93 100993 13ea023 4e8e93 100993
  //   13ea023 4e8e93 100993 13ea023 4e8e93 100993 13ea023 4e8e93 993 13ea023 4e8e93 300993 13ea023 4e8e93
  //   993 13ea023 4e8e93 100993 13ea023 4e8e93 100993 13ea023 4e8e93 100993 13ea023 4e8e93 100993 13ea023
  //   4e8e93 100993 13ea023 4e8e93 100993 13ea023 4e8e93 993 13ea023 4e8e93 993 13ea023 4e8e93 100993
  //   13ea023 4e8e93 993 13ea023 4e8e93 100993 13ea023 4e8e93 100993 13ea023 4e8e93 993 13ea023 4e8e93
  //   100993 13ea023 4e8e93 100993 13ea023 4e8e93 100993 13ea023 4e8e93 100993 13ea023 4e8e93 993 13ea023
  //   4e8e93 100993 13ea023 4e8e93 100993 13ea023 4e8e93 200073 40293 148313 28393 130e13 400006f 40293
  //   fff48313 28393 fff30e13 2c0006f fff40293 48313 fff28393 30e13 180006f 140293 48313 128393 30e13
  //   40006f e93 229f13 1ee8eb3 531693 de8eb3 ea983 f93 33f8263 100f93 73f8263 200f93 73f8063 300f93
  //   93f8e63 400f93 1d3f8c63 30513 429f13 1e50533 500f13 8f1f13 1e50533 b49f13 1e50533 f41f13 1e50533
  //   1391f13 1e50533 2200893 73 28413 30493 913 200073 200073 30513 429f13 1e50533 500f13 8f1f13 1e50533
  //   b49f13 1e50533 f41f13 1e50533 1391f13 1e50533 2200893 73 28413 30493 200913 f93 239f13 1ef8fb3
  //   5e1693 df8fb3 faa03 693 1468863 200693 9468a63 200073 e0513 439f13 1e50533 400f13 8f1f13 1e50533
  //   b31f13 1e50533 f29f13 1e50533 f13 13f1f13 1e50533 2200893 73 13fa023 12ea023 30513 429f13 1e50533
  //   500f13 8f1f13 1e50533 b49f13 1e50533 f41f13 1e50533 1391f13 1e50533 2200893 73 28413 30493 913
  //   200073 e0513 439f13 1e50533 300f13 8f1f13 1e50533 b31f13 1e50533 f29f13 1e50533 f13 13f1f13 1e50533
  //   2200893 73 13fa023 12ea023 30513 429f13 1e50533 500f13 8f1f13 1e50533 b49f13 1e50533 f41f13 1e50533
  //   1391f13 1e50533 2200893 73 28413 30493 913 200073 f93 239f13 1ef8fb3 5e1693 df8fb3 faa03 693 1468863
  //   200693 9468a63 200073 e0513 439f13 1e50533 400f13 8f1f13 1e50533 b31f13 1e50533 f29f13 1e50533
  //   200f13 13f1f13 1e50533 2200893 73 13fa023 12ea023 30513 429f13 1e50533 500f13 8f1f13 1e50533 b49f13
  //   1e50533 f41f13 1e50533 1391f13 1e50533 2200893 73 28413 30493 200913 200073 e0513 339f13 1e50533
  //   300f13 8f1f13 1e50533 b31f13 1e50533 f29f13 1e50533 200f13 13f1f13 1e50533 2200893 73 13fa023
  //   12ea023 30513 429f13 1e50533 500f13 8f1f13 1e50533 b49f13 1e50533 f41f13 1e50533 1391f13 1e50533
  //   2200893 73 28413 30493 200913 200073
  //   rd
  //   immI
  //   immS
  //   immB
  //   immJ
  //   Beq
  //   Bne
  //   MemToReg
  //   MemWrite
  //   AluOP
  //   AluSrcB
  //   RegWrite
  //   S_type
  //   contents of rom_2 (hex, n*v repeats v):
  //   0 10000 20000 30000 40000 50000 60000 70000 800000 810000 820000 830000 840000 850000 860000 870000
  //   1000000 1010000 1020000 1030000 1040000 1050000 1060000 1070000 1800000 1810000 1820000 1830000
  //   1840000 1850000 1860000 1870000 2000000 2010000 2020000 2030000 2040000 2050000 2060000 2070000
  //   2800000 2810000 2820000 2830000 2840000 2850000 2860000 2870000 3000000 3010000 3020000 3030000
  //   3040000 3050000 3060000 3070000 3800000 3810000 3820000 3830000 3840000 3850000 3860000 3870000 0
  //   10000 20000 30000 40000 50000 60000 70000 800000 810000 820000 830000 840000 850000 860000 870000
  //   1000000 1010000 1020000 1030000 1040000 1050000 1060000 1070000 1800000 1810000 1820000 1830000
  //   1840000 1850000 1860000 1870000 2000000 2010000 2020000 2030000 2040000 2050000 2060000 2070000
  //   2800000 2810000 2820000 2830000 2840000 2850000 2860000 2870000 3000000 3010000 3020000 3030000
  //   3040000 3050000 3060000 3070000 3800000 3810000 3820000 3830000 3840000 3850000 3860000 3870000 7ee0
  //   17ee0 27ee0 37ee0 47ee0 57ee0 67ee0 77ae4 807ee0 817ee0 827ee1 837b08 847ae5 857ee0 867ee0 877f03
  //   1007ee0 1017ee1 1027b93 1037f95 1047bb7 1057b2a 1067ee0 1077ee3 1807ee0 1817f27 1827f95 1837ec0
  //   1847f27 1857fb5 1867ee0 1877ee3 2007ee0 2017f04 2027bb7 2037b07 2047b4f 2057f92 2067ee0 2077f03
  //   2807ee0 2817ee0 2827f49 2837f95 2847f92 2857f02 2867ee0 2877f03 3007ee0 3017ee0 3027ee0 3037ee0
  //   3047ee0 3057ee0 3067ee0 3077ee3 3807f05 3817f04 3827f04 3837f04 3847f04 3857f04 3867f04 3877b2a 55e8
  //   159e8 255e8 355e8 455e8 555c8 659e8 759e8 8059e9 815e0a 8255e9 8351a7 844da7 8555e8 865e09 875a09
  //   10055e8 1015e09 1025e09 10355e8 10455e8 1055e09 1065e09 10759e9 18055c8 18151c8 1825a09 1835e09
  //   1845e09 1855e09 18651c8 18755c8 20055c8 20151a7 20259e9 2035e09 2045e0a 2055a09 20651a7 20755c8
  //   28055e8 28159e9 2825e09 2835a09 2845a09 2855e09 2865a09 28755e8 30059e9 3015e09 3025a09 30351c8
  //   30451a7 30559e9 3065e0a 3075a09 38059e8 3815a09 38255e8 38355c8 38455c8 38555c8 3865a09 38759e8 3ea5
  //   13ea4 23e84 33ea4 43e84 53e84 63ea4 742c5 803ea4 8142e3 823e84 833a44 843a44 853e83 8642e4 873ea4
  //   1003ea4 10142e3 10242e3 1033a84 1043ea4 10542e3 1063ec3 1073ea4 1803a84 1813a64 1823ec4 18342e4
  //   18442e4 1853ec4 1863a64 1873a84 2003a84 2013a44 2023ea4 2034303 20442e4 2053ea4 2063644 2073e84
  //   2803e84 2813ec4 2824303 2833ea4 2843ec4 2854303 2863ea4 2873e84 3003ea4 30142e4 3023ea3 3033a44
  //   3043a44 3053ea4 30642e4 3073ea4 3803aa4 3813ea4 3823e84 3833a84 3843a84 3853e84 3863ea4 3873ea4 0
  //   10000 20000 30000 40000 50000 60000 70000 800000 810420 8245a0 8365c4 8465e3 854180 860420 870000
  //   1000000 10155e0 1027f20 1037a44 1047a44 1057f20 1064dc0 1070000 1801880 1817ee0 1827f00 1837a24
  //   1847a44 1857f00 1867ac0 1871060 2001ca0 2017ee0 2027f00 2037a24 2047a44 2057f00 2067ee0 2071480
  //   2800420 2816660 2827f20 2837a24 2847a44 2857f20 2866240 2870400 3000000 3011480 3026260 3037624
  //   3047624 3055e40 3061060 3070000 3800000 3810000 3820000 3831861 3841861 3850000 3860000 3870000 56f7
  //   156f8 25718 35718 45718 55718 656f8 75b17 8056f7 815718 8256f7 8352f7 8456f7 8556f8 865718 875718
  //   10056f7 1015718 10252d6 1034ed6 10452d6 10556f7 1065718 1075718 18056f7 1815718 18252d6 18352d6
  //   18452d6 18556f7 1865718 1875718 20056f7 2015718 20256f7 20356f7 2045af7 2055b18 20656f8 2075718
  //   28056f7 2815718 2825718 2835718 2845f39 2855f39 28656f8 2875718 30056f7 3015718 3025718 3035718
  //   3045b18 3055b18 30656f8 3075718 38056f7 3815718 3825718 3835718 38456f7 38556f7 3865718 3875718
  //   856f7 956f8 a5718 b5718 c5718 d5718 e56f8 f5b17 8856f7 895718 8a56f7 8b52f7 8c56f7 8d56f8 8e5718
  //   8f5718 10856f7 1095718 10a52d6 10b4ed6 10c52d6 10d56f7 10e5718 10f5718 18856f7 1895718 18a52d6
  //   18b52d6 18c52d6 18d56f7 18e5718 18f5718 20856f7 2095718 20a56f7 20b56f7 20c5af7 20d5b18 20e56f8
  //   20f5718 28856f7 2895718 28a5718 28b5718 28c5f39 28d5f39 28e56f8 28f5718 30856f7 3095718 30a5718
  //   30b5718 30c5b18 30d5b18 30e56f8 30f5718 38856f7 3895718 38a5718 38b5718 38c56f7 38d56f7 38e5718
  //   38f5718 1056f7 1156f8 125718 135718 145718 155718 1656f8 175b17 9056f7 915718 9256f7 9352f7 9456f7
  //   9556f8 965718 975718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
  //   数据存储器
endmodule

module music (
  input  CLK,
  input  RST,
  input  Play,
  input  Mode,
  input  Success,
  output EN,
  output [13:0] \频率 
);

  wire and_1_out, and_2_out, and_3_out, CLKAfterSlow, comparator_1_eq, comparator_1_gt, comparator_2_eq,
       comparator_2_gt, comparator_3_eq, comparator_3_gt, comparator_4_lt, not_1_out, not_2_out, not_3_out,
       or_3_out, R, R1, R2, Success_t;
  wire [0:0] not_4_out, not_5_out;
  wire [15:0] counter_2_q, multiplexer_1_out, shifter_1_out;
  wire [31:0] adder_1_out, adder_2_out, adder_3_out, PC_2_q, PC_3_q, PC_q, rom_1_data, \背景音乐_data ,
       \过关音乐_data ;
  wire [31:14] multiplexer_3_out;

  Counter #(.width(1), .max('h1), .ongoal("wrap"), .trigger("rising"), .behavior("new")) counter_1 (
    .Q(Success_t), .clk(Success));  // open: load, D, count, carry, clr, preset, down
  not not_1 (not_1_out, Mode);
  Register #(.width(32), .trigger("rising"), .Select("low")) PC (
    .D(adder_1_out), .en(and_1_out), .Q(PC_q), .clk(CLKAfterSlow), .clr(R));
  and and_1 (and_1_out, Play, Mode, not_2_out);
  not not_2 (not_2_out, Success_t);
  Register #(.width(32), .trigger("rising"), .Select("low")) PC_2 (
    .D(adder_2_out), .en(and_2_out), .Q(PC_2_q), .clk(CLKAfterSlow), .clr(R));
  and and_2 (and_2_out, Play, not_1_out, not_3_out);
  not not_3 (not_3_out, Success_t);
  Register #(.width(32), .trigger("rising"), .Select("low")) PC_3 (
    .D(adder_3_out), .en(and_3_out), .Q(PC_3_q), .clk(CLKAfterSlow), .clr(R));
  and and_3 (and_3_out, Play, Success_t);
  Adder #(.width(32)) adder_1 (.a(PC_q), .b(32'h4), .out(adder_1_out));  // open: cin, cout
  Adder #(.width(32)) adder_2 (.a(PC_2_q), .b(32'h4), .out(adder_2_out));  // open: cin, cout
  Adder #(.width(32)) adder_3 (.a(PC_3_q), .b(32'h4), .out(adder_3_out));  // open: cin, cout
  Multiplexer #(.select(2), .width(16), .disabled("Z"), .enable("false")) multiplexer_1 (
    .in0(16'h30), .in1(16'h14), .in2(16'h1c), .in3(16'h1c), .out(multiplexer_1_out),
    .sel({Success_t, not_4_out[0]}));
  not not_4 (not_4_out[0], Mode);
  Comparator #(.width(16), .mode("twosComplement")) comparator_1 (
    .a(counter_2_q), .b(multiplexer_1_out), .gt(comparator_1_gt), .eq(comparator_1_eq));  // open: lt
  Comparator #(.width(10), .mode("unsigned")) comparator_2 (
    .a(PC_q[11:2]), .b(10'h250), .gt(comparator_2_gt), .eq(comparator_2_eq));  // open: lt
  or or_1 (R1, comparator_2_gt, comparator_2_eq);
  or or_2 (R2, comparator_3_gt, comparator_3_eq);
  Comparator #(.width(10), .mode("unsigned")) comparator_3 (
    .a(PC_2_q[11:2]), .b(10'h1f8), .gt(comparator_3_gt), .eq(comparator_3_eq));  // open: lt
  Shifter #(.width(16), .shift("lr")) shifter_1 (.in(multiplexer_1_out), .\dist (4'b0001), .out(shifter_1_out));
  or or_3 (or_3_out, comparator_1_gt, comparator_1_eq);
  Counter #(.width(16), .max('hffff), .ongoal("wrap"), .trigger("rising"), .behavior("new")) counter_2 (
    .load(or_3_out), .D({16{1'b0}}), .count(Play), .Q(counter_2_q), .clk(CLK), .clr(R));  // open: carry, preset, down
  Comparator #(.width(16), .mode("twosComplement")) comparator_4 (
    .a(shifter_1_out), .b(counter_2_q), .lt(comparator_4_lt));  // open: gt, eq
  ROM #(.addrWidth(10), .dataWidth(32), .Select("high")) rom_1 (.addr(PC_q[11:2]), .data(rom_1_data));
  ROM #(.addrWidth(10), .dataWidth(32), .Select("high")) \u_背景音乐  (.addr(PC_2_q[11:2]), .data(\背景音乐_data ));
  ROM #(.addrWidth(10), .dataWidth(32), .Select("high")) \u_过关音乐  (.addr(PC_3_q[11:2]), .data(\过关音乐_data ));
  Multiplexer #(.select(1), .width(1), .disabled("Z"), .enable("false")) multiplexer_2 (
    .in0(1'b0), .in1(1'b1), .out(CLKAfterSlow), .sel(comparator_4_lt));
  Multiplexer #(.select(2), .width(32), .disabled("Z"), .enable("false")) multiplexer_3 (
    .in0(rom_1_data), .in1(\背景音乐_data ), .in2(\过关音乐_data ), .in3(\过关音乐_data ),
    .out({multiplexer_3_out, \频率 }), .sel({Success_t, not_5_out[0]}));
  not not_5 (not_5_out[0], Mode);
  or or_4 (R, RST, R1, R2);

  assign EN = Play;

  // Notes on the sheet:
  //   菊花台
  //   contents of rom_1 (hex, n*v repeats v):
  //   0 0 0 5*293 0 293 293 293 24b 24b 24b 6*293 5*0 293 293 293 310 310 310 293 293 293 24b 24b 24b
  //   6*293 5*0 4*20b 0 0 20b 20b 20b 24b 24b 24b 293 293 293 310 310 310 4*293 0 0 4*24b 0 0 24b 24b 24b
  //   20b 20b 20b 6*24b 5*0 6*293 0 310 310 310 370 370 370 6*310 0 0 0 370 370 370 6*310 293 293 293
  //   6*310 4*0 20b 20b 4*293 0 0 24b 24b 24b 293 293 293 5*310 293 293 293 7*24b 0 24b 24b 24b 20b 20b
  //   20b 5*24b 6*0 5*293 0 293 293 293 24b 24b 24b 6*293 5*0 293 293 293 310 310 310 293 293 293 24b 24b
  //   24b 6*293 5*0 4*20b 0 0 20b 20b 20b 24b 24b 24b 293 293 293 310 310 310 4*293 0 0 4*24b 0 0 24b 24b
  //   24b 20b 20b 20b 6*24b 5*0 6*293 0 310 310 310 370 370 370 6*310 0 0 0 370 370 370 6*310 293 293 293
  //   6*310 4*0 4*293 0 0 24b 24b 24b 293 293 293 5*310 0 293 293 293 6*24b 5*20b 6*0 20b 20b 20b 24b 24b
  //   24b 4*293 0 0 293 293 293 310 310 310 4*370 0 0 370 370 370 4a3 4a3 4a3 43b 43b 43b 6*40b 370 370
  //   370 4*310 4*0 370 370 370 310 310 310 293 293 293 24b 24b 24b 4*20b 0 0 1ba 1ba 1ba 20b 20b 20b
  //   5*24b 0 24b 24b 24b 20b 20b 20b 4*24b 0 0 20b 20b 20b 24b 24b 24b 4*293 0 0 293 293 293 310 310 310
  //   4*370 0 0 370 370 370 4b3 4b3 4b3 44b 44b 44b 6*40b 44b 44b 44b 6*40b 4*0 5*310 0 310 310 310 293
  //   293 293 3d0 3d0 3d0 40b 40b 40b 20b 20b 20b 24b 24b 24b 6*293 5*0 5*24b 5*0 8*20b
  //   背景音乐
  //   contents of 背景音乐 (hex, n*v repeats v):
  //   4*0 293 293 0 293 293 0 0 293 293 0 0 20b 20b 0 293 293 0 0 310 310 310 4*0 193 193 193 5*0 20b 20b
  //   20b 0 0 0 193 193 193 0 0 0 10b 10b 0 0 1ba 1ba 0 0 1d4 1d4 0 1d4 1d4 0 1ba 1ba 0 0 193 193 0 293
  //   293 0 310 310 0 370 370 0 0 2ba 2ba 0 0 310 310 0 0 293 293 0 20b 20b 0 24b 24b 0 1d4 1d4 4*0 20b
  //   20b 20b 0 0 0 193 193 193 0 0 0 10b 10b 0 0 1ba 1ba 0 0 1d4 1d4 0 1d4 1d4 0 1ba 1ba 0 0 193 193 0
  //   293 293 0 310 310 0 370 370 0 0 2ba 2ba 0 0 310 310 0 0 293 293 0 24b 24b 0 20b 20b 0 1d4 1d4 8*0
  //   310 0 2ba 0 2ba 0 293 0 0 0 293 293 293 0 0 193 0 1ba 0 20b 0 0 1ba 0 20b 0 24b 24b 5*0 310 0 2ba 0
  //   2ba 0 293 0 0 0 293 293 293 0 0 4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
  //   contents of 过关音乐 (hex, n*v repeats v):
  //   4*0 310 0 20b 0 293 0 310 0 20b 0 293 0 0 310 310 310 0 0 0 293 293 293 5*0 370 0 20b 0 293 0 370 0
  //   20b 0 293 0 0 370 370 370 0 0 0 293 293 293 5*0 3d0 0 24b 0 2ba 0 3d0 0 24b 0 2ba 0 0 3d0 3d0 3d0 0
  //   0 0 3d0 0 3d0 0 3d0 0 0 5*40b
  //   频率转换电路
endmodule

module \键盘解析  (
  input  in_1,
  input  in_2,
  input  [6:0] \缓冲区最前端的ASCII码 ,
  output UP_W,
  output DOWN_S,
  output LEFT_A,
  output RIGHT_D
);

  wire comparator_1_eq, comparator_2_eq, comparator_3_eq, comparator_4_eq;

  Comparator #(.width(7), .mode("twosComplement")) comparator_1 (
    .a(\缓冲区最前端的ASCII码 ), .b(7'b1110111), .eq(comparator_1_eq));  // open: gt, lt
  Comparator #(.width(7), .mode("twosComplement")) comparator_2 (
    .a(\缓冲区最前端的ASCII码 ), .b(7'b1110011), .eq(comparator_2_eq));  // open: gt, lt
  Comparator #(.width(7), .mode("twosComplement")) comparator_3 (
    .a(\缓冲区最前端的ASCII码 ), .b(7'b1100001), .eq(comparator_3_eq));  // open: gt, lt
  Comparator #(.width(7), .mode("twosComplement")) comparator_4 (
    .a(\缓冲区最前端的ASCII码 ), .b(7'b1100100), .eq(comparator_4_eq));  // open: gt, lt
  Register #(.width(1), .trigger("rising"), .Select("low")) register_1 (
    .D(comparator_1_eq), .Q(UP_W), .clk(in_1), .clr(in_2));  // open: en
  Register #(.width(1), .trigger("rising"), .Select("low")) register_2 (
    .D(comparator_2_eq), .Q(DOWN_S), .clk(in_1), .clr(in_2));  // open: en
  Register #(.width(1), .trigger("rising"), .Select("low")) register_3 (
    .D(comparator_3_eq), .Q(LEFT_A), .clk(in_1), .clr(in_2));  // open: en
  Register #(.width(1), .trigger("rising"), .Select("low")) register_4 (
    .D(comparator_4_eq), .Q(RIGHT_D), .clk(in_1), .clr(in_2));  // open: en

  // Other names for the same wires on the sheet: CLK = in_1; RST = in_2
endmodule
