// Logisim project cpu21-riscv-ID-redirect-pipeline.circ as structural Verilog: 21 circuits, main circuit ◆单周期硬布线控制器
// 单周期硬布线控制器
module \单周期硬布线控制器  (
  input  [4:0] OP,
  input  [4:0] Funct,
  output [3:0] ALU_OP,
  output MemToReg,
  output MemWrite,
  output ALU_SRC,
  output RegWrite,
  output ecall,
  output S_type,
  output Beq,
  output Bne,
  output Jalr,
  output JAL,
  output Lui,
  output Lbu,
  output Bge,
  output rs1,
  output rs2
);

  \运算控制器自动生成  \u_运算控制器自动生成_1  (
    .OP2(OP[0]), .OP3(OP[1]), .OP4(OP[2]), .OP5(OP[3]), .OP6(OP[4]), .F12(Funct[0]), .F13(Funct[1]),
    .F14(Funct[2]), .F25(Funct[3]), .F30(Funct[4]), .S0(ALU_OP[0]), .S1(ALU_OP[1]), .S2(ALU_OP[2]),
    .S3(ALU_OP[3]));
  \控制信号自动生成  \u_控制信号自动生成_1  (
    .OP2(OP[0]), .OP3(OP[1]), .OP4(OP[2]), .OP5(OP[3]), .OP6(OP[4]), .MemToReg(MemToReg), .F12(Funct[0]),
    .F13(Funct[1]), .F14(Funct[2]), .F25(Funct[3]), .F30(Funct[4]), .MemWrite(MemWrite), .ALU_SRC(ALU_SRC),
    .RegWrite(RegWrite), .ecall(ecall), .S_Type(S_type), .BEQ(Beq), .BNE(Bne), .JALR(Jalr), .JAL(JAL),
    .LUI(Lui), .LBU(Lbu), .BGE(Bge), .rs1(rs1), .rs2(rs2));

  // Other names for the same wires on the sheet: OP_CODE[4:0] = OP

  // Notes on the sheet:
  //   运算器控制器，根据指令生成运算器功能选择信号
  //   控制信号生成，产生数据通路需要的其他控制信号
endmodule

// 运算器控制器
module \运算控制器自动生成  (
  input  OP2,
  input  OP3,
  input  OP4,
  input  OP5,
  input  OP6,
  input  F12,
  input  F13,
  input  F14,
  input  F25,
  input  F30,
  output S0,
  output S1,
  output S2,
  output S3
);

  wire and_1_out, and_2_out, and_3_out, and_4_out, and_5_out, and_6_out, and_7_out, and_8_out, and_9_out,
       and_10_out, and_11_out, and_12_out, and_13_out, and_14_out, and_15_out, and_16_out, and_17_out,
       and_18_out, and_19_out, and_20_out, and_21_out, and_22_out, and_23_out, not_1_out, not_2_out,
       not_3_out, not_4_out, not_5_out, not_6_out, not_7_out, not_8_out, not_9_out, not_10_out, not_11_out,
       not_12_out, not_13_out, not_14_out, not_15_out, not_16_out, not_17_out, not_18_out, not_19_out,
       not_20_out, not_21_out, not_22_out, not_23_out, not_24_out, not_25_out, not_26_out, not_27_out,
       not_28_out, not_29_out, not_30_out, not_31_out, not_32_out, not_33_out, not_34_out, not_35_out,
       not_36_out, not_37_out, not_38_out, not_39_out, not_40_out, not_41_out, not_42_out, not_43_out,
       not_44_out, not_45_out, not_46_out, not_47_out, not_48_out, not_49_out, not_50_out, not_51_out,
       not_52_out, not_53_out, not_54_out, not_55_out, not_56_out, not_57_out, not_58_out, not_59_out,
       not_60_out, not_61_out, not_62_out, not_63_out, not_64_out, not_65_out, not_66_out, not_67_out,
       not_68_out, not_69_out, not_70_out, not_71_out, not_72_out, not_73_out, not_74_out, not_75_out,
       not_76_out, not_77_out, not_78_out, not_79_out, not_80_out, not_81_out, not_82_out, not_83_out,
       not_84_out, not_85_out, not_86_out, not_87_out, not_88_out, not_89_out, not_90_out, not_91_out,
       not_92_out, not_93_out, not_94_out, not_95_out, not_96_out, not_97_out, not_98_out, not_99_out,
       not_100_out, not_101_out, not_102_out, not_103_out, not_104_out, not_105_out, not_106_out,
       not_107_out, not_108_out, not_109_out, not_110_out, not_111_out, not_112_out, not_113_out,
       not_114_out, not_115_out, not_116_out, not_117_out, not_118_out, not_119_out, not_120_out,
       not_121_out, not_122_out, not_123_out, not_124_out, not_125_out, not_126_out, not_127_out,
       not_128_out, not_129_out, not_130_out, not_131_out, not_132_out, not_133_out;

  not not_1 (not_1_out, OP2);
  not not_2 (not_2_out, OP3);
  not not_3 (not_3_out, OP4);
  not not_4 (not_4_out, OP6);
  not not_5 (not_5_out, F12);
  not not_6 (not_6_out, F14);
  not not_7 (not_7_out, OP2);
  not not_8 (not_8_out, OP3);
  not not_9 (not_9_out, OP5);
  not not_10 (not_10_out, OP6);
  not not_11 (not_11_out, F12);
  not not_12 (not_12_out, F13);
  not not_13 (not_13_out, OP2);
  not not_14 (not_14_out, OP3);
  not not_15 (not_15_out, OP5);
  not not_16 (not_16_out, OP6);
  not not_17 (not_17_out, F12);
  not not_18 (not_18_out, F14);
  not not_19 (not_19_out, OP2);
  not not_20 (not_20_out, OP3);
  not not_21 (not_21_out, OP6);
  not not_22 (not_22_out, F12);
  not not_23 (not_23_out, F13);
  not not_24 (not_24_out, F25);
  not not_25 (not_25_out, F30);
  not not_26 (not_26_out, OP2);
  not not_27 (not_27_out, OP3);
  not not_28 (not_28_out, OP6);
  not not_29 (not_29_out, F12);
  not not_30 (not_30_out, F14);
  not not_31 (not_31_out, F25);
  not not_32 (not_32_out, F30);
  not not_33 (not_33_out, OP2);
  not not_34 (not_34_out, OP3);
  not not_35 (not_35_out, OP5);
  not not_36 (not_36_out, OP6);
  not not_37 (not_37_out, F13);
  not not_38 (not_38_out, F25);
  not not_39 (not_39_out, OP2);
  not not_40 (not_40_out, OP3);
  not not_41 (not_41_out, OP5);
  not not_42 (not_42_out, OP6);
  not not_43 (not_43_out, OP2);
  not not_44 (not_44_out, OP3);
  not not_45 (not_45_out, OP6);
  not not_46 (not_46_out, F25);
  not not_47 (not_47_out, F30);
  not not_48 (not_48_out, OP2);
  not not_49 (not_49_out, OP3);
  not not_50 (not_50_out, OP5);
  not not_51 (not_51_out, OP6);
  not not_52 (not_52_out, F12);
  not not_53 (not_53_out, F14);
  not not_54 (not_54_out, OP2);
  not not_55 (not_55_out, OP3);
  not not_56 (not_56_out, OP6);
  not not_57 (not_57_out, F12);
  not not_58 (not_58_out, F14);
  not not_59 (not_59_out, F25);
  not not_60 (not_60_out, F30);
  not not_61 (not_61_out, OP2);
  not not_62 (not_62_out, OP3);
  not not_63 (not_63_out, OP5);
  not not_64 (not_64_out, OP6);
  not not_65 (not_65_out, F25);
  not not_66 (not_66_out, F30);
  not not_67 (not_67_out, OP2);
  not not_68 (not_68_out, OP3);
  not not_69 (not_69_out, OP5);
  not not_70 (not_70_out, OP6);
  not not_71 (not_71_out, OP2);
  not not_72 (not_72_out, OP3);
  not not_73 (not_73_out, OP6);
  not not_74 (not_74_out, F25);
  not not_75 (not_75_out, F30);
  not not_76 (not_76_out, OP2);
  not not_77 (not_77_out, OP3);
  not not_78 (not_78_out, OP6);
  not not_79 (not_79_out, F12);
  not not_80 (not_80_out, F13);
  not not_81 (not_81_out, F14);
  not not_82 (not_82_out, F25);
  not not_83 (not_83_out, OP2);
  not not_84 (not_84_out, OP3);
  not not_85 (not_85_out, OP4);
  not not_86 (not_86_out, OP6);
  not not_87 (not_87_out, F12);
  not not_88 (not_88_out, F14);
  not not_89 (not_89_out, OP2);
  not not_90 (not_90_out, OP3);
  not not_91 (not_91_out, OP5);
  not not_92 (not_92_out, OP6);
  not not_93 (not_93_out, F12);
  not not_94 (not_94_out, F13);
  not not_95 (not_95_out, F14);
  not not_96 (not_96_out, OP2);
  not not_97 (not_97_out, OP3);
  not not_98 (not_98_out, OP6);
  not not_99 (not_99_out, F12);
  not not_100 (not_100_out, F13);
  not not_101 (not_101_out, F14);
  not not_102 (not_102_out, F25);
  not not_103 (not_103_out, OP2);
  not not_104 (not_104_out, OP3);
  not not_105 (not_105_out, OP5);
  not not_106 (not_106_out, OP6);
  not not_107 (not_107_out, OP2);
  not not_108 (not_108_out, OP3);
  not not_109 (not_109_out, OP6);
  not not_110 (not_110_out, F25);
  not not_111 (not_111_out, F30);
  not not_112 (not_112_out, OP2);
  not not_113 (not_113_out, OP3);
  not not_114 (not_114_out, OP5);
  not not_115 (not_115_out, OP6);
  not not_116 (not_116_out, F12);
  not not_117 (not_117_out, OP2);
  not not_118 (not_118_out, OP3);
  not not_119 (not_119_out, OP6);
  not not_120 (not_120_out, F12);
  not not_121 (not_121_out, F25);
  not not_122 (not_122_out, F30);
  not not_123 (not_123_out, OP2);
  not not_124 (not_124_out, OP3);
  not not_125 (not_125_out, OP5);
  not not_126 (not_126_out, OP6);
  not not_127 (not_127_out, F12);
  not not_128 (not_128_out, OP2);
  not not_129 (not_129_out, OP3);
  not not_130 (not_130_out, OP6);
  not not_131 (not_131_out, F14);
  not not_132 (not_132_out, F25);
  not not_133 (not_133_out, F30);
  and and_1 (and_1_out, not_1_out, not_2_out, not_3_out, not_4_out, not_5_out, F13, not_6_out);
  and and_2 (and_2_out, not_7_out, not_8_out, OP4, not_9_out, not_10_out, not_11_out, not_12_out);
  and and_3 (and_3_out, not_13_out, not_14_out, OP4, not_15_out, not_16_out, not_17_out, not_18_out);
  and and_4 (and_4_out, not_19_out, not_20_out, OP4, not_21_out, not_22_out, not_23_out, not_24_out, not_25_out);
  and and_5 (and_5_out, not_26_out, not_27_out, OP4, not_28_out, not_29_out, not_30_out, not_31_out, not_32_out);
  and and_6 (and_6_out, not_33_out, not_34_out, OP4, not_35_out, not_36_out, not_37_out, F14, not_38_out, F30);
  and and_7 (and_7_out, not_39_out, not_40_out, OP4, not_41_out, not_42_out, F12, F13, F14);
  and and_8 (and_8_out, not_43_out, not_44_out, OP4, not_45_out, F12, F13, F14, not_46_out, not_47_out);
  and and_9 (and_9_out, not_48_out, not_49_out, OP4, not_50_out, not_51_out, not_52_out, F13, not_53_out);
  and and_10 (and_10_out, not_54_out, not_55_out, OP4, not_56_out, not_57_out, F13, not_58_out, not_59_out, not_60_out);
  and and_11 (and_11_out, not_61_out, not_62_out, OP4, not_63_out, not_64_out, F12, F14, not_65_out, not_66_out);
  and and_12 (and_12_out, not_67_out, not_68_out, OP4, not_69_out, not_70_out, F12, F13, F14);
  and and_13 (and_13_out, not_71_out, not_72_out, OP4, not_73_out, F12, F13, F14, not_74_out, not_75_out);
  and and_14 (and_14_out, not_76_out, not_77_out, OP4, OP5, not_78_out, not_79_out, not_80_out, not_81_out, not_82_out, F30);
  and and_15 (and_15_out, not_83_out, not_84_out, not_85_out, not_86_out, not_87_out, F13, not_88_out);
  and and_16 (and_16_out, not_89_out, not_90_out, OP4, not_91_out, not_92_out, not_93_out, not_94_out, not_95_out);
  and and_17 (and_17_out, not_96_out, not_97_out, OP4, not_98_out, not_99_out, not_100_out, not_101_out, not_102_out);
  and and_18 (and_18_out, not_103_out, not_104_out, OP4, not_105_out, not_106_out, F12, F13, F14);
  and and_19 (and_19_out, not_107_out, not_108_out, OP4, OP5, not_109_out, F12, F13, not_110_out, not_111_out);
  and and_20 (and_20_out, not_112_out, not_113_out, OP4, not_114_out, not_115_out, not_116_out, F14);
  and and_21 (and_21_out, not_117_out, not_118_out, OP4, not_119_out, not_120_out, F14, not_121_out, not_122_out);
  and and_22 (and_22_out, not_123_out, not_124_out, OP4, not_125_out, not_126_out, not_127_out, F13);
  and and_23 (and_23_out, not_128_out, not_129_out, OP4, OP5, not_130_out, F13, not_131_out, not_132_out, not_133_out);
  or or_1 (S2, and_15_out, and_16_out, and_17_out, and_18_out, and_19_out);
  or or_2 (S3, and_20_out, and_21_out, and_22_out, and_23_out);
  or or_3 (S0, and_1_out, and_2_out, and_3_out, and_4_out, and_5_out, and_6_out, and_7_out, and_8_out);
  or or_4 (S1, and_9_out, and_10_out, and_11_out, and_12_out, and_13_out, and_14_out);
endmodule

// 控制信号生成
module \控制信号自动生成  (
  input  OP2,
  input  OP3,
  input  OP4,
  input  OP5,
  input  OP6,
  input  F12,
  input  F13,
  input  F14,
  input  F25,
  input  F30,
  output MemToReg,
  output MemWrite,
  output ALU_SRC,
  output RegWrite,
  output ecall,
  output S_Type,
  output BEQ,
  output BNE,
  output JALR,
  output JAL,
  output LUI,
  output LBU,
  output BGE,
  output rs1,
  output rs2
);

  wire and_1_out, and_2_out, and_4_out, and_5_out, and_6_out, and_7_out, and_8_out, and_9_out, and_10_out,
       and_11_out, and_12_out, and_13_out, and_14_out, and_15_out, and_16_out, and_17_out, and_18_out,
       and_19_out, and_20_out, and_21_out, and_31_out, and_32_out, and_33_out, and_34_out, and_35_out,
       and_36_out, and_37_out, and_38_out, and_39_out, and_40_out, and_41_out, and_42_out, and_43_out,
       and_44_out, and_45_out, and_46_out, and_47_out, and_48_out, and_49_out, not_1_out, not_2_out,
       not_3_out, not_4_out, not_5_out, not_6_out, not_7_out, not_8_out, not_9_out, not_10_out, not_11_out,
       not_12_out, not_13_out, not_14_out, not_15_out, not_16_out, not_17_out, not_18_out, not_19_out,
       not_20_out, not_21_out, not_22_out, not_23_out, not_24_out, not_25_out, not_26_out, not_27_out,
       not_28_out, not_29_out, not_30_out, not_31_out, not_32_out, not_33_out, not_34_out, not_35_out,
       not_36_out, not_37_out, not_38_out, not_39_out, not_40_out, not_41_out, not_42_out, not_43_out,
       not_44_out, not_45_out, not_46_out, not_47_out, not_48_out, not_49_out, not_50_out, not_51_out,
       not_52_out, not_53_out, not_54_out, not_55_out, not_56_out, not_57_out, not_58_out, not_59_out,
       not_60_out, not_61_out, not_62_out, not_63_out, not_64_out, not_65_out, not_66_out, not_67_out,
       not_68_out, not_69_out, not_70_out, not_71_out, not_72_out, not_73_out, not_74_out, not_75_out,
       not_76_out, not_77_out, not_78_out, not_79_out, not_80_out, not_81_out, not_82_out, not_83_out,
       not_84_out, not_85_out, not_86_out, not_87_out, not_88_out, not_89_out, not_90_out, not_91_out,
       not_92_out, not_93_out, not_94_out, not_95_out, not_96_out, not_97_out, not_98_out, not_99_out,
       not_100_out, not_101_out, not_102_out, not_103_out, not_104_out, not_105_out, not_106_out,
       not_107_out, not_108_out, not_109_out, not_110_out, not_111_out, not_112_out, not_113_out,
       not_114_out, not_115_out, not_116_out, not_117_out, not_118_out, not_119_out, not_120_out,
       not_121_out, not_122_out, not_123_out, not_124_out, not_125_out, not_126_out, not_127_out,
       not_128_out, not_129_out, not_130_out, not_131_out, not_132_out, not_133_out, not_134_out,
       not_135_out, not_136_out, not_137_out, not_138_out, not_139_out, not_140_out, not_141_out,
       not_142_out, not_143_out, not_144_out, not_145_out, not_146_out, not_147_out, not_148_out,
       not_149_out, not_150_out, not_151_out, not_152_out, not_153_out, not_154_out, not_155_out,
       not_156_out, not_157_out, not_158_out, not_159_out, not_160_out, not_161_out, not_162_out,
       not_163_out, not_164_out, not_165_out, not_166_out, not_167_out, not_168_out, not_169_out,
       not_170_out, not_171_out, not_172_out, not_173_out, not_174_out, not_175_out, not_176_out,
       not_177_out, not_178_out, not_179_out, not_180_out, not_181_out, not_182_out, not_183_out,
       not_184_out, not_185_out, not_186_out, not_187_out, not_188_out, not_189_out, not_190_out,
       not_191_out, not_192_out, not_193_out, not_194_out, not_195_out, not_196_out, not_197_out,
       not_198_out, not_199_out, not_200_out, not_201_out, not_202_out, not_203_out, not_204_out,
       not_205_out, not_206_out, not_207_out, not_208_out, not_209_out, not_210_out, not_211_out,
       not_212_out, not_213_out, not_214_out, not_215_out, not_216_out, not_217_out, not_218_out,
       not_219_out, not_220_out, not_221_out, not_222_out, not_223_out, not_224_out, not_225_out,
       not_226_out, not_227_out, not_228_out, not_229_out, not_230_out, not_231_out, not_232_out,
       not_233_out, not_234_out, not_235_out, not_236_out, not_237_out, not_238_out, not_239_out,
       not_240_out, not_241_out, not_242_out, not_243_out, not_244_out, not_245_out, not_246_out,
       not_247_out, not_248_out, not_249_out, not_250_out, not_251_out, not_252_out, not_253_out,
       not_254_out, not_255_out, not_256_out, not_257_out, not_258_out, not_259_out, not_260_out;

  not not_1 (not_1_out, OP2);
  not not_2 (not_2_out, OP3);
  not not_3 (not_3_out, OP4);
  not not_4 (not_4_out, OP5);
  not not_5 (not_5_out, OP6);
  not not_6 (not_6_out, F12);
  not not_7 (not_7_out, F13);
  not not_8 (not_8_out, OP2);
  not not_9 (not_9_out, OP3);
  not not_10 (not_10_out, OP4);
  not not_11 (not_11_out, OP5);
  not not_12 (not_12_out, OP6);
  not not_13 (not_13_out, F12);
  not not_14 (not_14_out, F14);
  not not_15 (not_15_out, OP2);
  not not_16 (not_16_out, OP3);
  not not_17 (not_17_out, OP4);
  not not_18 (not_18_out, OP6);
  not not_19 (not_19_out, F12);
  not not_20 (not_20_out, F14);
  not not_21 (not_21_out, OP2);
  not not_22 (not_22_out, OP3);
  not not_23 (not_23_out, OP5);
  not not_24 (not_24_out, OP6);
  not not_25 (not_25_out, F12);
  not not_26 (not_26_out, F13);
  not not_27 (not_27_out, OP2);
  not not_28 (not_28_out, OP3);
  not not_29 (not_29_out, OP4);
  not not_30 (not_30_out, OP6);
  not not_31 (not_31_out, F12);
  not not_32 (not_32_out, F14);
  not not_33 (not_33_out, OP2);
  not not_34 (not_34_out, OP3);
  not not_35 (not_35_out, OP5);
  not not_36 (not_36_out, OP6);
  not not_37 (not_37_out, F12);
  not not_38 (not_38_out, OP2);
  not not_39 (not_39_out, OP3);
  not not_40 (not_40_out, OP5);
  not not_41 (not_41_out, OP6);
  not not_42 (not_42_out, F13);
  not not_43 (not_43_out, F25);
  not not_44 (not_44_out, F30);
  not not_45 (not_45_out, OP2);
  not not_46 (not_46_out, OP3);
  not not_47 (not_47_out, OP5);
  not not_48 (not_48_out, OP6);
  not not_49 (not_49_out, F25);
  not not_50 (not_50_out, OP2);
  not not_51 (not_51_out, OP3);
  not not_52 (not_52_out, OP5);
  not not_53 (not_53_out, OP6);
  not not_54 (not_54_out, OP2);
  not not_55 (not_55_out, OP3);
  not not_56 (not_56_out, OP5);
  not not_57 (not_57_out, OP6);
  not not_58 (not_58_out, F12);
  not not_59 (not_59_out, F13);
  not not_60 (not_60_out, OP2);
  not not_61 (not_61_out, OP3);
  not not_62 (not_62_out, OP5);
  not not_63 (not_63_out, OP6);
  not not_64 (not_64_out, F12);
  not not_65 (not_65_out, F14);
  not not_66 (not_66_out, OP2);
  not not_67 (not_67_out, OP3);
  not not_68 (not_68_out, OP5);
  not not_69 (not_69_out, OP6);
  not not_70 (not_70_out, F12);
  not not_71 (not_71_out, OP2);
  not not_72 (not_72_out, OP3);
  not not_73 (not_73_out, OP5);
  not not_74 (not_74_out, OP6);
  not not_75 (not_75_out, F13);
  not not_76 (not_76_out, F25);
  not not_77 (not_77_out, F30);
  not not_78 (not_78_out, OP2);
  not not_79 (not_79_out, OP3);
  not not_80 (not_80_out, OP6);
  not not_81 (not_81_out, F12);
  not not_82 (not_82_out, F13);
  not not_83 (not_83_out, F14);
  not not_84 (not_84_out, F25);
  not not_85 (not_85_out, OP2);
  not not_86 (not_86_out, OP3);
  not not_87 (not_87_out, OP6);
  not not_88 (not_88_out, F12);
  not not_89 (not_89_out, F25);
  not not_90 (not_90_out, F30);
  not not_91 (not_91_out, OP2);
  not not_92 (not_92_out, OP3);
  not not_93 (not_93_out, OP5);
  not not_94 (not_94_out, OP6);
  not not_95 (not_95_out, F25);
  not not_96 (not_96_out, OP2);
  not not_97 (not_97_out, OP3);
  not not_98 (not_98_out, OP5);
  not not_99 (not_99_out, OP6);
  not not_100 (not_100_out, OP3);
  not not_101 (not_101_out, OP6);
  not not_102 (not_102_out, F25);
  not not_103 (not_103_out, F30);
  not not_104 (not_104_out, OP4);
  not not_105 (not_105_out, F12);
  not not_106 (not_106_out, F13);
  not not_107 (not_107_out, F14);
  not not_108 (not_108_out, OP3);
  not not_109 (not_109_out, OP6);
  not not_110 (not_110_out, OP4);
  not not_111 (not_111_out, OP2);
  not not_112 (not_112_out, OP3);
  not not_113 (not_113_out, F12);
  not not_114 (not_114_out, F13);
  not not_115 (not_115_out, F14);
  not not_116 (not_116_out, F25);
  not not_117 (not_117_out, F30);
  not not_118 (not_118_out, OP2);
  not not_119 (not_119_out, OP3);
  not not_120 (not_120_out, OP4);
  not not_121 (not_121_out, OP6);
  not not_122 (not_122_out, F12);
  not not_123 (not_123_out, F14);
  not not_124 (not_124_out, OP2);
  not not_125 (not_125_out, OP3);
  not not_126 (not_126_out, OP4);
  not not_127 (not_127_out, F12);
  not not_128 (not_128_out, F13);
  not not_129 (not_129_out, F14);
  not not_130 (not_130_out, OP2);
  not not_131 (not_131_out, OP3);
  not not_132 (not_132_out, OP4);
  not not_133 (not_133_out, F13);
  not not_134 (not_134_out, F14);
  not not_135 (not_135_out, OP3);
  not not_136 (not_136_out, OP4);
  not not_137 (not_137_out, F12);
  not not_138 (not_138_out, F13);
  not not_139 (not_139_out, F14);
  not not_140 (not_140_out, OP4);
  not not_141 (not_141_out, OP3);
  not not_142 (not_142_out, OP6);
  not not_143 (not_143_out, OP2);
  not not_144 (not_144_out, OP3);
  not not_145 (not_145_out, OP4);
  not not_146 (not_146_out, OP5);
  not not_147 (not_147_out, OP6);
  not not_148 (not_148_out, F12);
  not not_149 (not_149_out, F13);
  not not_150 (not_150_out, OP2);
  not not_151 (not_151_out, OP3);
  not not_152 (not_152_out, OP4);
  not not_153 (not_153_out, F13);
  not not_154 (not_154_out, OP2);
  not not_155 (not_155_out, OP3);
  not not_156 (not_156_out, OP5);
  not not_157 (not_157_out, OP6);
  not not_158 (not_158_out, F12);
  not not_159 (not_159_out, F13);
  not not_160 (not_160_out, OP2);
  not not_161 (not_161_out, OP3);
  not not_162 (not_162_out, OP4);
  not not_163 (not_163_out, OP6);
  not not_164 (not_164_out, F12);
  not not_165 (not_165_out, F14);
  not not_166 (not_166_out, OP3);
  not not_167 (not_167_out, OP4);
  not not_168 (not_168_out, F12);
  not not_169 (not_169_out, F13);
  not not_170 (not_170_out, F14);
  not not_171 (not_171_out, OP2);
  not not_172 (not_172_out, OP3);
  not not_173 (not_173_out, OP4);
  not not_174 (not_174_out, F13);
  not not_175 (not_175_out, OP2);
  not not_176 (not_176_out, OP3);
  not not_177 (not_177_out, OP5);
  not not_178 (not_178_out, OP6);
  not not_179 (not_179_out, F12);
  not not_180 (not_180_out, OP2);
  not not_181 (not_181_out, OP3);
  not not_182 (not_182_out, OP5);
  not not_183 (not_183_out, OP6);
  not not_184 (not_184_out, F13);
  not not_185 (not_185_out, F25);
  not not_186 (not_186_out, F30);
  not not_187 (not_187_out, OP2);
  not not_188 (not_188_out, OP3);
  not not_189 (not_189_out, OP6);
  not not_190 (not_190_out, F12);
  not not_191 (not_191_out, F13);
  not not_192 (not_192_out, F14);
  not not_193 (not_193_out, F25);
  not not_194 (not_194_out, OP2);
  not not_195 (not_195_out, OP3);
  not not_196 (not_196_out, OP6);
  not not_197 (not_197_out, F12);
  not not_198 (not_198_out, F25);
  not not_199 (not_199_out, F30);
  not not_200 (not_200_out, OP2);
  not not_201 (not_201_out, OP3);
  not not_202 (not_202_out, OP5);
  not not_203 (not_203_out, OP6);
  not not_204 (not_204_out, F25);
  not not_205 (not_205_out, OP2);
  not not_206 (not_206_out, OP3);
  not not_207 (not_207_out, OP5);
  not not_208 (not_208_out, OP6);
  not not_209 (not_209_out, OP2);
  not not_210 (not_210_out, OP3);
  not not_211 (not_211_out, F12);
  not not_212 (not_212_out, F13);
  not not_213 (not_213_out, F14);
  not not_214 (not_214_out, F25);
  not not_215 (not_215_out, F30);
  not not_216 (not_216_out, OP2);
  not not_217 (not_217_out, OP3);
  not not_218 (not_218_out, OP6);
  not not_219 (not_219_out, F25);
  not not_220 (not_220_out, F30);
  not not_221 (not_221_out, OP2);
  not not_222 (not_222_out, OP3);
  not not_223 (not_223_out, OP4);
  not not_224 (not_224_out, OP6);
  not not_225 (not_225_out, F12);
  not not_226 (not_226_out, F14);
  not not_227 (not_227_out, OP2);
  not not_228 (not_228_out, OP3);
  not not_229 (not_229_out, OP4);
  not not_230 (not_230_out, F13);
  not not_231 (not_231_out, F14);
  not not_232 (not_232_out, OP2);
  not not_233 (not_233_out, OP3);
  not not_234 (not_234_out, OP4);
  not not_235 (not_235_out, F13);
  not not_236 (not_236_out, OP2);
  not not_237 (not_237_out, OP3);
  not not_238 (not_238_out, OP6);
  not not_239 (not_239_out, F12);
  not not_240 (not_240_out, F13);
  not not_241 (not_241_out, F14);
  not not_242 (not_242_out, F25);
  not not_243 (not_243_out, OP2);
  not not_244 (not_244_out, OP3);
  not not_245 (not_245_out, OP6);
  not not_246 (not_246_out, F12);
  not not_247 (not_247_out, F25);
  not not_248 (not_248_out, F30);
  not not_249 (not_249_out, OP2);
  not not_250 (not_250_out, OP3);
  not not_251 (not_251_out, F12);
  not not_252 (not_252_out, F13);
  not not_253 (not_253_out, F14);
  not not_254 (not_254_out, F25);
  not not_255 (not_255_out, F30);
  not not_256 (not_256_out, OP2);
  not not_257 (not_257_out, OP3);
  not not_258 (not_258_out, OP6);
  not not_259 (not_259_out, F25);
  not not_260 (not_260_out, F30);
  and and_1 (and_1_out, not_1_out, not_2_out, not_3_out, not_4_out, not_5_out, not_6_out, not_7_out, F14);
  and and_2 (and_2_out, not_8_out, not_9_out, not_10_out, not_11_out, not_12_out, not_13_out, F13, not_14_out);
  and and_3 (MemWrite, not_15_out, not_16_out, not_17_out, OP5, not_18_out, not_19_out, F13, not_20_out);
  and and_4 (and_4_out, not_21_out, not_22_out, not_23_out, not_24_out, not_25_out, not_26_out, F14);
  and and_5 (and_5_out, not_27_out, not_28_out, not_29_out, not_30_out, not_31_out, F13, not_32_out);
  and and_6 (and_6_out, not_33_out, not_34_out, OP4, not_35_out, not_36_out, not_37_out);
  and and_7 (and_7_out, not_38_out, not_39_out, OP4, not_40_out, not_41_out, not_42_out, not_43_out, not_44_out);
  and and_8 (and_8_out, not_45_out, not_46_out, OP4, not_47_out, not_48_out, F14, not_49_out);
  and and_9 (and_9_out, not_50_out, not_51_out, OP4, not_52_out, not_53_out, F13, F14);
  and and_10 (and_10_out, not_54_out, not_55_out, not_56_out, not_57_out, not_58_out, not_59_out, F14);
  and and_11 (and_11_out, not_60_out, not_61_out, not_62_out, not_63_out, not_64_out, F13, not_65_out);
  and and_12 (and_12_out, not_66_out, not_67_out, OP4, not_68_out, not_69_out, not_70_out);
  and and_13 (and_13_out, not_71_out, not_72_out, OP4, not_73_out, not_74_out, not_75_out, not_76_out, not_77_out);
  and and_14 (and_14_out, not_78_out, not_79_out, OP4, not_80_out, not_81_out, not_82_out, not_83_out, not_84_out);
  and and_15 (and_15_out, not_85_out, not_86_out, OP4, not_87_out, not_88_out, not_89_out, not_90_out);
  and and_16 (and_16_out, not_91_out, not_92_out, OP4, not_93_out, not_94_out, F14, not_95_out);
  and and_17 (and_17_out, not_96_out, not_97_out, OP4, not_98_out, not_99_out, F13, F14);
  and and_18 (and_18_out, not_100_out, OP4, OP5, not_101_out, F13, not_102_out, not_103_out);
  and and_19 (and_19_out, OP2, not_104_out, OP5, OP6, not_105_out, not_106_out, not_107_out);
  and and_20 (and_20_out, OP2, not_108_out, OP4, OP5, not_109_out);
  and and_21 (and_21_out, OP2, OP3, not_110_out, OP5, OP6);
  and and_22 (ecall, not_111_out, not_112_out, OP4, OP5, OP6, not_113_out, not_114_out, not_115_out, not_116_out, not_117_out);
  and and_23 (S_Type, not_118_out, not_119_out, not_120_out, OP5, not_121_out, not_122_out, F13, not_123_out);
  and and_24 (BEQ, not_124_out, not_125_out, not_126_out, OP5, OP6, not_127_out, not_128_out, not_129_out);
  and and_25 (BNE, not_130_out, not_131_out, not_132_out, OP5, OP6, F12, not_133_out, not_134_out);
  and and_26 (JALR, OP2, not_135_out, not_136_out, OP5, OP6, not_137_out, not_138_out, not_139_out);
  and and_27 (JAL, OP2, OP3, not_140_out, OP5, OP6);
  and and_28 (LUI, OP2, not_141_out, OP4, OP5, not_142_out);
  and and_29 (LBU, not_143_out, not_144_out, not_145_out, not_146_out, not_147_out, not_148_out, not_149_out, F14);
  and and_30 (BGE, not_150_out, not_151_out, not_152_out, OP5, OP6, F12, not_153_out, F14);
  and and_31 (and_31_out, not_154_out, not_155_out, not_156_out, not_157_out, not_158_out, not_159_out, F14);
  and and_32 (and_32_out, not_160_out, not_161_out, not_162_out, not_163_out, not_164_out, F13, not_165_out);
  and and_33 (and_33_out, not_166_out, not_167_out, OP5, OP6, not_168_out, not_169_out, not_170_out);
  and and_34 (and_34_out, not_171_out, not_172_out, not_173_out, OP5, OP6, F12, not_174_out);
  and and_35 (and_35_out, not_175_out, not_176_out, OP4, not_177_out, not_178_out, not_179_out);
  and and_36 (and_36_out, not_180_out, not_181_out, OP4, not_182_out, not_183_out, not_184_out, not_185_out, not_186_out);
  and and_37 (and_37_out, not_187_out, not_188_out, OP4, not_189_out, not_190_out, not_191_out, not_192_out, not_193_out);
  and and_38 (and_38_out, not_194_out, not_195_out, OP4, not_196_out, not_197_out, not_198_out, not_199_out);
  and and_39 (and_39_out, not_200_out, not_201_out, OP4, not_202_out, not_203_out, F14, not_204_out);
  and and_40 (and_40_out, not_205_out, not_206_out, OP4, not_207_out, not_208_out, F13, F14);
  and and_41 (and_41_out, not_209_out, not_210_out, OP4, OP5, not_211_out, not_212_out, not_213_out, not_214_out, not_215_out);
  and and_42 (and_42_out, not_216_out, not_217_out, OP4, OP5, not_218_out, F13, not_219_out, not_220_out);
  and and_43 (and_43_out, not_221_out, not_222_out, not_223_out, OP5, not_224_out, not_225_out, F13, not_226_out);
  and and_44 (and_44_out, not_227_out, not_228_out, not_229_out, OP5, OP6, not_230_out, not_231_out);
  and and_45 (and_45_out, not_232_out, not_233_out, not_234_out, OP5, OP6, F12, not_235_out);
  and and_46 (and_46_out, not_236_out, not_237_out, OP4, OP5, not_238_out, not_239_out, not_240_out, not_241_out, not_242_out);
  and and_47 (and_47_out, not_243_out, not_244_out, OP4, OP5, not_245_out, not_246_out, not_247_out, not_248_out);
  and and_48 (and_48_out, not_249_out, not_250_out, OP4, OP5, not_251_out, not_252_out, not_253_out, not_254_out, not_255_out);
  and and_49 (and_49_out, not_256_out, not_257_out, OP4, OP5, not_258_out, F13, not_259_out, not_260_out);
  or or_1 (MemToReg, and_1_out, and_2_out);
  or or_2 (ALU_SRC, and_4_out, and_5_out, and_6_out, and_7_out, and_8_out, and_9_out);
  or or_3 (rs2, and_43_out, and_44_out, and_45_out, and_46_out, and_47_out, and_48_out, and_49_out);
  or or_4 (RegWrite, and_10_out, and_11_out, and_12_out, and_13_out, and_14_out, and_15_out, and_16_out, and_17_out, and_18_out, and_19_out, and_20_out, and_21_out);
  or or_5 (rs1, and_31_out, and_32_out, and_33_out, and_34_out, and_35_out, and_36_out, and_37_out, and_38_out, and_39_out, and_40_out, and_41_out, and_42_out);
endmodule

// ALU
module ALU (
  input  [31:0] X,
  input  [31:0] Y,
  input  [3:0] AluOP,
  output out_4,
  output Equal,
  output out_6,
  output [31:0] Result,
  output [31:0] Result_2
);

  wire [0:0] comparator_2_lt;
  wire [31:0] adder_1_out, AND_out, divider_1_out, divider_1_rem, multiplier_1_cout, multiplier_1_out,
       NOR_out, OR_out, shifter_1_out, shifter_2_out, shifter_3_out, subtractor_1_out, XOR_out;

  assign AND_out = X & Y;  // AND_Gate AND, 32 bits wide
  assign OR_out = X | Y;  // OR_Gate OR, 32 bits wide
  Shifter #(.width(32), .shift("ll")) shifter_1 (.in(X), .\dist (Y[4:0]), .out(shifter_1_out));
  Shifter #(.width(32), .shift("ar")) shifter_2 (.in(X), .\dist (Y[4:0]), .out(shifter_2_out));
  Shifter #(.width(32), .shift("lr")) shifter_3 (.in(X), .\dist (Y[4:0]), .out(shifter_3_out));
  Multiplier #(.width(32)) multiplier_1 (.a(X), .b(Y), .out(multiplier_1_out), .cout(multiplier_1_cout));  // open: cin
  Divider #(.width(32)) divider_1 (.a(X), .b(Y), .out(divider_1_out), .rem(divider_1_rem));  // open: upper
  Adder #(.width(32)) adder_1 (.a(X), .b(Y), .out(adder_1_out));  // open: cin, cout
  Subtractor #(.width(32)) subtractor_1 (.a(X), .b(Y), .out(subtractor_1_out));  // open: bin, bout
  assign XOR_out = X ^ Y;  // XOR_Gate XOR, 32 bits wide
  assign NOR_out = ~(X | Y);  // NOR_Gate NOR, 32 bits wide
  Comparator #(.width(32), .mode("twosComplement")) comparator_1 (.a(X), .b(Y), .eq(Equal), .lt(out_6));  // open: gt
  Comparator #(.width(32), .mode("unsigned")) comparator_2 (.a(X), .b(Y), .lt(comparator_2_lt[0]));  // open: gt, eq
  Multiplexer #(.select(4), .width(32), .disabled("Z"), .enable("false")) multiplexer_1 (
    .in0(shifter_1_out), .in1(shifter_2_out), .in2(shifter_3_out), .in3(multiplier_1_out),
    .in4(divider_1_out), .in5(adder_1_out), .in6(subtractor_1_out), .in7(AND_out), .in8(OR_out),
    .in9(XOR_out), .in10(NOR_out), .in11({{31{1'b0}}, out_6}), .in12({{31{1'b0}}, comparator_2_lt[0]}),
    .in13({32{1'b0}}), .in14({32{1'b0}}), .in15({32{1'b0}}), .out(Result), .sel(AluOP));
  Multiplexer #(.select(4), .width(32), .disabled("Z"), .enable("false")) multiplexer_2 (
    .in0({32{1'b0}}), .in1({32{1'b0}}), .in2({32{1'b0}}), .in3(multiplier_1_cout), .in4(divider_1_rem),
    .in5({32{1'b0}}), .in6({32{1'b0}}), .in7({32{1'b0}}), .in8({32{1'b0}}), .in9({32{1'b0}}),
    .in10({32{1'b0}}), .in11({32{1'b0}}), .in12({32{1'b0}}), .in13({32{1'b0}}), .in14({32{1'b0}}),
    .in15({32{1'b0}}), .out(Result_2), .sel(AluOP));
  Multiplexer #(.select(4), .width(1), .disabled("Z"), .enable("false")) multiplexer_3 (
    .in0(1'b0), .in1(1'b0), .in2(1'b0), .in3(1'b0), .in4(1'b0), .in5(1'b0), .in6(1'b0), .in7(1'b0),
    .in8(1'b0), .in9(1'b0), .in10(1'b0), .in11(out_6), .in12(comparator_2_lt[0]), .in13(1'b0), .in14(1'b0),
    .in15(1'b0), .sel(AluOP));  // open: out
  not not_1 (out_4, out_6);

  // Other names for the same wires on the sheet: tunnel = out_6; Result2[31:0] = Result_2; S[3:0] = AluOP;
  //   tunnel_t = out_4

  // Notes on the sheet:
  //   不要改变此引脚区域内容，也不要改变ALU封装形式
  //   输入引脚
  //   输出引脚
endmodule

module Regifile (
  input  [31:0] Din,
  input  Clk,
  input  WE,
  input  [4:0] R1_num,
  input  [4:0] W_num,
  input  [4:0] R2_num,
  output [31:0] R1,
  output [31:0] R2
);

  // RegisterFile registerfile_1: pin names not known; wires that end beside it: Din, Clk, WE, W_num, R1_num, R2_num, R1, R2
endmodule

// branch\n test
module \条件分支逻辑设计  (
  input  Bge,
  input  in_2,
  input  Beq,
  input  in_4,
  input  Bne,
  output branch
);

  wire and_1_out, and_2_out, and_3_out, not_1_out;

  not not_1 (not_1_out, in_4);
  and and_1 (and_1_out, Bge, in_2);
  and and_2 (and_2_out, in_4, Beq);
  and and_3 (and_3_out, not_1_out, Bne);
  or or_1 (branch, and_1_out, and_2_out, and_3_out);
endmodule

// Jump\n Addr
module \无条件跳转逻辑设计  (
  input  JAL,
  input  JALR,
  input  [31:0] JALR_Addr,
  input  [31:0] JAL_Addr,
  input  [31:0] PC,
  output [31:0] J_Addr
);

  wire [31:0] adder_1_out;

  Adder #(.width(32)) adder_1 (.a(JAL_Addr), .b(PC), .out(adder_1_out));  // open: cin, cout
  Multiplexer #(.select(1), .width(32), .disabled("Z"), .enable("false")) multiplexer_1 (
    .in0(JALR_Addr), .in1(adder_1_out), .out(J_Addr), .sel(JAL));
endmodule

// New PC
module \流水线PC计算  (
  input  bJump,
  input  J,
  input  [31:0] PC_4,
  input  [31:0] bAddr,
  input  [31:0] jAddr,
  output [31:0] NPC
);

  wire or_1_out;
  wire [31:0] multiplexer_1_out;

  Multiplexer #(.select(1), .width(32), .disabled("Z"), .enable("false")) multiplexer_1 (
    .in0(bAddr), .in1(jAddr), .out(multiplexer_1_out), .sel(J));
  or or_1 (or_1_out, J, bJump);
  Multiplexer #(.select(1), .width(32), .disabled("Z"), .enable("false")) multiplexer_2 (
    .in0(PC_4), .in1(multiplexer_1_out), .out(NPC), .sel(or_1_out));
endmodule

// IR扩展器
module \气泡IR扩展器  (
  input  [31:0] IR,
  input  s,
  output [4:0] OP,
  output [4:0] Funct,
  output [4:0] rs1,
  output [4:0] rs2,
  output [4:0] rd,
  output [31:0] imm,
  output [31:0] imm_b,
  output [31:0] imm_lui,
  output [31:0] imm_jal
);

  wire [11:0] multiplexer_1_out;
  wire [31:0] bit_extender_1_out, bit_extender_3_out, bit_extender_4_out;

  assign bit_extender_1_out = {{12{IR[31]}}, IR[31:12]};  // Bit_Extender bit_extender_1
  Multiplexer #(.select(1), .width(12), .disabled("Z"), .enable("false")) multiplexer_1 (
    .in0(IR[31:20]), .in1({IR[31:25], IR[11:7]}), .out(multiplexer_1_out), .sel(s));
  assign imm = {{20{multiplexer_1_out[11]}}, multiplexer_1_out};  // Bit_Extender bit_extender_2
  assign bit_extender_3_out = {{20{IR[31]}}, {IR[31], IR[7], IR[30:25], IR[11:8]}};  // Bit_Extender bit_extender_3
  Shifter #(.width(32), .shift("ll")) shifter_1 (.in(bit_extender_1_out), .\dist (5'b01100), .out(imm_lui));
  assign bit_extender_4_out = {{12{IR[31]}}, {IR[31], IR[19:12], IR[20], IR[30:21]}};  // Bit_Extender bit_extender_4
  Shifter #(.width(32), .shift("ll")) shifter_2 (.in(bit_extender_3_out), .\dist (5'b00001), .out(imm_b));
  Shifter #(.width(32), .shift("ll")) shifter_3 (.in(bit_extender_4_out), .\dist (5'b00001), .out(imm_jal));

  assign Funct = {IR[30], IR[25], IR[14:12]};
  assign OP = IR[6:2];
  assign rd = IR[11:7];
  assign rs1 = IR[19:15];
  assign rs2 = IR[24:20];

  // Notes on the sheet:
  //   imm12 I
  //   imm12 S
  //   imm20 LUI
  //   rs1
  //   rs2
  //   rd
  //   imm20 Jal
endmodule

// IF/ID
module \气泡IF_ID  (
  input  [31:0] IF_PC,
  input  [31:0] IF_IR,
  input  clk,
  input  halt,
  input  rst,
  output [31:0] ID_PC,
  output [31:0] ID_IR
);

  wire [31:0] multiplexer_1_out, multiplexer_2_out;

  Multiplexer #(.select(1), .width(32), .disabled("Z"), .enable("false")) multiplexer_1 (
    .in0(IF_PC), .in1({32{1'b0}}), .out(multiplexer_1_out), .sel(rst));
  Multiplexer #(.select(1), .width(32), .disabled("Z"), .enable("false")) multiplexer_2 (
    .in0(IF_IR), .in1({32{1'b0}}), .out(multiplexer_2_out), .sel(rst));
  Register #(.width(32), .trigger("rising"), .Select("low")) PC (
    .D(multiplexer_1_out), .en(halt), .Q(ID_PC), .clk(clk));  // open: clr
  Register #(.width(32), .trigger("rising"), .Select("low")) IR (
    .D(multiplexer_2_out), .en(halt), .Q(ID_IR), .clk(clk));  // open: clr
endmodule

// ID/EX
module \气泡ID_EX  (
  input  [4:0] ID_rd,
  input  [31:0] ID_a,
  input  [31:0] ID_b,
  input  [31:0] ID_imm,
  input  [31:0] ID_imm_B,
  input  [31:0] ID_imm_Jal,
  input  [31:0] ID_imm_Lui,
  input  [31:0] ID_PC,
  input  [31:0] ID_IR,
  input  [15:0] ID_sgn,
  input  clk,
  input  rst,
  input  halt,
  output [4:0] EX_rd,
  output [31:0] EX_a,
  output [31:0] EX_b,
  output [31:0] EX_imm,
  output [31:0] EX_imm_B,
  output [31:0] EX_imm_Jal,
  output [31:0] EX_imm_Lui,
  output [31:0] EX_PC,
  output [31:0] EX_IR,
  output [15:0] EX_sgn
);

  wire [4:0] multiplexer_1_out;
  wire [15:0] multiplexer_10_out;
  wire [31:0] multiplexer_2_out, multiplexer_3_out, multiplexer_4_out, multiplexer_5_out, multiplexer_6_out,
       multiplexer_7_out, multiplexer_8_out, multiplexer_9_out;

  Multiplexer #(.select(1), .width(5), .disabled("Z"), .enable("false")) multiplexer_1 (
    .in0(ID_rd), .in1({5{1'b0}}), .out(multiplexer_1_out), .sel(rst));
  Multiplexer #(.select(1), .width(32), .disabled("Z"), .enable("false")) multiplexer_2 (
    .in0(ID_a), .in1({32{1'b0}}), .out(multiplexer_2_out), .sel(rst));
  Multiplexer #(.select(1), .width(32), .disabled("Z"), .enable("false")) multiplexer_3 (
    .in0(ID_b), .in1({32{1'b0}}), .out(multiplexer_3_out), .sel(rst));
  Multiplexer #(.select(1), .width(32), .disabled("Z"), .enable("false")) multiplexer_4 (
    .in0(ID_imm), .in1({32{1'b0}}), .out(multiplexer_4_out), .sel(rst));
  Multiplexer #(.select(1), .width(32), .disabled("Z"), .enable("false")) multiplexer_5 (
    .in0(ID_imm_B), .in1({32{1'b0}}), .out(multiplexer_5_out), .sel(rst));
  Multiplexer #(.select(1), .width(32), .disabled("Z"), .enable("false")) multiplexer_6 (
    .in0(ID_imm_Jal), .in1({32{1'b0}}), .out(multiplexer_6_out), .sel(rst));
  Multiplexer #(.select(1), .width(32), .disabled("Z"), .enable("false")) multiplexer_7 (
    .in0(ID_imm_Lui), .in1({32{1'b0}}), .out(multiplexer_7_out), .sel(rst));
  Multiplexer #(.select(1), .width(32), .disabled("Z"), .enable("false")) multiplexer_8 (
    .in0(ID_PC), .in1({32{1'b0}}), .out(multiplexer_8_out), .sel(rst));
  Multiplexer #(.select(1), .width(32), .disabled("Z"), .enable("false")) multiplexer_9 (
    .in0(ID_IR), .in1({32{1'b0}}), .out(multiplexer_9_out), .sel(rst));
  Multiplexer #(.select(1), .width(16), .disabled("Z"), .enable("false")) multiplexer_10 (
    .in0(ID_sgn), .in1({16{1'b0}}), .out(multiplexer_10_out), .sel(rst));
  Register #(.width(5), .trigger("rising"), .Select("low")) register_1 (
    .D(multiplexer_1_out), .en(halt), .Q(EX_rd), .clk(clk));  // open: clr
  Register #(.width(32), .trigger("rising"), .Select("low")) register_2 (
    .D(multiplexer_2_out), .en(halt), .Q(EX_a), .clk(clk));  // open: clr
  Register #(.width(32), .trigger("rising"), .Select("low")) register_3 (
    .D(multiplexer_3_out), .en(halt), .Q(EX_b), .clk(clk));  // open: clr
  Register #(.width(32), .trigger("rising"), .Select("low")) register_4 (
    .D(multiplexer_4_out), .en(halt), .Q(EX_imm), .clk(clk));  // open: clr
  Register #(.width(32), .trigger("rising"), .Select("low")) register_5 (
    .D(multiplexer_5_out), .en(halt), .Q(EX_imm_B), .clk(clk));  // open: clr
  Register #(.width(32), .trigger("rising"), .Select("low")) register_6 (
    .D(multiplexer_6_out), .en(halt), .Q(EX_imm_Jal), .clk(clk));  // open: clr
  Register #(.width(32), .trigger("rising"), .Select("low")) register_7 (
    .D(multiplexer_7_out), .en(halt), .Q(EX_imm_Lui), .clk(clk));  // open: clr
  Register #(.width(32), .trigger("rising"), .Select("low")) register_8 (
    .D(multiplexer_8_out), .en(halt), .Q(EX_PC), .clk(clk));  // open: clr
  Register #(.width(32), .trigger("rising"), .Select("low")) register_9 (
    .D(multiplexer_9_out), .en(halt), .Q(EX_IR), .clk(clk));  // open: clr
  Register #(.width(16), .trigger("rising"), .Select("low")) register_10 (
    .D(multiplexer_10_out), .en(halt), .Q(EX_sgn), .clk(clk));  // open: clr
endmodule

// EX/MEM
module \气泡EX_MEM  (
  input  [4:0] EX_rd,
  input  [31:0] EX_PC,
  input  [31:0] EX_IR,
  input  [31:0] EX_ALU_R,
  input  [31:0] EX_MDin,
  input  [31:0] EX_imm_Lui,
  input  EX_Equal,
  input  [15:0] EX_sgn,
  input  rst,
  input  halt,
  input  clk,
  output [4:0] MEM_rd,
  output [31:0] MEM_PC,
  output [31:0] MEM_IR,
  output [31:0] MEM_ALU_R,
  output [31:0] MEM_MDin,
  output [31:0] MEM_imm_Lui,
  output MEM_Equal,
  output [15:0] MEM_sgn
);

  wire multiplexer_7_out;
  wire [4:0] multiplexer_1_out;
  wire [15:0] multiplexer_8_out;
  wire [31:0] multiplexer_2_out, multiplexer_3_out, multiplexer_4_out, multiplexer_5_out, multiplexer_6_out;

  Multiplexer #(.select(1), .width(5), .disabled("Z"), .enable("false")) multiplexer_1 (
    .in0(EX_rd), .in1({5{1'b0}}), .out(multiplexer_1_out), .sel(rst));
  Multiplexer #(.select(1), .width(32), .disabled("Z"), .enable("false")) multiplexer_2 (
    .in0(EX_PC), .in1({32{1'b0}}), .out(multiplexer_2_out), .sel(rst));
  Multiplexer #(.select(1), .width(32), .disabled("Z"), .enable("false")) multiplexer_3 (
    .in0(EX_IR), .in1({32{1'b0}}), .out(multiplexer_3_out), .sel(rst));
  Multiplexer #(.select(1), .width(32), .disabled("Z"), .enable("false")) multiplexer_4 (
    .in0(EX_ALU_R), .in1({32{1'b0}}), .out(multiplexer_4_out), .sel(rst));
  Multiplexer #(.select(1), .width(32), .disabled("Z"), .enable("false")) multiplexer_5 (
    .in0(EX_MDin), .in1({32{1'b0}}), .out(multiplexer_5_out), .sel(rst));
  Multiplexer #(.select(1), .width(32), .disabled("Z"), .enable("false")) multiplexer_6 (
    .in0(EX_imm_Lui), .in1({32{1'b0}}), .out(multiplexer_6_out), .sel(rst));
  Multiplexer #(.select(1), .width(1), .disabled("Z"), .enable("false")) multiplexer_7 (
    .in0(EX_Equal), .in1(1'b0), .out(multiplexer_7_out), .sel(rst));
  Multiplexer #(.select(1), .width(16), .disabled("Z"), .enable("false")) multiplexer_8 (
    .in0(EX_sgn), .in1({16{1'b0}}), .out(multiplexer_8_out), .sel(rst));
  Register #(.width(5), .trigger("rising"), .Select("low")) register_1 (
    .D(multiplexer_1_out), .en(halt), .Q(MEM_rd), .clk(clk));  // open: clr
  Register #(.width(32), .trigger("rising"), .Select("low")) register_2 (
    .D(multiplexer_2_out), .en(halt), .Q(MEM_PC), .clk(clk));  // open: clr
  Register #(.width(32), .trigger("rising"), .Select("low")) register_3 (
    .D(multiplexer_3_out), .en(halt), .Q(MEM_IR), .clk(clk));  // open: clr
  Register #(.width(32), .trigger("rising"), .Select("low")) register_4 (
    .D(multiplexer_4_out), .en(halt), .Q(MEM_ALU_R), .clk(clk));  // open: clr
  Register #(.width(32), .trigger("rising"), .Select("low")) register_5 (
    .D(multiplexer_5_out), .en(halt), .Q(MEM_MDin), .clk(clk));  // open: clr
  Register #(.width(32), .trigger("rising"), .Select("low")) register_6 (
    .D(multiplexer_6_out), .en(halt), .Q(MEM_imm_Lui), .clk(clk));  // open: clr
  Register #(.width(1), .trigger("rising"), .Select("low")) register_7 (
    .D(multiplexer_7_out), .en(halt), .Q(MEM_Equal), .clk(clk));  // open: clr
  Register #(.width(16), .trigger("rising"), .Select("low")) register_8 (
    .D(multiplexer_8_out), .en(halt), .Q(MEM_sgn), .clk(clk));  // open: clr
endmodule

// MEM/WB
module \气泡MEM_WB  (
  input  [4:0] MEM_rd,
  input  [31:0] MEM_PC,
  input  [31:0] MEM_IR,
  input  [31:0] MEM_LED,
  input  [31:0] MEM_ALU_MD,
  input  MEM_Equal,
  input  [15:0] MEM_sgn,
  input  rst,
  input  halt,
  input  clk,
  output [4:0] WB_rd,
  output [31:0] WB_PC,
  output [31:0] WB_IR,
  output [31:0] WB_LED,
  output [31:0] WB_ALU_MD,
  output WB_Equal,
  output [15:0] WB_sgn
);

  wire multiplexer_6_out;
  wire [4:0] multiplexer_1_out;
  wire [15:0] multiplexer_7_out;
  wire [31:0] multiplexer_2_out, multiplexer_3_out, multiplexer_4_out, multiplexer_5_out;

  Multiplexer #(.select(1), .width(5), .disabled("Z"), .enable("false")) multiplexer_1 (
    .in0(MEM_rd), .in1({5{1'b0}}), .out(multiplexer_1_out), .sel(rst));
  Multiplexer #(.select(1), .width(32), .disabled("Z"), .enable("false")) multiplexer_2 (
    .in0(MEM_PC), .in1({32{1'b0}}), .out(multiplexer_2_out), .sel(rst));
  Multiplexer #(.select(1), .width(32), .disabled("Z"), .enable("false")) multiplexer_3 (
    .in0(MEM_IR), .in1({32{1'b0}}), .out(multiplexer_3_out), .sel(rst));
  Multiplexer #(.select(1), .width(32), .disabled("Z"), .enable("false")) multiplexer_4 (
    .in0(MEM_LED), .in1({32{1'b0}}), .out(multiplexer_4_out), .sel(rst));
  Multiplexer #(.select(1), .width(32), .disabled("Z"), .enable("false")) multiplexer_5 (
    .in0(MEM_ALU_MD), .in1({32{1'b0}}), .out(multiplexer_5_out), .sel(rst));
  Multiplexer #(.select(1), .width(1), .disabled("Z"), .enable("false")) multiplexer_6 (
    .in0(MEM_Equal), .in1(1'b0), .out(multiplexer_6_out), .sel(rst));
  Multiplexer #(.select(1), .width(16), .disabled("Z"), .enable("false")) multiplexer_7 (
    .in0(MEM_sgn), .in1({16{1'b0}}), .out(multiplexer_7_out), .sel(rst));
  Register #(.width(5), .trigger("rising"), .Select("low")) register_1 (
    .D(multiplexer_1_out), .en(halt), .Q(WB_rd), .clk(clk));  // open: clr
  Register #(.width(32), .trigger("rising"), .Select("low")) register_2 (
    .D(multiplexer_2_out), .en(halt), .Q(WB_PC), .clk(clk));  // open: clr
  Register #(.width(32), .trigger("rising"), .Select("low")) register_3 (
    .D(multiplexer_3_out), .en(halt), .Q(WB_IR), .clk(clk));  // open: clr
  Register #(.width(32), .trigger("rising"), .Select("low")) register_4 (
    .D(multiplexer_4_out), .en(halt), .Q(WB_LED), .clk(clk));  // open: clr
  Register #(.width(32), .trigger("rising"), .Select("low")) register_5 (
    .D(multiplexer_5_out), .en(halt), .Q(WB_ALU_MD), .clk(clk));  // open: clr
  Register #(.width(1), .trigger("rising"), .Select("low")) register_6 (
    .D(multiplexer_6_out), .en(halt), .Q(WB_Equal), .clk(clk));  // open: clr
  Register #(.width(16), .trigger("rising"), .Select("low")) register_7 (
    .D(multiplexer_7_out), .en(halt), .Q(WB_sgn), .clk(clk));  // open: clr
endmodule

module \气泡发生器  (
  input  bjump,
  input  J,
  input  EX_RegWrite,
  input  [4:0] rs1,
  input  [4:0] EX_rd,
  input  [4:0] MEM_rd,
  input  rs1_u,
  input  [4:0] rs2,
  input  rs2_u,
  input  MEM_RegWrite,
  output jrst,
  output datapop
);

  wire and_1_out, and_2_out, and_3_out, and_4_out, and_5_out, and_6_out, comparator_1_eq, comparator_2_eq,
       comparator_3_eq, comparator_4_eq, comparator_5_eq, comparator_6_eq, not_1_out, not_2_out, or_2_out,
       or_3_out;

  Comparator #(.width(5), .mode("twosComplement")) comparator_1 (
    .a(EX_rd), .b({5{1'b0}}), .eq(comparator_1_eq));  // open: gt, lt
  Comparator #(.width(5), .mode("twosComplement")) comparator_2 (
    .a(MEM_rd), .b({5{1'b0}}), .eq(comparator_2_eq));  // open: gt, lt
  or or_1 (jrst, bjump, J);
  not not_1 (not_1_out, comparator_1_eq);
  not not_2 (not_2_out, comparator_2_eq);
  Comparator #(.width(5), .mode("twosComplement")) comparator_3 (
    .a(rs1), .b(EX_rd), .eq(comparator_3_eq));  // open: gt, lt
  Comparator #(.width(5), .mode("twosComplement")) comparator_4 (
    .a(rs1), .b(MEM_rd), .eq(comparator_4_eq));  // open: gt, lt
  Comparator #(.width(5), .mode("twosComplement")) comparator_5 (
    .a(rs2), .b(EX_rd), .eq(comparator_5_eq));  // open: gt, lt
  Comparator #(.width(5), .mode("twosComplement")) comparator_6 (
    .a(rs2), .b(MEM_rd), .eq(comparator_6_eq));  // open: gt, lt
  and and_1 (and_1_out, comparator_3_eq, not_1_out, EX_RegWrite);
  and and_2 (and_2_out, comparator_4_eq, not_2_out, MEM_RegWrite);
  and and_3 (and_3_out, comparator_5_eq, not_1_out, EX_RegWrite);
  and and_4 (and_4_out, comparator_6_eq, not_2_out, MEM_RegWrite);
  or or_2 (or_2_out, and_1_out, and_2_out);
  or or_3 (or_3_out, and_3_out, and_4_out);
  and and_5 (and_5_out, or_2_out, rs1_u);
  or or_4 (datapop, and_5_out, and_6_out);
  and and_6 (and_6_out, or_3_out, rs2_u);
endmodule

module \重定向流水线  (
  output RegWrite,
  output MemWrite,
  output [31:0] IF_PC,
  output [31:0] ID_PC,
  output [31:0] EX_PC,
  output [31:0] M_PC,
  output [31:0] WB_PC,
  output [31:0] RDin,
  output [31:0] MDin,
  output [31:0] LedData
);

  wire alu_1_equal, and_1_out, and_2_out, and_3_out, and_4_out, and_5_out, and_6_out, and_7_out, and_8_out,
       Bge, bjump, CLK, clock_1_out, clock_2_out, comparator_1_eq, comparator_1_lt, comparator_2_eq,
       comparator_2_gt, d_ff_1_q, Ecall, Equal, EX_RegWrite, Go, halt, IR1, IR2, IR3, J, Jal, Jalr, Lbu,
       LoadUse, Lui, MEM_Lui, MEM_MemToReg, MEM_RegWrite, nand_1_out, not_1_out, not_2_out, not_3_out,
       not_4_out, not_5_out, or_1_out, or_2_out, or_4_out, or_6_out, RST, S, W1, W2, W3, \单周期硬布线控制器_1_rs1 ,
       \单周期硬布线控制器_1_rs2 , \气泡ex_mem_1_mem_equal , \重定向逻辑设计_1_jpop ;
  wire [1:0] \重定向逻辑设计_1_fwda , \重定向逻辑设计_1_fwdb ;
  wire [3:0] \重定向流水线id_ex_1_ex_sgn_2 ;
  wire [4:0] bit_extender_1_out, minus, multiplexer_1_out, multiplexer_2_out, subtractor_1_out, WB_rd,
       \气泡ex_mem_1_mem_rd , \气泡ir扩展器_1_funct , \气泡ir扩展器_1_op , \气泡ir扩展器_1_rd , \气泡ir扩展器_1_rs1 ,
       \气泡ir扩展器_1_rs2 , \重定向流水线id_ex_1_ex_rd ;
  wire [11:1] \单周期硬布线控制器_1_beq ;
  wire [12:0] CNT_num;
  wire [14:0] \气泡ex_mem_1_mem_sgn ;
  wire [15:0] \LoadUse次数 , \总周期数 , \插入气泡数 , \无条件分支数 , \条件分支成功数 , \气泡mem_wb_1_wb_sgn , \重定向流水线id_ex_1_ex_sgn ;
  wire [31:0] adder_1_out, adder_3_out, adder_4_out, alu_1_result, bAddr, EX_IR, ID_IR, IF_IR, jAddr,
       LedShow, MEM_IR, multiplexer_3_out, multiplexer_4_out, multiplexer_5_out, multiplexer_6_out,
       multiplexer_7_out, multiplexer_8_out, multiplexer_9_out, ram_1_data, regifile_1_r1, regifile_1_r2,
       shifter_1_out, shifter_2_out, WB_IR, \气泡ex_mem_1_mem_alu_r , \气泡ex_mem_1_mem_imm_lui ,
       \气泡ir扩展器_1_imm , \气泡ir扩展器_1_imm_b , \气泡ir扩展器_1_imm_jal , \气泡ir扩展器_1_imm_lui , \气泡mem_wb_1_wb_alu_md ,
       \流水线pc计算_1_npc , \重定向流水线id_ex_1_ex_a , \重定向流水线id_ex_1_ex_b , \重定向流水线id_ex_1_ex_imm ,
       \重定向流水线id_ex_1_ex_imm_lui ;

  Button \u_总复位  (.out(RST));
  Button _1 (.out(IR1));
  Button _2 (.out(IR2));
  Button _3 (.out(IR3));
  // Probe on \总周期数 
  // Probe on \总周期数 
  and and_1 (and_1_out, halt, not_1_out);
  Button \u_继续运行  (.out(Go));
  LED #(.active("true")) led_1 (.in(W1));
  LED #(.active("true")) led_2 (.in(W2));
  LED #(.active("true")) led_3 (.in(W3));
  not not_1 (not_1_out, LoadUse);
  Register #(.width(32), .trigger("rising"), .Select("low")) PC (
    .D(\流水线pc计算_1_npc ), .en(and_1_out), .Q(IF_PC), .clk(CLK), .clr(RST));
  Hex_Digit_Display hex_digit_display_1 (.value(LedData[31:28]));  // open: dp
  // Probe on IF_PC[19:0]
  // RiscV_Probe riscv_probe_1: pin names not known; wires that end beside it: IF_IR
  Hex_Digit_Display hex_digit_display_2 (.value(LedData[23:20]));  // open: dp
  Hex_Digit_Display hex_digit_display_3 (.value(LedData[27:24]));  // open: dp
  // Probe on ID_PC[19:0]
  // RiscV_Probe riscv_probe_2: pin names not known; wires that end beside it: ID_IR
  Adder #(.width(32)) adder_1 (.a(IF_PC), .b(32'h4), .out(adder_1_out));  // open: cin, cout
  \流水线PC计算  \u_流水线pc计算_1  (
    .bJump(bjump), .J(J), .PC_4(adder_1_out), .bAddr(bAddr), .jAddr(jAddr), .NPC(\流水线pc计算_1_npc ));
  Hex_Digit_Display hex_digit_display_4 (.value(LedData[19:16]));  // open: dp
  Hex_Digit_Display hex_digit_display_5 (.value(LedData[15:12]));  // open: dp
  ROM #(.addrWidth(10), .dataWidth(32), .Select("high")) rom_1 (.addr(IF_PC[11:2]), .data(IF_IR));
  Hex_Digit_Display hex_digit_display_6 (.value(LedData[7:4]));  // open: dp
  Hex_Digit_Display hex_digit_display_7 (.value(LedData[11:8]));  // open: dp
  Clock #(.highDuration(1), .lowDuration(1)) clock_1 (.out(clock_1_out));
  // Probe on EX_PC[19:0]
  // RiscV_Probe riscv_probe_3: pin names not known; wires that end beside it: clock_1_out, EX_IR, CLK
  Hex_Digit_Display hex_digit_display_8 (.value(LedData[3:0]));  // open: dp
  \气泡IF_ID  \u_气泡if_id_1  (
    .IF_PC(IF_PC), .IF_IR(IF_IR), .clk(CLK), .halt(and_2_out), .ID_PC(ID_PC), .ID_IR(ID_IR), .rst(or_1_out));
  or or_1 (or_1_out, and_3_out, RST);
  and and_2 (and_2_out, not_2_out, halt);
  // Probe on \总周期数 
  // Probe on M_PC[19:0]
  // RiscV_Probe riscv_probe_4: pin names not known; wires that end beside it: MEM_IR
  \气泡IR扩展器  \u_气泡ir扩展器_1  (
    .IR(ID_IR), .s(S), .OP(\气泡ir扩展器_1_op ), .Funct(\气泡ir扩展器_1_funct ), .rs1(\气泡ir扩展器_1_rs1 ),
    .rs2(\气泡ir扩展器_1_rs2 ), .rd(\气泡ir扩展器_1_rd ), .imm(\气泡ir扩展器_1_imm ), .imm_b(\气泡ir扩展器_1_imm_b ),
    .imm_lui(\气泡ir扩展器_1_imm_lui ), .imm_jal(\气泡ir扩展器_1_imm_jal ));
  and and_3 (and_3_out, \重定向逻辑设计_1_jpop , not_2_out);
  // Probe on \总周期数 
  // Probe on \无条件分支数 
  // Probe on \条件分支成功数 
  // Probe on \插入气泡数 
  // Probe on \LoadUse次数 
  \单周期硬布线控制器  \u_单周期硬布线控制器_1  (
    .Funct(\气泡ir扩展器_1_funct ), .OP(\气泡ir扩展器_1_op ), .ALU_OP(\单周期硬布线控制器_1_beq [8:5]),
    .MemToReg(\单周期硬布线控制器_1_beq [3]), .MemWrite(\单周期硬布线控制器_1_beq [4]), .ALU_SRC(\单周期硬布线控制器_1_beq [9]),
    .RegWrite(\单周期硬布线控制器_1_beq [10]), .ecall(\单周期硬布线控制器_1_beq [11]), .S_type(S), .Jalr(Jalr),
    .Beq(\单周期硬布线控制器_1_beq [1]), .JAL(Jal), .Bne(\单周期硬布线控制器_1_beq [2]), .Lui(Lui), .Lbu(Lbu), .Bge(Bge),
    .rs1(\单周期硬布线控制器_1_rs1 ), .rs2(\单周期硬布线控制器_1_rs2 ));
  not not_2 (not_2_out, LoadUse);
  // Probe on IF_PC[11:0]
  // Probe on WB_PC[19:0]
  // RiscV_Probe riscv_probe_5: pin names not known; wires that end beside it: WB_IR
  Multiplexer #(.select(1), .width(5), .disabled("Z"), .enable("false")) multiplexer_1 (
    .in0(\气泡ir扩展器_1_rs1 ), .in1(5'b10001), .out(multiplexer_1_out), .sel(\单周期硬布线控制器_1_beq [11]));
  Multiplexer #(.select(1), .width(5), .disabled("Z"), .enable("false")) multiplexer_2 (
    .in0(\气泡ir扩展器_1_rs2 ), .in1(5'b01010), .out(multiplexer_2_out), .sel(\单周期硬布线控制器_1_beq [11]));
  // Probe on ID_PC[11:0]
  // Probe on EX_PC[11:0]
  \重定向逻辑设计  \u_重定向逻辑设计_1  (
    .rs1_u(\单周期硬布线控制器_1_rs1 ), .bJump(bjump), .rs2_u(\单周期硬布线控制器_1_rs2 ), .J(J), .EX_RegWrite(EX_RegWrite),
    .MEM_RegWrite(MEM_RegWrite), .MemToReg(MEM_MemToReg), .rs1(multiplexer_1_out),
    .EX_rd(\重定向流水线id_ex_1_ex_rd ), .MEM_rd(\气泡ex_mem_1_mem_rd ), .rs2(multiplexer_2_out),
    .Jpop(\重定向逻辑设计_1_jpop ), .LoadUse(LoadUse), .fwdb(\重定向逻辑设计_1_fwdb ), .fwda(\重定向逻辑设计_1_fwda ));
  Counter #(.width(16), .max('hffff), .ongoal("wrap"), .trigger("rising"), .behavior("old")) counter_1 (
    .count(halt), .Q(\总周期数 ), .clk(CLK), .clr(RST));  // open: load, D, carry, preset
  // Probe on M_PC[11:0]
  D_Flip_Flop #(.trigger("high"), .Pre_Clr_Positions("LEGACY"), .NegatePresetClear("false"), .enable("true"), .NewFFLayout("false")) d_ff_1 (.Q(d_ff_1_q));  // open: clk, D, Qn, preset, en, reset
  // Probe on 13'h320
  Regifile regifile_1 (
    .Din(RDin), .Clk(CLK), .R1(regifile_1_r1), .R2(regifile_1_r2), .WE(RegWrite), .W_num(WB_rd),
    .R1_num(multiplexer_1_out), .R2_num(multiplexer_2_out));
  // Probe on WB_PC[11:0]
  Comparator #(.width(13), .mode("twosComplement")) comparator_1 (
    .a(CNT_num), .b(13'h320), .eq(comparator_1_eq), .lt(comparator_1_lt));  // open: gt
  Clock #(.highDuration(1), .lowDuration(1)) clock_2 (.out(clock_2_out));
  and and_4 (and_4_out, halt, J);
  nand nand_1 (nand_1_out, d_ff_1_q, comparator_1_eq);
  Counter #(.width(13), .max('h1fff), .ongoal("stay"), .trigger("rising"), .behavior("old")) counter_2 (
    .count(comparator_1_lt), .Q(CNT_num), .clk(clock_2_out));  // open: load, D, carry, clr, preset
  Multiplexer #(.select(2), .width(32), .disabled("Z"), .enable("false")) multiplexer_3 (
    .in0(regifile_1_r1), .in1(multiplexer_7_out), .in2(alu_1_result), .out(multiplexer_3_out),
    .sel(\重定向逻辑设计_1_fwda ));  // open: in3
  Multiplexer #(.select(2), .width(32), .disabled("Z"), .enable("false")) multiplexer_4 (
    .in0(regifile_1_r2), .in1(multiplexer_7_out), .in2(alu_1_result), .out(multiplexer_4_out),
    .sel(\重定向逻辑设计_1_fwdb ));  // open: in3
  Counter #(.width(16), .max('hffff), .ongoal("wrap"), .trigger("rising"), .behavior("old")) counter_3 (
    .count(and_4_out), .Q(\无条件分支数 ), .clk(CLK), .clr(RST));  // open: load, D, carry, preset
  assign CLK = nand_1_out ? clock_2_out : 1'bz;  // Controlled_Buffer controlled_buffer_1
  Comparator #(.width(32), .mode("twosComplement")) comparator_2 (
    .a(multiplexer_3_out), .b(multiplexer_4_out), .gt(comparator_2_gt), .eq(comparator_2_eq));  // open: lt
  Adder #(.width(32)) adder_2 (.a(ID_PC), .b(\气泡ir扩展器_1_imm_b ), .out(bAddr));  // open: cin, cout
  Pull_Resistor #(.pull(1)) pull_resistor_1 (.node(CLK));
  \条件分支逻辑设计  \u_条件分支逻辑设计_1  (
    .Bge(Bge), .in_4(comparator_2_eq), .Beq(\单周期硬布线控制器_1_beq [1]), .in_2(or_2_out),
    .Bne(\单周期硬布线控制器_1_beq [2]), .branch(bjump));
  or or_2 (or_2_out, comparator_2_gt, comparator_2_eq);
  Counter #(.width(16), .max('hffff), .ongoal("wrap"), .trigger("rising"), .behavior("old")) counter_4 (
    .count(and_5_out), .Q(\条件分支成功数 ), .clk(CLK), .clr(RST));  // open: load, D, carry, preset
  and and_5 (and_5_out, halt, bjump);
  or or_3 (J, Jalr, Jal);
  Adder #(.width(32)) adder_3 (.a(multiplexer_3_out), .b(\气泡ir扩展器_1_imm ), .out(adder_3_out));  // open: cin, cout
  \无条件跳转逻辑设计  \u_无条件跳转逻辑设计_1  (
    .JAL(Jal), .JALR(Jalr), .JALR_Addr(adder_3_out), .JAL_Addr(\气泡ir扩展器_1_imm_jal ), .J_Addr(jAddr),
    .PC(ID_PC));
  and and_6 (and_6_out, halt, LoadUse);
  \重定向流水线ID_EX  \u_重定向流水线id_ex_1  (
    .ID_rd(\气泡ir扩展器_1_rd ), .ID_a(multiplexer_3_out), .ID_b(multiplexer_4_out), .ID_imm(\气泡ir扩展器_1_imm ),
    .ID_imm_Lui(\气泡ir扩展器_1_imm_lui ), .ID_PC(ID_PC), .ID_IR(ID_IR),
    .ID_sgn({Lui, Lbu, Jalr, Jal, \单周期硬布线控制器_1_beq , Bge}), .EX_rd(\重定向流水线id_ex_1_ex_rd ),
    .EX_a(\重定向流水线id_ex_1_ex_a ), .EX_b(\重定向流水线id_ex_1_ex_b ), .EX_imm(\重定向流水线id_ex_1_ex_imm ),
    .EX_imm_Lui(\重定向流水线id_ex_1_ex_imm_lui ), .EX_PC(EX_PC), .EX_IR(EX_IR),
    .EX_sgn({\重定向流水线id_ex_1_ex_sgn [15:11], EX_RegWrite, \重定向流水线id_ex_1_ex_sgn [9], \重定向流水线id_ex_1_ex_sgn_2 , \重定向流水线id_ex_1_ex_sgn [4:0]}),
    .clk(CLK), .rst(or_4_out), .halt(halt));
  Counter #(.width(16), .max('hffff), .ongoal("wrap"), .trigger("rising"), .behavior("old")) counter_5 (
    .count(and_6_out), .Q(\LoadUse次数 ), .clk(CLK), .clr(RST));  // open: load, D, carry, preset
  or or_4 (or_4_out, LoadUse, RST);
  Multiplexer #(.select(1), .width(32), .disabled("Z"), .enable("false")) multiplexer_5 (
    .in0(\重定向流水线id_ex_1_ex_b ), .in1(\重定向流水线id_ex_1_ex_imm ), .out(multiplexer_5_out),
    .sel(\重定向流水线id_ex_1_ex_sgn [9]));
  Multiplexer #(.select(1), .width(32), .disabled("Z"), .enable("false")) multiplexer_6 (
    .in0(multiplexer_5_out), .in1(32'ha), .out(multiplexer_6_out), .sel(\重定向流水线id_ex_1_ex_sgn [11]));
  ALU alu_1 (
    .X(\重定向流水线id_ex_1_ex_a ), .Y(multiplexer_6_out), .AluOP(\重定向流水线id_ex_1_ex_sgn_2 ), .Equal(alu_1_equal),
    .Result(alu_1_result));  // open: Result_2, out_4, out_6
  \气泡EX_MEM  \u_气泡ex_mem_1  (
    .EX_rd(\重定向流水线id_ex_1_ex_rd ), .EX_PC(EX_PC), .EX_IR(EX_IR), .EX_ALU_R(alu_1_result),
    .EX_imm_Lui(\重定向流水线id_ex_1_ex_imm_lui ),
    .EX_sgn({\重定向流水线id_ex_1_ex_sgn [15:11], EX_RegWrite, \重定向流水线id_ex_1_ex_sgn [9], \重定向流水线id_ex_1_ex_sgn_2 , \重定向流水线id_ex_1_ex_sgn [4:0]}),
    .MEM_rd(\气泡ex_mem_1_mem_rd ), .MEM_PC(M_PC), .MEM_IR(MEM_IR), .MEM_ALU_R(\气泡ex_mem_1_mem_alu_r ),
    .MEM_imm_Lui(\气泡ex_mem_1_mem_imm_lui ),
    .MEM_sgn({MEM_Lui, \气泡ex_mem_1_mem_sgn [14:11], MEM_RegWrite, \气泡ex_mem_1_mem_sgn [9:5], MemWrite, MEM_MemToReg, \气泡ex_mem_1_mem_sgn [2:0]}),
    .rst(RST), .halt(halt), .clk(CLK), .EX_MDin(\重定向流水线id_ex_1_ex_b ), .MEM_MDin(MDin),
    .EX_Equal(alu_1_equal), .MEM_Equal(\气泡ex_mem_1_mem_equal ));
  and and_7 (and_7_out, Ecall, Equal);
  and and_8 (and_8_out, Ecall, not_3_out);
  not not_3 (not_3_out, Equal);
  not not_4 (not_4_out, MemWrite);
  not not_5 (not_5_out, and_7_out);
  RAM #(.addrWidth(10), .dataWidth(32), .bus("separate"), .Select("high")) ram_1 (
    .addr(\气泡ex_mem_1_mem_alu_r [11:2]), .din(MDin), .data(ram_1_data), .str(MemWrite), .clk(CLK),
    .ld(not_4_out));  // open: sel, clr
  or or_5 (halt, Go, not_5_out);
  Register #(.width(32), .trigger("rising"), .Select("low")) register_1 (
    .D(LedShow), .en(and_8_out), .Q(LedData), .clk(CLK));  // open: clr
  Subtractor #(.width(5)) subtractor_1 (.a(5'b11000), .b(minus), .out(subtractor_1_out));  // open: bin, bout
  Multiplexer #(.select(1), .width(32), .disabled("Z"), .enable("false")) multiplexer_7 (
    .in0(\气泡ex_mem_1_mem_alu_r ), .in1(\气泡ex_mem_1_mem_imm_lui ), .out(multiplexer_7_out), .sel(MEM_Lui));
  assign bit_extender_1_out = {{3{1'b0}}, \气泡ex_mem_1_mem_alu_r [1:0]};  // Bit_Extender bit_extender_1
  Shifter #(.width(32), .shift("ll")) shifter_1 (.in(ram_1_data), .\dist (subtractor_1_out), .out(shifter_1_out));
  Shifter #(.width(32), .shift("lr")) shifter_2 (.in(shifter_1_out), .\dist (5'b11000), .out(shifter_2_out));
  Shifter #(.width(5), .shift("ll")) shifter_3 (.in(bit_extender_1_out), .\dist (3'b011), .out(minus));
  Multiplexer #(.select(1), .width(32), .disabled("Z"), .enable("false")) multiplexer_8 (
    .in0(ram_1_data), .in1(shifter_2_out), .out(multiplexer_8_out), .sel(\气泡ex_mem_1_mem_sgn [14]));
  Multiplexer #(.select(1), .width(32), .disabled("Z"), .enable("false")) multiplexer_9 (
    .in0(multiplexer_7_out), .in1(multiplexer_8_out), .out(multiplexer_9_out), .sel(MEM_MemToReg));
  \气泡MEM_WB  \u_气泡mem_wb_1  (
    .MEM_rd(\气泡ex_mem_1_mem_rd ), .MEM_PC(M_PC), .MEM_IR(MEM_IR), .MEM_ALU_MD(multiplexer_9_out),
    .MEM_sgn({MEM_Lui, \气泡ex_mem_1_mem_sgn [14:11], MEM_RegWrite, \气泡ex_mem_1_mem_sgn [9:5], MemWrite, MEM_MemToReg, \气泡ex_mem_1_mem_sgn [2:0]}),
    .WB_rd(WB_rd), .WB_PC(WB_PC), .WB_IR(WB_IR), .WB_ALU_MD(\气泡mem_wb_1_wb_alu_md ),
    .WB_sgn({\气泡mem_wb_1_wb_sgn [15:12], Ecall, RegWrite, \气泡mem_wb_1_wb_sgn [9:0]}), .rst(RST), .halt(halt),
    .clk(CLK), .MEM_Equal(\气泡ex_mem_1_mem_equal ), .WB_Equal(Equal), .MEM_LED(MDin), .WB_LED(LedShow));
  Adder #(.width(32)) adder_4 (.a(WB_PC), .b(32'h4), .out(adder_4_out));  // open: cin, cout
  or or_6 (or_6_out, \气泡mem_wb_1_wb_sgn [13], \气泡mem_wb_1_wb_sgn [12]);
  Multiplexer #(.select(1), .width(32), .disabled("Z"), .enable("false")) multiplexer_10 (
    .in0(\气泡mem_wb_1_wb_alu_md ), .in1(adder_4_out), .out(RDin), .sel(or_6_out));

  // Other names for the same wires on the sheet: MEM_PC[31:0] = M_PC

  // Notes on the sheet:
  //   中断源
  //   时空图监测，可删除
  //   中断等待指示
  //   数码管输出
  //   指令存储器
  //   contents of rom_1 (hex, n*v repeats v):
  //   100493 100006f 100493 200913 300993 100006f 100493 200913 300993 100006f 100493 200913 300993
  //   100006f 100493 200913 300993 29c000ef 100413 100493 1f49493 900533 2200893 73 24d493 48463 fedff06f
  //   900533 2200893 73 100493 249493 900533 2200893 73 48463 fedff06f 100493 1f49493 900533 2200893 73
  //   4034d493 900533 2200893 73 4044d493 900533 2200893 73 4044d493 900533 2200893 73 4044d493 900533
  //   2200893 73 4044d493 900533 2200893 73 4044d493 900533 2200893 73 4044d493 900533 2200893 73 4044d493
  //   900533 2200893 73 100413 1f41993 41f9d993 433 c00913 300b13 140413 f47413 800293 100313 499993
  //   89e9b3 1300533 2200893 73 406282b3 fe0294e3 140413 f00f93 1f47433 1c41413 800293 100313 49d993
  //   89e9b3 1300533 2200893 73 406282b3 fe0294e3 1c45413 406b0b33 b0463 f95ff06f 2b3 fff2c293 829293
  //   ff2e293 500533 2200893 73 fff00413 493 84a023 140413 448493 84a023 140413 448493 84a023 140413
  //   448493 84a023 140413 448493 84a023 140413 448493 84a023 140413 448493 84a023 140413 448493 84a023
  //   140413 448493 84a023 140413 448493 84a023 140413 448493 84a023 140413 448493 84a023 140413 448493
  //   84a023 140413 448493 84a023 140413 448493 84a023 140413 448493 84a023 140413 448493 140413 433
  //   3c00493 42983 4aa03 149a2b3 28663 134a023 1442023 ffc48493 fe9412e3 800533 2200893 73 440413 3c00493
  //   fc9416e3 a00893 73 413 140413 800533 2200893 73 240413 800533 2200893 73 340413 800533 2200893 73
  //   440413 800533 2200893 73 540413 800533 2200893 73 640413 800533 2200893 73 740413 800533 2200893 73
  //   840413 800533 2200893 2200893 73 8067
  //   跳转需要清除IF和ID的误取指令，连接reset同步清零
  //   控制位
  //   流水调试日志用
  //   暂停节拍，不能为0
  //   戳工具置1进入计数暂停模式，ctrl+k时钟自动运行到对应节拍暂停
  //   ctrl+k关闭时钟连续运行，将控制位置零，进入单步调试模式调试
  //   数据记录
  //   可计数暂停的时钟源
  //   instruction分配关系
  //   0：Bge指令
  //   1：Beq指令
  //   2：Bne指令
  //   10：RegWrite信号
  //   14：Lbu信号
  //   为方便自动评测，需要输出流水线各段保存的PC值，注意是PC不是PC+4，另外ID段寄存器写入信息，Mem段内存写入信息也要输出
  //   3：MemToReg信号
  //   4：MemWrite信号
  //   11：Ecall信号
  //   15：Lui信号
  //   5-8：AluOP信号
  //   9：Alu_src信号
  //   12：Jal信号
  //   13：Jalr信号
  //   Ecall选项
  //   做修改是因为重定向Lui的结果不应当等待内存访问
  //   数据存储器
endmodule

// 重定向逻辑
module \重定向逻辑设计  (
  input  rs1_u,
  input  bJump,
  input  rs2_u,
  input  J,
  input  EX_RegWrite,
  input  MEM_RegWrite,
  input  MemToReg,
  input  [4:0] rs1,
  input  [4:0] EX_rd,
  input  [4:0] MEM_rd,
  input  [4:0] rs2,
  output Jpop,
  output LoadUse,
  output [1:0] fwdb,
  output [1:0] fwda
);

  wire and_1_out, and_2_out, comparator_1_eq, comparator_2_eq, not_3_out, not_4_out, rs1__0, rs1_EX_rd,
       rs1_MEM_rd, rs2__0, rs2_EX_rd, rs2_MEM_rd;

  or or_1 (Jpop, bJump, J);
  Comparator #(.width(5), .mode("twosComplement")) comparator_1 (
    .a(rs1), .b({5{1'b0}}), .eq(comparator_1_eq));  // open: gt, lt
  Comparator #(.width(5), .mode("twosComplement")) comparator_2 (
    .a(rs2), .b({5{1'b0}}), .eq(comparator_2_eq));  // open: gt, lt
  not not_1 (rs1__0, comparator_1_eq);
  not not_2 (rs2__0, comparator_2_eq);
  and and_1 (and_1_out, rs1_u, rs1__0, rs1_MEM_rd, MemToReg);
  and and_2 (and_2_out, rs2_u, rs2__0, rs2_MEM_rd, MemToReg);
  Comparator #(.width(5), .mode("twosComplement")) comparator_3 (.a(rs1), .b(EX_rd), .eq(rs1_EX_rd));  // open: gt, lt
  Comparator #(.width(5), .mode("twosComplement")) comparator_4 (.a(rs1), .b(MEM_rd), .eq(rs1_MEM_rd));  // open: gt, lt
  Comparator #(.width(5), .mode("twosComplement")) comparator_5 (.a(rs2), .b(EX_rd), .eq(rs2_EX_rd));  // open: gt, lt
  Comparator #(.width(5), .mode("twosComplement")) comparator_6 (.a(rs2), .b(MEM_rd), .eq(rs2_MEM_rd));  // open: gt, lt
  or or_2 (LoadUse, and_1_out, and_2_out);
  not not_3 (not_3_out, fwdb[1]);
  and and_3 (fwdb[1], rs2_u, rs2__0, rs2_EX_rd, EX_RegWrite);
  not not_4 (not_4_out, fwda[1]);
  and and_4 (fwda[1], rs1_u, rs1__0, rs1_EX_rd, EX_RegWrite);
  and and_5 (fwdb[0], rs2_u, rs2__0, not_3_out, rs2_MEM_rd, MEM_RegWrite);
  and and_6 (fwda[0], rs1_u, rs1__0, not_4_out, rs1_MEM_rd, MEM_RegWrite);
endmodule

// ID/EX
module \重定向流水线ID_EX  (
  input  [4:0] ID_rd,
  input  [31:0] ID_a,
  input  [31:0] ID_b,
  input  [31:0] ID_imm,
  input  [31:0] ID_imm_Lui,
  input  [31:0] ID_PC,
  input  [31:0] ID_IR,
  input  [15:0] ID_sgn,
  input  clk,
  input  rst,
  input  halt,
  output [4:0] EX_rd,
  output [31:0] EX_a,
  output [31:0] EX_b,
  output [31:0] EX_imm,
  output [31:0] EX_imm_Lui,
  output [31:0] EX_PC,
  output [31:0] EX_IR,
  output [15:0] EX_sgn
);

  wire [4:0] multiplexer_1_out;
  wire [15:0] multiplexer_8_out;
  wire [31:0] multiplexer_2_out, multiplexer_3_out, multiplexer_4_out, multiplexer_5_out, multiplexer_6_out,
       multiplexer_7_out;

  Multiplexer #(.select(1), .width(5), .disabled("Z"), .enable("false")) multiplexer_1 (
    .in0(ID_rd), .in1({5{1'b0}}), .out(multiplexer_1_out), .sel(rst));
  Multiplexer #(.select(1), .width(32), .disabled("Z"), .enable("false")) multiplexer_2 (
    .in0(ID_a), .in1({32{1'b0}}), .out(multiplexer_2_out), .sel(rst));
  Multiplexer #(.select(1), .width(32), .disabled("Z"), .enable("false")) multiplexer_3 (
    .in0(ID_b), .in1({32{1'b0}}), .out(multiplexer_3_out), .sel(rst));
  Multiplexer #(.select(1), .width(32), .disabled("Z"), .enable("false")) multiplexer_4 (
    .in0(ID_imm), .in1({32{1'b0}}), .out(multiplexer_4_out), .sel(rst));
  Multiplexer #(.select(1), .width(32), .disabled("Z"), .enable("false")) multiplexer_5 (
    .in0(ID_imm_Lui), .in1({32{1'b0}}), .out(multiplexer_5_out), .sel(rst));
  Multiplexer #(.select(1), .width(32), .disabled("Z"), .enable("false")) multiplexer_6 (
    .in0(ID_PC), .in1({32{1'b0}}), .out(multiplexer_6_out), .sel(rst));
  Multiplexer #(.select(1), .width(32), .disabled("Z"), .enable("false")) multiplexer_7 (
    .in0(ID_IR), .in1({32{1'b0}}), .out(multiplexer_7_out), .sel(rst));
  Multiplexer #(.select(1), .width(16), .disabled("Z"), .enable("false")) multiplexer_8 (
    .in0(ID_sgn), .in1({16{1'b0}}), .out(multiplexer_8_out), .sel(rst));
  Register #(.width(5), .trigger("rising"), .Select("low")) register_1 (
    .D(multiplexer_1_out), .en(halt), .Q(EX_rd), .clk(clk));  // open: clr
  Register #(.width(32), .trigger("rising"), .Select("low")) register_2 (
    .D(multiplexer_2_out), .en(halt), .Q(EX_a), .clk(clk));  // open: clr
  Register #(.width(32), .trigger("rising"), .Select("low")) register_3 (
    .D(multiplexer_3_out), .en(halt), .Q(EX_b), .clk(clk));  // open: clr
  Register #(.width(32), .trigger("rising"), .Select("low")) register_4 (
    .D(multiplexer_4_out), .en(halt), .Q(EX_imm), .clk(clk));  // open: clr
  Register #(.width(32), .trigger("rising"), .Select("low")) register_5 (
    .D(multiplexer_5_out), .en(halt), .Q(EX_imm_Lui), .clk(clk));  // open: clr
  Register #(.width(32), .trigger("rising"), .Select("low")) register_6 (
    .D(multiplexer_6_out), .en(halt), .Q(EX_PC), .clk(clk));  // open: clr
  Register #(.width(32), .trigger("rising"), .Select("low")) register_7 (
    .D(multiplexer_7_out), .en(halt), .Q(EX_IR), .clk(clk));  // open: clr
  Register #(.width(16), .trigger("rising"), .Select("low")) register_8 (
    .D(multiplexer_8_out), .en(halt), .Q(EX_sgn), .clk(clk));  // open: clr
endmodule

module \中断按键参考电路  (
  input  \同步清零信号 ,
  output \与中断屏蔽位与 
);

  wire \_1号中断_out , and_1_out, clock_1_out, d_ff_1_q, or_1_out, or_2_out;

  Clock #(.highDuration(1), .lowDuration(1)) clock_1 (.out(clock_1_out));
  Button \_1号中断  (.out(\_1号中断_out ));
  LED #(.active("true")) \_1号中断等待指示灯  (.in(or_1_out));
  or or_1 (or_1_out, \与中断屏蔽位与 , d_ff_1_q);
  D_Flip_Flop #(.trigger("rising"), .Pre_Clr_Positions("LEGACY"), .NegatePresetClear("false"), .enable("true"), .NewFFLayout("false")) d_ff_1 (
    .clk(\_1号中断_out ), .D(1'b1), .Q(d_ff_1_q), .reset(\与中断屏蔽位与 ));  // open: Qn, preset, en
  or or_2 (or_2_out, d_ff_1_q, \与中断屏蔽位与 );
  and and_1 (and_1_out, or_2_out, ~\同步清零信号 );  // AND_Gate
  D_Flip_Flop #(.trigger("rising"), .Pre_Clr_Positions("LEGACY"), .NegatePresetClear("false"), .enable("true"), .NewFFLayout("false")) IR1 (
    .clk(clock_1_out), .D(and_1_out), .Q(\与中断屏蔽位与 ));  // open: Qn, preset, en, reset

  // Notes on the sheet:
  //   中断信号采样参考电路
  //   Reset 
endmodule

module \单周期_单级中断  (
  input  IR1,
  input  IR2,
  input  IR3,
  output RegWrite,
  output MemWrite,
  output [31:0] PC,
  output [31:0] IR,
  output [31:0] RDin,
  output [31:0] MDin,
  output [31:0] LedData
);

  wire CLK, comparator_1_eq, comparator_2_eq, comparator_3_eq, comparator_4_eq, Go, IR1_t, IR2_t, IR3_t, IRA,
       IRB, IRC, or_1_out, W1, W2, W3;
  wire [15:0] \总周期数 ;

  Clock #(.highDuration(1), .lowDuration(1)) clock_1 (.out(CLK));
  Button _1 ();  // open: out
  Button _2 ();  // open: out
  Button _3 ();  // open: out
  Button \u_继续运行  (.out(Go));
  LED #(.active("true")) led_1 (.in(W1));
  LED #(.active("true")) led_2 (.in(W2));
  LED #(.active("true")) led_3 (.in(W3));
  Hex_Digit_Display hex_digit_display_1 (.value(LedData[31:28]));  // open: dp
  Comparator #(.width(16), .mode("twosComplement")) comparator_1 (
    .a(16'h23b), .b(\总周期数 ), .eq(comparator_1_eq));  // open: gt, lt
  Comparator #(.width(16), .mode("twosComplement")) comparator_2 (
    .a(\总周期数 ), .b(16'h1), .eq(comparator_2_eq));  // open: gt, lt
  Comparator #(.width(16), .mode("twosComplement")) comparator_3 (
    .a(\总周期数 ), .b(16'h4), .eq(comparator_3_eq));  // open: gt, lt
  Comparator #(.width(16), .mode("twosComplement")) comparator_4 (
    .a(\总周期数 ), .b(16'h7), .eq(comparator_4_eq));  // open: gt, lt
  Hex_Digit_Display hex_digit_display_2 (.value(LedData[23:20]));  // open: dp
  Hex_Digit_Display hex_digit_display_3 (.value(LedData[27:24]));  // open: dp
  or or_1 (or_1_out, comparator_1_eq, comparator_2_eq);
  assign IRA = or_1_out ? ~CLK : 1'bz;  // Controlled_Inverter controlled_inverter_1
  assign IRB = comparator_3_eq ? ~CLK : 1'bz;  // Controlled_Inverter controlled_inverter_2
  assign IRC = comparator_4_eq ? ~CLK : 1'bz;  // Controlled_Inverter controlled_inverter_3
  Hex_Digit_Display hex_digit_display_4 (.value(LedData[19:16]));  // open: dp
  Hex_Digit_Display hex_digit_display_5 (.value(LedData[15:12]));  // open: dp
  Pull_Resistor #(.pull(0)) pull_resistor_1 (.node(IRA));
  Pull_Resistor #(.pull(0)) pull_resistor_2 (.node(IRB));
  Pull_Resistor #(.pull(0)) pull_resistor_3 (.node(IRC));
  Hex_Digit_Display hex_digit_display_6 (.value(LedData[7:4]));  // open: dp
  Hex_Digit_Display hex_digit_display_7 (.value(LedData[11:8]));  // open: dp
  // Probe on \总周期数 
  Hex_Digit_Display hex_digit_display_8 (.value(LedData[3:0]));  // open: dp
  or or_2 (IR1_t, IR1, IRA);
  or or_3 (IR2_t, IR2, IRB);
  or or_4 (IR3_t, IR3, IRC);

  // Notes on the sheet:
  //   中断源
  //   中断等待指示
  //   总复位信号应将除ROM以外所有存储组件全部清零
  //   单级中断测试信号模拟器
  //   数码管输出
  //   数码管输出应该用寄存器锁存，否则显示数据只能一闪而过
  //   为方便自动评测，需要输出PC，IR，寄存器堆写如数据RDin
  //   RAM写使能MemWrite、RAM写入数据MDin等信号
endmodule

module \单周期_多级中断  (
  input  IR1,
  input  IR2,
  input  IR3,
  output RegWrite,
  output MemWrite,
  output [31:0] PC,
  output [31:0] IR,
  output [31:0] RDin,
  output [31:0] MDin,
  output [31:0] LedData
);

  wire CLK, comparator_1_eq, comparator_2_eq, comparator_3_eq, comparator_4_eq, comparator_5_eq, Go, IR1_t,
       IR2_t, IR3_t, IRA, IRB, IRC, or_1_out, or_2_out, W1, W2, W3;
  wire [15:0] \总周期数 ;

  Clock #(.highDuration(1), .lowDuration(1)) clock_1 (.out(CLK));
  Button _1 ();  // open: out
  Button _2 ();  // open: out
  Button _3 ();  // open: out
  Button \u_继续运行  (.out(Go));
  LED #(.active("true")) led_1 (.in(W1));
  LED #(.active("true")) led_2 (.in(W2));
  LED #(.active("true")) led_3 (.in(W3));
  Hex_Digit_Display hex_digit_display_1 (.value(LedData[31:28]));  // open: dp
  Comparator #(.width(16), .mode("twosComplement")) comparator_1 (
    .a(\总周期数 ), .b(16'h7), .eq(comparator_1_eq));  // open: gt, lt
  Comparator #(.width(16), .mode("twosComplement")) comparator_2 (
    .a(\总周期数 ), .b(16'h241), .eq(comparator_2_eq));  // open: gt, lt
  Hex_Digit_Display hex_digit_display_2 (.value(LedData[23:20]));  // open: dp
  Hex_Digit_Display hex_digit_display_3 (.value(LedData[27:24]));  // open: dp
  Comparator #(.width(16), .mode("twosComplement")) comparator_3 (
    .a(16'h258), .b(\总周期数 ), .eq(comparator_3_eq));  // open: gt, lt
  or or_1 (or_1_out, comparator_3_eq, comparator_4_eq);
  Comparator #(.width(16), .mode("twosComplement")) comparator_4 (
    .a(\总周期数 ), .b(16'h1), .eq(comparator_4_eq));  // open: gt, lt
  Comparator #(.width(16), .mode("twosComplement")) comparator_5 (
    .a(\总周期数 ), .b(16'h4), .eq(comparator_5_eq));  // open: gt, lt
  or or_2 (or_2_out, comparator_1_eq, comparator_2_eq);
  Hex_Digit_Display hex_digit_display_4 (.value(LedData[19:16]));  // open: dp
  Hex_Digit_Display hex_digit_display_5 (.value(LedData[15:12]));  // open: dp
  Pull_Resistor #(.pull(0)) pull_resistor_1 (.node(IRA));
  assign IRA = or_1_out ? ~CLK : 1'bz;  // Controlled_Inverter controlled_inverter_1
  Pull_Resistor #(.pull(0)) pull_resistor_2 (.node(IRB));
  assign IRB = comparator_5_eq ? ~CLK : 1'bz;  // Controlled_Inverter controlled_inverter_2
  Pull_Resistor #(.pull(0)) pull_resistor_3 (.node(IRC));
  assign IRC = or_2_out ? ~CLK : 1'bz;  // Controlled_Inverter controlled_inverter_3
  Hex_Digit_Display hex_digit_display_6 (.value(LedData[7:4]));  // open: dp
  Hex_Digit_Display hex_digit_display_7 (.value(LedData[11:8]));  // open: dp
  // Probe on \总周期数 
  Hex_Digit_Display hex_digit_display_8 (.value(LedData[3:0]));  // open: dp
  or or_3 (IR1_t, IR1, IRA);
  or or_4 (IR2_t, IR2, IRB);
  or or_5 (IR3_t, IR3, IRC);

  // Notes on the sheet:
  //   中断源
  //   中断等待指示
  //   总复位信号应将除ROM以外所有存储组件全部清零
  //   多级中断测试信号模拟器
  //   数码管输出
  //   数码管输出应该用寄存器锁存，否则显示数据只能一闪而过
  //   为方便自动评测，需要输出PC，IR，寄存器堆写如数据RDin
  //   RAM写使能MemWrite、RAM写入数据MDin等信号
endmodule

module \封装正确性测试  (
);

  wire MemW, RegW;
  wire [31:0] EX_PC, ID_PC, IF_PC, LED, MDinr, MEM_PC, RDinr, WB_PC;

  \重定向流水线  \u_重定向流水线_1  (
    .RegWrite(RegW), .MemWrite(MemW), .IF_PC(IF_PC), .ID_PC(ID_PC), .EX_PC(EX_PC), .M_PC(MEM_PC),
    .WB_PC(WB_PC), .RDin(RDinr), .MDin(MDinr), .LedData(LED));

  // Notes on the sheet:
  //   请检查上面封装有无位宽不匹配，引脚标签是否和连接的标签相对应，否则无法在educoder平台上正确测试
  //   重定向流水封装测试
endmodule
