// Logisim project cpu21-riscv.circ as structural Verilog: 37 circuits, main circuit ◇单周期RISC-V
module \单周期RISC_V  (
  input  IR1,
  input  IR2,
  input  IR3,
  output RegWrite,
  output MemWrite,
  output [31:0] PC,
  output [31:0] IR,
  output [31:0] RDin,
  output [31:0] MDin,
  output [31:0] LedData
);

  wire and_1_out, and_2_out, and_3_out, and_4_out, and_5_out, Beq, Bge, Bne, CLK, clock_2_out, com_pc,
       comparator_1_eq, comparator_1_lt, d_ff_1_q, Ecall, Equal, Go, halt, IR1_t, IR2_t, IR3_t, IRA, IRB,
       IRC, JAL, JALR, Lbu, Lui, nand_1_out, not_1_out, not_2_out, not_3_out, not_4_out, or_5_out, S, tunnel,
       W1, W2, W3, \单周期硬布线控制器_1_alu_src , \单周期硬布线控制器_1_memtoreg ;
  wire [3:0] \单周期硬布线控制器_1_alu_op ;
  wire [4:0] bit_extender_5_out, minus, multiplexer_4_out, multiplexer_5_out, subtractor_1_out;
  wire [11:0] multiplexer_6_out;
  wire [12:0] CNT_num;
  wire [15:0] \总周期数 ;
  wire [31:0] adder_2_out, bit_extender_1_out, bit_extender_2_out, bit_extender_3_out, bit_extender_4_out,
       calc, multiplexer_1_out, multiplexer_2_out, multiplexer_3_out, multiplexer_7_out, multiplexer_9_out,
       multiplexer_10_out, multiplexer_11_out, multiplexer_12_out, PC_4, ram_1_data, regifile_1_r1,
       shifter_1_out, shifter_2_out, shifter_3_out, shifter_4_out;

  Clock #(.highDuration(1), .lowDuration(1)) clock_1 ();  // open: out
  Button _1 (.out(IRA));
  Button _2 (.out(IRB));
  Button _3 (.out(IRC));
  Button \u_继续运行  (.out(Go));
  LED #(.active("true")) led_1 (.in(W1));
  LED #(.active("true")) led_2 (.in(W2));
  LED #(.active("true")) led_3 (.in(W3));
  Hex_Digit_Display hex_digit_display_1 (.value(LedData[31:28]));  // open: dp
  Counter #(.width(16), .max('hffff), .ongoal("wrap"), .trigger("rising"), .behavior("old")) counter_1 (
    .count(halt), .Q(\总周期数 ), .clk(CLK));  // open: load, D, carry, clr, preset
  Register #(.width(32), .trigger("rising"), .Select("low")) u_PC (
    .D(multiplexer_2_out), .en(halt), .Q(PC), .clk(CLK));  // open: clr
  assign bit_extender_1_out = {{20{IR[31]}}, {IR[31], IR[7], IR[30:25], IR[11:8]}};  // Bit_Extender bit_extender_1
  Multiplexer #(.select(1), .width(32), .disabled("Z"), .enable("false")) multiplexer_1 (
    .in0(bit_extender_1_out), .in1(bit_extender_2_out), .out(multiplexer_1_out), .sel(JAL));
  assign bit_extender_2_out = {{12{IR[31]}}, {IR[31], IR[19:12], IR[20], IR[30:21]}};  // Bit_Extender bit_extender_2
  and and_1 (and_1_out, Beq, Equal);
  not not_1 (not_1_out, Equal);
  and and_2 (and_2_out, not_1_out, Bne);
  and and_3 (and_3_out, Bge, tunnel);
  Hex_Digit_Display hex_digit_display_2 (.value(LedData[23:20]));  // open: dp
  Hex_Digit_Display hex_digit_display_3 (.value(LedData[27:24]));  // open: dp
  Adder #(.width(32)) adder_1 (.a(PC), .b(32'h4), .out(PC_4));  // open: cin, cout
  Shifter #(.width(32), .shift("ll")) shifter_1 (.in(multiplexer_1_out), .\dist (5'b00001), .out(shifter_1_out));
  or or_1 (com_pc, JAL, and_1_out, and_2_out, and_3_out);
  Hex_Digit_Display hex_digit_display_4 (.value(LedData[15:12]));  // open: dp
  Hex_Digit_Display hex_digit_display_5 (.value(LedData[19:16]));  // open: dp
  // RiscV_Probe riscv_probe_1: pin names not known; wires that end beside it: IR
  Adder #(.width(32)) adder_2 (.a(PC), .b(shifter_1_out), .out(adder_2_out));  // open: cin, cout
  Multiplexer #(.select(1), .width(32), .disabled("Z"), .enable("false")) multiplexer_2 (
    .in0(multiplexer_3_out), .in1(calc), .out(multiplexer_2_out), .sel(JALR));
  Hex_Digit_Display hex_digit_display_6 (.value(LedData[7:4]));  // open: dp
  Hex_Digit_Display hex_digit_display_7 (.value(LedData[11:8]));  // open: dp
  // Probe on \总周期数 
  ROM #(.addrWidth(10), .dataWidth(32), .Select("high")) rom_1 (.addr(PC[11:2]), .data(IR));
  Multiplexer #(.select(1), .width(32), .disabled("Z"), .enable("false")) multiplexer_3 (
    .in0(PC_4), .in1(adder_2_out), .out(multiplexer_3_out), .sel(com_pc));
  Hex_Digit_Display hex_digit_display_8 (.value(LedData[3:0]));  // open: dp
  \单周期硬布线控制器  \u_单周期硬布线控制器_1  (
    .Funct({IR[30], IR[25], IR[14:12]}), .OP(IR[6:2]), .ALU_OP(\单周期硬布线控制器_1_alu_op ),
    .MemToReg(\单周期硬布线控制器_1_memtoreg ), .MemWrite(MemWrite), .ALU_SRC(\单周期硬布线控制器_1_alu_src ),
    .RegWrite(RegWrite), .ecall(Ecall), .S_type(S), .Jalr(JALR), .Beq(Beq), .JAL(JAL), .Bne(Bne), .Lui(Lui),
    .Lbu(Lbu), .Bge(Bge), .IR21(IR[21]));  // open: rs1, rs2, uret, csrrsi, csrrci
  assign bit_extender_3_out = {{12{IR[31]}}, IR[31:12]};  // Bit_Extender bit_extender_3
  or or_2 (IR1_t, IR1, IRA);
  Multiplexer #(.select(1), .width(5), .disabled("Z"), .enable("false")) multiplexer_4 (
    .in0(IR[19:15]), .in1(5'b10001), .out(multiplexer_4_out), .sel(Ecall));
  Multiplexer #(.select(1), .width(5), .disabled("Z"), .enable("false")) multiplexer_5 (
    .in0(IR[24:20]), .in1(5'b01010), .out(multiplexer_5_out), .sel(Ecall));
  Shifter #(.width(32), .shift("ll")) shifter_2 (.in(bit_extender_3_out), .\dist (5'b01100), .out(shifter_2_out));
  or or_3 (IR2_t, IR2, IRB);
  Regifile regifile_1 (
    .Din(RDin), .Clk(CLK), .R1(regifile_1_r1), .R2(MDin), .WE(RegWrite), .W_num(IR[11:7]),
    .R1_num(multiplexer_4_out), .R2_num(multiplexer_5_out));
  Multiplexer #(.select(1), .width(12), .disabled("Z"), .enable("false")) multiplexer_6 (
    .in0(IR[31:20]), .in1({IR[31:25], IR[11:7]}), .out(multiplexer_6_out), .sel(S));
  assign bit_extender_4_out = {{20{multiplexer_6_out[11]}}, multiplexer_6_out};  // Bit_Extender bit_extender_4
  Multiplexer #(.select(1), .width(32), .disabled("Z"), .enable("false")) multiplexer_7 (
    .in0(multiplexer_11_out), .in1(shifter_4_out), .out(multiplexer_7_out), .sel(Lbu));
  Multiplexer #(.select(1), .width(32), .disabled("Z"), .enable("false")) multiplexer_8 (
    .in0(multiplexer_7_out), .in1(shifter_2_out), .out(RDin), .sel(Lui));
  Multiplexer #(.select(1), .width(32), .disabled("Z"), .enable("false")) multiplexer_9 (
    .in0(MDin), .in1(bit_extender_4_out), .out(multiplexer_9_out), .sel(\单周期硬布线控制器_1_alu_src ));
  or or_4 (IR3_t, IR3, IRC);
  Multiplexer #(.select(1), .width(32), .disabled("Z"), .enable("false")) multiplexer_10 (
    .in0(multiplexer_9_out), .in1(32'ha), .out(multiplexer_10_out), .sel(Ecall));
  Subtractor #(.width(5)) subtractor_1 (.a(5'b11000), .b(minus), .out(subtractor_1_out));  // open: bin, bout
  ALU alu_1 (
    .X(regifile_1_r1), .Y(multiplexer_10_out), .AluOP(\单周期硬布线控制器_1_alu_op ), .Equal(Equal), .Result(calc),
    .out_4(tunnel));  // open: Result_2, out_6
  Shifter #(.width(32), .shift("ll")) shifter_3 (
    .in(multiplexer_11_out), .\dist (subtractor_1_out), .out(shifter_3_out));
  Shifter #(.width(32), .shift("lr")) shifter_4 (.in(shifter_3_out), .\dist (5'b11000), .out(shifter_4_out));
  not not_2 (not_2_out, Equal);
  assign bit_extender_5_out = {{3{1'b0}}, calc[1:0]};  // Bit_Extender bit_extender_5
  not not_3 (not_3_out, MemWrite);
  Multiplexer #(.select(1), .width(32), .disabled("Z"), .enable("false")) multiplexer_11 (
    .in0(multiplexer_12_out), .in1(PC_4), .out(multiplexer_11_out), .sel(or_5_out));
  or or_5 (or_5_out, JAL, JALR);
  not not_4 (not_4_out, and_4_out);
  and and_4 (and_4_out, Ecall, Equal);
  and and_5 (and_5_out, Ecall, not_2_out);
  Shifter #(.width(5), .shift("ll")) shifter_5 (.in(bit_extender_5_out), .\dist (3'b011), .out(minus));
  RAM #(.addrWidth(10), .dataWidth(32), .bus("separate"), .Select("high")) ram_1 (
    .addr(calc[11:2]), .din(MDin), .data(ram_1_data), .str(MemWrite), .clk(CLK), .ld(not_3_out));  // open: sel, clr
  or or_6 (halt, Go, not_4_out);
  Register #(.width(32), .trigger("rising"), .Select("low")) register_1 (
    .D(MDin), .en(and_5_out), .Q(LedData), .clk(CLK));  // open: clr
  Multiplexer #(.select(1), .width(32), .disabled("Z"), .enable("false")) multiplexer_12 (
    .in0(calc), .in1(ram_1_data), .out(multiplexer_12_out), .sel(\单周期硬布线控制器_1_memtoreg ));
  D_Flip_Flop #(.trigger("high"), .Pre_Clr_Positions("LEGACY"), .NegatePresetClear("false"), .enable("true"), .NewFFLayout("false")) d_ff_1 (.Q(d_ff_1_q));  // open: clk, D, Qn, preset, en, reset
  // Probe on 13'hc
  Comparator #(.width(13), .mode("twosComplement")) comparator_1 (
    .a(CNT_num), .b(13'hc), .eq(comparator_1_eq), .lt(comparator_1_lt));  // open: gt
  Clock #(.highDuration(1), .lowDuration(1)) clock_2 (.out(clock_2_out));
  Counter #(.width(13), .max('h1fff), .ongoal("stay"), .trigger("rising"), .behavior("old")) counter_2 (
    .count(comparator_1_lt), .Q(CNT_num), .clk(clock_2_out));  // open: load, D, carry, clr, preset
  nand nand_1 (nand_1_out, d_ff_1_q, comparator_1_eq);
  assign CLK = nand_1_out ? clock_2_out : 1'bz;  // Controlled_Buffer controlled_buffer_1
  Pull_Resistor #(.pull(1)) pull_resistor_1 (.node(CLK));

  // Other names for the same wires on the sheet: imm12_B[11:0] = {IR[31], IR[7], IR[30:25], IR[11:8]};
  //   imm20_JAL[19:0] = {IR[31], IR[19:12], IR[20], IR[30:21]}

  // Notes on the sheet:
  //   中断源
  //   中断等待指示
  //   总复位信号应将除ROM以外所有存储组件全部清零
  //   周期数记录
  //   计算新PC
  //   数码管输出
  //   指令存储器
  //   数码管输出应该用寄存器锁存，否则显示数据只能一闪而过
  //   指令字
  //   contents of rom_1 (hex, n*v repeats v):
  //   100493 100006f 100493 200913 300993 100006f 100493 200913 300993 100006f 100493 200913 300993
  //   100006f 100493 200913 300993 3d0000ef 100413 100493 1f49493 900533 2200893 73 24d493 48463 fedff06f
  //   900533 2200893 73 100493 249493 900533 2200893 73 48463 fedff06f 100493 1f49493 900533 2200893 73
  //   4034d493 900533 2200893 73 4044d493 900533 2200893 73 4044d493 900533 2200893 73 4044d493 900533
  //   2200893 73 4044d493 900533 2200893 73 4044d493 900533 2200893 73 4044d493 900533 2200893 73 4044d493
  //   900533 2200893 73 100413 1f41993 41f9d993 433 c00913 300b13 140413 f47413 800293 100313 499993
  //   89e9b3 1300533 2200893 73 406282b3 fe0294e3 140413 f00f93 1f47433 1c41413 800293 100313 49d993
  //   89e9b3 1300533 2200893 73 406282b3 fe0294e3 1c45413 406b0b33 b0463 f95ff06f 2b3 fff2c293 829293
  //   ff2e293 500533 2200893 73 fff00413 493 84a023 140413 448493 84a023 140413 448493 84a023 140413
  //   448493 84a023 140413 448493 84a023 140413 448493 84a023 140413 448493 84a023 140413 448493 84a023
  //   140413 448493 84a023 140413 448493 84a023 140413 448493 84a023 140413 448493 84a023 140413 448493
  //   84a023 140413 448493 84a023 140413 448493 84a023 140413 448493 84a023 140413 448493 140413 433
  //   3c00493 42983 4aa03 149a2b3 28663 134a023 1442023 ffc48493 fe9412e3 800533 2200893 73 440413 3c00493
  //   fc9416e3 a00893 73 fff00293 7700493 849493 7748493 900533 2200893 73 1000e13 54c4b3 900533 2200893
  //   73 fffe0e13 fe0e16e3 a00893 73 800e13 fedc04b7 fff00413 1045413 84e4b3 900533 2200893 73 ba984b7
  //   900533 73 76544b7 900533 73 32104b7 900533 73 fffe0e13 fa0e1ee3 a00893 73 313 1000e13 8400493 849493
  //   8348493 400913 891913 490913 849493 8248493 849493 8148493 891913 490913 891913 490913 932023
  //   12484b3 430313 fffe0e13 fe0e18e3 2000e13 313 34483 900533 2200893 73 130313 fffe0e13 fe0e14e3 a00893
  //   73 f00493 900533 2200893 73 fff48493 fe04d8e3 a00893 73 413 140413 800533 2200893 73 240413 800533
  //   2200893 73 340413 800533 2200893 73 440413 800533 2200893 73 540413 800533 2200893 73 640413 800533
  //   2200893 73 740413 800533 2200893 73 840413 800533 2200893 2200893 73 8067
  //   rs1
  //   rs2
  //   rd
  //   imm20 LUI
  //   Beq
  //   Bne
  //   MemToReg
  //   MemWrite
  //   AluOP
  //   AluSrcB
  //   RegWrite
  //   imm12 I
  //   imm12 S
  //   LBU stores the lowest byte
  //   Ecall选项
  //   为方便自动评测，需要输出PC，IR，寄存器堆写如数据RDin
  //   数据存储器
  //   RAM写使能MemWrite、RAM写入数据MDin等信号
  //   控制位
  //   暂停节拍，不能为0
  //   戳工具置1进入计数暂停模式，ctrl+k时钟自动运行到对应节拍暂停
  //   ctrl+k关闭时钟连续运行，将控制位置零，进入单步调试模式调试
  //   用这个时钟源需要去掉电路中的其他时钟源
  //   可计数暂停的时钟源
endmodule

// 单周期硬布线控制器
module \单周期硬布线控制器  (
  input  [4:0] OP,
  input  [4:0] Funct,
  input  IR21,
  output [3:0] ALU_OP,
  output uret,
  output ecall,
  output MemToReg,
  output MemWrite,
  output ALU_SRC,
  output RegWrite,
  output S_type,
  output Beq,
  output Bne,
  output Jalr,
  output JAL,
  output Lui,
  output Lbu,
  output Bge,
  output csrrsi,
  output rs1,
  output rs2,
  output csrrci
);

  wire not_1_out, \控制信号自动生成_1_ecall ;

  \运算控制器自动生成  \u_运算控制器自动生成_1  (
    .OP2(OP[0]), .OP3(OP[1]), .OP4(OP[2]), .OP5(OP[3]), .OP6(OP[4]), .F12(Funct[0]), .F13(Funct[1]),
    .F14(Funct[2]), .F25(Funct[3]), .F30(Funct[4]), .S0(ALU_OP[0]), .S1(ALU_OP[1]), .S2(ALU_OP[2]),
    .S3(ALU_OP[3]));
  \控制信号自动生成  \u_控制信号自动生成_1  (
    .OP2(OP[0]), .OP3(OP[1]), .OP4(OP[2]), .OP5(OP[3]), .OP6(OP[4]), .MemToReg(MemToReg), .F12(Funct[0]),
    .F13(Funct[1]), .F14(Funct[2]), .F25(Funct[3]), .F30(Funct[4]), .MemWrite(MemWrite), .ALU_SRC(ALU_SRC),
    .RegWrite(RegWrite), .ecall(\控制信号自动生成_1_ecall ), .S_Type(S_type), .BEQ(Beq), .BNE(Bne), .JALR(Jalr),
    .JAL(JAL), .LUI(Lui), .LBU(Lbu), .BGE(Bge), .rs1(rs1), .rs2(rs2), .CSRRSI(csrrsi), .CSRRCI(csrrci));
  not not_1 (not_1_out, IR21);
  and and_1 (uret, IR21, \控制信号自动生成_1_ecall );
  and and_2 (ecall, not_1_out, \控制信号自动生成_1_ecall );

  // Other names for the same wires on the sheet: OP_CODE[4:0] = OP

  // Notes on the sheet:
  //   运算器控制器，根据指令生成运算器功能选择信号
  //   控制信号生成，产生数据通路需要的其他控制信号
endmodule

// 运算器控制器
module \运算控制器自动生成  (
  input  OP2,
  input  OP3,
  input  OP4,
  input  OP5,
  input  OP6,
  input  F12,
  input  F13,
  input  F14,
  input  F25,
  input  F30,
  output S0,
  output S1,
  output S2,
  output S3
);

  wire and_1_out, and_2_out, and_3_out, and_4_out, and_5_out, and_6_out, and_7_out, and_8_out, and_9_out,
       and_10_out, and_11_out, and_12_out, and_13_out, and_14_out, and_15_out, and_16_out, and_17_out,
       and_18_out, and_19_out, and_20_out, and_21_out, and_22_out, and_23_out, not_1_out, not_2_out,
       not_3_out, not_4_out, not_5_out, not_6_out, not_7_out, not_8_out, not_9_out, not_10_out, not_11_out,
       not_12_out, not_13_out, not_14_out, not_15_out, not_16_out, not_17_out, not_18_out, not_19_out,
       not_20_out, not_21_out, not_22_out, not_23_out, not_24_out, not_25_out, not_26_out, not_27_out,
       not_28_out, not_29_out, not_30_out, not_31_out, not_32_out, not_33_out, not_34_out, not_35_out,
       not_36_out, not_37_out, not_38_out, not_39_out, not_40_out, not_41_out, not_42_out, not_43_out,
       not_44_out, not_45_out, not_46_out, not_47_out, not_48_out, not_49_out, not_50_out, not_51_out,
       not_52_out, not_53_out, not_54_out, not_55_out, not_56_out, not_57_out, not_58_out, not_59_out,
       not_60_out, not_61_out, not_62_out, not_63_out, not_64_out, not_65_out, not_66_out, not_67_out,
       not_68_out, not_69_out, not_70_out, not_71_out, not_72_out, not_73_out, not_74_out, not_75_out,
       not_76_out, not_77_out, not_78_out, not_79_out, not_80_out, not_81_out, not_82_out, not_83_out,
       not_84_out, not_85_out, not_86_out, not_87_out, not_88_out, not_89_out, not_90_out, not_91_out,
       not_92_out, not_93_out, not_94_out, not_95_out, not_96_out, not_97_out, not_98_out, not_99_out,
       not_100_out, not_101_out, not_102_out, not_103_out, not_104_out, not_105_out, not_106_out,
       not_107_out, not_108_out, not_109_out, not_110_out, not_111_out, not_112_out, not_113_out,
       not_114_out, not_115_out, not_116_out, not_117_out, not_118_out, not_119_out, not_120_out,
       not_121_out, not_122_out, not_123_out, not_124_out, not_125_out, not_126_out, not_127_out,
       not_128_out, not_129_out, not_130_out, not_131_out, not_132_out, not_133_out;

  not not_1 (not_1_out, OP2);
  not not_2 (not_2_out, OP3);
  not not_3 (not_3_out, OP4);
  not not_4 (not_4_out, OP6);
  not not_5 (not_5_out, F12);
  not not_6 (not_6_out, F14);
  not not_7 (not_7_out, OP2);
  not not_8 (not_8_out, OP3);
  not not_9 (not_9_out, OP5);
  not not_10 (not_10_out, OP6);
  not not_11 (not_11_out, F12);
  not not_12 (not_12_out, F13);
  not not_13 (not_13_out, OP2);
  not not_14 (not_14_out, OP3);
  not not_15 (not_15_out, OP5);
  not not_16 (not_16_out, OP6);
  not not_17 (not_17_out, F12);
  not not_18 (not_18_out, F14);
  not not_19 (not_19_out, OP2);
  not not_20 (not_20_out, OP3);
  not not_21 (not_21_out, OP6);
  not not_22 (not_22_out, F12);
  not not_23 (not_23_out, F13);
  not not_24 (not_24_out, F25);
  not not_25 (not_25_out, F30);
  not not_26 (not_26_out, OP2);
  not not_27 (not_27_out, OP3);
  not not_28 (not_28_out, OP6);
  not not_29 (not_29_out, F12);
  not not_30 (not_30_out, F14);
  not not_31 (not_31_out, F25);
  not not_32 (not_32_out, F30);
  not not_33 (not_33_out, OP2);
  not not_34 (not_34_out, OP3);
  not not_35 (not_35_out, OP5);
  not not_36 (not_36_out, OP6);
  not not_37 (not_37_out, F13);
  not not_38 (not_38_out, F25);
  not not_39 (not_39_out, OP2);
  not not_40 (not_40_out, OP3);
  not not_41 (not_41_out, OP5);
  not not_42 (not_42_out, OP6);
  not not_43 (not_43_out, OP2);
  not not_44 (not_44_out, OP3);
  not not_45 (not_45_out, OP6);
  not not_46 (not_46_out, F25);
  not not_47 (not_47_out, F30);
  not not_48 (not_48_out, OP2);
  not not_49 (not_49_out, OP3);
  not not_50 (not_50_out, OP5);
  not not_51 (not_51_out, OP6);
  not not_52 (not_52_out, F12);
  not not_53 (not_53_out, F14);
  not not_54 (not_54_out, OP2);
  not not_55 (not_55_out, OP3);
  not not_56 (not_56_out, OP6);
  not not_57 (not_57_out, F12);
  not not_58 (not_58_out, F14);
  not not_59 (not_59_out, F25);
  not not_60 (not_60_out, F30);
  not not_61 (not_61_out, OP2);
  not not_62 (not_62_out, OP3);
  not not_63 (not_63_out, OP5);
  not not_64 (not_64_out, OP6);
  not not_65 (not_65_out, F25);
  not not_66 (not_66_out, F30);
  not not_67 (not_67_out, OP2);
  not not_68 (not_68_out, OP3);
  not not_69 (not_69_out, OP5);
  not not_70 (not_70_out, OP6);
  not not_71 (not_71_out, OP2);
  not not_72 (not_72_out, OP3);
  not not_73 (not_73_out, OP6);
  not not_74 (not_74_out, F25);
  not not_75 (not_75_out, F30);
  not not_76 (not_76_out, OP2);
  not not_77 (not_77_out, OP3);
  not not_78 (not_78_out, OP6);
  not not_79 (not_79_out, F12);
  not not_80 (not_80_out, F13);
  not not_81 (not_81_out, F14);
  not not_82 (not_82_out, F25);
  not not_83 (not_83_out, OP2);
  not not_84 (not_84_out, OP3);
  not not_85 (not_85_out, OP4);
  not not_86 (not_86_out, OP6);
  not not_87 (not_87_out, F12);
  not not_88 (not_88_out, F14);
  not not_89 (not_89_out, OP2);
  not not_90 (not_90_out, OP3);
  not not_91 (not_91_out, OP5);
  not not_92 (not_92_out, OP6);
  not not_93 (not_93_out, F12);
  not not_94 (not_94_out, F13);
  not not_95 (not_95_out, F14);
  not not_96 (not_96_out, OP2);
  not not_97 (not_97_out, OP3);
  not not_98 (not_98_out, OP6);
  not not_99 (not_99_out, F12);
  not not_100 (not_100_out, F13);
  not not_101 (not_101_out, F14);
  not not_102 (not_102_out, F25);
  not not_103 (not_103_out, OP2);
  not not_104 (not_104_out, OP3);
  not not_105 (not_105_out, OP5);
  not not_106 (not_106_out, OP6);
  not not_107 (not_107_out, OP2);
  not not_108 (not_108_out, OP3);
  not not_109 (not_109_out, OP6);
  not not_110 (not_110_out, F25);
  not not_111 (not_111_out, F30);
  not not_112 (not_112_out, OP2);
  not not_113 (not_113_out, OP3);
  not not_114 (not_114_out, OP5);
  not not_115 (not_115_out, OP6);
  not not_116 (not_116_out, F12);
  not not_117 (not_117_out, OP2);
  not not_118 (not_118_out, OP3);
  not not_119 (not_119_out, OP6);
  not not_120 (not_120_out, F12);
  not not_121 (not_121_out, F25);
  not not_122 (not_122_out, F30);
  not not_123 (not_123_out, OP2);
  not not_124 (not_124_out, OP3);
  not not_125 (not_125_out, OP5);
  not not_126 (not_126_out, OP6);
  not not_127 (not_127_out, F12);
  not not_128 (not_128_out, OP2);
  not not_129 (not_129_out, OP3);
  not not_130 (not_130_out, OP6);
  not not_131 (not_131_out, F14);
  not not_132 (not_132_out, F25);
  not not_133 (not_133_out, F30);
  and and_1 (and_1_out, not_1_out, not_2_out, not_3_out, not_4_out, not_5_out, F13, not_6_out);
  and and_2 (and_2_out, not_7_out, not_8_out, OP4, not_9_out, not_10_out, not_11_out, not_12_out);
  and and_3 (and_3_out, not_13_out, not_14_out, OP4, not_15_out, not_16_out, not_17_out, not_18_out);
  and and_4 (and_4_out, not_19_out, not_20_out, OP4, not_21_out, not_22_out, not_23_out, not_24_out, not_25_out);
  and and_5 (and_5_out, not_26_out, not_27_out, OP4, not_28_out, not_29_out, not_30_out, not_31_out, not_32_out);
  and and_6 (and_6_out, not_33_out, not_34_out, OP4, not_35_out, not_36_out, not_37_out, F14, not_38_out, F30);
  and and_7 (and_7_out, not_39_out, not_40_out, OP4, not_41_out, not_42_out, F12, F13, F14);
  and and_8 (and_8_out, not_43_out, not_44_out, OP4, not_45_out, F12, F13, F14, not_46_out, not_47_out);
  and and_9 (and_9_out, not_48_out, not_49_out, OP4, not_50_out, not_51_out, not_52_out, F13, not_53_out);
  and and_10 (and_10_out, not_54_out, not_55_out, OP4, not_56_out, not_57_out, F13, not_58_out, not_59_out, not_60_out);
  and and_11 (and_11_out, not_61_out, not_62_out, OP4, not_63_out, not_64_out, F12, F14, not_65_out, not_66_out);
  and and_12 (and_12_out, not_67_out, not_68_out, OP4, not_69_out, not_70_out, F12, F13, F14);
  and and_13 (and_13_out, not_71_out, not_72_out, OP4, not_73_out, F12, F13, F14, not_74_out, not_75_out);
  and and_14 (and_14_out, not_76_out, not_77_out, OP4, OP5, not_78_out, not_79_out, not_80_out, not_81_out, not_82_out, F30);
  and and_15 (and_15_out, not_83_out, not_84_out, not_85_out, not_86_out, not_87_out, F13, not_88_out);
  and and_16 (and_16_out, not_89_out, not_90_out, OP4, not_91_out, not_92_out, not_93_out, not_94_out, not_95_out);
  and and_17 (and_17_out, not_96_out, not_97_out, OP4, not_98_out, not_99_out, not_100_out, not_101_out, not_102_out);
  and and_18 (and_18_out, not_103_out, not_104_out, OP4, not_105_out, not_106_out, F12, F13, F14);
  and and_19 (and_19_out, not_107_out, not_108_out, OP4, OP5, not_109_out, F12, F13, not_110_out, not_111_out);
  and and_20 (and_20_out, not_112_out, not_113_out, OP4, not_114_out, not_115_out, not_116_out, F14);
  and and_21 (and_21_out, not_117_out, not_118_out, OP4, not_119_out, not_120_out, F14, not_121_out, not_122_out);
  and and_22 (and_22_out, not_123_out, not_124_out, OP4, not_125_out, not_126_out, not_127_out, F13);
  and and_23 (and_23_out, not_128_out, not_129_out, OP4, OP5, not_130_out, F13, not_131_out, not_132_out, not_133_out);
  or or_1 (S2, and_15_out, and_16_out, and_17_out, and_18_out, and_19_out);
  or or_2 (S3, and_20_out, and_21_out, and_22_out, and_23_out);
  or or_3 (S0, and_1_out, and_2_out, and_3_out, and_4_out, and_5_out, and_6_out, and_7_out, and_8_out);
  or or_4 (S1, and_9_out, and_10_out, and_11_out, and_12_out, and_13_out, and_14_out);
endmodule

// 控制信号生成
module \控制信号自动生成  (
  input  OP2,
  input  OP3,
  input  OP4,
  input  OP5,
  input  OP6,
  input  F12,
  input  F13,
  input  F14,
  input  F25,
  input  F30,
  output MemToReg,
  output MemWrite,
  output ALU_SRC,
  output RegWrite,
  output ecall,
  output S_Type,
  output BEQ,
  output BNE,
  output JALR,
  output JAL,
  output LUI,
  output LBU,
  output BGE,
  output rs1,
  output rs2,
  output CSRRSI,
  output CSRRCI
);

  wire and_1_out, and_2_out, and_4_out, and_5_out, and_6_out, and_7_out, and_8_out, and_9_out, and_10_out,
       and_11_out, and_12_out, and_13_out, and_14_out, and_15_out, and_16_out, and_17_out, and_18_out,
       and_19_out, and_20_out, and_21_out, and_31_out, and_32_out, and_33_out, and_34_out, and_35_out,
       and_36_out, and_37_out, and_38_out, and_39_out, and_40_out, and_41_out, and_42_out, and_43_out,
       and_44_out, and_45_out, and_46_out, and_47_out, and_48_out, and_49_out, not_1_out, not_2_out,
       not_3_out, not_4_out, not_5_out, not_6_out, not_7_out, not_8_out, not_9_out, not_10_out, not_11_out,
       not_12_out, not_13_out, not_14_out, not_15_out, not_16_out, not_17_out, not_18_out, not_19_out,
       not_20_out, not_21_out, not_22_out, not_23_out, not_24_out, not_25_out, not_26_out, not_27_out,
       not_28_out, not_29_out, not_30_out, not_31_out, not_32_out, not_33_out, not_34_out, not_35_out,
       not_36_out, not_37_out, not_38_out, not_39_out, not_40_out, not_41_out, not_42_out, not_43_out,
       not_44_out, not_45_out, not_46_out, not_47_out, not_48_out, not_49_out, not_50_out, not_51_out,
       not_52_out, not_53_out, not_54_out, not_55_out, not_56_out, not_57_out, not_58_out, not_59_out,
       not_60_out, not_61_out, not_62_out, not_63_out, not_64_out, not_65_out, not_66_out, not_67_out,
       not_68_out, not_69_out, not_70_out, not_71_out, not_72_out, not_73_out, not_74_out, not_75_out,
       not_76_out, not_77_out, not_78_out, not_79_out, not_80_out, not_81_out, not_82_out, not_83_out,
       not_84_out, not_85_out, not_86_out, not_87_out, not_88_out, not_89_out, not_90_out, not_91_out,
       not_92_out, not_93_out, not_94_out, not_95_out, not_96_out, not_97_out, not_98_out, not_99_out,
       not_100_out, not_101_out, not_102_out, not_103_out, not_104_out, not_105_out, not_106_out,
       not_107_out, not_108_out, not_109_out, not_110_out, not_111_out, not_112_out, not_113_out,
       not_114_out, not_115_out, not_116_out, not_117_out, not_118_out, not_119_out, not_120_out,
       not_121_out, not_122_out, not_123_out, not_124_out, not_125_out, not_126_out, not_127_out,
       not_128_out, not_129_out, not_130_out, not_131_out, not_132_out, not_133_out, not_134_out,
       not_135_out, not_136_out, not_137_out, not_138_out, not_139_out, not_140_out, not_141_out,
       not_142_out, not_143_out, not_144_out, not_145_out, not_146_out, not_147_out, not_148_out,
       not_149_out, not_150_out, not_151_out, not_152_out, not_153_out, not_154_out, not_155_out,
       not_156_out, not_157_out, not_158_out, not_159_out, not_160_out, not_161_out, not_162_out,
       not_163_out, not_164_out, not_165_out, not_166_out, not_167_out, not_168_out, not_169_out,
       not_170_out, not_171_out, not_172_out, not_173_out, not_174_out, not_175_out, not_176_out,
       not_177_out, not_178_out, not_179_out, not_180_out, not_181_out, not_182_out, not_183_out,
       not_184_out, not_185_out, not_186_out, not_187_out, not_188_out, not_189_out, not_190_out,
       not_191_out, not_192_out, not_193_out, not_194_out, not_195_out, not_196_out, not_197_out,
       not_198_out, not_199_out, not_200_out, not_201_out, not_202_out, not_203_out, not_204_out,
       not_205_out, not_206_out, not_207_out, not_208_out, not_209_out, not_210_out, not_211_out,
       not_212_out, not_213_out, not_214_out, not_215_out, not_216_out, not_217_out, not_218_out,
       not_219_out, not_220_out, not_221_out, not_222_out, not_223_out, not_224_out, not_225_out,
       not_226_out, not_227_out, not_228_out, not_229_out, not_230_out, not_231_out, not_232_out,
       not_233_out, not_234_out, not_235_out, not_236_out, not_237_out, not_238_out, not_239_out,
       not_240_out, not_241_out, not_242_out, not_243_out, not_244_out, not_245_out, not_246_out,
       not_247_out, not_248_out, not_249_out, not_250_out, not_251_out, not_252_out, not_253_out,
       not_254_out, not_255_out, not_256_out, not_257_out, not_258_out, not_259_out, not_260_out,
       not_261_out, not_262_out, not_263_out, not_264_out, not_265_out;

  not not_1 (not_1_out, OP2);
  not not_2 (not_2_out, OP3);
  not not_3 (not_3_out, OP4);
  not not_4 (not_4_out, OP5);
  not not_5 (not_5_out, OP6);
  not not_6 (not_6_out, F12);
  not not_7 (not_7_out, F13);
  not not_8 (not_8_out, OP2);
  not not_9 (not_9_out, OP3);
  not not_10 (not_10_out, OP4);
  not not_11 (not_11_out, OP5);
  not not_12 (not_12_out, OP6);
  not not_13 (not_13_out, F12);
  not not_14 (not_14_out, F14);
  not not_15 (not_15_out, OP2);
  not not_16 (not_16_out, OP3);
  not not_17 (not_17_out, OP4);
  not not_18 (not_18_out, OP6);
  not not_19 (not_19_out, F12);
  not not_20 (not_20_out, F14);
  not not_21 (not_21_out, OP2);
  not not_22 (not_22_out, OP3);
  not not_23 (not_23_out, OP5);
  not not_24 (not_24_out, OP6);
  not not_25 (not_25_out, F12);
  not not_26 (not_26_out, F13);
  not not_27 (not_27_out, OP2);
  not not_28 (not_28_out, OP3);
  not not_29 (not_29_out, OP4);
  not not_30 (not_30_out, OP6);
  not not_31 (not_31_out, F12);
  not not_32 (not_32_out, F14);
  not not_33 (not_33_out, OP2);
  not not_34 (not_34_out, OP3);
  not not_35 (not_35_out, OP5);
  not not_36 (not_36_out, OP6);
  not not_37 (not_37_out, F12);
  not not_38 (not_38_out, OP2);
  not not_39 (not_39_out, OP3);
  not not_40 (not_40_out, OP5);
  not not_41 (not_41_out, OP6);
  not not_42 (not_42_out, F13);
  not not_43 (not_43_out, F25);
  not not_44 (not_44_out, F30);
  not not_45 (not_45_out, OP2);
  not not_46 (not_46_out, OP3);
  not not_47 (not_47_out, OP5);
  not not_48 (not_48_out, OP6);
  not not_49 (not_49_out, F25);
  not not_50 (not_50_out, OP2);
  not not_51 (not_51_out, OP3);
  not not_52 (not_52_out, OP5);
  not not_53 (not_53_out, OP6);
  not not_54 (not_54_out, OP2);
  not not_55 (not_55_out, OP3);
  not not_56 (not_56_out, OP5);
  not not_57 (not_57_out, OP6);
  not not_58 (not_58_out, F12);
  not not_59 (not_59_out, F13);
  not not_60 (not_60_out, OP2);
  not not_61 (not_61_out, OP3);
  not not_62 (not_62_out, OP5);
  not not_63 (not_63_out, OP6);
  not not_64 (not_64_out, F12);
  not not_65 (not_65_out, F14);
  not not_66 (not_66_out, OP2);
  not not_67 (not_67_out, OP3);
  not not_68 (not_68_out, OP5);
  not not_69 (not_69_out, OP6);
  not not_70 (not_70_out, F12);
  not not_71 (not_71_out, OP2);
  not not_72 (not_72_out, OP3);
  not not_73 (not_73_out, OP5);
  not not_74 (not_74_out, OP6);
  not not_75 (not_75_out, F13);
  not not_76 (not_76_out, F25);
  not not_77 (not_77_out, F30);
  not not_78 (not_78_out, OP2);
  not not_79 (not_79_out, OP3);
  not not_80 (not_80_out, OP6);
  not not_81 (not_81_out, F12);
  not not_82 (not_82_out, F13);
  not not_83 (not_83_out, F14);
  not not_84 (not_84_out, F25);
  not not_85 (not_85_out, OP2);
  not not_86 (not_86_out, OP3);
  not not_87 (not_87_out, OP6);
  not not_88 (not_88_out, F12);
  not not_89 (not_89_out, F25);
  not not_90 (not_90_out, F30);
  not not_91 (not_91_out, OP2);
  not not_92 (not_92_out, OP3);
  not not_93 (not_93_out, OP5);
  not not_94 (not_94_out, OP6);
  not not_95 (not_95_out, F25);
  not not_96 (not_96_out, OP2);
  not not_97 (not_97_out, OP3);
  not not_98 (not_98_out, OP5);
  not not_99 (not_99_out, OP6);
  not not_100 (not_100_out, OP3);
  not not_101 (not_101_out, OP6);
  not not_102 (not_102_out, F25);
  not not_103 (not_103_out, F30);
  not not_104 (not_104_out, OP4);
  not not_105 (not_105_out, F12);
  not not_106 (not_106_out, F13);
  not not_107 (not_107_out, F14);
  not not_108 (not_108_out, OP3);
  not not_109 (not_109_out, OP6);
  not not_110 (not_110_out, OP4);
  not not_111 (not_111_out, OP2);
  not not_112 (not_112_out, OP3);
  not not_113 (not_113_out, F12);
  not not_114 (not_114_out, F13);
  not not_115 (not_115_out, F14);
  not not_116 (not_116_out, F25);
  not not_117 (not_117_out, F30);
  not not_118 (not_118_out, OP2);
  not not_119 (not_119_out, OP3);
  not not_120 (not_120_out, OP4);
  not not_121 (not_121_out, OP6);
  not not_122 (not_122_out, F12);
  not not_123 (not_123_out, F14);
  not not_124 (not_124_out, OP2);
  not not_125 (not_125_out, OP3);
  not not_126 (not_126_out, OP4);
  not not_127 (not_127_out, F12);
  not not_128 (not_128_out, F13);
  not not_129 (not_129_out, F14);
  not not_130 (not_130_out, OP2);
  not not_131 (not_131_out, OP3);
  not not_132 (not_132_out, OP4);
  not not_133 (not_133_out, F13);
  not not_134 (not_134_out, F14);
  not not_135 (not_135_out, OP3);
  not not_136 (not_136_out, OP4);
  not not_137 (not_137_out, F12);
  not not_138 (not_138_out, F13);
  not not_139 (not_139_out, F14);
  not not_140 (not_140_out, OP4);
  not not_141 (not_141_out, OP3);
  not not_142 (not_142_out, OP6);
  not not_143 (not_143_out, OP2);
  not not_144 (not_144_out, OP3);
  not not_145 (not_145_out, OP4);
  not not_146 (not_146_out, OP5);
  not not_147 (not_147_out, OP6);
  not not_148 (not_148_out, F12);
  not not_149 (not_149_out, F13);
  not not_150 (not_150_out, OP2);
  not not_151 (not_151_out, OP3);
  not not_152 (not_152_out, OP4);
  not not_153 (not_153_out, F13);
  not not_154 (not_154_out, OP2);
  not not_155 (not_155_out, OP3);
  not not_156 (not_156_out, OP5);
  not not_157 (not_157_out, OP6);
  not not_158 (not_158_out, F12);
  not not_159 (not_159_out, F13);
  not not_160 (not_160_out, OP2);
  not not_161 (not_161_out, OP3);
  not not_162 (not_162_out, OP4);
  not not_163 (not_163_out, OP6);
  not not_164 (not_164_out, F12);
  not not_165 (not_165_out, F14);
  not not_166 (not_166_out, OP3);
  not not_167 (not_167_out, OP4);
  not not_168 (not_168_out, F12);
  not not_169 (not_169_out, F13);
  not not_170 (not_170_out, F14);
  not not_171 (not_171_out, OP2);
  not not_172 (not_172_out, OP3);
  not not_173 (not_173_out, OP4);
  not not_174 (not_174_out, F13);
  not not_175 (not_175_out, OP2);
  not not_176 (not_176_out, OP3);
  not not_177 (not_177_out, OP5);
  not not_178 (not_178_out, OP6);
  not not_179 (not_179_out, F12);
  not not_180 (not_180_out, OP2);
  not not_181 (not_181_out, OP3);
  not not_182 (not_182_out, OP5);
  not not_183 (not_183_out, OP6);
  not not_184 (not_184_out, F13);
  not not_185 (not_185_out, F25);
  not not_186 (not_186_out, F30);
  not not_187 (not_187_out, OP2);
  not not_188 (not_188_out, OP3);
  not not_189 (not_189_out, OP6);
  not not_190 (not_190_out, F12);
  not not_191 (not_191_out, F13);
  not not_192 (not_192_out, F14);
  not not_193 (not_193_out, F25);
  not not_194 (not_194_out, OP2);
  not not_195 (not_195_out, OP3);
  not not_196 (not_196_out, OP6);
  not not_197 (not_197_out, F12);
  not not_198 (not_198_out, F25);
  not not_199 (not_199_out, F30);
  not not_200 (not_200_out, OP2);
  not not_201 (not_201_out, OP3);
  not not_202 (not_202_out, OP5);
  not not_203 (not_203_out, OP6);
  not not_204 (not_204_out, F25);
  not not_205 (not_205_out, OP2);
  not not_206 (not_206_out, OP3);
  not not_207 (not_207_out, OP5);
  not not_208 (not_208_out, OP6);
  not not_209 (not_209_out, OP2);
  not not_210 (not_210_out, OP3);
  not not_211 (not_211_out, F12);
  not not_212 (not_212_out, F13);
  not not_213 (not_213_out, F14);
  not not_214 (not_214_out, F25);
  not not_215 (not_215_out, F30);
  not not_216 (not_216_out, OP2);
  not not_217 (not_217_out, OP3);
  not not_218 (not_218_out, OP6);
  not not_219 (not_219_out, F25);
  not not_220 (not_220_out, F30);
  not not_221 (not_221_out, OP2);
  not not_222 (not_222_out, OP3);
  not not_223 (not_223_out, OP4);
  not not_224 (not_224_out, OP6);
  not not_225 (not_225_out, F12);
  not not_226 (not_226_out, F14);
  not not_227 (not_227_out, OP2);
  not not_228 (not_228_out, OP3);
  not not_229 (not_229_out, OP4);
  not not_230 (not_230_out, F13);
  not not_231 (not_231_out, F14);
  not not_232 (not_232_out, OP2);
  not not_233 (not_233_out, OP3);
  not not_234 (not_234_out, OP4);
  not not_235 (not_235_out, F13);
  not not_236 (not_236_out, OP2);
  not not_237 (not_237_out, OP3);
  not not_238 (not_238_out, OP6);
  not not_239 (not_239_out, F12);
  not not_240 (not_240_out, F13);
  not not_241 (not_241_out, F14);
  not not_242 (not_242_out, F25);
  not not_243 (not_243_out, OP2);
  not not_244 (not_244_out, OP3);
  not not_245 (not_245_out, OP6);
  not not_246 (not_246_out, F12);
  not not_247 (not_247_out, F25);
  not not_248 (not_248_out, F30);
  not not_249 (not_249_out, OP2);
  not not_250 (not_250_out, OP3);
  not not_251 (not_251_out, F12);
  not not_252 (not_252_out, F13);
  not not_253 (not_253_out, F14);
  not not_254 (not_254_out, F25);
  not not_255 (not_255_out, F30);
  not not_256 (not_256_out, OP2);
  not not_257 (not_257_out, OP3);
  not not_258 (not_258_out, OP6);
  not not_259 (not_259_out, F25);
  not not_260 (not_260_out, F30);
  not not_261 (not_261_out, OP2);
  not not_262 (not_262_out, OP3);
  not not_263 (not_263_out, F12);
  not not_264 (not_264_out, OP2);
  not not_265 (not_265_out, OP3);
  and and_1 (and_1_out, not_1_out, not_2_out, not_3_out, not_4_out, not_5_out, not_6_out, not_7_out, F14);
  and and_2 (and_2_out, not_8_out, not_9_out, not_10_out, not_11_out, not_12_out, not_13_out, F13, not_14_out);
  and and_3 (MemWrite, not_15_out, not_16_out, not_17_out, OP5, not_18_out, not_19_out, F13, not_20_out);
  and and_4 (and_4_out, not_21_out, not_22_out, not_23_out, not_24_out, not_25_out, not_26_out, F14);
  and and_5 (and_5_out, not_27_out, not_28_out, not_29_out, not_30_out, not_31_out, F13, not_32_out);
  and and_6 (and_6_out, not_33_out, not_34_out, OP4, not_35_out, not_36_out, not_37_out);
  and and_7 (and_7_out, not_38_out, not_39_out, OP4, not_40_out, not_41_out, not_42_out, not_43_out, not_44_out);
  and and_8 (and_8_out, not_45_out, not_46_out, OP4, not_47_out, not_48_out, F14, not_49_out);
  and and_9 (and_9_out, not_50_out, not_51_out, OP4, not_52_out, not_53_out, F13, F14);
  and and_10 (and_10_out, not_54_out, not_55_out, not_56_out, not_57_out, not_58_out, not_59_out, F14);
  and and_11 (and_11_out, not_60_out, not_61_out, not_62_out, not_63_out, not_64_out, F13, not_65_out);
  and and_12 (and_12_out, not_66_out, not_67_out, OP4, not_68_out, not_69_out, not_70_out);
  and and_13 (and_13_out, not_71_out, not_72_out, OP4, not_73_out, not_74_out, not_75_out, not_76_out, not_77_out);
  and and_14 (and_14_out, not_78_out, not_79_out, OP4, not_80_out, not_81_out, not_82_out, not_83_out, not_84_out);
  and and_15 (and_15_out, not_85_out, not_86_out, OP4, not_87_out, not_88_out, not_89_out, not_90_out);
  and and_16 (and_16_out, not_91_out, not_92_out, OP4, not_93_out, not_94_out, F14, not_95_out);
  and and_17 (and_17_out, not_96_out, not_97_out, OP4, not_98_out, not_99_out, F13, F14);
  and and_18 (and_18_out, not_100_out, OP4, OP5, not_101_out, F13, not_102_out, not_103_out);
  and and_19 (and_19_out, OP2, not_104_out, OP5, OP6, not_105_out, not_106_out, not_107_out);
  and and_20 (and_20_out, OP2, not_108_out, OP4, OP5, not_109_out);
  and and_21 (and_21_out, OP2, OP3, not_110_out, OP5, OP6);
  and and_22 (ecall, not_111_out, not_112_out, OP4, OP5, OP6, not_113_out, not_114_out, not_115_out, not_116_out, not_117_out);
  and and_23 (S_Type, not_118_out, not_119_out, not_120_out, OP5, not_121_out, not_122_out, F13, not_123_out);
  and and_24 (BEQ, not_124_out, not_125_out, not_126_out, OP5, OP6, not_127_out, not_128_out, not_129_out);
  and and_25 (BNE, not_130_out, not_131_out, not_132_out, OP5, OP6, F12, not_133_out, not_134_out);
  and and_26 (JALR, OP2, not_135_out, not_136_out, OP5, OP6, not_137_out, not_138_out, not_139_out);
  and and_27 (JAL, OP2, OP3, not_140_out, OP5, OP6);
  and and_28 (LUI, OP2, not_141_out, OP4, OP5, not_142_out);
  and and_29 (LBU, not_143_out, not_144_out, not_145_out, not_146_out, not_147_out, not_148_out, not_149_out, F14);
  and and_30 (BGE, not_150_out, not_151_out, not_152_out, OP5, OP6, F12, not_153_out, F14);
  and and_31 (and_31_out, not_154_out, not_155_out, not_156_out, not_157_out, not_158_out, not_159_out, F14);
  and and_32 (and_32_out, not_160_out, not_161_out, not_162_out, not_163_out, not_164_out, F13, not_165_out);
  and and_33 (and_33_out, not_166_out, not_167_out, OP5, OP6, not_168_out, not_169_out, not_170_out);
  and and_34 (and_34_out, not_171_out, not_172_out, not_173_out, OP5, OP6, F12, not_174_out);
  and and_35 (and_35_out, not_175_out, not_176_out, OP4, not_177_out, not_178_out, not_179_out);
  and and_36 (and_36_out, not_180_out, not_181_out, OP4, not_182_out, not_183_out, not_184_out, not_185_out, not_186_out);
  and and_37 (and_37_out, not_187_out, not_188_out, OP4, not_189_out, not_190_out, not_191_out, not_192_out, not_193_out);
  and and_38 (and_38_out, not_194_out, not_195_out, OP4, not_196_out, not_197_out, not_198_out, not_199_out);
  and and_39 (and_39_out, not_200_out, not_201_out, OP4, not_202_out, not_203_out, F14, not_204_out);
  and and_40 (and_40_out, not_205_out, not_206_out, OP4, not_207_out, not_208_out, F13, F14);
  and and_41 (and_41_out, not_209_out, not_210_out, OP4, OP5, not_211_out, not_212_out, not_213_out, not_214_out, not_215_out);
  and and_42 (and_42_out, not_216_out, not_217_out, OP4, OP5, not_218_out, F13, not_219_out, not_220_out);
  and and_43 (and_43_out, not_221_out, not_222_out, not_223_out, OP5, not_224_out, not_225_out, F13, not_226_out);
  and and_44 (and_44_out, not_227_out, not_228_out, not_229_out, OP5, OP6, not_230_out, not_231_out);
  and and_45 (and_45_out, not_232_out, not_233_out, not_234_out, OP5, OP6, F12, not_235_out);
  and and_46 (and_46_out, not_236_out, not_237_out, OP4, OP5, not_238_out, not_239_out, not_240_out, not_241_out, not_242_out);
  and and_47 (and_47_out, not_243_out, not_244_out, OP4, OP5, not_245_out, not_246_out, not_247_out, not_248_out);
  and and_48 (and_48_out, not_249_out, not_250_out, OP4, OP5, not_251_out, not_252_out, not_253_out, not_254_out, not_255_out);
  and and_49 (and_49_out, not_256_out, not_257_out, OP4, OP5, not_258_out, F13, not_259_out, not_260_out);
  and and_50 (CSRRSI, not_261_out, not_262_out, OP4, OP5, OP6, not_263_out, F13, F14);
  and and_51 (CSRRCI, not_264_out, not_265_out, OP4, OP5, OP6, F12, F13, F14);
  or or_1 (MemToReg, and_1_out, and_2_out);
  or or_2 (ALU_SRC, and_4_out, and_5_out, and_6_out, and_7_out, and_8_out, and_9_out);
  or or_3 (rs2, and_43_out, and_44_out, and_45_out, and_46_out, and_47_out, and_48_out, and_49_out);
  or or_4 (RegWrite, and_10_out, and_11_out, and_12_out, and_13_out, and_14_out, and_15_out, and_16_out, and_17_out, and_18_out, and_19_out, and_20_out, and_21_out);
  or or_5 (rs1, and_31_out, and_32_out, and_33_out, and_34_out, and_35_out, and_36_out, and_37_out, and_38_out, and_39_out, and_40_out, and_41_out, and_42_out);
endmodule

// ALU
module ALU (
  input  [31:0] X,
  input  [31:0] Y,
  input  [3:0] AluOP,
  output out_4,
  output Equal,
  output out_6,
  output [31:0] Result,
  output [31:0] Result_2
);

  wire [0:0] comparator_2_lt;
  wire [31:0] adder_1_out, AND_out, divider_1_out, divider_1_rem, multiplier_1_cout, multiplier_1_out,
       NOR_out, OR_out, shifter_1_out, shifter_2_out, shifter_3_out, subtractor_1_out, XOR_out;

  assign AND_out = X & Y;  // AND_Gate AND, 32 bits wide
  assign OR_out = X | Y;  // OR_Gate OR, 32 bits wide
  Shifter #(.width(32), .shift("ll")) shifter_1 (.in(X), .\dist (Y[4:0]), .out(shifter_1_out));
  Shifter #(.width(32), .shift("ar")) shifter_2 (.in(X), .\dist (Y[4:0]), .out(shifter_2_out));
  Shifter #(.width(32), .shift("lr")) shifter_3 (.in(X), .\dist (Y[4:0]), .out(shifter_3_out));
  Multiplier #(.width(32)) multiplier_1 (.a(X), .b(Y), .out(multiplier_1_out), .cout(multiplier_1_cout));  // open: cin
  Divider #(.width(32)) divider_1 (.a(X), .b(Y), .out(divider_1_out), .rem(divider_1_rem));  // open: upper
  Adder #(.width(32)) adder_1 (.a(X), .b(Y), .out(adder_1_out));  // open: cin, cout
  Subtractor #(.width(32)) subtractor_1 (.a(X), .b(Y), .out(subtractor_1_out));  // open: bin, bout
  assign XOR_out = X ^ Y;  // XOR_Gate XOR, 32 bits wide
  assign NOR_out = ~(X | Y);  // NOR_Gate NOR, 32 bits wide
  Comparator #(.width(32), .mode("twosComplement")) comparator_1 (.a(X), .b(Y), .eq(Equal), .lt(out_6));  // open: gt
  Comparator #(.width(32), .mode("unsigned")) comparator_2 (.a(X), .b(Y), .lt(comparator_2_lt[0]));  // open: gt, eq
  Multiplexer #(.select(4), .width(32), .disabled("Z"), .enable("false")) multiplexer_1 (
    .in0(shifter_1_out), .in1(shifter_2_out), .in2(shifter_3_out), .in3(multiplier_1_out),
    .in4(divider_1_out), .in5(adder_1_out), .in6(subtractor_1_out), .in7(AND_out), .in8(OR_out),
    .in9(XOR_out), .in10(NOR_out), .in11({{31{1'b0}}, out_6}), .in12({{31{1'b0}}, comparator_2_lt[0]}),
    .in13({32{1'b0}}), .in14({32{1'b0}}), .in15({32{1'b0}}), .out(Result), .sel(AluOP));
  Multiplexer #(.select(4), .width(32), .disabled("Z"), .enable("false")) multiplexer_2 (
    .in0({32{1'b0}}), .in1({32{1'b0}}), .in2({32{1'b0}}), .in3(multiplier_1_cout), .in4(divider_1_rem),
    .in5({32{1'b0}}), .in6({32{1'b0}}), .in7({32{1'b0}}), .in8({32{1'b0}}), .in9({32{1'b0}}),
    .in10({32{1'b0}}), .in11({32{1'b0}}), .in12({32{1'b0}}), .in13({32{1'b0}}), .in14({32{1'b0}}),
    .in15({32{1'b0}}), .out(Result_2), .sel(AluOP));
  Multiplexer #(.select(4), .width(1), .disabled("Z"), .enable("false")) multiplexer_3 (
    .in0(1'b0), .in1(1'b0), .in2(1'b0), .in3(1'b0), .in4(1'b0), .in5(1'b0), .in6(1'b0), .in7(1'b0),
    .in8(1'b0), .in9(1'b0), .in10(1'b0), .in11(out_6), .in12(comparator_2_lt[0]), .in13(1'b0), .in14(1'b0),
    .in15(1'b0), .sel(AluOP));  // open: out
  not not_1 (out_4, out_6);

  // Other names for the same wires on the sheet: tunnel = out_6; Result2[31:0] = Result_2; S[3:0] = AluOP;
  //   tunnel_t = out_4

  // Notes on the sheet:
  //   不要改变此引脚区域内容，也不要改变ALU封装形式
  //   输入引脚
  //   输出引脚
endmodule

module Regifile (
  input  [31:0] Din,
  input  Clk,
  input  WE,
  input  [4:0] R1_num,
  input  [4:0] W_num,
  input  [4:0] R2_num,
  output [31:0] R1,
  output [31:0] R2
);

  // RegisterFile registerfile_1: pin names not known; wires that end beside it: Din, Clk, WE, W_num, R1_num, R2_num, R1, R2
endmodule

module \理想流水线  (
  output RegWrite,
  output MemWrite,
  output [31:0] IF_PC,
  output [31:0] ID_PC,
  output [31:0] EX_PC,
  output [31:0] M_PC,
  output [31:0] WB_PC,
  output [31:0] RDin,
  output [31:0] MDin,
  output [31:0] LedData
);

  wire alu_1_equal, alu_1_out_4, and_1_out, and_2_out, and_3_out, and_4_out, Bge, bjump, CLK, clock_1_out,
       clock_2_out, comparator_1_eq, comparator_1_lt, d_ff_1_q, Ecall, Equal, Go, halt, IR1, IR2, IR3, J,
       Jal, Jalr, Lbu, Lui, nand_1_out, not_1_out, not_2_out, not_3_out, RST, S, W1, W2, W3,
       \单周期硬布线控制器_1_alu_src , \单周期硬布线控制器_1_beq , \单周期硬布线控制器_1_bne , \单周期硬布线控制器_1_ecall ,
       \单周期硬布线控制器_1_memtoreg , \单周期硬布线控制器_1_memwrite , \单周期硬布线控制器_1_regwrite , \理想流水线ex_mem_1_ex_lbu ,
       \理想流水线ex_mem_1_ex_lui , \理想流水线ex_mem_1_mem_ecall , \理想流水线ex_mem_1_mem_equal , \理想流水线ex_mem_1_mem_jal ,
       \理想流水线ex_mem_1_mem_jalr , \理想流水线ex_mem_1_mem_memtoreg , \理想流水线ex_mem_1_mem_regwrite ,
       \理想流水线id_ex_1_ex_alusrcb , \理想流水线id_ex_1_ex_beq , \理想流水线id_ex_1_ex_bge , \理想流水线id_ex_1_ex_bne ,
       \理想流水线id_ex_1_ex_ecall , \理想流水线id_ex_1_ex_jal , \理想流水线id_ex_1_ex_jalr , \理想流水线id_ex_1_ex_lbu ,
       \理想流水线id_ex_1_ex_lui , \理想流水线id_ex_1_ex_memtoreg , \理想流水线id_ex_1_ex_memwrite ,
       \理想流水线id_ex_1_ex_regwrite , \理想流水线mem_wb_1_wb_jal , \理想流水线mem_wb_1_wb_jalr , \理想流水线mem_wb_1_wb_lui ;
  wire [3:0] \单周期硬布线控制器_1_alu_op , \理想流水线id_ex_1_ex_aluop ;
  wire [4:0] bit_extender_5_out, minus, multiplexer_1_out, multiplexer_2_out, subtractor_1_out, WB_rd,
       \理想流水线ex_mem_1_mem_rd , \理想流水线id_ex_1_ex_rd ;
  wire [9:0] \理想流水线ex_mem_1_mem_calc_2 ;
  wire [11:0] multiplexer_3_out;
  wire [12:0] CNT_num;
  wire [15:0] \LoadUse次数 , \总周期数 , \插入气泡数 , \无条件分支数 , \条件分支成功数 ;
  wire [31:0] adder_1_out, adder_3_out, alu_1_result, bAddr, bAddri, bit_extender_1_out, bit_extender_2_out,
       bit_extender_3_out, bit_extender_4_out, EX_IR, ID_IR, IF_IR, jAddr, LedShow, MEM_IR,
       multiplexer_4_out, multiplexer_5_out, multiplexer_6_out, multiplexer_7_out, multiplexer_8_out,
       ram_1_data, regifile_1_r1, regifile_1_r2, shifter_1_out, shifter_2_out, shifter_3_out, shifter_4_out,
       shifter_6_out, WB_IR, \流水线pc计算_1_npc , \理想流水线ex_mem_1_ex_imm_jal , \理想流水线ex_mem_1_ex_imm_lui ,
       \理想流水线ex_mem_1_mem_calc , \理想流水线id_ex_1_ex_a , \理想流水线id_ex_1_ex_imm , \理想流水线id_ex_1_ex_imm_jal ,
       \理想流水线id_ex_1_ex_imm_lui , \理想流水线mem_wb_1_wb_calc_mdout , \理想流水线mem_wb_1_wb_imm_jal ,
       \理想流水线mem_wb_1_wb_imm_lui ;

  Button \u_总复位  (.out(RST));
  Button _1 (.out(IR1));
  Button _2 (.out(IR2));
  Button _3 (.out(IR3));
  // Probe on \总周期数 
  // Probe on \总周期数 
  Button \u_继续运行  (.out(Go));
  LED #(.active("true")) led_1 (.in(W1));
  LED #(.active("true")) led_2 (.in(W2));
  LED #(.active("true")) led_3 (.in(W3));
  Hex_Digit_Display hex_digit_display_1 (.value(LedData[31:28]));  // open: dp
  // Probe on IF_PC[19:0]
  // RiscV_Probe riscv_probe_1: pin names not known; wires that end beside it: IF_IR
  Register #(.width(32), .trigger("rising"), .Select("low")) PC (
    .D(\流水线pc计算_1_npc ), .en(halt), .Q(IF_PC), .clk(CLK), .clr(RST));
  Hex_Digit_Display hex_digit_display_2 (.value(LedData[27:24]));  // open: dp
  Hex_Digit_Display hex_digit_display_3 (.value(LedData[23:20]));  // open: dp
  // Probe on ID_PC[19:0]
  // RiscV_Probe riscv_probe_2: pin names not known; wires that end beside it: ID_IR
  Adder #(.width(32)) adder_1 (.a(IF_PC), .b(32'h4), .out(adder_1_out));  // open: cin, cout
  \流水线PC计算  \u_流水线pc计算_1  (
    .bJump(bjump), .J(J), .PC_4(adder_1_out), .bAddr(bAddr), .jAddr(jAddr), .NPC(\流水线pc计算_1_npc ));
  Hex_Digit_Display hex_digit_display_4 (.value(LedData[15:12]));  // open: dp
  Hex_Digit_Display hex_digit_display_5 (.value(LedData[19:16]));  // open: dp
  Hex_Digit_Display hex_digit_display_6 (.value(LedData[7:4]));  // open: dp
  Hex_Digit_Display hex_digit_display_7 (.value(LedData[11:8]));  // open: dp
  Clock #(.highDuration(1), .lowDuration(1)) clock_1 (.out(clock_1_out));
  // Probe on EX_PC[19:0]
  // RiscV_Probe riscv_probe_3: pin names not known; wires that end beside it: clock_1_out, EX_IR, CLK
  ROM #(.addrWidth(10), .dataWidth(32), .Select("high")) rom_1 (.addr(IF_PC[11:2]), .data(IF_IR));
  Hex_Digit_Display hex_digit_display_8 (.value(LedData[3:0]));  // open: dp
  \理想流水线IF_ID  \u_理想流水线if_id_1  (
    .IF_PC(IF_PC), .IF_IR(IF_IR), .clk(CLK), .halt(halt), .ID_PC(ID_PC), .ID_IR(ID_IR), .rst(RST));
  // Probe on \总周期数 
  // Probe on M_PC[19:0]
  // RiscV_Probe riscv_probe_4: pin names not known; wires that end beside it: MEM_IR
  // Probe on \总周期数 
  // Probe on \无条件分支数 
  // Probe on \条件分支成功数 
  // Probe on \插入气泡数 
  // Probe on \LoadUse次数 
  \单周期硬布线控制器  \u_单周期硬布线控制器_1  (
    .Funct({ID_IR[30], ID_IR[25], ID_IR[14:12]}), .OP(ID_IR[6:2]), .ALU_OP(\单周期硬布线控制器_1_alu_op ),
    .MemToReg(\单周期硬布线控制器_1_memtoreg ), .MemWrite(\单周期硬布线控制器_1_memwrite ), .ALU_SRC(\单周期硬布线控制器_1_alu_src ),
    .RegWrite(\单周期硬布线控制器_1_regwrite ), .ecall(\单周期硬布线控制器_1_ecall ), .S_type(S), .Jalr(Jalr),
    .Beq(\单周期硬布线控制器_1_beq ), .JAL(Jal), .Bne(\单周期硬布线控制器_1_bne ), .Lui(Lui), .Lbu(Lbu), .Bge(Bge));  // open: rs1, rs2, uret, IR21, csrrsi, csrrci
  assign bit_extender_1_out = {{12{ID_IR[31]}}, ID_IR[31:12]};  // Bit_Extender bit_extender_1
  // Probe on IF_PC[11:0]
  // Probe on WB_PC[19:0]
  // RiscV_Probe riscv_probe_5: pin names not known; wires that end beside it: WB_IR
  Multiplexer #(.select(1), .width(5), .disabled("Z"), .enable("false")) multiplexer_1 (
    .in0(ID_IR[19:15]), .in1(5'b10001), .out(multiplexer_1_out), .sel(\单周期硬布线控制器_1_ecall ));
  Multiplexer #(.select(1), .width(5), .disabled("Z"), .enable("false")) multiplexer_2 (
    .in0(ID_IR[24:20]), .in1(5'b01010), .out(multiplexer_2_out), .sel(\单周期硬布线控制器_1_ecall ));
  Shifter #(.width(32), .shift("ll")) shifter_1 (.in(bit_extender_1_out), .\dist (5'b01100), .out(shifter_1_out));
  assign bit_extender_2_out = {{12{ID_IR[31]}}, {ID_IR[31], ID_IR[19:12], ID_IR[20], ID_IR[30:21]}};  // Bit_Extender bit_extender_2
  Counter #(.width(16), .max('hffff), .ongoal("wrap"), .trigger("rising"), .behavior("old")) counter_1 (
    .count(halt), .Q(\总周期数 ), .clk(CLK));  // open: load, D, carry, clr, preset
  // Probe on ID_PC[11:0]
  // Probe on EX_PC[11:0]
  Regifile regifile_1 (
    .Din(RDin), .Clk(CLK), .R1(regifile_1_r1), .R2(regifile_1_r2), .WE(RegWrite), .W_num(WB_rd),
    .R1_num(multiplexer_1_out), .R2_num(multiplexer_2_out));
  Multiplexer #(.select(1), .width(12), .disabled("Z"), .enable("false")) multiplexer_3 (
    .in0(ID_IR[31:20]), .in1({ID_IR[31:25], ID_IR[11:7]}), .out(multiplexer_3_out), .sel(S));
  assign bit_extender_3_out = {{20{multiplexer_3_out[11]}}, multiplexer_3_out};  // Bit_Extender bit_extender_3
  assign bit_extender_4_out = {{20{ID_IR[31]}}, {ID_IR[31], ID_IR[7], ID_IR[30:25], ID_IR[11:8]}};  // Bit_Extender bit_extender_4
  Shifter #(.width(32), .shift("ll")) shifter_2 (.in(bit_extender_2_out), .\dist (5'b00001), .out(shifter_2_out));
  // Probe on M_PC[11:0]
  D_Flip_Flop #(.trigger("high"), .Pre_Clr_Positions("LEGACY"), .NegatePresetClear("false"), .enable("true"), .NewFFLayout("false")) d_ff_1 (.Q(d_ff_1_q));  // open: clk, D, Qn, preset, en, reset
  // Probe on 13'hc
  Shifter #(.width(32), .shift("ll")) shifter_3 (.in(bit_extender_4_out), .\dist (5'b00001), .out(shifter_3_out));
  and and_1 (and_1_out, halt, J);
  // Probe on WB_PC[11:0]
  Comparator #(.width(13), .mode("twosComplement")) comparator_1 (
    .a(CNT_num), .b(13'hc), .eq(comparator_1_eq), .lt(comparator_1_lt));  // open: gt
  Clock #(.highDuration(1), .lowDuration(1)) clock_2 (.out(clock_2_out));
  Counter #(.width(16), .max('hffff), .ongoal("wrap"), .trigger("rising"), .behavior("old")) counter_2 (
    .count(and_1_out), .Q(\无条件分支数 ), .clk(CLK));  // open: load, D, carry, clr, preset
  nand nand_1 (nand_1_out, d_ff_1_q, comparator_1_eq);
  Counter #(.width(13), .max('h1fff), .ongoal("stay"), .trigger("rising"), .behavior("old")) counter_3 (
    .count(comparator_1_lt), .Q(CNT_num), .clk(clock_2_out));  // open: load, D, carry, clr, preset
  \理想流水线ID_EX  \u_理想流水线id_ex_1  (
    .ID_PC(ID_PC), .ID_MemToReg(\单周期硬布线控制器_1_memtoreg ), .ID_MemWrite(\单周期硬布线控制器_1_memwrite ),
    .ID_AluOP(\单周期硬布线控制器_1_alu_op ), .ID_AluSrcB(\单周期硬布线控制器_1_alu_src ), .ID_Ecall(\单周期硬布线控制器_1_ecall ),
    .ID_R1(regifile_1_r1), .ID_R2(regifile_1_r2), .ID_imm(bit_extender_3_out), .clk(CLK), .halt(halt),
    .EX_PC(EX_PC), .EX_MemToReg(\理想流水线id_ex_1_ex_memtoreg ), .EX_MemWrite(\理想流水线id_ex_1_ex_memwrite ),
    .EX_AluOP(\理想流水线id_ex_1_ex_aluop ), .EX_AluSrcB(\理想流水线id_ex_1_ex_alusrcb ),
    .EX_Ecall(\理想流水线id_ex_1_ex_ecall ), .EX_A(\理想流水线id_ex_1_ex_a ), .EX_B(LedShow),
    .EX_imm(\理想流水线id_ex_1_ex_imm ), .rst(RST), .ID_IR(ID_IR), .EX_IR(EX_IR), .ID_Beq(\单周期硬布线控制器_1_beq ),
    .EX_Beq(\理想流水线id_ex_1_ex_beq ), .ID_Bne(\单周期硬布线控制器_1_bne ), .EX_Bne(\理想流水线id_ex_1_ex_bne ),
    .ID_RegWrite(\单周期硬布线控制器_1_regwrite ), .EX_RegWrite(\理想流水线id_ex_1_ex_regwrite ), .ID_rd(ID_IR[11:7]),
    .EX_rd(\理想流水线id_ex_1_ex_rd ), .ID_Jal(Jal), .ID_Jalr(Jalr), .EX_Jal(\理想流水线id_ex_1_ex_jal ),
    .EX_Jalr(\理想流水线id_ex_1_ex_jalr ), .ID_Bge(Bge), .EX_Bge(\理想流水线id_ex_1_ex_bge ),
    .ID_imm_Lui(shifter_1_out), .EX_imm_Lui(\理想流水线id_ex_1_ex_imm_lui ), .ID_Lui(Lui),
    .EX_Lui(\理想流水线id_ex_1_ex_lui ), .ID_Lbu(Lbu), .EX_Lbu(\理想流水线id_ex_1_ex_lbu ), .ID_imm_Jal(shifter_2_out),
    .EX_imm_Jal(\理想流水线id_ex_1_ex_imm_jal ), .ID_imm_B(shifter_3_out), .EX_imm_B(bAddri));
  assign CLK = nand_1_out ? clock_2_out : 1'bz;  // Controlled_Buffer controlled_buffer_1
  Multiplexer #(.select(1), .width(32), .disabled("Z"), .enable("false")) multiplexer_4 (
    .in0(LedShow), .in1(\理想流水线id_ex_1_ex_imm ), .out(multiplexer_4_out), .sel(\理想流水线id_ex_1_ex_alusrcb ));
  and and_2 (and_2_out, halt, bjump);
  Pull_Resistor #(.pull(1)) pull_resistor_1 (.node(CLK));
  Multiplexer #(.select(1), .width(32), .disabled("Z"), .enable("false")) multiplexer_5 (
    .in0(multiplexer_4_out), .in1(32'ha), .out(multiplexer_5_out), .sel(\理想流水线id_ex_1_ex_ecall ));
  Counter #(.width(16), .max('hffff), .ongoal("wrap"), .trigger("rising"), .behavior("old")) counter_4 (
    .count(and_2_out), .Q(\条件分支成功数 ), .clk(CLK));  // open: load, D, carry, clr, preset
  ALU alu_1 (
    .X(\理想流水线id_ex_1_ex_a ), .Y(multiplexer_5_out), .AluOP(\理想流水线id_ex_1_ex_aluop ), .Equal(alu_1_equal),
    .Result(alu_1_result), .out_4(alu_1_out_4));  // open: Result_2, out_6
  \条件分支逻辑设计  \u_条件分支逻辑设计_1  (
    .Bge(\理想流水线id_ex_1_ex_bge ), .in_4(alu_1_equal), .Beq(\理想流水线id_ex_1_ex_beq ), .in_2(alu_1_out_4),
    .Bne(\理想流水线id_ex_1_ex_bne ), .branchtaken(bjump));
  Adder #(.width(32)) adder_2 (.a(bAddri), .b(EX_PC), .out(bAddr));  // open: cin, cout
  \理想流水线EX_MEM  \u_理想流水线ex_mem_1  (
    .EX_PC(EX_PC), .EX_MemToReg(\理想流水线id_ex_1_ex_memtoreg ), .EX_MemWrite(\理想流水线id_ex_1_ex_memwrite ),
    .EX_MDin(LedShow), .EX_Calc(alu_1_result), .clk(CLK), .halt(halt), .MEM_PC(M_PC),
    .MEM_MemToReg(\理想流水线ex_mem_1_mem_memtoreg ), .MEM_MemWrite(MemWrite), .MEM_MDin(MDin),
    .MEM_Calc({\理想流水线ex_mem_1_mem_calc [31:12], \理想流水线ex_mem_1_mem_calc_2 , \理想流水线ex_mem_1_mem_calc [1:0]}),
    .rst(RST), .EX_IR(EX_IR), .MEM_IR(MEM_IR), .EX_RegWrite(\理想流水线id_ex_1_ex_regwrite ),
    .MEM_RegWrite(\理想流水线ex_mem_1_mem_regwrite ), .EX_rd(\理想流水线id_ex_1_ex_rd ),
    .Mem_Rd(\理想流水线ex_mem_1_mem_rd ), .EX_Ecall(\理想流水线id_ex_1_ex_ecall ),
    .MEM_Ecall(\理想流水线ex_mem_1_mem_ecall ), .EX_Equal(alu_1_equal), .MEM_Equal(\理想流水线ex_mem_1_mem_equal ),
    .EX_Jal(\理想流水线id_ex_1_ex_jal ), .MEM_Jal(\理想流水线ex_mem_1_mem_jal ), .EX_Jalr(\理想流水线id_ex_1_ex_jalr ),
    .MEM_Jalr(\理想流水线ex_mem_1_mem_jalr ), .ID_imm_Jal(\理想流水线id_ex_1_ex_imm_jal ),
    .EX_imm_Jal(\理想流水线ex_mem_1_ex_imm_jal ), .ID_Lui(\理想流水线id_ex_1_ex_lui ), .EX_Lui(\理想流水线ex_mem_1_ex_lui ),
    .ID_Lbu(\理想流水线id_ex_1_ex_lbu ), .EX_Lbu(\理想流水线ex_mem_1_ex_lbu ), .ID_imm_Lui(\理想流水线id_ex_1_ex_imm_lui ),
    .EX_imm_Lui(\理想流水线ex_mem_1_ex_imm_lui ));
  not not_1 (not_1_out, MemWrite);
  RAM #(.addrWidth(10), .dataWidth(32), .bus("separate"), .Select("high")) ram_1 (
    .addr(\理想流水线ex_mem_1_mem_calc_2 ), .din(MDin), .data(ram_1_data), .str(MemWrite), .clk(CLK),
    .ld(not_1_out));  // open: sel, clr
  Multiplexer #(.select(1), .width(32), .disabled("Z"), .enable("false")) multiplexer_6 (
    .in0({\理想流水线ex_mem_1_mem_calc [31:12], \理想流水线ex_mem_1_mem_calc_2 , \理想流水线ex_mem_1_mem_calc [1:0]}),
    .in1(ram_1_data), .out(multiplexer_6_out), .sel(\理想流水线ex_mem_1_mem_memtoreg ));
  Subtractor #(.width(5)) subtractor_1 (.a(5'b11000), .b(minus), .out(subtractor_1_out));  // open: bin, bout
  assign bit_extender_5_out = {{3{1'b0}}, \理想流水线ex_mem_1_mem_calc [1:0]};  // Bit_Extender bit_extender_5
  Shifter #(.width(32), .shift("ll")) shifter_4 (
    .in(multiplexer_6_out), .\dist (subtractor_1_out), .out(shifter_4_out));
  Shifter #(.width(5), .shift("ll")) shifter_5 (.in(bit_extender_5_out), .\dist (3'b011), .out(minus));
  Shifter #(.width(32), .shift("lr")) shifter_6 (.in(shifter_4_out), .\dist (5'b11000), .out(shifter_6_out));
  Multiplexer #(.select(1), .width(32), .disabled("Z"), .enable("false")) multiplexer_7 (
    .in0(multiplexer_6_out), .in1(shifter_6_out), .out(multiplexer_7_out), .sel(\理想流水线ex_mem_1_ex_lbu ));
  \理想流水线MEM_WB  \u_理想流水线mem_wb_1  (
    .MEM_PC(M_PC), .MEM_IR(MEM_IR), .MEM_Lui(\理想流水线ex_mem_1_ex_lui ),
    .MEM_RegWrite(\理想流水线ex_mem_1_mem_regwrite ), .MEM_Jal(\理想流水线ex_mem_1_mem_jal ),
    .MEM_Jalr(\理想流水线ex_mem_1_mem_jalr ), .Mem_Clac_MDout(multiplexer_7_out),
    .MEM_imm_Jal(\理想流水线ex_mem_1_ex_imm_jal ), .MEM_Rd(\理想流水线ex_mem_1_mem_rd ),
    .MEM_imm_Lui(\理想流水线ex_mem_1_ex_imm_lui ), .clk(CLK), .halt(halt), .WB_PC(WB_PC), .WB_IR(WB_IR),
    .WB_Lui(\理想流水线mem_wb_1_wb_lui ), .WB_RegWrite(RegWrite), .WB_Jal(\理想流水线mem_wb_1_wb_jal ),
    .WB_Jalr(\理想流水线mem_wb_1_wb_jalr ), .WB_Calc_MDout(\理想流水线mem_wb_1_wb_calc_mdout ),
    .WB_imm_Jal(\理想流水线mem_wb_1_wb_imm_jal ), .WB_Rd(WB_rd), .WB_imm_Lui(\理想流水线mem_wb_1_wb_imm_lui ),
    .rst(RST), .MEM_Equal(\理想流水线ex_mem_1_mem_equal ), .WB_Equal(Equal),
    .MEM_Ecall(\理想流水线ex_mem_1_mem_ecall ), .WB_Ecall(Ecall));
  Adder #(.width(32)) adder_3 (.a(WB_PC), .b(32'h4), .out(adder_3_out));  // open: cin, cout
  Multiplexer #(.select(1), .width(32), .disabled("Z"), .enable("false")) multiplexer_8 (
    .in0(\理想流水线mem_wb_1_wb_calc_mdout ), .in1(\理想流水线mem_wb_1_wb_imm_lui ), .out(multiplexer_8_out),
    .sel(\理想流水线mem_wb_1_wb_lui ));
  not not_2 (not_2_out, Equal);
  or or_1 (J, \理想流水线mem_wb_1_wb_jal , \理想流水线mem_wb_1_wb_jalr );
  Multiplexer #(.select(1), .width(32), .disabled("Z"), .enable("false")) multiplexer_9 (
    .in0(multiplexer_8_out), .in1(adder_3_out), .out(RDin), .sel(J));
  not not_3 (not_3_out, and_3_out);
  and and_3 (and_3_out, Ecall, Equal);
  and and_4 (and_4_out, Ecall, not_2_out);
  or or_2 (halt, Go, not_3_out);
  Register #(.width(32), .trigger("rising"), .Select("low")) register_1 (
    .D(LedShow), .en(and_4_out), .Q(LedData), .clk(CLK));  // open: clr
  \无条件跳转逻辑设计  \u_无条件跳转逻辑设计_1  (
    .JAL(\理想流水线mem_wb_1_wb_jal ), .JALR(\理想流水线mem_wb_1_wb_jalr ), .JALR_Addr(\理想流水线mem_wb_1_wb_calc_mdout ),
    .JAL_Addr(\理想流水线mem_wb_1_wb_imm_jal ), .J_Addr(jAddr), .PC(WB_PC));

  // Other names for the same wires on the sheet: rd[4:0] = ID_IR[11:7]; MEM_PC[31:0] = M_PC

  // Notes on the sheet:
  //   中断源
  //   时空图监测，可删除
  //   中断等待指示
  //   最后在气泡流水线电路中修改为正确模式
  //   该电路采用异步清零的方式处理分支跳转指令，这种方式是错误的
  //   数码管输出
  //   指令存储器
  //   contents of rom_1 (hex, n*v repeats v):
  //   413 493 913 993 46413 14e493 296913 39e993 842023 942223 1242423 1342623 a00893 493 913 993 73
  //   rs1
  //   rs2
  //   rd
  //   imm20 LUI
  //   imm20 Jal
  //   imm12 I
  //   imm12 S
  //   控制位
  //   流水调试日志用
  //   暂停节拍，不能为0
  //   戳工具置1进入计数暂停模式，ctrl+k时钟自动运行到对应节拍暂停
  //   ctrl+k关闭时钟连续运行，将控制位置零，进入单步调试模式调试
  //   用这个时钟源需要去掉电路中的其他时钟源
  //   周期数、分支数记录
  //   可计数暂停的时钟源
  //   为方便自动评测，需要输出流水线各段保存的PC值，注意是PC不是PC+4，另外ID段寄存器写入信息，Mem段内存写入信息也要输出
  //   数据存储器
  //   Ecall选项
endmodule

// IF/ID
module \理想流水线IF_ID  (
  input  [31:0] IF_PC,
  input  [31:0] IF_IR,
  input  clk,
  input  rst,
  input  halt,
  output [31:0] ID_PC,
  output [31:0] ID_IR
);

  Register #(.width(32), .trigger("rising"), .Select("low")) PC (.D(IF_PC), .en(halt), .Q(ID_PC), .clk(clk), .clr(rst));
  Register #(.width(32), .trigger("rising"), .Select("low")) IR (.D(IF_IR), .en(halt), .Q(ID_IR), .clk(clk), .clr(rst));
endmodule

// ID/EX
module \理想流水线ID_EX  (
  input  [31:0] ID_PC,
  input  [31:0] ID_IR,
  input  ID_Bge,
  input  ID_Beq,
  input  ID_Bne,
  input  ID_MemToReg,
  input  ID_MemWrite,
  input  [3:0] ID_AluOP,
  input  ID_AluSrcB,
  input  ID_RegWrite,
  input  ID_Jal,
  input  ID_Jalr,
  input  [4:0] ID_rd,
  input  ID_Ecall,
  input  [31:0] ID_R1,
  input  [31:0] ID_R2,
  input  [31:0] ID_imm,
  input  [31:0] ID_imm_B,
  input  [31:0] ID_imm_Jal,
  input  ID_Lui,
  input  ID_Lbu,
  input  [31:0] ID_imm_Lui,
  input  clk,
  input  rst,
  input  halt,
  output [31:0] EX_PC,
  output [31:0] EX_IR,
  output EX_Bge,
  output EX_Beq,
  output EX_Bne,
  output EX_MemToReg,
  output EX_MemWrite,
  output [3:0] EX_AluOP,
  output EX_AluSrcB,
  output EX_RegWrite,
  output EX_Jal,
  output EX_Jalr,
  output [4:0] EX_rd,
  output EX_Ecall,
  output [31:0] EX_A,
  output [31:0] EX_B,
  output [31:0] EX_imm,
  output [31:0] EX_imm_B,
  output [31:0] EX_imm_Jal,
  output EX_Lui,
  output EX_Lbu,
  output [31:0] EX_imm_Lui
);

  Register #(.width(32), .trigger("rising"), .Select("low")) register_1 (
    .D(ID_PC), .en(halt), .Q(EX_PC), .clk(clk), .clr(rst));
  Register #(.width(32), .trigger("rising"), .Select("low")) register_2 (
    .D(ID_IR), .en(halt), .Q(EX_IR), .clk(clk), .clr(rst));
  Register #(.width(1), .trigger("rising"), .Select("low")) register_3 (
    .D(ID_Bge), .en(halt), .Q(EX_Bge), .clk(clk), .clr(rst));
  Register #(.width(1), .trigger("rising"), .Select("low")) register_4 (
    .D(ID_Beq), .en(halt), .Q(EX_Beq), .clk(clk), .clr(rst));
  Register #(.width(1), .trigger("rising"), .Select("low")) register_5 (
    .D(ID_Bne), .en(halt), .Q(EX_Bne), .clk(clk), .clr(rst));
  Register #(.width(1), .trigger("rising"), .Select("low")) register_6 (
    .D(ID_MemToReg), .en(halt), .Q(EX_MemToReg), .clk(clk), .clr(rst));
  Register #(.width(1), .trigger("rising"), .Select("low")) register_7 (
    .D(ID_MemWrite), .en(halt), .Q(EX_MemWrite), .clk(clk), .clr(rst));
  Register #(.width(4), .trigger("rising"), .Select("low")) register_8 (
    .D(ID_AluOP), .en(halt), .Q(EX_AluOP), .clk(clk), .clr(rst));
  Register #(.width(1), .trigger("rising"), .Select("low")) register_9 (
    .D(ID_AluSrcB), .en(halt), .Q(EX_AluSrcB), .clk(clk), .clr(rst));
  Register #(.width(1), .trigger("rising"), .Select("low")) register_10 (
    .D(ID_RegWrite), .en(halt), .Q(EX_RegWrite), .clk(clk), .clr(rst));
  Register #(.width(1), .trigger("rising"), .Select("low")) register_11 (
    .D(ID_Jal), .en(halt), .Q(EX_Jal), .clk(clk), .clr(rst));
  Register #(.width(1), .trigger("rising"), .Select("low")) register_12 (
    .D(ID_Jalr), .en(halt), .Q(EX_Jalr), .clk(clk), .clr(rst));
  Register #(.width(5), .trigger("rising"), .Select("low")) register_13 (
    .D(ID_rd), .en(halt), .Q(EX_rd), .clk(clk), .clr(rst));
  Register #(.width(1), .trigger("rising"), .Select("low")) register_14 (
    .D(ID_Ecall), .en(halt), .Q(EX_Ecall), .clk(clk), .clr(rst));
  Register #(.width(32), .trigger("rising"), .Select("low")) register_15 (
    .D(ID_R1), .en(halt), .Q(EX_A), .clk(clk), .clr(rst));
  Register #(.width(32), .trigger("rising"), .Select("low")) register_16 (
    .D(ID_R2), .en(halt), .Q(EX_B), .clk(clk), .clr(rst));
  Register #(.width(32), .trigger("rising"), .Select("low")) register_17 (
    .D(ID_imm), .en(halt), .Q(EX_imm), .clk(clk), .clr(rst));
  Register #(.width(32), .trigger("rising"), .Select("low")) register_18 (
    .D(ID_imm_B), .en(halt), .Q(EX_imm_B), .clk(clk), .clr(rst));
  Register #(.width(32), .trigger("rising"), .Select("low")) register_19 (
    .D(ID_imm_Jal), .en(halt), .Q(EX_imm_Jal), .clk(clk), .clr(rst));
  Register #(.width(1), .trigger("rising"), .Select("low")) register_20 (
    .D(ID_Lui), .en(halt), .Q(EX_Lui), .clk(clk), .clr(rst));
  Register #(.width(1), .trigger("rising"), .Select("low")) register_21 (
    .D(ID_Lbu), .en(halt), .Q(EX_Lbu), .clk(clk), .clr(rst));
  Register #(.width(32), .trigger("rising"), .Select("low")) register_22 (
    .D(ID_imm_Lui), .en(halt), .Q(EX_imm_Lui), .clk(clk), .clr(rst));
endmodule

// EX/MEM
module \理想流水线EX_MEM  (
  input  [31:0] EX_PC,
  input  [31:0] EX_IR,
  input  EX_MemToReg,
  input  EX_MemWrite,
  input  EX_RegWrite,
  input  EX_Jal,
  input  EX_Jalr,
  input  [31:0] EX_MDin,
  input  [31:0] EX_Calc,
  input  [4:0] EX_rd,
  input  EX_Ecall,
  input  EX_Equal,
  input  [31:0] ID_imm_Jal,
  input  ID_Lui,
  input  ID_Lbu,
  input  [31:0] ID_imm_Lui,
  input  clk,
  input  rst,
  input  halt,
  output [31:0] MEM_PC,
  output [31:0] MEM_IR,
  output MEM_MemToReg,
  output MEM_MemWrite,
  output MEM_RegWrite,
  output MEM_Jal,
  output MEM_Jalr,
  output [31:0] MEM_MDin,
  output [31:0] MEM_Calc,
  output [4:0] Mem_Rd,
  output MEM_Ecall,
  output MEM_Equal,
  output [31:0] EX_imm_Jal,
  output EX_Lui,
  output EX_Lbu,
  output [31:0] EX_imm_Lui
);

  Register #(.width(32), .trigger("rising"), .Select("low")) register_1 (
    .D(EX_PC), .en(halt), .Q(MEM_PC), .clk(clk), .clr(rst));
  Register #(.width(32), .trigger("rising"), .Select("low")) register_2 (
    .D(EX_IR), .en(halt), .Q(MEM_IR), .clk(clk), .clr(rst));
  Register #(.width(1), .trigger("rising"), .Select("low")) register_3 (
    .D(EX_MemToReg), .en(halt), .Q(MEM_MemToReg), .clk(clk), .clr(rst));
  Register #(.width(1), .trigger("rising"), .Select("low")) register_4 (
    .D(EX_MemWrite), .en(halt), .Q(MEM_MemWrite), .clk(clk), .clr(rst));
  Register #(.width(1), .trigger("rising"), .Select("low")) register_5 (
    .D(EX_RegWrite), .en(halt), .Q(MEM_RegWrite), .clk(clk), .clr(rst));
  Register #(.width(1), .trigger("rising"), .Select("low")) register_6 (
    .D(EX_Jal), .en(halt), .Q(MEM_Jal), .clk(clk), .clr(rst));
  Register #(.width(1), .trigger("rising"), .Select("low")) register_7 (
    .D(EX_Jalr), .en(halt), .Q(MEM_Jalr), .clk(clk), .clr(rst));
  Register #(.width(32), .trigger("rising"), .Select("low")) register_8 (
    .D(EX_MDin), .en(halt), .Q(MEM_MDin), .clk(clk), .clr(rst));
  Register #(.width(32), .trigger("rising"), .Select("low")) register_9 (
    .D(EX_Calc), .en(halt), .Q(MEM_Calc), .clk(clk), .clr(rst));
  Register #(.width(5), .trigger("rising"), .Select("low")) register_10 (
    .D(EX_rd), .en(halt), .Q(Mem_Rd), .clk(clk), .clr(rst));
  Register #(.width(1), .trigger("rising"), .Select("low")) register_11 (
    .D(EX_Ecall), .en(halt), .Q(MEM_Ecall), .clk(clk), .clr(rst));
  Register #(.width(1), .trigger("rising"), .Select("low")) register_12 (
    .D(EX_Equal), .en(halt), .Q(MEM_Equal), .clk(clk), .clr(rst));
  Register #(.width(32), .trigger("rising"), .Select("low")) register_13 (
    .D(ID_imm_Jal), .en(halt), .Q(EX_imm_Jal), .clk(clk), .clr(rst));
  Register #(.width(1), .trigger("rising"), .Select("low")) register_14 (
    .D(ID_Lui), .en(halt), .Q(EX_Lui), .clk(clk), .clr(rst));
  Register #(.width(1), .trigger("rising"), .Select("low")) register_15 (
    .D(ID_Lbu), .en(halt), .Q(EX_Lbu), .clk(clk), .clr(rst));
  Register #(.width(32), .trigger("rising"), .Select("low")) register_16 (
    .D(ID_imm_Lui), .en(halt), .Q(EX_imm_Lui), .clk(clk), .clr(rst));
endmodule

// MEM/WB
module \理想流水线MEM_WB  (
  input  [31:0] MEM_PC,
  input  [31:0] MEM_IR,
  input  MEM_Lui,
  input  MEM_RegWrite,
  input  MEM_Jal,
  input  MEM_Jalr,
  input  [31:0] Mem_Clac_MDout,
  input  [31:0] MEM_imm_Jal,
  input  [4:0] MEM_Rd,
  input  MEM_Equal,
  input  MEM_Ecall,
  input  [31:0] MEM_imm_Lui,
  input  clk,
  input  rst,
  input  halt,
  output [31:0] WB_PC,
  output [31:0] WB_IR,
  output WB_Lui,
  output WB_RegWrite,
  output WB_Jal,
  output WB_Jalr,
  output [31:0] WB_Calc_MDout,
  output [31:0] WB_imm_Jal,
  output [4:0] WB_Rd,
  output WB_Equal,
  output WB_Ecall,
  output [31:0] WB_imm_Lui
);

  Register #(.width(32), .trigger("rising"), .Select("low")) register_1 (
    .D(MEM_PC), .en(halt), .Q(WB_PC), .clk(clk), .clr(rst));
  Register #(.width(32), .trigger("rising"), .Select("low")) register_2 (
    .D(MEM_IR), .en(halt), .Q(WB_IR), .clk(clk), .clr(rst));
  Register #(.width(1), .trigger("rising"), .Select("low")) register_3 (
    .D(MEM_Lui), .en(halt), .Q(WB_Lui), .clk(clk), .clr(rst));
  Register #(.width(1), .trigger("rising"), .Select("low")) register_4 (
    .D(MEM_RegWrite), .en(halt), .Q(WB_RegWrite), .clk(clk), .clr(rst));
  Register #(.width(1), .trigger("rising"), .Select("low")) register_5 (
    .D(MEM_Jal), .en(halt), .Q(WB_Jal), .clk(clk), .clr(rst));
  Register #(.width(1), .trigger("rising"), .Select("low")) register_6 (
    .D(MEM_Jalr), .en(halt), .Q(WB_Jalr), .clk(clk), .clr(rst));
  Register #(.width(32), .trigger("rising"), .Select("low")) register_7 (
    .D(Mem_Clac_MDout), .en(halt), .Q(WB_Calc_MDout), .clk(clk), .clr(rst));
  Register #(.width(32), .trigger("rising"), .Select("low")) register_8 (
    .D(MEM_imm_Jal), .en(halt), .Q(WB_imm_Jal), .clk(clk), .clr(rst));
  Register #(.width(5), .trigger("rising"), .Select("low")) register_9 (
    .D(MEM_Rd), .en(halt), .Q(WB_Rd), .clk(clk), .clr(rst));
  Register #(.width(1), .trigger("rising"), .Select("low")) register_10 (
    .D(MEM_Equal), .en(halt), .Q(WB_Equal), .clk(clk), .clr(rst));
  Register #(.width(1), .trigger("rising"), .Select("low")) register_11 (
    .D(MEM_Ecall), .en(halt), .Q(WB_Ecall), .clk(clk), .clr(rst));
  Register #(.width(32), .trigger("rising"), .Select("low")) register_12 (
    .D(MEM_imm_Lui), .en(halt), .Q(WB_imm_Lui), .clk(clk), .clr(rst));
endmodule

// branch\n test
module \条件分支逻辑设计  (
  input  Bge,
  input  in_2,
  input  Beq,
  input  in_4,
  input  Bne,
  output branchtaken
);

  wire and_1_out, and_2_out, and_3_out, not_1_out;

  not not_1 (not_1_out, in_4);
  and and_1 (and_1_out, Bge, in_2);
  and and_2 (and_2_out, in_4, Beq);
  and and_3 (and_3_out, not_1_out, Bne);
  or or_1 (branchtaken, and_1_out, and_2_out, and_3_out);
endmodule

// Jump\n Addr
module \无条件跳转逻辑设计  (
  input  JAL,
  input  JALR,
  input  [31:0] JALR_Addr,
  input  [31:0] JAL_Addr,
  input  [31:0] PC,
  output [31:0] J_Addr
);

  wire [31:0] adder_1_out;

  Adder #(.width(32)) adder_1 (.a(JAL_Addr), .b(PC), .out(adder_1_out));  // open: cin, cout
  Multiplexer #(.select(1), .width(32), .disabled("Z"), .enable("false")) multiplexer_1 (
    .in0(JALR_Addr), .in1(adder_1_out), .out(J_Addr), .sel(JAL));
endmodule

// New PC
module \流水线PC计算  (
  input  bJump,
  input  J,
  input  [31:0] PC_4,
  input  [31:0] bAddr,
  input  [31:0] jAddr,
  output [31:0] NPC
);

  wire or_1_out;
  wire [31:0] multiplexer_1_out;

  Multiplexer #(.select(1), .width(32), .disabled("Z"), .enable("false")) multiplexer_1 (
    .in0(bAddr), .in1(jAddr), .out(multiplexer_1_out), .sel(J));
  or or_1 (or_1_out, J, bJump);
  Multiplexer #(.select(1), .width(32), .disabled("Z"), .enable("false")) multiplexer_2 (
    .in0(PC_4), .in1(multiplexer_1_out), .out(NPC), .sel(or_1_out));
endmodule

module \气泡流水线  (
  output RegWrite,
  output MemWrite,
  output [31:0] IF_PC,
  output [31:0] ID_PC,
  output [31:0] EX_PC,
  output [31:0] M_PC,
  output [31:0] WB_PC,
  output [31:0] RDin,
  output [31:0] MDin,
  output [31:0] LedData
);

  wire alu_1_equal, alu_1_out_4, and_1_out, and_2_out, and_3_out, and_4_out, and_5_out, and_6_out, and_7_out,
       Bge, bjump, CLK, clock_1_out, clock_2_out, comparator_1_eq, comparator_1_lt, d_ff_1_q, Dpop, Ecall,
       Equal, EX_RegWrite, Go, halt, IR1, IR2, IR3, J, Jal, Jalr, Jpop, Lbu, Lui, MEM_Lui, MEM_RegWrite,
       nand_1_out, not_1_out, not_2_out, not_3_out, not_4_out, not_5_out, or_1_out, or_2_out, or_4_out,
       or_6_out, RST, S, W1, W2, W3, \单周期硬布线控制器_1_rs1 , \单周期硬布线控制器_1_rs2 , \气泡ex_mem_1_mem_equal ;
  wire [3:0] \单周期硬布线控制器_1_alu_op ;
  wire [4:0] bit_extender_1_out, minus, multiplexer_1_out, multiplexer_2_out, subtractor_1_out, WB_rd,
       \气泡ex_mem_1_mem_rd , \气泡id_ex_1_ex_rd , \气泡ir扩展器_1_funct , \气泡ir扩展器_1_op , \气泡ir扩展器_1_rd ,
       \气泡ir扩展器_1_rs1 , \气泡ir扩展器_1_rs2 ;
  wire [11:1] \单周期硬布线控制器_1_beq ;
  wire [12:0] CNT_num;
  wire [14:0] \气泡ex_mem_1_mem_sgn ;
  wire [15:0] \LoadUse次数 , \总周期数 , \插入气泡数 , \无条件分支数 , \条件分支成功数 , \气泡id_ex_1_ex_sgn , \气泡mem_wb_1_wb_sgn ;
  wire [31:0] adder_1_out, adder_3_out, alu_1_result, bAddr, EX_IR, ID_IR, IF_IR, jAddr, LedShow, MEM_IR,
       multiplexer_3_out, multiplexer_4_out, multiplexer_5_out, multiplexer_6_out, multiplexer_7_out,
       ram_1_data, regifile_1_r1, regifile_1_r2, shifter_2_out, shifter_3_out, WB_IR, \气泡ex_mem_1_mem_alu_r ,
       \气泡ex_mem_1_mem_imm_lui , \气泡id_ex_1_ex_a , \气泡id_ex_1_ex_b , \气泡id_ex_1_ex_imm ,
       \气泡id_ex_1_ex_imm_b , \气泡id_ex_1_ex_imm_jal , \气泡id_ex_1_ex_imm_lui , \气泡ir扩展器_1_imm ,
       \气泡ir扩展器_1_imm_b , \气泡ir扩展器_1_imm_jal , \气泡ir扩展器_1_imm_lui , \气泡mem_wb_1_wb_alu_md , \流水线pc计算_1_npc ;

  Button \u_总复位  (.out(RST));
  Button _1 (.out(IR1));
  Button _2 (.out(IR2));
  Button _3 (.out(IR3));
  // Probe on \总周期数 
  // Probe on \总周期数 
  and and_1 (and_1_out, halt, not_1_out);
  Button \u_继续运行  (.out(Go));
  LED #(.active("true")) led_1 (.in(W1));
  LED #(.active("true")) led_2 (.in(W2));
  LED #(.active("true")) led_3 (.in(W3));
  not not_1 (not_1_out, Dpop);
  Register #(.width(32), .trigger("rising"), .Select("low")) PC (
    .D(\流水线pc计算_1_npc ), .en(and_1_out), .Q(IF_PC), .clk(CLK), .clr(RST));
  Hex_Digit_Display hex_digit_display_1 (.value(LedData[31:28]));  // open: dp
  // Probe on IF_PC[19:0]
  // RiscV_Probe riscv_probe_1: pin names not known; wires that end beside it: IF_IR
  Hex_Digit_Display hex_digit_display_2 (.value(LedData[27:24]));  // open: dp
  Hex_Digit_Display hex_digit_display_3 (.value(LedData[23:20]));  // open: dp
  // Probe on ID_PC[19:0]
  // RiscV_Probe riscv_probe_2: pin names not known; wires that end beside it: ID_IR
  Adder #(.width(32)) adder_1 (.a(IF_PC), .b(32'h4), .out(adder_1_out));  // open: cin, cout
  \流水线PC计算  \u_流水线pc计算_1  (
    .bJump(bjump), .J(J), .PC_4(adder_1_out), .bAddr(bAddr), .jAddr(jAddr), .NPC(\流水线pc计算_1_npc ));
  Hex_Digit_Display hex_digit_display_4 (.value(LedData[19:16]));  // open: dp
  Hex_Digit_Display hex_digit_display_5 (.value(LedData[15:12]));  // open: dp
  ROM #(.addrWidth(10), .dataWidth(32), .Select("high")) rom_1 (.addr(IF_PC[11:2]), .data(IF_IR));
  Hex_Digit_Display hex_digit_display_6 (.value(LedData[11:8]));  // open: dp
  Hex_Digit_Display hex_digit_display_7 (.value(LedData[7:4]));  // open: dp
  Clock #(.highDuration(1), .lowDuration(1)) clock_1 (.out(clock_1_out));
  // Probe on EX_PC[19:0]
  // RiscV_Probe riscv_probe_3: pin names not known; wires that end beside it: EX_IR, clock_1_out, CLK
  Hex_Digit_Display hex_digit_display_8 (.value(LedData[3:0]));  // open: dp
  \气泡IF_ID  \u_气泡if_id_1  (
    .IF_PC(IF_PC), .IF_IR(IF_IR), .clk(CLK), .halt(and_2_out), .ID_PC(ID_PC), .ID_IR(ID_IR), .rst(or_1_out));
  or or_1 (or_1_out, Jpop, RST);
  and and_2 (and_2_out, not_2_out, halt);
  // Probe on \总周期数 
  // Probe on M_PC[19:0]
  // RiscV_Probe riscv_probe_4: pin names not known; wires that end beside it: MEM_IR
  \气泡IR扩展器  \u_气泡ir扩展器_1  (
    .IR(ID_IR), .s(S), .OP(\气泡ir扩展器_1_op ), .Funct(\气泡ir扩展器_1_funct ), .rs1(\气泡ir扩展器_1_rs1 ),
    .rs2(\气泡ir扩展器_1_rs2 ), .rd(\气泡ir扩展器_1_rd ), .imm(\气泡ir扩展器_1_imm ), .imm_b(\气泡ir扩展器_1_imm_b ),
    .imm_lui(\气泡ir扩展器_1_imm_lui ), .imm_jal(\气泡ir扩展器_1_imm_jal ));
  not not_2 (not_2_out, Dpop);
  // Probe on \总周期数 
  // Probe on \无条件分支数 
  // Probe on \条件分支成功数 
  // Probe on \插入气泡数 
  // Probe on \LoadUse次数 
  \单周期硬布线控制器  \u_单周期硬布线控制器_1  (
    .Funct(\气泡ir扩展器_1_funct ), .OP(\气泡ir扩展器_1_op ), .ALU_OP(\单周期硬布线控制器_1_alu_op ),
    .MemToReg(\单周期硬布线控制器_1_beq [3]), .MemWrite(\单周期硬布线控制器_1_beq [4]), .ALU_SRC(\单周期硬布线控制器_1_beq [9]),
    .RegWrite(\单周期硬布线控制器_1_beq [10]), .ecall(\单周期硬布线控制器_1_beq [11]), .S_type(S), .Jalr(Jalr),
    .Beq(\单周期硬布线控制器_1_beq [1]), .JAL(Jal), .Bne(\单周期硬布线控制器_1_beq [2]), .Lui(Lui), .Lbu(Lbu), .Bge(Bge),
    .rs1(\单周期硬布线控制器_1_rs1 ), .rs2(\单周期硬布线控制器_1_rs2 ), .IR21(ID_IR[21]));  // open: uret, csrrsi, csrrci
  // Probe on IF_PC[11:0]
  // Probe on WB_PC[19:0]
  // RiscV_Probe riscv_probe_5: pin names not known; wires that end beside it: WB_IR
  Multiplexer #(.select(1), .width(5), .disabled("Z"), .enable("false")) multiplexer_1 (
    .in0(\气泡ir扩展器_1_rs1 ), .in1(5'b10001), .out(multiplexer_1_out), .sel(\单周期硬布线控制器_1_beq [11]));
  Multiplexer #(.select(1), .width(5), .disabled("Z"), .enable("false")) multiplexer_2 (
    .in0(\气泡ir扩展器_1_rs2 ), .in1(5'b01010), .out(multiplexer_2_out), .sel(\单周期硬布线控制器_1_beq [11]));
  // Probe on EX_PC[11:0]
  // Probe on ID_PC[11:0]
  \气泡发生器  \u_气泡发生器_1  (
    .bjump(bjump), .J(J), .EX_RegWrite(EX_RegWrite), .rs1(multiplexer_1_out), .EX_rd(\气泡id_ex_1_ex_rd ),
    .MEM_rd(\气泡ex_mem_1_mem_rd ), .rs1_u(\单周期硬布线控制器_1_rs1 ), .rs2(multiplexer_2_out),
    .rs2_u(\单周期硬布线控制器_1_rs2 ), .MEM_RegWrite(MEM_RegWrite), .jrst(Jpop), .datapop(Dpop));
  Counter #(.width(16), .max('hffff), .ongoal("wrap"), .trigger("rising"), .behavior("old")) counter_1 (
    .count(halt), .Q(\总周期数 ), .clk(CLK));  // open: load, D, carry, clr, preset
  // Probe on M_PC[11:0]
  D_Flip_Flop #(.trigger("high"), .Pre_Clr_Positions("LEGACY"), .NegatePresetClear("false"), .enable("true"), .NewFFLayout("false")) d_ff_1 (.Q(d_ff_1_q));  // open: clk, D, Qn, preset, en, reset
  // Probe on 13'hc
  Regifile regifile_1 (
    .Din(RDin), .Clk(CLK), .R1(regifile_1_r1), .R2(regifile_1_r2), .WE(RegWrite), .W_num(WB_rd),
    .R1_num(multiplexer_1_out), .R2_num(multiplexer_2_out));
  // Probe on WB_PC[11:0]
  Comparator #(.width(13), .mode("twosComplement")) comparator_1 (
    .a(CNT_num), .b(13'hc), .eq(comparator_1_eq), .lt(comparator_1_lt));  // open: gt
  Clock #(.highDuration(1), .lowDuration(1)) clock_2 (.out(clock_2_out));
  and and_3 (and_3_out, halt, J);
  nand nand_1 (nand_1_out, d_ff_1_q, comparator_1_eq);
  Counter #(.width(13), .max('h1fff), .ongoal("stay"), .trigger("rising"), .behavior("old")) counter_2 (
    .count(comparator_1_lt), .Q(CNT_num), .clk(clock_2_out));  // open: load, D, carry, clr, preset
  \气泡ID_EX  \u_气泡id_ex_1  (
    .ID_rd(\气泡ir扩展器_1_rd ), .ID_a(regifile_1_r1), .ID_b(regifile_1_r2), .ID_imm(\气泡ir扩展器_1_imm ),
    .ID_imm_B(\气泡ir扩展器_1_imm_b ), .ID_imm_Jal(\气泡ir扩展器_1_imm_jal ), .ID_imm_Lui(\气泡ir扩展器_1_imm_lui ),
    .ID_PC(ID_PC), .ID_IR(ID_IR), .EX_rd(\气泡id_ex_1_ex_rd ), .EX_a(\气泡id_ex_1_ex_a ),
    .EX_b(\气泡id_ex_1_ex_b ), .EX_imm(\气泡id_ex_1_ex_imm ), .EX_imm_B(\气泡id_ex_1_ex_imm_b ),
    .EX_imm_Jal(\气泡id_ex_1_ex_imm_jal ), .EX_imm_Lui(\气泡id_ex_1_ex_imm_lui ), .EX_PC(EX_PC), .EX_IR(EX_IR),
    .clk(CLK), .rst(or_2_out), .halt(halt),
    .ID_sgn({Lui, Lbu, Jalr, Jal, \单周期硬布线控制器_1_beq [11:9], \单周期硬布线控制器_1_alu_op , \单周期硬布线控制器_1_beq [4:1], Bge}),
    .EX_sgn({\气泡id_ex_1_ex_sgn [15:11], EX_RegWrite, \气泡id_ex_1_ex_sgn [9:0]}));
  or or_2 (or_2_out, Dpop, RST, Jpop);
  Counter #(.width(16), .max('hffff), .ongoal("wrap"), .trigger("rising"), .behavior("old")) counter_3 (
    .count(and_3_out), .Q(\无条件分支数 ), .clk(CLK));  // open: load, D, carry, clr, preset
  assign CLK = nand_1_out ? clock_2_out : 1'bz;  // Controlled_Buffer controlled_buffer_1
  Multiplexer #(.select(1), .width(32), .disabled("Z"), .enable("false")) multiplexer_3 (
    .in0(\气泡id_ex_1_ex_b ), .in1(\气泡id_ex_1_ex_imm ), .out(multiplexer_3_out), .sel(\气泡id_ex_1_ex_sgn [9]));
  Pull_Resistor #(.pull(1)) pull_resistor_1 (.node(CLK));
  Multiplexer #(.select(1), .width(32), .disabled("Z"), .enable("false")) multiplexer_4 (
    .in0(multiplexer_3_out), .in1(32'ha), .out(multiplexer_4_out), .sel(\气泡id_ex_1_ex_sgn [11]));
  Counter #(.width(16), .max('hffff), .ongoal("wrap"), .trigger("rising"), .behavior("old")) counter_4 (
    .count(and_4_out), .Q(\条件分支成功数 ), .clk(CLK));  // open: load, D, carry, clr, preset
  and and_4 (and_4_out, halt, bjump);
  \条件分支逻辑设计  \u_条件分支逻辑设计_1  (
    .Bge(\气泡id_ex_1_ex_sgn [0]), .in_4(alu_1_equal), .Beq(\气泡id_ex_1_ex_sgn [1]), .in_2(alu_1_out_4),
    .Bne(\气泡id_ex_1_ex_sgn [2]), .branchtaken(bjump));
  ALU alu_1 (
    .X(\气泡id_ex_1_ex_a ), .Y(multiplexer_4_out), .AluOP(\气泡id_ex_1_ex_sgn [8:5]), .Equal(alu_1_equal),
    .Result(alu_1_result), .out_4(alu_1_out_4));  // open: Result_2, out_6
  Adder #(.width(32)) adder_2 (.a(EX_PC), .b(\气泡id_ex_1_ex_imm_b ), .out(bAddr));  // open: cin, cout
  or or_3 (J, \气泡id_ex_1_ex_sgn [12], \气泡id_ex_1_ex_sgn [13]);
  \无条件跳转逻辑设计  \u_无条件跳转逻辑设计_1  (
    .JAL(\气泡id_ex_1_ex_sgn [12]), .JALR(\气泡id_ex_1_ex_sgn [13]), .JALR_Addr(alu_1_result),
    .JAL_Addr(\气泡id_ex_1_ex_imm_jal ), .J_Addr(jAddr), .PC(EX_PC));
  Counter #(.width(16), .max('hffff), .ongoal("wrap"), .trigger("rising"), .behavior("old")) counter_5 (
    .count(and_5_out), .Q(\插入气泡数 ), .clk(CLK));  // open: load, D, carry, clr, preset
  and and_5 (and_5_out, halt, or_4_out);
  or or_4 (or_4_out, Jpop, Dpop);
  \气泡EX_MEM  \u_气泡ex_mem_1  (
    .EX_rd(\气泡id_ex_1_ex_rd ), .EX_PC(EX_PC), .EX_IR(EX_IR), .EX_ALU_R(alu_1_result),
    .EX_imm_Lui(\气泡id_ex_1_ex_imm_lui ),
    .EX_sgn({\气泡id_ex_1_ex_sgn [15:11], EX_RegWrite, \气泡id_ex_1_ex_sgn [9:0]}), .MEM_rd(\气泡ex_mem_1_mem_rd ),
    .MEM_PC(M_PC), .MEM_IR(MEM_IR), .MEM_ALU_R(\气泡ex_mem_1_mem_alu_r ),
    .MEM_imm_Lui(\气泡ex_mem_1_mem_imm_lui ),
    .MEM_sgn({MEM_Lui, \气泡ex_mem_1_mem_sgn [14:11], MEM_RegWrite, \气泡ex_mem_1_mem_sgn [9:5], MemWrite, \气泡ex_mem_1_mem_sgn [3:0]}),
    .rst(RST), .halt(halt), .clk(CLK), .EX_MDin(\气泡id_ex_1_ex_b ), .MEM_MDin(MDin), .EX_Equal(alu_1_equal),
    .MEM_Equal(\气泡ex_mem_1_mem_equal ));
  not not_3 (not_3_out, MemWrite);
  RAM #(.addrWidth(10), .dataWidth(32), .bus("separate"), .Select("high")) ram_1 (
    .addr(\气泡ex_mem_1_mem_alu_r [11:2]), .din(MDin), .data(ram_1_data), .str(MemWrite), .clk(CLK),
    .ld(not_3_out));  // open: sel, clr
  assign bit_extender_1_out = {{3{1'b0}}, \气泡ex_mem_1_mem_alu_r [1:0]};  // Bit_Extender bit_extender_1
  Subtractor #(.width(5)) subtractor_1 (.a(5'b11000), .b(minus), .out(subtractor_1_out));  // open: bin, bout
  Multiplexer #(.select(1), .width(32), .disabled("Z"), .enable("false")) multiplexer_5 (
    .in0(\气泡ex_mem_1_mem_alu_r ), .in1(\气泡ex_mem_1_mem_imm_lui ), .out(multiplexer_5_out), .sel(MEM_Lui));
  Shifter #(.width(5), .shift("ll")) shifter_1 (.in(bit_extender_1_out), .\dist (3'b011), .out(minus));
  Shifter #(.width(32), .shift("ll")) shifter_2 (.in(ram_1_data), .\dist (subtractor_1_out), .out(shifter_2_out));
  Shifter #(.width(32), .shift("lr")) shifter_3 (.in(shifter_2_out), .\dist (5'b11000), .out(shifter_3_out));
  and and_6 (and_6_out, Ecall, Equal);
  and and_7 (and_7_out, Ecall, not_4_out);
  not not_4 (not_4_out, Equal);
  Multiplexer #(.select(1), .width(32), .disabled("Z"), .enable("false")) multiplexer_6 (
    .in0(ram_1_data), .in1(shifter_3_out), .out(multiplexer_6_out), .sel(\气泡ex_mem_1_mem_sgn [14]));
  not not_5 (not_5_out, and_6_out);
  Multiplexer #(.select(1), .width(32), .disabled("Z"), .enable("false")) multiplexer_7 (
    .in0(multiplexer_5_out), .in1(multiplexer_6_out), .out(multiplexer_7_out), .sel(\气泡ex_mem_1_mem_sgn [3]));
  or or_5 (halt, Go, not_5_out);
  Register #(.width(32), .trigger("rising"), .Select("low")) register_1 (
    .D(LedShow), .en(and_7_out), .Q(LedData), .clk(CLK));  // open: clr
  \气泡MEM_WB  \u_气泡mem_wb_1  (
    .MEM_rd(\气泡ex_mem_1_mem_rd ), .MEM_PC(M_PC), .MEM_IR(MEM_IR), .MEM_ALU_MD(multiplexer_7_out),
    .MEM_sgn({MEM_Lui, \气泡ex_mem_1_mem_sgn [14:11], MEM_RegWrite, \气泡ex_mem_1_mem_sgn [9:5], MemWrite, \气泡ex_mem_1_mem_sgn [3:0]}),
    .WB_rd(WB_rd), .WB_PC(WB_PC), .WB_IR(WB_IR), .WB_ALU_MD(\气泡mem_wb_1_wb_alu_md ),
    .WB_sgn({\气泡mem_wb_1_wb_sgn [15:12], Ecall, RegWrite, \气泡mem_wb_1_wb_sgn [9:0]}), .rst(RST), .halt(halt),
    .clk(CLK), .MEM_Equal(\气泡ex_mem_1_mem_equal ), .WB_Equal(Equal), .MEM_LED(MDin), .WB_LED(LedShow));
  Adder #(.width(32)) adder_3 (.a(WB_PC), .b(32'h4), .out(adder_3_out));  // open: cin, cout
  or or_6 (or_6_out, \气泡mem_wb_1_wb_sgn [13], \气泡mem_wb_1_wb_sgn [12]);
  Multiplexer #(.select(1), .width(32), .disabled("Z"), .enable("false")) multiplexer_8 (
    .in0(\气泡mem_wb_1_wb_alu_md ), .in1(adder_3_out), .out(RDin), .sel(or_6_out));

  // Other names for the same wires on the sheet: MEM_PC[31:0] = M_PC

  // Notes on the sheet:
  //   中断源
  //   时空图监测，可删除
  //   中断等待指示
  //   数码管输出
  //   指令存储器
  //   contents of rom_1 (hex, n*v repeats v):
  //   100493 100006f 100493 200913 300993 100006f 100493 200913 300993 100006f 100493 200913 300993
  //   100006f 100493 200913 300993 3d0000ef 100413 100493 1f49493 900533 2200893 73 24d493 48463 fedff06f
  //   900533 2200893 73 100493 249493 900533 2200893 73 48463 fedff06f 100493 1f49493 900533 2200893 73
  //   4034d493 900533 2200893 73 4044d493 900533 2200893 73 4044d493 900533 2200893 73 4044d493 900533
  //   2200893 73 4044d493 900533 2200893 73 4044d493 900533 2200893 73 4044d493 900533 2200893 73 4044d493
  //   900533 2200893 73 100413 1f41993 41f9d993 433 c00913 300b13 140413 f47413 800293 100313 499993
  //   89e9b3 1300533 2200893 73 406282b3 fe0294e3 140413 f00f93 1f47433 1c41413 800293 100313 49d993
  //   89e9b3 1300533 2200893 73 406282b3 fe0294e3 1c45413 406b0b33 b0463 f95ff06f 2b3 fff2c293 829293
  //   ff2e293 500533 2200893 73 fff00413 493 84a023 140413 448493 84a023 140413 448493 84a023 140413
  //   448493 84a023 140413 448493 84a023 140413 448493 84a023 140413 448493 84a023 140413 448493 84a023
  //   140413 448493 84a023 140413 448493 84a023 140413 448493 84a023 140413 448493 84a023 140413 448493
  //   84a023 140413 448493 84a023 140413 448493 84a023 140413 448493 84a023 140413 448493 140413 433
  //   3c00493 42983 4aa03 149a2b3 28663 134a023 1442023 ffc48493 fe9412e3 800533 2200893 73 440413 3c00493
  //   fc9416e3 a00893 73 fff00293 7700493 849493 7748493 900533 2200893 73 1000e13 54c4b3 900533 2200893
  //   73 fffe0e13 fe0e16e3 a00893 73 800e13 fedc04b7 fff00413 1045413 84e4b3 900533 2200893 73 ba984b7
  //   900533 73 76544b7 900533 73 32104b7 900533 73 fffe0e13 fa0e1ee3 a00893 73 313 1000e13 8400493 849493
  //   8348493 400913 891913 490913 849493 8248493 849493 8148493 891913 490913 891913 490913 932023
  //   12484b3 430313 fffe0e13 fe0e18e3 2000e13 313 34483 900533 2200893 73 130313 fffe0e13 fe0e14e3 a00893
  //   73 f00493 900533 2200893 73 fff48493 fe04d8e3 a00893 73 413 140413 800533 2200893 73 240413 800533
  //   2200893 73 340413 800533 2200893 73 440413 800533 2200893 73 540413 800533 2200893 73 640413 800533
  //   2200893 73 740413 800533 2200893 73 840413 800533 2200893 2200893 73 8067
  //   此处数据冲突需要IF和ID阶段的指令等待，不产生气泡，连接halt接口
  //   控制位
  //   跳转需要清除IF和ID的误取指令，连接reset同步清零
  //   流水调试日志用
  //   暂停节拍，不能为0
  //   戳工具置1进入计数暂停模式，ctrl+k时钟自动运行到对应节拍暂停
  //   ctrl+k关闭时钟连续运行，将控制位置零，进入单步调试模式调试
  //   周期数、分支数记录
  //   可计数暂停的时钟源
  //   此处不论是跳转还是数据冲突都需要产生气泡，因此都需要连接reset同步清零
  //   instruction分配关系
  //   0：Bge指令
  //   1：Beq指令
  //   2：Bne指令
  //   10：RegWrite信号
  //   14：Lbu信号
  //   为方便自动评测，需要输出流水线各段保存的PC值，注意是PC不是PC+4，另外ID段寄存器写入信息，Mem段内存写入信息也要输出
  //   3：MemToReg信号
  //   4：MemWrite信号
  //   11：Ecall信号
  //   15：Lui信号
  //   5-8：AluOP信号
  //   9：Alu_src信号
  //   12：Jal信号
  //   13：Jalr信号
  //   数据存储器
  //   Ecall选项
endmodule

// IR扩展器
module \气泡IR扩展器  (
  input  [31:0] IR,
  input  s,
  output [4:0] OP,
  output [4:0] Funct,
  output [4:0] rs1,
  output [4:0] rs2,
  output [4:0] rd,
  output [31:0] imm,
  output [31:0] imm_b,
  output [31:0] imm_lui,
  output [31:0] imm_jal
);

  wire [11:0] multiplexer_1_out;
  wire [31:0] bit_extender_1_out, bit_extender_3_out, bit_extender_4_out;

  assign bit_extender_1_out = {{12{IR[31]}}, IR[31:12]};  // Bit_Extender bit_extender_1
  Multiplexer #(.select(1), .width(12), .disabled("Z"), .enable("false")) multiplexer_1 (
    .in0(IR[31:20]), .in1({IR[31:25], IR[11:7]}), .out(multiplexer_1_out), .sel(s));
  assign imm = {{20{multiplexer_1_out[11]}}, multiplexer_1_out};  // Bit_Extender bit_extender_2
  assign bit_extender_3_out = {{20{IR[31]}}, {IR[31], IR[7], IR[30:25], IR[11:8]}};  // Bit_Extender bit_extender_3
  Shifter #(.width(32), .shift("ll")) shifter_1 (.in(bit_extender_1_out), .\dist (5'b01100), .out(imm_lui));
  assign bit_extender_4_out = {{12{IR[31]}}, {IR[31], IR[19:12], IR[20], IR[30:21]}};  // Bit_Extender bit_extender_4
  Shifter #(.width(32), .shift("ll")) shifter_2 (.in(bit_extender_3_out), .\dist (5'b00001), .out(imm_b));
  Shifter #(.width(32), .shift("ll")) shifter_3 (.in(bit_extender_4_out), .\dist (5'b00001), .out(imm_jal));

  assign Funct = {IR[30], IR[25], IR[14:12]};
  assign OP = IR[6:2];
  assign rd = IR[11:7];
  assign rs1 = IR[19:15];
  assign rs2 = IR[24:20];

  // Notes on the sheet:
  //   imm12 I
  //   imm12 S
  //   imm20 LUI
  //   rs1
  //   rs2
  //   rd
  //   imm20 Jal
endmodule

// IF/ID
module \气泡IF_ID  (
  input  [31:0] IF_PC,
  input  [31:0] IF_IR,
  input  clk,
  input  halt,
  input  rst,
  output [31:0] ID_PC,
  output [31:0] ID_IR
);

  wire [31:0] multiplexer_1_out, multiplexer_2_out;

  Multiplexer #(.select(1), .width(32), .disabled("Z"), .enable("false")) multiplexer_1 (
    .in0(IF_PC), .in1({32{1'b0}}), .out(multiplexer_1_out), .sel(rst));
  Multiplexer #(.select(1), .width(32), .disabled("Z"), .enable("false")) multiplexer_2 (
    .in0(IF_IR), .in1({32{1'b0}}), .out(multiplexer_2_out), .sel(rst));
  Register #(.width(32), .trigger("rising"), .Select("low")) PC (
    .D(multiplexer_1_out), .en(halt), .Q(ID_PC), .clk(clk));  // open: clr
  Register #(.width(32), .trigger("rising"), .Select("low")) IR (
    .D(multiplexer_2_out), .en(halt), .Q(ID_IR), .clk(clk));  // open: clr
endmodule

// ID/EX
module \气泡ID_EX  (
  input  [4:0] ID_rd,
  input  [31:0] ID_a,
  input  [31:0] ID_b,
  input  [31:0] ID_imm,
  input  [31:0] ID_imm_B,
  input  [31:0] ID_imm_Jal,
  input  [31:0] ID_imm_Lui,
  input  [31:0] ID_PC,
  input  [31:0] ID_IR,
  input  [15:0] ID_sgn,
  input  clk,
  input  rst,
  input  halt,
  output [4:0] EX_rd,
  output [31:0] EX_a,
  output [31:0] EX_b,
  output [31:0] EX_imm,
  output [31:0] EX_imm_B,
  output [31:0] EX_imm_Jal,
  output [31:0] EX_imm_Lui,
  output [31:0] EX_PC,
  output [31:0] EX_IR,
  output [15:0] EX_sgn
);

  wire [4:0] multiplexer_1_out;
  wire [15:0] multiplexer_10_out;
  wire [31:0] multiplexer_2_out, multiplexer_3_out, multiplexer_4_out, multiplexer_5_out, multiplexer_6_out,
       multiplexer_7_out, multiplexer_8_out, multiplexer_9_out;

  Multiplexer #(.select(1), .width(5), .disabled("Z"), .enable("false")) multiplexer_1 (
    .in0(ID_rd), .in1({5{1'b0}}), .out(multiplexer_1_out), .sel(rst));
  Multiplexer #(.select(1), .width(32), .disabled("Z"), .enable("false")) multiplexer_2 (
    .in0(ID_a), .in1({32{1'b0}}), .out(multiplexer_2_out), .sel(rst));
  Multiplexer #(.select(1), .width(32), .disabled("Z"), .enable("false")) multiplexer_3 (
    .in0(ID_b), .in1({32{1'b0}}), .out(multiplexer_3_out), .sel(rst));
  Multiplexer #(.select(1), .width(32), .disabled("Z"), .enable("false")) multiplexer_4 (
    .in0(ID_imm), .in1({32{1'b0}}), .out(multiplexer_4_out), .sel(rst));
  Multiplexer #(.select(1), .width(32), .disabled("Z"), .enable("false")) multiplexer_5 (
    .in0(ID_imm_B), .in1({32{1'b0}}), .out(multiplexer_5_out), .sel(rst));
  Multiplexer #(.select(1), .width(32), .disabled("Z"), .enable("false")) multiplexer_6 (
    .in0(ID_imm_Jal), .in1({32{1'b0}}), .out(multiplexer_6_out), .sel(rst));
  Multiplexer #(.select(1), .width(32), .disabled("Z"), .enable("false")) multiplexer_7 (
    .in0(ID_imm_Lui), .in1({32{1'b0}}), .out(multiplexer_7_out), .sel(rst));
  Multiplexer #(.select(1), .width(32), .disabled("Z"), .enable("false")) multiplexer_8 (
    .in0(ID_PC), .in1({32{1'b0}}), .out(multiplexer_8_out), .sel(rst));
  Multiplexer #(.select(1), .width(32), .disabled("Z"), .enable("false")) multiplexer_9 (
    .in0(ID_IR), .in1({32{1'b0}}), .out(multiplexer_9_out), .sel(rst));
  Multiplexer #(.select(1), .width(16), .disabled("Z"), .enable("false")) multiplexer_10 (
    .in0(ID_sgn), .in1({16{1'b0}}), .out(multiplexer_10_out), .sel(rst));
  Register #(.width(5), .trigger("rising"), .Select("low")) register_1 (
    .D(multiplexer_1_out), .en(halt), .Q(EX_rd), .clk(clk));  // open: clr
  Register #(.width(32), .trigger("rising"), .Select("low")) register_2 (
    .D(multiplexer_2_out), .en(halt), .Q(EX_a), .clk(clk));  // open: clr
  Register #(.width(32), .trigger("rising"), .Select("low")) register_3 (
    .D(multiplexer_3_out), .en(halt), .Q(EX_b), .clk(clk));  // open: clr
  Register #(.width(32), .trigger("rising"), .Select("low")) register_4 (
    .D(multiplexer_4_out), .en(halt), .Q(EX_imm), .clk(clk));  // open: clr
  Register #(.width(32), .trigger("rising"), .Select("low")) register_5 (
    .D(multiplexer_5_out), .en(halt), .Q(EX_imm_B), .clk(clk));  // open: clr
  Register #(.width(32), .trigger("rising"), .Select("low")) register_6 (
    .D(multiplexer_6_out), .en(halt), .Q(EX_imm_Jal), .clk(clk));  // open: clr
  Register #(.width(32), .trigger("rising"), .Select("low")) register_7 (
    .D(multiplexer_7_out), .en(halt), .Q(EX_imm_Lui), .clk(clk));  // open: clr
  Register #(.width(32), .trigger("rising"), .Select("low")) register_8 (
    .D(multiplexer_8_out), .en(halt), .Q(EX_PC), .clk(clk));  // open: clr
  Register #(.width(32), .trigger("rising"), .Select("low")) register_9 (
    .D(multiplexer_9_out), .en(halt), .Q(EX_IR), .clk(clk));  // open: clr
  Register #(.width(16), .trigger("rising"), .Select("low")) register_10 (
    .D(multiplexer_10_out), .en(halt), .Q(EX_sgn), .clk(clk));  // open: clr
endmodule

// EX/MEM
module \气泡EX_MEM  (
  input  [4:0] EX_rd,
  input  [31:0] EX_PC,
  input  [31:0] EX_IR,
  input  [31:0] EX_ALU_R,
  input  [31:0] EX_MDin,
  input  [31:0] EX_imm_Lui,
  input  EX_Equal,
  input  [15:0] EX_sgn,
  input  rst,
  input  halt,
  input  clk,
  output [4:0] MEM_rd,
  output [31:0] MEM_PC,
  output [31:0] MEM_IR,
  output [31:0] MEM_ALU_R,
  output [31:0] MEM_MDin,
  output [31:0] MEM_imm_Lui,
  output MEM_Equal,
  output [15:0] MEM_sgn
);

  wire multiplexer_7_out;
  wire [4:0] multiplexer_1_out;
  wire [15:0] multiplexer_8_out;
  wire [31:0] multiplexer_2_out, multiplexer_3_out, multiplexer_4_out, multiplexer_5_out, multiplexer_6_out;

  Multiplexer #(.select(1), .width(5), .disabled("Z"), .enable("false")) multiplexer_1 (
    .in0(EX_rd), .in1({5{1'b0}}), .out(multiplexer_1_out), .sel(rst));
  Multiplexer #(.select(1), .width(32), .disabled("Z"), .enable("false")) multiplexer_2 (
    .in0(EX_PC), .in1({32{1'b0}}), .out(multiplexer_2_out), .sel(rst));
  Multiplexer #(.select(1), .width(32), .disabled("Z"), .enable("false")) multiplexer_3 (
    .in0(EX_IR), .in1({32{1'b0}}), .out(multiplexer_3_out), .sel(rst));
  Multiplexer #(.select(1), .width(32), .disabled("Z"), .enable("false")) multiplexer_4 (
    .in0(EX_ALU_R), .in1({32{1'b0}}), .out(multiplexer_4_out), .sel(rst));
  Multiplexer #(.select(1), .width(32), .disabled("Z"), .enable("false")) multiplexer_5 (
    .in0(EX_MDin), .in1({32{1'b0}}), .out(multiplexer_5_out), .sel(rst));
  Multiplexer #(.select(1), .width(32), .disabled("Z"), .enable("false")) multiplexer_6 (
    .in0(EX_imm_Lui), .in1({32{1'b0}}), .out(multiplexer_6_out), .sel(rst));
  Multiplexer #(.select(1), .width(1), .disabled("Z"), .enable("false")) multiplexer_7 (
    .in0(EX_Equal), .in1(1'b0), .out(multiplexer_7_out), .sel(rst));
  Multiplexer #(.select(1), .width(16), .disabled("Z"), .enable("false")) multiplexer_8 (
    .in0(EX_sgn), .in1({16{1'b0}}), .out(multiplexer_8_out), .sel(rst));
  Register #(.width(5), .trigger("rising"), .Select("low")) register_1 (
    .D(multiplexer_1_out), .en(halt), .Q(MEM_rd), .clk(clk));  // open: clr
  Register #(.width(32), .trigger("rising"), .Select("low")) register_2 (
    .D(multiplexer_2_out), .en(halt), .Q(MEM_PC), .clk(clk));  // open: clr
  Register #(.width(32), .trigger("rising"), .Select("low")) register_3 (
    .D(multiplexer_3_out), .en(halt), .Q(MEM_IR), .clk(clk));  // open: clr
  Register #(.width(32), .trigger("rising"), .Select("low")) register_4 (
    .D(multiplexer_4_out), .en(halt), .Q(MEM_ALU_R), .clk(clk));  // open: clr
  Register #(.width(32), .trigger("rising"), .Select("low")) register_5 (
    .D(multiplexer_5_out), .en(halt), .Q(MEM_MDin), .clk(clk));  // open: clr
  Register #(.width(32), .trigger("rising"), .Select("low")) register_6 (
    .D(multiplexer_6_out), .en(halt), .Q(MEM_imm_Lui), .clk(clk));  // open: clr
  Register #(.width(1), .trigger("rising"), .Select("low")) register_7 (
    .D(multiplexer_7_out), .en(halt), .Q(MEM_Equal), .clk(clk));  // open: clr
  Register #(.width(16), .trigger("rising"), .Select("low")) register_8 (
    .D(multiplexer_8_out), .en(halt), .Q(MEM_sgn), .clk(clk));  // open: clr
endmodule
// MEM/WB
module \气泡MEM_WB  (
  input  [4:0] MEM_rd,
  input  [31:0] MEM_PC,
  input  [31:0] MEM_IR,
  input  [31:0] MEM_LED,
  input  [31:0] MEM_ALU_MD,
  input  MEM_Equal,
  input  [15:0] MEM_sgn,
  input  rst,
  input  halt,
  input  clk,
  output [4:0] WB_rd,
  output [31:0] WB_PC,
  output [31:0] WB_IR,
  output [31:0] WB_LED,
  output [31:0] WB_ALU_MD,
  output WB_Equal,
  output [15:0] WB_sgn
);

  wire multiplexer_6_out;
  wire [4:0] multiplexer_1_out;
  wire [15:0] multiplexer_7_out;
  wire [31:0] multiplexer_2_out, multiplexer_3_out, multiplexer_4_out, multiplexer_5_out;

  Multiplexer #(.select(1), .width(5), .disabled("Z"), .enable("false")) multiplexer_1 (
    .in0(MEM_rd), .in1({5{1'b0}}), .out(multiplexer_1_out), .sel(rst));
  Multiplexer #(.select(1), .width(32), .disabled("Z"), .enable("false")) multiplexer_2 (
    .in0(MEM_PC), .in1({32{1'b0}}), .out(multiplexer_2_out), .sel(rst));
  Multiplexer #(.select(1), .width(32), .disabled("Z"), .enable("false")) multiplexer_3 (
    .in0(MEM_IR), .in1({32{1'b0}}), .out(multiplexer_3_out), .sel(rst));
  Multiplexer #(.select(1), .width(32), .disabled("Z"), .enable("false")) multiplexer_4 (
    .in0(MEM_LED), .in1({32{1'b0}}), .out(multiplexer_4_out), .sel(rst));
  Multiplexer #(.select(1), .width(32), .disabled("Z"), .enable("false")) multiplexer_5 (
    .in0(MEM_ALU_MD), .in1({32{1'b0}}), .out(multiplexer_5_out), .sel(rst));
  Multiplexer #(.select(1), .width(1), .disabled("Z"), .enable("false")) multiplexer_6 (
    .in0(MEM_Equal), .in1(1'b0), .out(multiplexer_6_out), .sel(rst));
  Multiplexer #(.select(1), .width(16), .disabled("Z"), .enable("false")) multiplexer_7 (
    .in0(MEM_sgn), .in1({16{1'b0}}), .out(multiplexer_7_out), .sel(rst));
  Register #(.width(5), .trigger("rising"), .Select("low")) register_1 (
    .D(multiplexer_1_out), .en(halt), .Q(WB_rd), .clk(clk));  // open: clr
  Register #(.width(32), .trigger("rising"), .Select("low")) register_2 (
    .D(multiplexer_2_out), .en(halt), .Q(WB_PC), .clk(clk));  // open: clr
  Register #(.width(32), .trigger("rising"), .Select("low")) register_3 (
    .D(multiplexer_3_out), .en(halt), .Q(WB_IR), .clk(clk));  // open: clr
  Register #(.width(32), .trigger("rising"), .Select("low")) register_4 (
    .D(multiplexer_4_out), .en(halt), .Q(WB_LED), .clk(clk));  // open: clr
  Register #(.width(32), .trigger("rising"), .Select("low")) register_5 (
    .D(multiplexer_5_out), .en(halt), .Q(WB_ALU_MD), .clk(clk));  // open: clr
  Register #(.width(1), .trigger("rising"), .Select("low")) register_6 (
    .D(multiplexer_6_out), .en(halt), .Q(WB_Equal), .clk(clk));  // open: clr
  Register #(.width(16), .trigger("rising"), .Select("low")) register_7 (
    .D(multiplexer_7_out), .en(halt), .Q(WB_sgn), .clk(clk));  // open: clr
endmodule

module \气泡发生器  (
  input  bjump,
  input  J,
  input  EX_RegWrite,
  input  [4:0] rs1,
  input  [4:0] EX_rd,
  input  [4:0] MEM_rd,
  input  rs1_u,
  input  [4:0] rs2,
  input  rs2_u,
  input  MEM_RegWrite,
  output jrst,
  output datapop
);

  wire and_1_out, and_2_out, and_3_out, and_4_out, and_5_out, and_6_out, comparator_1_eq, comparator_2_eq,
       comparator_3_eq, comparator_4_eq, comparator_5_eq, comparator_6_eq, not_1_out, not_2_out, or_2_out,
       or_3_out;

  Comparator #(.width(5), .mode("twosComplement")) comparator_1 (
    .a(EX_rd), .b({5{1'b0}}), .eq(comparator_1_eq));  // open: gt, lt
  Comparator #(.width(5), .mode("twosComplement")) comparator_2 (
    .a(MEM_rd), .b({5{1'b0}}), .eq(comparator_2_eq));  // open: gt, lt
  or or_1 (jrst, bjump, J);
  not not_1 (not_1_out, comparator_1_eq);
  not not_2 (not_2_out, comparator_2_eq);
  Comparator #(.width(5), .mode("twosComplement")) comparator_3 (
    .a(rs1), .b(EX_rd), .eq(comparator_3_eq));  // open: gt, lt
  Comparator #(.width(5), .mode("twosComplement")) comparator_4 (
    .a(rs1), .b(MEM_rd), .eq(comparator_4_eq));  // open: gt, lt
  Comparator #(.width(5), .mode("twosComplement")) comparator_5 (
    .a(rs2), .b(EX_rd), .eq(comparator_5_eq));  // open: gt, lt
  Comparator #(.width(5), .mode("twosComplement")) comparator_6 (
    .a(rs2), .b(MEM_rd), .eq(comparator_6_eq));  // open: gt, lt
  and and_1 (and_1_out, comparator_3_eq, not_1_out, EX_RegWrite);
  and and_2 (and_2_out, comparator_4_eq, not_2_out, MEM_RegWrite);
  and and_3 (and_3_out, comparator_5_eq, not_1_out, EX_RegWrite);
  and and_4 (and_4_out, comparator_6_eq, not_2_out, MEM_RegWrite);
  or or_2 (or_2_out, and_1_out, and_2_out);
  or or_3 (or_3_out, and_3_out, and_4_out);
  and and_5 (and_5_out, or_2_out, rs1_u);
  or or_4 (datapop, and_5_out, and_6_out);
  and and_6 (and_6_out, or_3_out, rs2_u);
endmodule

module \重定向流水线  (
  output RegWrite,
  output MemWrite,
  output [31:0] IF_PC,
  output [31:0] ID_PC,
  output [31:0] EX_PC,
  output [31:0] M_PC,
  output [31:0] WB_PC,
  output [31:0] RDin,
  output [31:0] MDin,
  output [31:0] LedData
);

  wire alu_1_equal, alu_1_out_4, and_1_out, and_2_out, and_3_out, and_4_out, and_5_out, and_6_out, and_7_out,
       and_8_out, Bge, bjump, CLK, clock_1_out, clock_2_out, comparator_1_eq, comparator_1_lt, d_ff_1_q,
       Ecall, Equal, EX_MemToReg, EX_RegWrite, Go, halt, IR1, IR2, IR3, J, Jal, Jalr, Jpop, Lbu, LoadUse,
       Lui, MEM_Lui, MEM_RegWrite, nand_1_out, not_1_out, not_2_out, not_3_out, not_4_out, not_5_out,
       or_1_out, or_2_out, or_5_out, RST, S, W1, W2, W3, \单周期硬布线控制器_1_rs1 , \单周期硬布线控制器_1_rs2 ,
       \气泡ex_mem_1_mem_equal ;
  wire [1:0] \重定向流水线id_ex_1_ex_fwda , \重定向流水线id_ex_1_ex_fwdb , \重定向逻辑设计_1_fwda , \重定向逻辑设计_1_fwdb ;
  wire [3:0] \单周期硬布线控制器_1_alu_op ;
  wire [4:0] bit_extender_1_out, minus, multiplexer_1_out, multiplexer_2_out, subtractor_1_out, WB_rd,
       \气泡ex_mem_1_mem_rd , \气泡ir扩展器_1_funct , \气泡ir扩展器_1_op , \气泡ir扩展器_1_rd , \气泡ir扩展器_1_rs1 ,
       \气泡ir扩展器_1_rs2 , \重定向流水线id_ex_1_ex_rd ;
  wire [11:1] \单周期硬布线控制器_1_beq ;
  wire [12:0] CNT_num;
  wire [14:0] \气泡ex_mem_1_mem_sgn ;
  wire [15:0] \LoadUse次数 , \总周期数 , \插入气泡数 , \无条件分支数 , \条件分支成功数 , \气泡mem_wb_1_wb_sgn , \重定向流水线id_ex_1_ex_sgn ;
  wire [31:0] adder_1_out, adder_3_out, alu_1_result, bAddr, EX_IR, ID_IR, IF_IR, jAddr, LedShow, MEM_IR,
       multiplexer_3_out, multiplexer_4_out, multiplexer_5_out, multiplexer_6_out, multiplexer_7_out,
       multiplexer_8_out, multiplexer_9_out, ram_1_data, regifile_1_r1, regifile_1_r2, shifter_2_out,
       shifter_3_out, WB_IR, \气泡ex_mem_1_mem_alu_r , \气泡ex_mem_1_mem_imm_lui , \气泡ir扩展器_1_imm ,
       \气泡ir扩展器_1_imm_b , \气泡ir扩展器_1_imm_jal , \气泡ir扩展器_1_imm_lui , \气泡mem_wb_1_wb_alu_md , \流水线pc计算_1_npc ,
       \重定向流水线id_ex_1_ex_a , \重定向流水线id_ex_1_ex_b , \重定向流水线id_ex_1_ex_imm , \重定向流水线id_ex_1_ex_imm_b ,
       \重定向流水线id_ex_1_ex_imm_jal , \重定向流水线id_ex_1_ex_imm_lui ;

  Button \u_总复位  (.out(RST));
  Button _1 (.out(IR1));
  Button _2 (.out(IR2));
  Button _3 (.out(IR3));
  // Probe on \总周期数 
  // Probe on \总周期数 
  and and_1 (and_1_out, halt, not_1_out);
  Button \u_继续运行  (.out(Go));
  LED #(.active("true")) led_1 (.in(W1));
  LED #(.active("true")) led_2 (.in(W2));
  LED #(.active("true")) led_3 (.in(W3));
  not not_1 (not_1_out, LoadUse);
  Register #(.width(32), .trigger("rising"), .Select("low")) PC (
    .D(\流水线pc计算_1_npc ), .en(and_1_out), .Q(IF_PC), .clk(CLK), .clr(RST));
  Hex_Digit_Display hex_digit_display_1 (.value(LedData[31:28]));  // open: dp
  // Probe on IF_PC[19:0]
  // RiscV_Probe riscv_probe_1: pin names not known; wires that end beside it: IF_IR
  Hex_Digit_Display hex_digit_display_2 (.value(LedData[23:20]));  // open: dp
  Hex_Digit_Display hex_digit_display_3 (.value(LedData[27:24]));  // open: dp
  // Probe on ID_PC[19:0]
  // RiscV_Probe riscv_probe_2: pin names not known; wires that end beside it: ID_IR
  Adder #(.width(32)) adder_1 (.a(IF_PC), .b(32'h4), .out(adder_1_out));  // open: cin, cout
  \流水线PC计算  \u_流水线pc计算_1  (
    .bJump(bjump), .J(J), .PC_4(adder_1_out), .bAddr(bAddr), .jAddr(jAddr), .NPC(\流水线pc计算_1_npc ));
  Hex_Digit_Display hex_digit_display_4 (.value(LedData[19:16]));  // open: dp
  Hex_Digit_Display hex_digit_display_5 (.value(LedData[15:12]));  // open: dp
  ROM #(.addrWidth(10), .dataWidth(32), .Select("high")) rom_1 (.addr(IF_PC[11:2]), .data(IF_IR));
  Hex_Digit_Display hex_digit_display_6 (.value(LedData[11:8]));  // open: dp
  Hex_Digit_Display hex_digit_display_7 (.value(LedData[7:4]));  // open: dp
  Clock #(.highDuration(1), .lowDuration(1)) clock_1 (.out(clock_1_out));
  // Probe on EX_PC[19:0]
  // RiscV_Probe riscv_probe_3: pin names not known; wires that end beside it: EX_IR, clock_1_out, CLK
  Hex_Digit_Display hex_digit_display_8 (.value(LedData[3:0]));  // open: dp
  \气泡IF_ID  \u_气泡if_id_1  (
    .IF_PC(IF_PC), .IF_IR(IF_IR), .clk(CLK), .halt(and_2_out), .ID_PC(ID_PC), .ID_IR(ID_IR), .rst(or_1_out));
  or or_1 (or_1_out, Jpop, RST);
  and and_2 (and_2_out, not_2_out, halt);
  // Probe on \总周期数 
  // Probe on M_PC[19:0]
  // RiscV_Probe riscv_probe_4: pin names not known; wires that end beside it: MEM_IR
  \气泡IR扩展器  \u_气泡ir扩展器_1  (
    .IR(ID_IR), .s(S), .OP(\气泡ir扩展器_1_op ), .Funct(\气泡ir扩展器_1_funct ), .rs1(\气泡ir扩展器_1_rs1 ),
    .rs2(\气泡ir扩展器_1_rs2 ), .rd(\气泡ir扩展器_1_rd ), .imm(\气泡ir扩展器_1_imm ), .imm_b(\气泡ir扩展器_1_imm_b ),
    .imm_lui(\气泡ir扩展器_1_imm_lui ), .imm_jal(\气泡ir扩展器_1_imm_jal ));
  not not_2 (not_2_out, LoadUse);
  // Probe on \总周期数 
  // Probe on \无条件分支数 
  // Probe on \条件分支成功数 
  // Probe on \插入气泡数 
  // Probe on \LoadUse次数 
  \单周期硬布线控制器  \u_单周期硬布线控制器_1  (
    .Funct(\气泡ir扩展器_1_funct ), .OP(\气泡ir扩展器_1_op ), .ALU_OP(\单周期硬布线控制器_1_alu_op ),
    .MemToReg(\单周期硬布线控制器_1_beq [3]), .MemWrite(\单周期硬布线控制器_1_beq [4]), .ALU_SRC(\单周期硬布线控制器_1_beq [9]),
    .RegWrite(\单周期硬布线控制器_1_beq [10]), .ecall(\单周期硬布线控制器_1_beq [11]), .S_type(S), .Jalr(Jalr),
    .Beq(\单周期硬布线控制器_1_beq [1]), .JAL(Jal), .Bne(\单周期硬布线控制器_1_beq [2]), .Lui(Lui), .Lbu(Lbu), .Bge(Bge),
    .rs1(\单周期硬布线控制器_1_rs1 ), .rs2(\单周期硬布线控制器_1_rs2 ), .IR21(ID_IR[21]));  // open: uret, csrrsi, csrrci
  // Probe on IF_PC[11:0]
  // Probe on WB_PC[19:0]
  // RiscV_Probe riscv_probe_5: pin names not known; wires that end beside it: WB_IR
  Multiplexer #(.select(1), .width(5), .disabled("Z"), .enable("false")) multiplexer_1 (
    .in0(\气泡ir扩展器_1_rs1 ), .in1(5'b10001), .out(multiplexer_1_out), .sel(\单周期硬布线控制器_1_beq [11]));
  Multiplexer #(.select(1), .width(5), .disabled("Z"), .enable("false")) multiplexer_2 (
    .in0(\气泡ir扩展器_1_rs2 ), .in1(5'b01010), .out(multiplexer_2_out), .sel(\单周期硬布线控制器_1_beq [11]));
  // Probe on EX_PC[11:0]
  // Probe on ID_PC[11:0]
  \重定向逻辑设计  \u_重定向逻辑设计_1  (
    .rs1_u(\单周期硬布线控制器_1_rs1 ), .bJump(bjump), .rs2_u(\单周期硬布线控制器_1_rs2 ), .J(J), .EX_RegWrite(EX_RegWrite),
    .MEM_RegWrite(MEM_RegWrite), .MemToReg(EX_MemToReg), .rs1(multiplexer_1_out),
    .EX_rd(\重定向流水线id_ex_1_ex_rd ), .MEM_rd(\气泡ex_mem_1_mem_rd ), .rs2(multiplexer_2_out), .Jpop(Jpop),
    .LoadUse(LoadUse), .fwdb(\重定向逻辑设计_1_fwdb ), .fwda(\重定向逻辑设计_1_fwda ));
  Counter #(.width(16), .max('hffff), .ongoal("wrap"), .trigger("rising"), .behavior("old")) counter_1 (
    .count(halt), .Q(\总周期数 ), .clk(CLK), .clr(RST));  // open: load, D, carry, preset
  // Probe on M_PC[11:0]
  D_Flip_Flop #(.trigger("high"), .Pre_Clr_Positions("LEGACY"), .NegatePresetClear("false"), .enable("true"), .NewFFLayout("false")) d_ff_1 (.Q(d_ff_1_q));  // open: clk, D, Qn, preset, en, reset
  // Probe on 13'h342
  Regifile regifile_1 (
    .Din(RDin), .Clk(CLK), .R1(regifile_1_r1), .R2(regifile_1_r2), .WE(RegWrite), .W_num(WB_rd),
    .R1_num(multiplexer_1_out), .R2_num(multiplexer_2_out));
  // Probe on WB_PC[11:0]
  Comparator #(.width(13), .mode("twosComplement")) comparator_1 (
    .a(CNT_num), .b(13'h342), .eq(comparator_1_eq), .lt(comparator_1_lt));  // open: gt
  Clock #(.highDuration(1), .lowDuration(1)) clock_2 (.out(clock_2_out));
  and and_3 (and_3_out, halt, J);
  nand nand_1 (nand_1_out, d_ff_1_q, comparator_1_eq);
  Counter #(.width(13), .max('h1fff), .ongoal("stay"), .trigger("rising"), .behavior("old")) counter_2 (
    .count(comparator_1_lt), .Q(CNT_num), .clk(clock_2_out));  // open: load, D, carry, clr, preset
  \重定向流水线ID_EX  \u_重定向流水线id_ex_1  (
    .ID_rd(\气泡ir扩展器_1_rd ), .ID_a(regifile_1_r1), .ID_b(regifile_1_r2), .ID_imm(\气泡ir扩展器_1_imm ),
    .ID_imm_B(\气泡ir扩展器_1_imm_b ), .ID_imm_Jal(\气泡ir扩展器_1_imm_jal ), .ID_imm_Lui(\气泡ir扩展器_1_imm_lui ),
    .ID_PC(ID_PC), .ID_IR(ID_IR),
    .ID_sgn({Lui, Lbu, Jalr, Jal, \单周期硬布线控制器_1_beq [11:9], \单周期硬布线控制器_1_alu_op , \单周期硬布线控制器_1_beq [4:1], Bge}),
    .EX_rd(\重定向流水线id_ex_1_ex_rd ), .EX_a(\重定向流水线id_ex_1_ex_a ), .EX_b(\重定向流水线id_ex_1_ex_b ),
    .EX_imm(\重定向流水线id_ex_1_ex_imm ), .EX_imm_B(\重定向流水线id_ex_1_ex_imm_b ),
    .EX_imm_Jal(\重定向流水线id_ex_1_ex_imm_jal ), .EX_imm_Lui(\重定向流水线id_ex_1_ex_imm_lui ), .EX_PC(EX_PC),
    .EX_IR(EX_IR), .EX_FwdA(\重定向流水线id_ex_1_ex_fwda ), .EX_FwdB(\重定向流水线id_ex_1_ex_fwdb ),
    .EX_sgn({\重定向流水线id_ex_1_ex_sgn [15:11], EX_RegWrite, \重定向流水线id_ex_1_ex_sgn [9:4], EX_MemToReg, \重定向流水线id_ex_1_ex_sgn [2:0]}),
    .clk(CLK), .rst(or_2_out), .halt(halt), .ID_FwdB(\重定向逻辑设计_1_fwdb ), .ID_FwdA(\重定向逻辑设计_1_fwda ));
  Counter #(.width(16), .max('hffff), .ongoal("wrap"), .trigger("rising"), .behavior("old")) counter_3 (
    .count(and_3_out), .Q(\无条件分支数 ), .clk(CLK), .clr(RST));  // open: load, D, carry, preset
  assign CLK = nand_1_out ? clock_2_out : 1'bz;  // Controlled_Buffer controlled_buffer_1
  Multiplexer #(.select(2), .width(32), .disabled("Z"), .enable("false")) multiplexer_3 (
    .in0(\重定向流水线id_ex_1_ex_a ), .in1(RDin), .in2(multiplexer_7_out), .out(multiplexer_3_out),
    .sel(\重定向流水线id_ex_1_ex_fwda ));  // open: in3
  Multiplexer #(.select(2), .width(32), .disabled("Z"), .enable("false")) multiplexer_4 (
    .in0(\重定向流水线id_ex_1_ex_b ), .in1(RDin), .in2(multiplexer_7_out), .out(multiplexer_4_out),
    .sel(\重定向流水线id_ex_1_ex_fwdb ));  // open: in3
  Pull_Resistor #(.pull(1)) pull_resistor_1 (.node(CLK));
  or or_2 (or_2_out, LoadUse, RST, Jpop);
  Counter #(.width(16), .max('hffff), .ongoal("wrap"), .trigger("rising"), .behavior("old")) counter_4 (
    .count(and_4_out), .Q(\条件分支成功数 ), .clk(CLK), .clr(RST));  // open: load, D, carry, preset
  and and_4 (and_4_out, halt, bjump);
  Multiplexer #(.select(1), .width(32), .disabled("Z"), .enable("false")) multiplexer_5 (
    .in0(multiplexer_4_out), .in1(\重定向流水线id_ex_1_ex_imm ), .out(multiplexer_5_out),
    .sel(\重定向流水线id_ex_1_ex_sgn [9]));
  Multiplexer #(.select(1), .width(32), .disabled("Z"), .enable("false")) multiplexer_6 (
    .in0(multiplexer_5_out), .in1(32'ha), .out(multiplexer_6_out), .sel(\重定向流水线id_ex_1_ex_sgn [11]));
  ALU alu_1 (
    .X(multiplexer_3_out), .Y(multiplexer_6_out), .AluOP(\重定向流水线id_ex_1_ex_sgn [8:5]), .Equal(alu_1_equal),
    .Result(alu_1_result), .out_4(alu_1_out_4));  // open: Result_2, out_6
  Adder #(.width(32)) adder_2 (.a(EX_PC), .b(\重定向流水线id_ex_1_ex_imm_b ), .out(bAddr));  // open: cin, cout
  \条件分支逻辑设计  \u_条件分支逻辑设计_1  (
    .Bge(\重定向流水线id_ex_1_ex_sgn [0]), .in_4(alu_1_equal), .Beq(\重定向流水线id_ex_1_ex_sgn [1]), .in_2(alu_1_out_4),
    .Bne(\重定向流水线id_ex_1_ex_sgn [2]), .branchtaken(bjump));
  or or_3 (J, \重定向流水线id_ex_1_ex_sgn [12], \重定向流水线id_ex_1_ex_sgn [13]);
  and and_5 (and_5_out, halt, LoadUse);
  Counter #(.width(16), .max('hffff), .ongoal("wrap"), .trigger("rising"), .behavior("old")) counter_5 (
    .count(and_5_out), .Q(\LoadUse次数 ), .clk(CLK), .clr(RST));  // open: load, D, carry, preset
  \无条件跳转逻辑设计  \u_无条件跳转逻辑设计_1  (
    .JAL(\重定向流水线id_ex_1_ex_sgn [12]), .JALR(\重定向流水线id_ex_1_ex_sgn [13]), .JALR_Addr(alu_1_result),
    .JAL_Addr(\重定向流水线id_ex_1_ex_imm_jal ), .J_Addr(jAddr), .PC(EX_PC));
  Counter #(.width(16), .max('hffff), .ongoal("wrap"), .trigger("rising"), .behavior("old")) counter_6 (
    .count(and_6_out), .Q(\插入气泡数 ), .clk(CLK));  // open: load, D, carry, clr, preset
  and and_6 (and_6_out, halt, Jpop);
  \气泡EX_MEM  \u_气泡ex_mem_1  (
    .EX_rd(\重定向流水线id_ex_1_ex_rd ), .EX_PC(EX_PC), .EX_IR(EX_IR), .EX_ALU_R(alu_1_result),
    .EX_imm_Lui(\重定向流水线id_ex_1_ex_imm_lui ),
    .EX_sgn({\重定向流水线id_ex_1_ex_sgn [15:11], EX_RegWrite, \重定向流水线id_ex_1_ex_sgn [9:4], EX_MemToReg, \重定向流水线id_ex_1_ex_sgn [2:0]}),
    .MEM_rd(\气泡ex_mem_1_mem_rd ), .MEM_PC(M_PC), .MEM_IR(MEM_IR), .MEM_ALU_R(\气泡ex_mem_1_mem_alu_r ),
    .MEM_imm_Lui(\气泡ex_mem_1_mem_imm_lui ),
    .MEM_sgn({MEM_Lui, \气泡ex_mem_1_mem_sgn [14:11], MEM_RegWrite, \气泡ex_mem_1_mem_sgn [9:5], MemWrite, \气泡ex_mem_1_mem_sgn [3:0]}),
    .rst(RST), .halt(halt), .clk(CLK), .EX_MDin(multiplexer_4_out), .MEM_MDin(MDin), .EX_Equal(alu_1_equal),
    .MEM_Equal(\气泡ex_mem_1_mem_equal ));
  not not_3 (not_3_out, MemWrite);
  RAM #(.addrWidth(10), .dataWidth(32), .bus("separate"), .Select("high")) ram_1 (
    .addr(\气泡ex_mem_1_mem_alu_r [11:2]), .din(MDin), .data(ram_1_data), .str(MemWrite), .clk(CLK),
    .ld(not_3_out));  // open: sel, clr
  and and_7 (and_7_out, Ecall, Equal);
  and and_8 (and_8_out, Ecall, not_4_out);
  not not_4 (not_4_out, Equal);
  assign bit_extender_1_out = {{3{1'b0}}, \气泡ex_mem_1_mem_alu_r [1:0]};  // Bit_Extender bit_extender_1
  Subtractor #(.width(5)) subtractor_1 (.a(5'b11000), .b(minus), .out(subtractor_1_out));  // open: bin, bout
  Multiplexer #(.select(1), .width(32), .disabled("Z"), .enable("false")) multiplexer_7 (
    .in0(\气泡ex_mem_1_mem_alu_r ), .in1(\气泡ex_mem_1_mem_imm_lui ), .out(multiplexer_7_out), .sel(MEM_Lui));
  not not_5 (not_5_out, and_7_out);
  Shifter #(.width(5), .shift("ll")) shifter_1 (.in(bit_extender_1_out), .\dist (3'b011), .out(minus));
  Shifter #(.width(32), .shift("ll")) shifter_2 (.in(ram_1_data), .\dist (subtractor_1_out), .out(shifter_2_out));
  Shifter #(.width(32), .shift("lr")) shifter_3 (.in(shifter_2_out), .\dist (5'b11000), .out(shifter_3_out));
  or or_4 (halt, Go, not_5_out);
  Register #(.width(32), .trigger("rising"), .Select("low")) register_1 (
    .D(LedShow), .en(and_8_out), .Q(LedData), .clk(CLK));  // open: clr
  Multiplexer #(.select(1), .width(32), .disabled("Z"), .enable("false")) multiplexer_8 (
    .in0(ram_1_data), .in1(shifter_3_out), .out(multiplexer_8_out), .sel(\气泡ex_mem_1_mem_sgn [14]));
  Multiplexer #(.select(1), .width(32), .disabled("Z"), .enable("false")) multiplexer_9 (
    .in0(multiplexer_7_out), .in1(multiplexer_8_out), .out(multiplexer_9_out), .sel(\气泡ex_mem_1_mem_sgn [3]));
  \气泡MEM_WB  \u_气泡mem_wb_1  (
    .MEM_rd(\气泡ex_mem_1_mem_rd ), .MEM_PC(M_PC), .MEM_IR(MEM_IR), .MEM_ALU_MD(multiplexer_9_out),
    .MEM_sgn({MEM_Lui, \气泡ex_mem_1_mem_sgn [14:11], MEM_RegWrite, \气泡ex_mem_1_mem_sgn [9:5], MemWrite, \气泡ex_mem_1_mem_sgn [3:0]}),
    .WB_rd(WB_rd), .WB_PC(WB_PC), .WB_IR(WB_IR), .WB_ALU_MD(\气泡mem_wb_1_wb_alu_md ),
    .WB_sgn({\气泡mem_wb_1_wb_sgn [15:12], Ecall, RegWrite, \气泡mem_wb_1_wb_sgn [9:0]}), .rst(RST), .halt(halt),
    .clk(CLK), .MEM_Equal(\气泡ex_mem_1_mem_equal ), .WB_Equal(Equal), .MEM_LED(MDin), .WB_LED(LedShow));
  Adder #(.width(32)) adder_3 (.a(WB_PC), .b(32'h4), .out(adder_3_out));  // open: cin, cout
  or or_5 (or_5_out, \气泡mem_wb_1_wb_sgn [13], \气泡mem_wb_1_wb_sgn [12]);
  Multiplexer #(.select(1), .width(32), .disabled("Z"), .enable("false")) multiplexer_10 (
    .in0(\气泡mem_wb_1_wb_alu_md ), .in1(adder_3_out), .out(RDin), .sel(or_5_out));

  // Other names for the same wires on the sheet: MEM_PC[31:0] = M_PC

  // Notes on the sheet:
  //   中断源
  //   时空图监测，可删除
  //   中断等待指示
  //   数码管输出
  //   指令存储器
  //   contents of rom_1 (hex, n*v repeats v):
  //   100493 100006f 100493 200913 300993 100006f 100493 200913 300993 100006f 100493 200913 300993
  //   100006f 100493 200913 300993 3d0000ef 100413 100493 1f49493 900533 2200893 73 24d493 48463 fedff06f
  //   900533 2200893 73 100493 249493 900533 2200893 73 48463 fedff06f 100493 1f49493 900533 2200893 73
  //   4034d493 900533 2200893 73 4044d493 900533 2200893 73 4044d493 900533 2200893 73 4044d493 900533
  //   2200893 73 4044d493 900533 2200893 73 4044d493 900533 2200893 73 4044d493 900533 2200893 73 4044d493
  //   900533 2200893 73 100413 1f41993 41f9d993 433 c00913 300b13 140413 f47413 800293 100313 499993
  //   89e9b3 1300533 2200893 73 406282b3 fe0294e3 140413 f00f93 1f47433 1c41413 800293 100313 49d993
  //   89e9b3 1300533 2200893 73 406282b3 fe0294e3 1c45413 406b0b33 b0463 f95ff06f 2b3 fff2c293 829293
  //   ff2e293 500533 2200893 73 fff00413 493 84a023 140413 448493 84a023 140413 448493 84a023 140413
  //   448493 84a023 140413 448493 84a023 140413 448493 84a023 140413 448493 84a023 140413 448493 84a023
  //   140413 448493 84a023 140413 448493 84a023 140413 448493 84a023 140413 448493 84a023 140413 448493
  //   84a023 140413 448493 84a023 140413 448493 84a023 140413 448493 84a023 140413 448493 140413 433
  //   3c00493 42983 4aa03 149a2b3 28663 134a023 1442023 ffc48493 fe9412e3 800533 2200893 73 440413 3c00493
  //   fc9416e3 a00893 73 fff00293 7700493 849493 7748493 900533 2200893 73 1000e13 54c4b3 900533 2200893
  //   73 fffe0e13 fe0e16e3 a00893 73 800e13 fedc04b7 fff00413 1045413 84e4b3 900533 2200893 73 ba984b7
  //   900533 73 76544b7 900533 73 32104b7 900533 73 fffe0e13 fa0e1ee3 a00893 73 313 1000e13 8400493 849493
  //   8348493 400913 891913 490913 849493 8248493 849493 8148493 891913 490913 891913 490913 932023
  //   12484b3 430313 fffe0e13 fe0e18e3 2000e13 313 34483 900533 2200893 73 130313 fffe0e13 fe0e14e3 a00893
  //   73 f00493 900533 2200893 73 fff48493 fe04d8e3 a00893 73 413 140413 800533 2200893 73 240413 800533
  //   2200893 73 340413 800533 2200893 73 440413 800533 2200893 73 540413 800533 2200893 73 640413 800533
  //   2200893 73 740413 800533 2200893 73 840413 800533 2200893 2200893 73 8067
  //   跳转需要清除IF和ID的误取指令，连接reset同步清零
  //   控制位
  //   流水调试日志用
  //   暂停节拍，不能为0
  //   戳工具置1进入计数暂停模式，ctrl+k时钟自动运行到对应节拍暂停
  //   ctrl+k关闭时钟连续运行，将控制位置零，进入单步调试模式调试
  //   数据记录
  //   可计数暂停的时钟源
  //   instruction分配关系
  //   0：Bge指令
  //   1：Beq指令
  //   2：Bne指令
  //   10：RegWrite信号
  //   14：Lbu信号
  //   为方便自动评测，需要输出流水线各段保存的PC值，注意是PC不是PC+4，另外ID段寄存器写入信息，Mem段内存写入信息也要输出
  //   3：MemToReg信号
  //   4：MemWrite信号
  //   11：Ecall信号
  //   15：Lui信号
  //   此处不论是跳转还是数据冲突都需要产生气泡，因此都需要连接reset同步清零
  //   5-8：AluOP信号
  //   9：Alu_src信号
  //   12：Jal信号
  //   13：Jalr信号
  //   数据存储器
  //   Ecall选项
endmodule

// 重定向逻辑
module \重定向逻辑设计  (
  input  rs1_u,
  input  bJump,
  input  rs2_u,
  input  J,
  input  EX_RegWrite,
  input  MEM_RegWrite,
  input  MemToReg,
  input  [4:0] rs1,
  input  [4:0] EX_rd,
  input  [4:0] MEM_rd,
  input  [4:0] rs2,
  output Jpop,
  output LoadUse,
  output [1:0] fwdb,
  output [1:0] fwda
);

  wire and_1_out, and_2_out, comparator_1_eq, comparator_2_eq, not_3_out, not_4_out, rs1__0, rs1_EX_rd,
       rs1_MEM_rd, rs2__0, rs2_EX_rd, rs2_MEM_rd;

  or or_1 (Jpop, bJump, J);
  Comparator #(.width(5), .mode("twosComplement")) comparator_1 (
    .a(rs1), .b({5{1'b0}}), .eq(comparator_1_eq));  // open: gt, lt
  Comparator #(.width(5), .mode("twosComplement")) comparator_2 (
    .a(rs2), .b({5{1'b0}}), .eq(comparator_2_eq));  // open: gt, lt
  not not_1 (rs1__0, comparator_1_eq);
  not not_2 (rs2__0, comparator_2_eq);
  and and_1 (and_1_out, rs1_u, rs1__0, rs1_EX_rd, MemToReg);
  and and_2 (and_2_out, rs2_u, rs2__0, rs2_EX_rd, MemToReg);
  Comparator #(.width(5), .mode("twosComplement")) comparator_3 (.a(rs1), .b(EX_rd), .eq(rs1_EX_rd));  // open: gt, lt
  Comparator #(.width(5), .mode("twosComplement")) comparator_4 (.a(rs1), .b(MEM_rd), .eq(rs1_MEM_rd));  // open: gt, lt
  Comparator #(.width(5), .mode("twosComplement")) comparator_5 (.a(rs2), .b(EX_rd), .eq(rs2_EX_rd));  // open: gt, lt
  Comparator #(.width(5), .mode("twosComplement")) comparator_6 (.a(rs2), .b(MEM_rd), .eq(rs2_MEM_rd));  // open: gt, lt
  or or_2 (LoadUse, and_1_out, and_2_out);
  not not_3 (not_3_out, fwdb[1]);
  and and_3 (fwdb[1], rs2_u, rs2__0, rs2_EX_rd, EX_RegWrite);
  not not_4 (not_4_out, fwda[1]);
  and and_4 (fwda[1], rs1_u, rs1__0, rs1_EX_rd, EX_RegWrite);
  and and_5 (fwdb[0], rs2_u, rs2__0, not_3_out, rs2_MEM_rd, MEM_RegWrite);
  and and_6 (fwda[0], rs1_u, rs1__0, not_4_out, rs1_MEM_rd, MEM_RegWrite);
endmodule

// ID/EX
module \重定向流水线ID_EX  (
  input  [4:0] ID_rd,
  input  [31:0] ID_a,
  input  [31:0] ID_b,
  input  [31:0] ID_imm,
  input  [31:0] ID_imm_B,
  input  [31:0] ID_imm_Jal,
  input  [31:0] ID_imm_Lui,
  input  [31:0] ID_PC,
  input  [31:0] ID_IR,
  input  [1:0] ID_FwdA,
  input  [1:0] ID_FwdB,
  input  [15:0] ID_sgn,
  input  clk,
  input  rst,
  input  halt,
  output [4:0] EX_rd,
  output [31:0] EX_a,
  output [31:0] EX_b,
  output [31:0] EX_imm,
  output [31:0] EX_imm_B,
  output [31:0] EX_imm_Jal,
  output [31:0] EX_imm_Lui,
  output [31:0] EX_PC,
  output [31:0] EX_IR,
  output [1:0] EX_FwdA,
  output [1:0] EX_FwdB,
  output [15:0] EX_sgn
);

  wire [1:0] multiplexer_10_out, multiplexer_11_out;
  wire [4:0] multiplexer_1_out;
  wire [15:0] multiplexer_12_out;
  wire [31:0] multiplexer_2_out, multiplexer_3_out, multiplexer_4_out, multiplexer_5_out, multiplexer_6_out,
       multiplexer_7_out, multiplexer_8_out, multiplexer_9_out;

  Multiplexer #(.select(1), .width(5), .disabled("Z"), .enable("false")) multiplexer_1 (
    .in0(ID_rd), .in1({5{1'b0}}), .out(multiplexer_1_out), .sel(rst));
  Multiplexer #(.select(1), .width(32), .disabled("Z"), .enable("false")) multiplexer_2 (
    .in0(ID_a), .in1({32{1'b0}}), .out(multiplexer_2_out), .sel(rst));
  Multiplexer #(.select(1), .width(32), .disabled("Z"), .enable("false")) multiplexer_3 (
    .in0(ID_b), .in1({32{1'b0}}), .out(multiplexer_3_out), .sel(rst));
  Multiplexer #(.select(1), .width(32), .disabled("Z"), .enable("false")) multiplexer_4 (
    .in0(ID_imm), .in1({32{1'b0}}), .out(multiplexer_4_out), .sel(rst));
  Multiplexer #(.select(1), .width(32), .disabled("Z"), .enable("false")) multiplexer_5 (
    .in0(ID_imm_B), .in1({32{1'b0}}), .out(multiplexer_5_out), .sel(rst));
  Multiplexer #(.select(1), .width(32), .disabled("Z"), .enable("false")) multiplexer_6 (
    .in0(ID_imm_Jal), .in1({32{1'b0}}), .out(multiplexer_6_out), .sel(rst));
  Multiplexer #(.select(1), .width(32), .disabled("Z"), .enable("false")) multiplexer_7 (
    .in0(ID_imm_Lui), .in1({32{1'b0}}), .out(multiplexer_7_out), .sel(rst));
  Multiplexer #(.select(1), .width(32), .disabled("Z"), .enable("false")) multiplexer_8 (
    .in0(ID_PC), .in1({32{1'b0}}), .out(multiplexer_8_out), .sel(rst));
  Multiplexer #(.select(1), .width(32), .disabled("Z"), .enable("false")) multiplexer_9 (
    .in0(ID_IR), .in1({32{1'b0}}), .out(multiplexer_9_out), .sel(rst));
  Multiplexer #(.select(1), .width(2), .disabled("Z"), .enable("false")) multiplexer_10 (
    .in0(ID_FwdA), .in1(2'b00), .out(multiplexer_10_out), .sel(rst));
  Multiplexer #(.select(1), .width(2), .disabled("Z"), .enable("false")) multiplexer_11 (
    .in0(ID_FwdB), .in1(2'b00), .out(multiplexer_11_out), .sel(rst));
  Multiplexer #(.select(1), .width(16), .disabled("Z"), .enable("false")) multiplexer_12 (
    .in0(ID_sgn), .in1({16{1'b0}}), .out(multiplexer_12_out), .sel(rst));
  Register #(.width(5), .trigger("rising"), .Select("low")) register_1 (
    .D(multiplexer_1_out), .en(halt), .Q(EX_rd), .clk(clk));  // open: clr
  Register #(.width(32), .trigger("rising"), .Select("low")) register_2 (
    .D(multiplexer_2_out), .en(halt), .Q(EX_a), .clk(clk));  // open: clr
  Register #(.width(32), .trigger("rising"), .Select("low")) register_3 (
    .D(multiplexer_3_out), .en(halt), .Q(EX_b), .clk(clk));  // open: clr
  Register #(.width(32), .trigger("rising"), .Select("low")) register_4 (
    .D(multiplexer_4_out), .en(halt), .Q(EX_imm), .clk(clk));  // open: clr
  Register #(.width(32), .trigger("rising"), .Select("low")) register_5 (
    .D(multiplexer_5_out), .en(halt), .Q(EX_imm_B), .clk(clk));  // open: clr
  Register #(.width(32), .trigger("rising"), .Select("low")) register_6 (
    .D(multiplexer_6_out), .en(halt), .Q(EX_imm_Jal), .clk(clk));  // open: clr
  Register #(.width(32), .trigger("rising"), .Select("low")) register_7 (
    .D(multiplexer_7_out), .en(halt), .Q(EX_imm_Lui), .clk(clk));  // open: clr
  Register #(.width(32), .trigger("rising"), .Select("low")) register_8 (
    .D(multiplexer_8_out), .en(halt), .Q(EX_PC), .clk(clk));  // open: clr
  Register #(.width(32), .trigger("rising"), .Select("low")) register_9 (
    .D(multiplexer_9_out), .en(halt), .Q(EX_IR), .clk(clk));  // open: clr
  Register #(.width(2), .trigger("rising"), .Select("low")) register_10 (
    .D(multiplexer_10_out), .en(halt), .Q(EX_FwdA), .clk(clk));  // open: clr
  Register #(.width(2), .trigger("rising"), .Select("low")) register_11 (
    .D(multiplexer_11_out), .en(halt), .Q(EX_FwdB), .clk(clk));  // open: clr
  Register #(.width(16), .trigger("rising"), .Select("low")) register_12 (
    .D(multiplexer_12_out), .en(halt), .Q(EX_sgn), .clk(clk));  // open: clr
endmodule

module \中断按键参考电路  (
  input  \同步清零信号 ,
  output \与中断屏蔽位与 
);

  wire \_1号中断_out , and_1_out, clock_1_out, d_ff_1_q, or_1_out, or_2_out;

  Clock #(.highDuration(1), .lowDuration(1)) clock_1 (.out(clock_1_out));
  Button \_1号中断  (.out(\_1号中断_out ));
  LED #(.active("true")) \_1号中断等待指示灯  (.in(or_1_out));
  or or_1 (or_1_out, \与中断屏蔽位与 , d_ff_1_q);
  D_Flip_Flop #(.trigger("rising"), .Pre_Clr_Positions("LEGACY"), .NegatePresetClear("false"), .enable("true"), .NewFFLayout("false")) d_ff_1 (
    .clk(\_1号中断_out ), .D(1'b1), .Q(d_ff_1_q), .reset(\与中断屏蔽位与 ));  // open: Qn, preset, en
  or or_2 (or_2_out, d_ff_1_q, \与中断屏蔽位与 );
  and and_1 (and_1_out, or_2_out, ~\同步清零信号 );  // AND_Gate
  D_Flip_Flop #(.trigger("rising"), .Pre_Clr_Positions("LEGACY"), .NegatePresetClear("false"), .enable("true"), .NewFFLayout("false")) IR1 (
    .clk(clock_1_out), .D(and_1_out), .Q(\与中断屏蔽位与 ));  // open: Qn, preset, en, reset

  // Notes on the sheet:
  //   中断信号采样参考电路
  //   Reset 
endmodule

module \单周期_单级中断  (
  input  IR1,
  input  IR2,
  input  IR3,
  output RegWrite,
  output MemWrite,
  output [31:0] PC,
  output [31:0] IR,
  output [31:0] RDin,
  output [31:0] MDin,
  output [31:0] LedData
);

  wire and_1_out, and_2_out, and_3_out, and_4_out, and_5_out, and_6_out, and_7_out, and_11_out, and_12_out,
       Beq, Bge, Bne, CLK, com_pc, comparator_1_eq, comparator_2_eq, comparator_3_eq, comparator_4_eq,
       d_ff_1_q, d_ff_2_q, d_ff_3_q, decoder_1_out1, decoder_1_out2, decoder_1_out3, Ecall, Equal, Go, halt,
       IE, INT, IR1_q, IR1_t, IR2_q, IR2_t, IR3_q, IR3_t, IRA, IRB, IRC, ISIR, JAL, JALR, Lbu, Lui,
       not_1_out, not_2_out, not_4_out, not_5_out, or_1_out, or_7_out, or_8_out, or_9_out, or_12_out,
       register_2_q, rst1, rst2, rst3, S, tunnel, Uret, W1, W2, W3, \单周期硬布线控制器_1_alu_src ,
       \单周期硬布线控制器_1_memtoreg ;
  wire [1:0] cause_q, priority_encoder_1_out;
  wire [3:0] \单周期硬布线控制器_1_alu_op ;
  wire [4:0] bit_extender_5_out, minus, multiplexer_6_out, multiplexer_7_out, subtractor_1_out;
  wire [11:0] multiplexer_8_out;
  wire [15:0] \总周期数 ;
  wire [31:0] adder_2_out, bit_extender_1_out, bit_extender_2_out, bit_extender_3_out, bit_extender_4_out,
       calc, INTPC, multiplexer_1_out, multiplexer_2_out, multiplexer_3_out, multiplexer_5_out,
       multiplexer_10_out, multiplexer_11_out, multiplexer_12_out, multiplexer_14_out, multiplexer_15_out,
       NEXTPC, PC_4, ram_1_data, regifile_1_r1, RETPC, shifter_1_out, shifter_2_out, shifter_3_out,
       shifter_4_out;

  Clock #(.highDuration(1), .lowDuration(1)) clock_1 (.out(CLK));
  Button _1 ();  // open: out
  Button _2 ();  // open: out
  Button _3 ();  // open: out
  Button \u_继续运行  (.out(Go));
  LED #(.active("true")) led_1 (.in(W1));
  LED #(.active("true")) led_2 (.in(W2));
  LED #(.active("true")) led_3 (.in(W3));
  Multiplexer #(.select(1), .width(32), .disabled("Z"), .enable("false")) multiplexer_1 (
    .in0(NEXTPC), .in1(INTPC), .out(multiplexer_1_out), .sel(INT));
  Hex_Digit_Display hex_digit_display_1 (.value(LedData[31:28]));  // open: dp
  Comparator #(.width(16), .mode("twosComplement")) comparator_1 (
    .a(16'h23b), .b(\总周期数 ), .eq(comparator_1_eq));  // open: gt, lt
  or or_1 (or_1_out, comparator_1_eq, comparator_2_eq);
  Comparator #(.width(16), .mode("twosComplement")) comparator_2 (
    .a(\总周期数 ), .b(16'h1), .eq(comparator_2_eq));  // open: gt, lt
  Comparator #(.width(16), .mode("twosComplement")) comparator_3 (
    .a(\总周期数 ), .b(16'h4), .eq(comparator_3_eq));  // open: gt, lt
  Comparator #(.width(16), .mode("twosComplement")) comparator_4 (
    .a(\总周期数 ), .b(16'h7), .eq(comparator_4_eq));  // open: gt, lt
  Counter #(.width(16), .max('hffff), .ongoal("wrap"), .trigger("rising"), .behavior("old")) counter_1 (
    .count(halt), .Q(\总周期数 ), .clk(CLK));  // open: load, D, carry, clr, preset
  Multiplexer #(.select(1), .width(32), .disabled("Z"), .enable("false")) multiplexer_2 (
    .in0(multiplexer_1_out), .in1(RETPC), .out(multiplexer_2_out), .sel(Uret));
  assign bit_extender_1_out = {{20{IR[31]}}, {IR[31], IR[7], IR[30:25], IR[11:8]}};  // Bit_Extender bit_extender_1
  assign bit_extender_2_out = {{12{IR[31]}}, {IR[31], IR[19:12], IR[20], IR[30:21]}};  // Bit_Extender bit_extender_2
  not not_1 (not_1_out, Equal);
  Hex_Digit_Display hex_digit_display_2 (.value(LedData[23:20]));  // open: dp
  Hex_Digit_Display hex_digit_display_3 (.value(LedData[27:24]));  // open: dp
  Pull_Resistor #(.pull(0)) pull_resistor_1 (.node(IRA));
  assign IRA = or_1_out ? ~CLK : 1'bz;  // Controlled_Inverter controlled_inverter_1
  Pull_Resistor #(.pull(0)) pull_resistor_2 (.node(IRB));
  assign IRB = comparator_3_eq ? ~CLK : 1'bz;  // Controlled_Inverter controlled_inverter_2
  Pull_Resistor #(.pull(0)) pull_resistor_3 (.node(IRC));
  assign IRC = comparator_4_eq ? ~CLK : 1'bz;  // Controlled_Inverter controlled_inverter_3
  Register #(.width(32), .trigger("rising"), .Select("low")) u_PC (
    .D(multiplexer_2_out), .en(halt), .Q(PC), .clk(CLK));  // open: clr
  Multiplexer #(.select(1), .width(32), .disabled("Z"), .enable("false")) multiplexer_3 (
    .in0(bit_extender_1_out), .in1(bit_extender_2_out), .out(multiplexer_3_out), .sel(JAL));
  and and_1 (and_1_out, Beq, Equal);
  and and_2 (and_2_out, not_1_out, Bne);
  and and_3 (and_3_out, Bge, tunnel);
  Hex_Digit_Display hex_digit_display_4 (.value(LedData[19:16]));  // open: dp
  Hex_Digit_Display hex_digit_display_5 (.value(LedData[15:12]));  // open: dp
  Adder #(.width(32)) adder_1 (.a(PC), .b(32'h4), .out(PC_4));  // open: cin, cout
  Shifter #(.width(32), .shift("ll")) shifter_1 (.in(multiplexer_3_out), .\dist (5'b00001), .out(shifter_1_out));
  Multiplexer #(.select(1), .width(32), .disabled("Z"), .enable("false")) multiplexer_4 (
    .in0(multiplexer_5_out), .in1(calc), .out(NEXTPC), .sel(JALR));
  or or_2 (com_pc, JAL, and_1_out, and_2_out, and_3_out);
  Hex_Digit_Display hex_digit_display_6 (.value(LedData[11:8]));  // open: dp
  Hex_Digit_Display hex_digit_display_7 (.value(LedData[7:4]));  // open: dp
  // Probe on \总周期数 
  // RiscV_Probe riscv_probe_1: pin names not known; wires that end beside it: IR
  ROM #(.addrWidth(10), .dataWidth(32), .Select("high")) rom_1 (.addr(PC[11:2]), .data(IR));
  Adder #(.width(32)) adder_2 (.a(PC), .b(shifter_1_out), .out(adder_2_out));  // open: cin, cout
  Hex_Digit_Display hex_digit_display_8 (.value(LedData[3:0]));  // open: dp
  or or_3 (W1, IR1_q, d_ff_1_q);
  or or_4 (W2, IR2_q, d_ff_2_q);
  or or_5 (W3, IR3_q, d_ff_3_q);
  Multiplexer #(.select(1), .width(32), .disabled("Z"), .enable("false")) multiplexer_5 (
    .in0(PC_4), .in1(adder_2_out), .out(multiplexer_5_out), .sel(com_pc));
  D_Flip_Flop #(.trigger("rising"), .Pre_Clr_Positions("LEGACY"), .NegatePresetClear("false"), .enable("true"), .NewFFLayout("false")) d_ff_1 (
    .clk(IRA), .D(1'b1), .Q(d_ff_1_q), .reset(IR1_q));  // open: Qn, preset, en
  D_Flip_Flop #(.trigger("rising"), .Pre_Clr_Positions("LEGACY"), .NegatePresetClear("false"), .enable("true"), .NewFFLayout("false")) d_ff_2 (
    .clk(IRB), .D(1'b1), .Q(d_ff_2_q), .reset(IR2_q));  // open: Qn, preset, en
  D_Flip_Flop #(.trigger("rising"), .Pre_Clr_Positions("LEGACY"), .NegatePresetClear("false"), .enable("true"), .NewFFLayout("false")) d_ff_3 (
    .clk(IRC), .D(1'b1), .Q(d_ff_3_q), .reset(IR3_q));  // open: Qn, preset, en
  assign bit_extender_3_out = {{12{IR[31]}}, IR[31:12]};  // Bit_Extender bit_extender_3
  or or_6 (IR1_t, IR1, IRA);
  or or_7 (or_7_out, d_ff_1_q, IR1_q);
  and and_4 (and_4_out, or_7_out, ~rst1);  // AND_Gate
  or or_8 (or_8_out, d_ff_2_q, IR2_q);
  and and_5 (and_5_out, or_8_out, ~rst2);  // AND_Gate
  or or_9 (or_9_out, d_ff_3_q, IR3_q);
  and and_6 (and_6_out, or_9_out, ~rst3);  // AND_Gate
  \单周期硬布线控制器  \u_单周期硬布线控制器_1  (
    .Funct({IR[30], IR[25], IR[14:12]}), .OP(IR[6:2]), .ALU_OP(\单周期硬布线控制器_1_alu_op ),
    .MemToReg(\单周期硬布线控制器_1_memtoreg ), .MemWrite(MemWrite), .ALU_SRC(\单周期硬布线控制器_1_alu_src ),
    .RegWrite(RegWrite), .ecall(Ecall), .S_type(S), .Jalr(JALR), .Beq(Beq), .JAL(JAL), .Bne(Bne), .Lui(Lui),
    .Lbu(Lbu), .Bge(Bge), .uret(Uret), .IR21(IR[21]));  // open: rs1, rs2, csrrsi, csrrci
  Multiplexer #(.select(1), .width(5), .disabled("Z"), .enable("false")) multiplexer_6 (
    .in0(IR[19:15]), .in1(5'b10001), .out(multiplexer_6_out), .sel(Ecall));
  Multiplexer #(.select(1), .width(5), .disabled("Z"), .enable("false")) multiplexer_7 (
    .in0(IR[24:20]), .in1(5'b01010), .out(multiplexer_7_out), .sel(Ecall));
  Shifter #(.width(32), .shift("ll")) shifter_2 (.in(bit_extender_3_out), .\dist (5'b01100), .out(shifter_2_out));
  or or_10 (IR2_t, IR2, IRB);
  D_Flip_Flop #(.trigger("rising"), .Pre_Clr_Positions("LEGACY"), .NegatePresetClear("false"), .enable("true"), .NewFFLayout("false")) u_IR1 (
    .clk(CLK), .D(and_4_out), .Q(IR1_q));  // open: Qn, preset, en, reset
  D_Flip_Flop #(.trigger("rising"), .Pre_Clr_Positions("LEGACY"), .NegatePresetClear("false"), .enable("true"), .NewFFLayout("false")) u_IR2 (
    .clk(CLK), .D(and_5_out), .Q(IR2_q));  // open: Qn, preset, en, reset
  D_Flip_Flop #(.trigger("rising"), .Pre_Clr_Positions("LEGACY"), .NegatePresetClear("false"), .enable("true"), .NewFFLayout("false")) u_IR3 (
    .clk(CLK), .D(and_6_out), .Q(IR3_q));  // open: Qn, preset, en, reset
  Multiplexer #(.select(1), .width(12), .disabled("Z"), .enable("false")) multiplexer_8 (
    .in0(IR[31:20]), .in1({IR[31:25], IR[11:7]}), .out(multiplexer_8_out), .sel(S));
  Multiplexer #(.select(1), .width(32), .disabled("Z"), .enable("false")) multiplexer_9 (
    .in0(multiplexer_10_out), .in1(shifter_2_out), .out(RDin), .sel(Lui));
  Regifile regifile_1 (
    .Din(RDin), .Clk(CLK), .R1(regifile_1_r1), .R2(MDin), .WE(RegWrite), .W_num(IR[11:7]),
    .R1_num(multiplexer_6_out), .R2_num(multiplexer_7_out));
  assign bit_extender_4_out = {{20{multiplexer_8_out[11]}}, multiplexer_8_out};  // Bit_Extender bit_extender_4
  Multiplexer #(.select(1), .width(32), .disabled("Z"), .enable("false")) multiplexer_10 (
    .in0(multiplexer_14_out), .in1(shifter_4_out), .out(multiplexer_10_out), .sel(Lbu));
  or or_11 (IR3_t, IR3, IRC);
  Priority_Encoder #(.select(2), .disabled("Z")) priority_encoder_1 (
    .in0(1'b0), .in1(IR1_q), .in2(IR2_q), .in3(IR3_q), .out(priority_encoder_1_out), .gs(ISIR));  // open: en_out, en_in
  and and_7 (and_7_out, ISIR, IE);
  Multiplexer #(.select(1), .width(32), .disabled("Z"), .enable("false")) multiplexer_11 (
    .in0(MDin), .in1(bit_extender_4_out), .out(multiplexer_11_out), .sel(\单周期硬布线控制器_1_alu_src ));
  Multiplexer #(.select(1), .width(32), .disabled("Z"), .enable("false")) multiplexer_12 (
    .in0(multiplexer_11_out), .in1(32'ha), .out(multiplexer_12_out), .sel(Ecall));
  Register #(.width(2), .trigger("rising"), .Select("low")) cause (
    .D(priority_encoder_1_out), .Q(cause_q), .clk(INT));  // open: en, clr
  Multiplexer #(.select(2), .width(32), .disabled("Z"), .enable("false")) multiplexer_13 (
    .in1(32'h30ac), .in2(32'h3150), .in3(32'h31f4), .out(INTPC), .sel(priority_encoder_1_out));  // open: in0
  Register #(.width(1), .trigger("falling"), .Select("low")) register_1 (
    .D(and_7_out), .Q(INT), .clk(CLK));  // open: en, clr
  Subtractor #(.width(5)) subtractor_1 (.a(5'b11000), .b(minus), .out(subtractor_1_out));  // open: bin, bout
  Decoder #(.select(2), .tristate("false"), .disabled("Z"), .enable("false")) decoder_1 (
    .out1(decoder_1_out1), .out2(decoder_1_out2), .out3(decoder_1_out3), .sel(cause_q));  // open: out0
  ALU alu_1 (
    .X(regifile_1_r1), .Y(multiplexer_12_out), .AluOP(\单周期硬布线控制器_1_alu_op ), .Equal(Equal), .Result(calc),
    .out_4(tunnel));  // open: Result_2, out_6
  Shifter #(.width(32), .shift("ll")) shifter_3 (
    .in(multiplexer_14_out), .\dist (subtractor_1_out), .out(shifter_3_out));
  Shifter #(.width(32), .shift("lr")) shifter_4 (.in(shifter_3_out), .\dist (5'b11000), .out(shifter_4_out));
  not not_2 (not_2_out, Equal);
  and and_8 (rst1, Uret, decoder_1_out1);
  and and_9 (rst2, Uret, decoder_1_out2);
  and and_10 (rst3, decoder_1_out3, Uret);
  Register #(.width(32), .trigger("rising"), .Select("low")) EPC (
    .D(NEXTPC), .en(INT), .Q(RETPC), .clk(CLK));  // open: clr
  Register #(.width(1), .trigger("falling"), .Select("low")) register_2 (
    .D(1'b0), .en(Uret), .Q(register_2_q), .clk(CLK), .preset(INT));  // open: clr, cs
  not not_3 (IE, register_2_q);
  assign bit_extender_5_out = {{3{1'b0}}, calc[1:0]};  // Bit_Extender bit_extender_5
  Multiplexer #(.select(1), .width(32), .disabled("Z"), .enable("false")) multiplexer_14 (
    .in0(multiplexer_15_out), .in1(PC_4), .out(multiplexer_14_out), .sel(or_12_out));
  or or_12 (or_12_out, JAL, JALR);
  and and_11 (and_11_out, Ecall, Equal);
  and and_12 (and_12_out, Ecall, not_2_out);
  Shifter #(.width(5), .shift("ll")) shifter_5 (.in(bit_extender_5_out), .\dist (3'b011), .out(minus));
  RAM #(.addrWidth(10), .dataWidth(32), .bus("separate"), .Select("high")) ram_1 (
    .addr(calc[11:2]), .din(MDin), .data(ram_1_data), .str(MemWrite), .clk(CLK), .ld(not_4_out));  // open: sel, clr
  not not_4 (not_4_out, MemWrite);
  or or_13 (halt, Go, not_5_out);
  not not_5 (not_5_out, and_11_out);
  Register #(.width(32), .trigger("rising"), .Select("low")) register_3 (
    .D(MDin), .en(and_12_out), .Q(LedData), .clk(CLK));  // open: clr
  Multiplexer #(.select(1), .width(32), .disabled("Z"), .enable("false")) multiplexer_15 (
    .in0(calc), .in1(ram_1_data), .out(multiplexer_15_out), .sel(\单周期硬布线控制器_1_memtoreg ));

  // Other names for the same wires on the sheet: imm12_B[11:0] = {IR[31], IR[7], IR[30:25], IR[11:8]};
  //   imm20_JAL[19:0] = {IR[31], IR[19:12], IR[20], IR[30:21]}

  // Notes on the sheet:
  //   中断源
  //   中断等待指示
  //   总复位信号应将除ROM以外所有存储组件全部清零
  //   单级中断测试信号模拟器
  //   周期数记录
  //   计算新PC
  //   数码管输出
  //   指令存储器
  //   数码管输出应该用寄存器锁存，否则显示数据只能一闪而过
  //   contents of rom_1 (hex, n*v repeats v):
  //   7d000113 100413 1f41993 41f9d993 433 c00913 800b13 140413 f47413 800293 100313 499993 89e9b3 1300533
  //   2200893 73 406282b3 fe0294e3 140413 f00f93 1f47433 1c41413 800293 100313 49d993 89e9b3 1300533
  //   2200893 73 406282b3 fe0294e3 1c45413 406b0b33 b0463 f95ff06f 2b3 fff2c293 1029293 fff2e293 500533
  //   2200893 73 f5dff06f 1112023 410113 a12023 410113 812023 410113 1312023 410113 1412023 410113 1512023
  //   410113 1612023 410113 100b13 300a13 100a93 1600433 441413 14469b3 1300533 2200893 73 fe0416e3
  //   415a0a33 fe0a10e3 ffc10113 12b03 ffc10113 12a83 ffc10113 12a03 ffc10113 12983 ffc10113 12403
  //   ffc10113 12503 ffc10113 12883 200073 1112023 410113 a12023 410113 812023 410113 1312023 410113
  //   1412023 410113 1512023 410113 1612023 410113 200b13 300a13 100a93 1600433 441413 14469b3 1300533
  //   2200893 73 fe0416e3 415a0a33 fe0a10e3 ffc10113 12b03 ffc10113 12a83 ffc10113 12a03 ffc10113 12983
  //   ffc10113 12403 ffc10113 12503 ffc10113 12883 200073 1112023 410113 a12023 410113 812023 410113
  //   1312023 410113 1412023 410113 1512023 410113 1612023 410113 300b13 300a13 100a93 1600433 441413
  //   14469b3 1300533 2200893 73 fe0416e3 415a0a33 fe0a10e3 ffc10113 12b03 ffc10113 12a83 ffc10113 12a03
  //   ffc10113 12983 ffc10113 12403 ffc10113 12503 ffc10113 12883 200073
  //   指令字
  //   rs1
  //   rs2
  //   rd
  //   imm12 I
  //   imm12 S
  //   imm20 LUI
  //   Beq
  //   Bne
  //   MemToReg
  //   MemWrite
  //   AluOP
  //   AluSrcB
  //   RegWrite
  //   Reset 
  //   Reset 
  //   Reset 
  //   LBU stores the lowest byte
  //   为方便自动评测，需要输出PC，IR，寄存器堆写如数据RDin
  //   数据存储器
  //   Ecall选项
  //   RAM写使能MemWrite、RAM写入数据MDin等信号
endmodule

module \单周期_多级中断  (
  input  IR1,
  input  IR2,
  input  IR3,
  output RegWrite,
  output MemWrite,
  output [31:0] PC,
  output [31:0] IR,
  output [31:0] RDin,
  output [31:0] MDin,
  output [31:0] LedData
);

  wire and_1_out, and_2_out, and_3_out, and_4_out, and_5_out, and_6_out, and_7_out, and_8_out, and_9_out,
       and_10_out, and_11_out, and_12_out, Beq, Bge, Bne, CLK, com_pc, comparator_1_eq, comparator_2_eq,
       comparator_3_eq, comparator_4_eq, comparator_5_eq, csrrci, csrrsi, d_ff_1_q, d_ff_2_q, d_ff_3_q,
       decoder_1_out0, decoder_1_out1, decoder_1_out2, decoder_2_out1, decoder_2_out2, decoder_2_out3,
       decoder_3_out1, decoder_3_out2, decoder_3_out3, Ecall, Equal, Go, halt, IE, INT, IR1_q, IR1_t, IR2_q,
       IR2_t, IR3_q, IR3_t, IRA, IRB, IRC, JAL, JALR, Lbu, Lui, not_1_out, not_3_out, not_4_out, not_5_out,
       or_1_out, or_2_out, or_7_out, or_8_out, or_9_out, or_12_out, or_14_out, or_15_out, or_16_out, pHigh,
       register_2_q, rst1, rst2, rst3, S, tunnel, Uret, W1, W2, W3, \单周期硬布线控制器_1_alu_src ,
       \单周期硬布线控制器_1_memtoreg ;
  wire [1:0] cause0_q, cause1_q, cause2_q, counter_2_q, curCause, priority_encoder_1_out, subtractor_2_out;
  wire [3:0] \单周期硬布线控制器_1_alu_op ;
  wire [4:0] bit_extender_5_out, minus, multiplexer_6_out, multiplexer_7_out, subtractor_1_out;
  wire [11:0] multiplexer_8_out;
  wire [15:0] \总周期数 ;
  wire [31:0] adder_2_out, bit_extender_1_out, bit_extender_2_out, bit_extender_3_out, bit_extender_4_out,
       calc, INTPC, multiplexer_1_out, multiplexer_2_out, multiplexer_3_out, multiplexer_5_out,
       multiplexer_11_out, multiplexer_12_out, multiplexer_13_out, multiplexer_15_out, multiplexer_17_out,
       NEXTPC, PC_4, ram_1_data, regifile_1_r1, RETPC, RETPC1, RETPC2, RETPC3, shifter_1_out, shifter_2_out,
       shifter_3_out, shifter_4_out;

  Clock #(.highDuration(1), .lowDuration(1)) clock_1 (.out(CLK));
  Button _1 ();  // open: out
  Button _2 ();  // open: out
  Button _3 ();  // open: out
  Button \u_继续运行  (.out(Go));
  LED #(.active("true")) led_1 (.in(W1));
  LED #(.active("true")) led_2 (.in(W2));
  LED #(.active("true")) led_3 (.in(W3));
  Hex_Digit_Display hex_digit_display_1 (.value(LedData[31:28]));  // open: dp
  Comparator #(.width(16), .mode("twosComplement")) comparator_1 (
    .a(\总周期数 ), .b(16'h7), .eq(comparator_1_eq));  // open: gt, lt
  Comparator #(.width(16), .mode("twosComplement")) comparator_2 (
    .a(\总周期数 ), .b(16'h241), .eq(comparator_2_eq));  // open: gt, lt
  Multiplexer #(.select(1), .width(32), .disabled("Z"), .enable("false")) multiplexer_1 (
    .in0(NEXTPC), .in1(INTPC), .out(multiplexer_1_out), .sel(INT));
  Multiplexer #(.select(1), .width(32), .disabled("Z"), .enable("false")) multiplexer_2 (
    .in0(multiplexer_1_out), .in1(RETPC), .out(multiplexer_2_out), .sel(Uret));
  not not_1 (not_1_out, Equal);
  Hex_Digit_Display hex_digit_display_2 (.value(LedData[27:24]));  // open: dp
  Hex_Digit_Display hex_digit_display_3 (.value(LedData[23:20]));  // open: dp
  Comparator #(.width(16), .mode("twosComplement")) comparator_3 (
    .a(16'h258), .b(\总周期数 ), .eq(comparator_3_eq));  // open: gt, lt
  or or_1 (or_1_out, comparator_3_eq, comparator_4_eq);
  Comparator #(.width(16), .mode("twosComplement")) comparator_4 (
    .a(\总周期数 ), .b(16'h1), .eq(comparator_4_eq));  // open: gt, lt
  Comparator #(.width(16), .mode("twosComplement")) comparator_5 (
    .a(\总周期数 ), .b(16'h4), .eq(comparator_5_eq));  // open: gt, lt
  or or_2 (or_2_out, comparator_1_eq, comparator_2_eq);
  or or_3 (W1, IR1_q, d_ff_1_q);
  or or_4 (W2, IR2_q, d_ff_2_q);
  or or_5 (W3, IR3_q, d_ff_3_q);
  Counter #(.width(16), .max('hffff), .ongoal("wrap"), .trigger("rising"), .behavior("old")) counter_1 (
    .count(halt), .Q(\总周期数 ), .clk(CLK));  // open: load, D, carry, clr, preset
  Register #(.width(32), .trigger("rising"), .Select("low")) u_PC (
    .D(multiplexer_2_out), .en(halt), .Q(PC), .clk(CLK));  // open: clr
  assign bit_extender_1_out = {{20{IR[31]}}, {IR[31], IR[7], IR[30:25], IR[11:8]}};  // Bit_Extender bit_extender_1
  Multiplexer #(.select(1), .width(32), .disabled("Z"), .enable("false")) multiplexer_3 (
    .in0(bit_extender_1_out), .in1(bit_extender_2_out), .out(multiplexer_3_out), .sel(JAL));
  assign bit_extender_2_out = {{12{IR[31]}}, {IR[31], IR[19:12], IR[20], IR[30:21]}};  // Bit_Extender bit_extender_2
  and and_1 (and_1_out, Beq, Equal);
  and and_2 (and_2_out, not_1_out, Bne);
  and and_3 (and_3_out, Bge, tunnel);
  Hex_Digit_Display hex_digit_display_4 (.value(LedData[15:12]));  // open: dp
  Hex_Digit_Display hex_digit_display_5 (.value(LedData[19:16]));  // open: dp
  Pull_Resistor #(.pull(0)) pull_resistor_1 (.node(IRA));
  assign IRA = or_1_out ? ~CLK : 1'bz;  // Controlled_Inverter controlled_inverter_1
  Pull_Resistor #(.pull(0)) pull_resistor_2 (.node(IRB));
  assign IRB = comparator_5_eq ? ~CLK : 1'bz;  // Controlled_Inverter controlled_inverter_2
  Pull_Resistor #(.pull(0)) pull_resistor_3 (.node(IRC));
  assign IRC = or_2_out ? ~CLK : 1'bz;  // Controlled_Inverter controlled_inverter_3
  D_Flip_Flop #(.trigger("rising"), .Pre_Clr_Positions("LEGACY"), .NegatePresetClear("false"), .enable("true"), .NewFFLayout("false")) d_ff_1 (
    .clk(IRA), .D(1'b1), .Q(d_ff_1_q), .reset(IR1_q));  // open: Qn, preset, en
  D_Flip_Flop #(.trigger("rising"), .Pre_Clr_Positions("LEGACY"), .NegatePresetClear("false"), .enable("true"), .NewFFLayout("false")) d_ff_2 (
    .clk(IRB), .D(1'b1), .Q(d_ff_2_q), .reset(IR2_q));  // open: Qn, preset, en
  D_Flip_Flop #(.trigger("rising"), .Pre_Clr_Positions("LEGACY"), .NegatePresetClear("false"), .enable("true"), .NewFFLayout("false")) d_ff_3 (
    .clk(IRC), .D(1'b1), .Q(d_ff_3_q), .reset(IR3_q));  // open: Qn, preset, en
  Adder #(.width(32)) adder_1 (.a(PC), .b(32'h4), .out(PC_4));  // open: cin, cout
  Shifter #(.width(32), .shift("ll")) shifter_1 (.in(multiplexer_3_out), .\dist (5'b00001), .out(shifter_1_out));
  or or_6 (com_pc, JAL, and_1_out, and_2_out, and_3_out);
  Hex_Digit_Display hex_digit_display_6 (.value(LedData[11:8]));  // open: dp
  Hex_Digit_Display hex_digit_display_7 (.value(LedData[7:4]));  // open: dp
  // Probe on \总周期数 
  or or_7 (or_7_out, d_ff_1_q, IR1_q);
  or or_8 (or_8_out, d_ff_2_q, IR2_q);
  or or_9 (or_9_out, d_ff_3_q, IR3_q);
  // RiscV_Probe riscv_probe_1: pin names not known; wires that end beside it: IR
  Adder #(.width(32)) adder_2 (.a(PC), .b(shifter_1_out), .out(adder_2_out));  // open: cin, cout
  Multiplexer #(.select(1), .width(32), .disabled("Z"), .enable("false")) multiplexer_4 (
    .in0(multiplexer_5_out), .in1(calc), .out(NEXTPC), .sel(JALR));
  Hex_Digit_Display hex_digit_display_8 (.value(LedData[3:0]));  // open: dp
  and and_4 (and_4_out, or_7_out, ~rst1);  // AND_Gate
  and and_5 (and_5_out, or_8_out, ~rst2);  // AND_Gate
  and and_6 (and_6_out, or_9_out, ~rst3);  // AND_Gate
  ROM #(.addrWidth(10), .dataWidth(32), .Select("high")) rom_1 (.addr(PC[11:2]), .data(IR));
  Multiplexer #(.select(1), .width(32), .disabled("Z"), .enable("false")) multiplexer_5 (
    .in0(PC_4), .in1(adder_2_out), .out(multiplexer_5_out), .sel(com_pc));
  D_Flip_Flop #(.trigger("rising"), .Pre_Clr_Positions("LEGACY"), .NegatePresetClear("false"), .enable("true"), .NewFFLayout("false")) u_IR1 (
    .clk(CLK), .D(and_4_out), .Q(IR1_q));  // open: Qn, preset, en, reset
  D_Flip_Flop #(.trigger("rising"), .Pre_Clr_Positions("LEGACY"), .NegatePresetClear("false"), .enable("true"), .NewFFLayout("false")) u_IR2 (
    .clk(CLK), .D(and_5_out), .Q(IR2_q));  // open: Qn, preset, en, reset
  D_Flip_Flop #(.trigger("rising"), .Pre_Clr_Positions("LEGACY"), .NegatePresetClear("false"), .enable("true"), .NewFFLayout("false")) u_IR3 (
    .clk(CLK), .D(and_6_out), .Q(IR3_q));  // open: Qn, preset, en, reset
  or or_10 (IR1_t, IR1, IRA);
  \单周期硬布线控制器  \u_单周期硬布线控制器_1  (
    .Funct({IR[30], IR[25], IR[14:12]}), .OP(IR[6:2]), .ALU_OP(\单周期硬布线控制器_1_alu_op ),
    .MemToReg(\单周期硬布线控制器_1_memtoreg ), .MemWrite(MemWrite), .ALU_SRC(\单周期硬布线控制器_1_alu_src ),
    .RegWrite(RegWrite), .ecall(Ecall), .S_type(S), .Jalr(JALR), .Beq(Beq), .JAL(JAL), .Bne(Bne), .Lui(Lui),
    .Lbu(Lbu), .Bge(Bge), .uret(Uret), .IR21(IR[21]), .csrrsi(csrrsi), .csrrci(csrrci));  // open: rs1, rs2
  Multiplexer #(.select(1), .width(5), .disabled("Z"), .enable("false")) multiplexer_6 (
    .in0(IR[19:15]), .in1(5'b10001), .out(multiplexer_6_out), .sel(Ecall));
  assign bit_extender_3_out = {{12{IR[31]}}, IR[31:12]};  // Bit_Extender bit_extender_3
  or or_11 (IR2_t, IR2, IRB);
  or or_12 (or_12_out, INT, Uret);
  Priority_Encoder #(.select(2), .disabled("Z")) priority_encoder_1 (
    .in0(1'b1), .in1(IR1_q), .in2(IR2_q), .in3(IR3_q), .out(priority_encoder_1_out));  // open: gs, en_out, en_in
  and and_7 (and_7_out, pHigh, IE);
  Multiplexer #(.select(1), .width(5), .disabled("Z"), .enable("false")) multiplexer_7 (
    .in0(IR[24:20]), .in1(5'b01010), .out(multiplexer_7_out), .sel(Ecall));
  Multiplexer #(.select(1), .width(12), .disabled("Z"), .enable("false")) multiplexer_8 (
    .in0(IR[31:20]), .in1({IR[31:25], IR[11:7]}), .out(multiplexer_8_out), .sel(S));
  Multiplexer #(.select(1), .width(32), .disabled("Z"), .enable("false")) multiplexer_9 (
    .in0(multiplexer_11_out), .in1(shifter_2_out), .out(RDin), .sel(Lui));
  Shifter #(.width(32), .shift("ll")) shifter_2 (.in(bit_extender_3_out), .\dist (5'b01100), .out(shifter_2_out));
  Decoder #(.select(2), .tristate("false"), .disabled("Z"), .enable("false")) decoder_1 (
    .out0(decoder_1_out0), .out1(decoder_1_out1), .out2(decoder_1_out2), .sel(counter_2_q));  // open: out3
  Counter #(.width(2), .max('h3), .ongoal("wrap"), .trigger("rising"), .behavior("new")) counter_2 (
    .count(or_12_out), .Q(counter_2_q), .clk(CLK), .down(Uret));  // open: load, D, carry, clr, preset
  Multiplexer #(.select(2), .width(32), .disabled("Z"), .enable("false")) multiplexer_10 (
    .in1(32'h30ac), .in2(32'h3158), .in3(32'h3204), .out(INTPC), .sel(priority_encoder_1_out));  // open: in0
  Register #(.width(1), .trigger("falling"), .Select("low")) register_1 (
    .D(and_7_out), .Q(INT), .clk(CLK));  // open: en, clr
  Regifile regifile_1 (
    .Din(RDin), .Clk(CLK), .R1(regifile_1_r1), .R2(MDin), .WE(RegWrite), .W_num(IR[11:7]),
    .R1_num(multiplexer_6_out), .R2_num(multiplexer_7_out));
  assign bit_extender_4_out = {{20{multiplexer_8_out[11]}}, multiplexer_8_out};  // Bit_Extender bit_extender_4
  Multiplexer #(.select(1), .width(32), .disabled("Z"), .enable("false")) multiplexer_11 (
    .in0(multiplexer_15_out), .in1(shifter_4_out), .out(multiplexer_11_out), .sel(Lbu));
  or or_13 (IR3_t, IR3, IRC);
  Decoder #(.select(2), .tristate("false"), .disabled("Z"), .enable("false")) decoder_2 (
    .out1(decoder_2_out1), .out2(decoder_2_out2), .out3(decoder_2_out3), .sel(priority_encoder_1_out));  // open: out0
  and and_8 (and_8_out, INT, decoder_2_out1);
  Register #(.width(32), .trigger("rising"), .Select("low")) EPC1 (
    .D(NEXTPC), .en(and_8_out), .Q(RETPC1), .clk(CLK));  // open: clr
  Multiplexer #(.select(1), .width(32), .disabled("Z"), .enable("false")) multiplexer_12 (
    .in0(MDin), .in1(bit_extender_4_out), .out(multiplexer_12_out), .sel(\单周期硬布线控制器_1_alu_src ));
  Register #(.width(2), .trigger("rising"), .Select("low")) cause0 (
    .D(priority_encoder_1_out), .en(decoder_1_out0), .Q(cause0_q), .clk(CLK));  // open: clr
  Register #(.width(2), .trigger("rising"), .Select("low")) cause1 (
    .D(priority_encoder_1_out), .en(decoder_1_out1), .Q(cause1_q), .clk(CLK));  // open: clr
  Register #(.width(2), .trigger("rising"), .Select("low")) cause2 (
    .D(priority_encoder_1_out), .en(decoder_1_out2), .Q(cause2_q), .clk(CLK));  // open: clr
  and and_9 (and_9_out, INT, decoder_2_out2);
  or or_14 (or_14_out, Uret, csrrsi);
  Multiplexer #(.select(1), .width(32), .disabled("Z"), .enable("false")) multiplexer_13 (
    .in0(multiplexer_12_out), .in1(32'ha), .out(multiplexer_13_out), .sel(Ecall));
  Subtractor #(.width(5)) subtractor_1 (.a(5'b11000), .b(minus), .out(subtractor_1_out));  // open: bin, bout
  Multiplexer #(.select(2), .width(2), .disabled("Z"), .enable("false")) multiplexer_14 (
    .in0(cause0_q), .in1(cause1_q), .in2(cause2_q), .in3(2'b00), .out(curCause), .sel(subtractor_2_out));
  Subtractor #(.width(2)) subtractor_2 (.a(counter_2_q), .b(2'b01), .out(subtractor_2_out));  // open: bin, bout
  Register #(.width(32), .trigger("rising"), .Select("low")) EPC2 (
    .D(NEXTPC), .en(and_9_out), .Q(RETPC2), .clk(CLK));  // open: clr
  or or_15 (or_15_out, INT, csrrci);
  Register #(.width(1), .trigger("falling"), .Select("low")) register_2 (
    .D(1'b0), .en(or_14_out), .Q(register_2_q), .clk(CLK), .preset(or_15_out));  // open: clr, cs
  ALU alu_1 (
    .X(regifile_1_r1), .Y(multiplexer_13_out), .AluOP(\单周期硬布线控制器_1_alu_op ), .Equal(Equal), .Result(calc),
    .out_4(tunnel));  // open: Result_2, out_6
  Shifter #(.width(32), .shift("ll")) shifter_3 (
    .in(multiplexer_15_out), .\dist (subtractor_1_out), .out(shifter_3_out));
  Shifter #(.width(32), .shift("lr")) shifter_4 (.in(shifter_3_out), .\dist (5'b11000), .out(shifter_4_out));
  Decoder #(.select(2), .tristate("false"), .disabled("Z"), .enable("false")) decoder_3 (
    .out1(decoder_3_out1), .out2(decoder_3_out2), .out3(decoder_3_out3), .sel(curCause));  // open: out0
  and and_10 (and_10_out, INT, decoder_2_out3);
  not not_2 (IE, register_2_q);
  and and_11 (and_11_out, Ecall, Equal);
  and and_12 (and_12_out, Ecall, not_3_out);
  not not_3 (not_3_out, Equal);
  Comparator #(.width(2), .mode("unsigned")) comparator_6 (
    .a(curCause), .b(priority_encoder_1_out), .lt(pHigh));  // open: gt, eq
  Register #(.width(32), .trigger("rising"), .Select("low")) EPC3 (
    .D(NEXTPC), .en(and_10_out), .Q(RETPC3), .clk(CLK));  // open: clr
  assign bit_extender_5_out = {{3{1'b0}}, calc[1:0]};  // Bit_Extender bit_extender_5
  Shifter #(.width(5), .shift("ll")) shifter_5 (.in(bit_extender_5_out), .\dist (3'b011), .out(minus));
  not not_4 (not_4_out, MemWrite);
  Multiplexer #(.select(1), .width(32), .disabled("Z"), .enable("false")) multiplexer_15 (
    .in0(multiplexer_17_out), .in1(PC_4), .out(multiplexer_15_out), .sel(or_16_out));
  or or_16 (or_16_out, JAL, JALR);
  not not_5 (not_5_out, and_11_out);
  Multiplexer #(.select(2), .width(32), .disabled("Z"), .enable("false")) multiplexer_16 (
    .in1(RETPC1), .in2(RETPC2), .in3(RETPC3), .out(RETPC), .sel(priority_encoder_1_out));  // open: in0
  and and_13 (rst1, Uret, decoder_3_out1);
  and and_14 (rst2, Uret, decoder_3_out2);
  and and_15 (rst3, decoder_3_out3, Uret);
  RAM #(.addrWidth(10), .dataWidth(32), .bus("separate"), .Select("high")) ram_1 (
    .addr(calc[11:2]), .din(MDin), .data(ram_1_data), .str(MemWrite), .clk(CLK), .ld(not_4_out));  // open: sel, clr
  or or_17 (halt, Go, not_5_out);
  Register #(.width(32), .trigger("rising"), .Select("low")) register_3 (
    .D(MDin), .en(and_12_out), .Q(LedData), .clk(CLK));  // open: clr
  Multiplexer #(.select(1), .width(32), .disabled("Z"), .enable("false")) multiplexer_17 (
    .in0(calc), .in1(ram_1_data), .out(multiplexer_17_out), .sel(\单周期硬布线控制器_1_memtoreg ));

  // Other names for the same wires on the sheet: imm12_B[11:0] = {IR[31], IR[7], IR[30:25], IR[11:8]};
  //   imm20_JAL[19:0] = {IR[31], IR[19:12], IR[20], IR[30:21]}

  // Notes on the sheet:
  //   中断源
  //   中断等待指示
  //   总复位信号应将除ROM以外所有存储组件全部清零
  //   多级中断测试信号模拟器
  //   周期数记录
  //   计算新PC
  //   数码管输出
  //   数码管输出应该用寄存器锁存，否则显示数据只能一闪而过
  //   指令存储器
  //   Reset 
  //   Reset 
  //   Reset 
  //   指令字
  //   contents of rom_1 (hex, n*v repeats v):
  //   7d000113 100413 1f41993 41f9d993 433 c00913 800b13 140413 f47413 800293 100313 499993 89e9b3 1300533
  //   2200893 73 406282b3 fe0294e3 140413 f00f93 1f47433 1c41413 800293 100313 49d993 89e9b3 1300533
  //   2200893 73 406282b3 fe0294e3 1c45413 406b0b33 b0463 f95ff06f 2b3 fff2c293 1029293 fff2e293 500533
  //   2200893 73 f5dff06f 1112023 410113 a12023 410113 812023 410113 1312023 410113 1412023 410113 1512023
  //   410113 1612023 410113 40e073 100b13 300a13 100a93 1600433 441413 14469b3 1300533 2200893 73 fe0416e3
  //   415a0a33 fe0a10e3 40f073 ffc10113 12b03 ffc10113 12a83 ffc10113 12a03 ffc10113 12983 ffc10113 12403
  //   ffc10113 12503 ffc10113 12883 200073 1112023 410113 a12023 410113 812023 410113 1312023 410113
  //   1412023 410113 1512023 410113 1612023 410113 40e073 200b13 300a13 100a93 1600433 441413 14469b3
  //   1300533 2200893 73 fe0416e3 415a0a33 fe0a10e3 40f073 ffc10113 12b03 ffc10113 12a83 ffc10113 12a03
  //   ffc10113 12983 ffc10113 12403 ffc10113 12503 ffc10113 12883 200073 1112023 410113 a12023 410113
  //   812023 410113 1312023 410113 1412023 410113 1512023 410113 1612023 410113 40e073 300b13 300a13
  //   100a93 1600433 441413 14469b3 1300533 2200893 73 fe0416e3 415a0a33 fe0a10e3 40f073 ffc10113 12b03
  //   ffc10113 12a83 ffc10113 12a03 ffc10113 12983 ffc10113 12403 ffc10113 12503 ffc10113 12883 200073
  //   rs1
  //   rs2
  //   rd
  //   imm12 I
  //   imm12 S
  //   imm20 LUI
  //   Beq
  //   Bne
  //   MemToReg
  //   MemWrite
  //   AluOP
  //   AluSrcB
  //   RegWrite
  //   LBU stores the lowest byte
  //   为方便自动评测，需要输出PC，IR，寄存器堆写如数据RDin
  //   Ecall选项
  //   RAM写使能MemWrite、RAM写入数据MDin等信号
  //   数据存储器
endmodule

module \封装正确性测试  (
);

  wire IR1, IR2, IR3, MemW, RegW;
  wire [31:0] EX_PC, ID_PC, IF_PC, IR, LED, MDin, MDinr, MEM_PC, PC, RDin, RDinr, WB_PC;

  \单周期RISC_V  \u_单周期risc_v_1  (
    .IR1(IR1), .IR2(IR2), .IR3(IR3), .RegWrite(RegW), .MemWrite(MemW), .PC(PC), .IR(IR), .RDin(RDin),
    .MDin(MDin), .LedData(LED));
  \气泡流水线  \u_气泡流水线_1  (
    .RegWrite(RegW), .MemWrite(MemW), .IF_PC(IF_PC), .ID_PC(ID_PC), .EX_PC(EX_PC), .M_PC(MEM_PC),
    .WB_PC(WB_PC), .RDin(RDinr), .MDin(MDinr), .LedData(LED));
  \单周期_单级中断  \u_单周期_单级中断_1  (
    .IR1(IR1), .IR2(IR2), .IR3(IR3), .RegWrite(RegW), .MemWrite(MemW), .PC(PC), .IR(IR), .RDin(RDin),
    .MDin(MDin), .LedData(LED));
  \理想流水线  \u_理想流水线_1  (
    .RegWrite(RegW), .MemWrite(MemW), .IF_PC(IF_PC), .ID_PC(ID_PC), .EX_PC(EX_PC), .M_PC(MEM_PC),
    .WB_PC(WB_PC), .RDin(RDinr), .MDin(MDinr), .LedData(LED));
  \重定向流水线  \u_重定向流水线_1  (
    .RegWrite(RegW), .MemWrite(MemW), .IF_PC(IF_PC), .ID_PC(ID_PC), .EX_PC(EX_PC), .M_PC(MEM_PC),
    .WB_PC(WB_PC), .RDin(RDinr), .MDin(MDinr), .LedData(LED));
  \单周期_多级中断  \u_单周期_多级中断_1  (
    .IR1(IR1), .IR2(IR2), .IR3(IR3), .RegWrite(RegW), .MemWrite(MemW), .PC(PC), .IR(IR), .RDin(RDin),
    .MDin(MDin), .LedData(LED));

  // Notes on the sheet:
  //   单周期封装测试
  //   气泡流水封装测试
  //   单周期+单级中断封装测试
  //   请检查上面封装有无位宽不匹配，引脚标签是否和连接的标签相对应，否则无法在educoder平台上正确测试
  //   理想流水封装测试
  //   重定向流水封装测试
  //   单周期+多级中断封装测试
endmodule

module \动态分支预测  (
  output RegWrite,
  output MemWrite,
  output [31:0] IF_PC,
  output [31:0] ID_PC,
  output [31:0] EX_PC,
  output [31:0] M_PC,
  output [31:0] WB_PC,
  output [31:0] RDin,
  output [31:0] MDin,
  output [31:0] LedData
);

  wire alu_1_equal, alu_1_out_4, and_1_out, and_2_out, and_3_out, and_4_out, and_5_out, and_6_out, and_7_out,
       and_8_out, Bge, bjump, Branch, btb_1_predictjump, CLK, clock_1_out, clock_2_out, comparator_1_eq,
       comparator_2_eq, comparator_2_lt, d_ff_1_q, Ecall, Equal, EX_branchtaken, EX_isbranch, EX_jumpPredict,
       EX_MemToReg, EX_RegWrite, Go, halt, IR1, IR2, IR3, J, Jal, Jalr, Lbu, LoadUse, Lui, MEM_Lui,
       MEM_RegWrite, nand_1_out, not_1_out, not_3_out, not_4_out, not_5_out, not_6_out, or_1_out, or_3_out,
       or_6_out, predictError, RST, S, W1, W2, W3, \动态分支预测if_id_1_id_predictjump , \单周期硬布线控制器_1_rs1 ,
       \单周期硬布线控制器_1_rs2 , \气泡ex_mem_1_mem_equal ;
  wire [1:0] \动态分支预测id_ex_1_ex_fwda , \动态分支预测id_ex_1_ex_fwdb , \重定向逻辑设计_1_fwda , \重定向逻辑设计_1_fwdb ;
  wire [3:0] \单周期硬布线控制器_1_alu_op ;
  wire [4:0] bit_extender_1_out, minus, multiplexer_2_out, multiplexer_3_out, subtractor_1_out, WB_rd,
       \动态分支预测id_ex_1_ex_rd , \气泡ex_mem_1_mem_rd , \气泡ir扩展器_1_funct , \气泡ir扩展器_1_op , \气泡ir扩展器_1_rd ,
       \气泡ir扩展器_1_rs1 , \气泡ir扩展器_1_rs2 ;
  wire [11:1] \单周期硬布线控制器_1_beq ;
  wire [12:0] CNT_num;
  wire [14:0] \气泡ex_mem_1_mem_sgn ;
  wire [15:0] \LoadUse次数 , \动态分支预测id_ex_1_ex_sgn , \总周期数 , \无条件分支数 , \条件分支成功数 , \气泡mem_wb_1_wb_sgn , \预测错误数 ;
  wire [31:0] adder_1_out, adder_2_out, adder_4_out, alu_1_result, bAddr, EX_bAddr, EX_IR, ID_IR, IF_IR,
       jAddr, jumpAddr, LedShow, MEM_IR, multiplexer_4_out, multiplexer_5_out, multiplexer_6_out,
       multiplexer_7_out, multiplexer_8_out, multiplexer_9_out, multiplexer_10_out, ram_1_data,
       regifile_1_r1, regifile_1_r2, shifter_2_out, shifter_3_out, WB_IR, \动态分支预测id_ex_1_ex_a ,
       \动态分支预测id_ex_1_ex_b , \动态分支预测id_ex_1_ex_imm , \动态分支预测id_ex_1_ex_imm_b , \动态分支预测id_ex_1_ex_imm_jal ,
       \动态分支预测id_ex_1_ex_imm_lui , \动态分支预测pc计算_1_new_pc , \气泡ex_mem_1_mem_alu_r , \气泡ex_mem_1_mem_imm_lui ,
       \气泡ir扩展器_1_imm , \气泡ir扩展器_1_imm_b , \气泡ir扩展器_1_imm_jal , \气泡ir扩展器_1_imm_lui , \气泡mem_wb_1_wb_alu_md ;

  Button \u_总复位  (.out(RST));
  Button _1 (.out(IR1));
  Button _2 (.out(IR2));
  Button _3 (.out(IR3));
  // Probe on \总周期数 
  // Probe on \总周期数 
  and and_1 (and_1_out, halt, not_1_out);
  Button \u_继续运行  (.out(Go));
  LED #(.active("true")) led_1 (.in(W1));
  LED #(.active("true")) led_2 (.in(W2));
  LED #(.active("true")) led_3 (.in(W3));
  not not_1 (not_1_out, LoadUse);
  Register #(.width(32), .trigger("rising"), .Select("low")) PC (
    .D(\动态分支预测pc计算_1_new_pc ), .en(and_1_out), .Q(IF_PC), .clk(CLK), .clr(RST));
  Hex_Digit_Display hex_digit_display_1 (.value(LedData[31:28]));  // open: dp
  // Probe on IF_PC[19:0]
  // RiscV_Probe riscv_probe_1: pin names not known; wires that end beside it: IF_IR
  \动态分支预测PC计算  \u_动态分支预测pc计算_1  (
    .PC_4(adder_1_out), .JumpAddr(jumpAddr), .EX_PC___4(adder_2_out), .EX_BranchAddr(EX_bAddr),
    .new_PC(\动态分支预测pc计算_1_new_pc ), .predict(btb_1_predictjump), .EX_bjump(EX_branchtaken),
    .predictError(predictError));
  Comparator #(.width(1), .mode("twosComplement")) comparator_1 (
    .a(EX_jumpPredict), .b(EX_branchtaken), .eq(comparator_1_eq));  // open: gt, lt
  not not_2 (predictError, comparator_1_eq);
  Hex_Digit_Display hex_digit_display_2 (.value(LedData[27:24]));  // open: dp
  Hex_Digit_Display hex_digit_display_3 (.value(LedData[23:20]));  // open: dp
  // Probe on ID_PC[19:0]
  // RiscV_Probe riscv_probe_2: pin names not known; wires that end beside it: ID_IR
  BTB btb_1 (
    .EX_branchAddr(EX_bAddr), .EX_PC(EX_PC), .CLK(CLK), .JumpAddr(jumpAddr), .PC(IF_PC),
    .EX_BranchTaken(EX_branchtaken), .PredictJump(btb_1_predictjump), .EX_IsBranch(EX_isbranch));
  Hex_Digit_Display hex_digit_display_4 (.value(LedData[19:16]));  // open: dp
  Hex_Digit_Display hex_digit_display_5 (.value(LedData[15:12]));  // open: dp
  ROM #(.addrWidth(10), .dataWidth(32), .Select("high")) rom_1 (.addr(IF_PC[11:2]), .data(IF_IR));
  Adder #(.width(32)) adder_1 (.a(IF_PC), .b(32'h4), .out(adder_1_out));  // open: cin, cout
  Adder #(.width(32)) adder_2 (.a(EX_PC), .b(32'h4), .out(adder_2_out));  // open: cin, cout
  Hex_Digit_Display hex_digit_display_6 (.value(LedData[11:8]));  // open: dp
  Hex_Digit_Display hex_digit_display_7 (.value(LedData[7:4]));  // open: dp
  Clock #(.highDuration(1), .lowDuration(1)) clock_1 (.out(clock_1_out));
  // Probe on EX_PC[19:0]
  // RiscV_Probe riscv_probe_3: pin names not known; wires that end beside it: EX_IR, clock_1_out, CLK
  Hex_Digit_Display hex_digit_display_8 (.value(LedData[3:0]));  // open: dp
  \动态分支预测IF_ID  \u_动态分支预测if_id_1  (
    .IF_PredictJump(btb_1_predictjump), .IF_PC(IF_PC), .IF_IR(IF_IR), .clk(CLK), .halt(and_2_out),
    .ID_PredictJump(\动态分支预测if_id_1_id_predictjump ), .ID_PC(ID_PC), .ID_IR(ID_IR), .rst(or_1_out));
  or or_1 (or_1_out, predictError, RST);
  and and_2 (and_2_out, not_3_out, halt);
  // Probe on \总周期数 
  // Probe on M_PC[19:0]
  // RiscV_Probe riscv_probe_4: pin names not known; wires that end beside it: MEM_IR
  \气泡IR扩展器  \u_气泡ir扩展器_1  (
    .IR(ID_IR), .s(S), .OP(\气泡ir扩展器_1_op ), .Funct(\气泡ir扩展器_1_funct ), .rs1(\气泡ir扩展器_1_rs1 ),
    .rs2(\气泡ir扩展器_1_rs2 ), .rd(\气泡ir扩展器_1_rd ), .imm(\气泡ir扩展器_1_imm ), .imm_b(\气泡ir扩展器_1_imm_b ),
    .imm_lui(\气泡ir扩展器_1_imm_lui ), .imm_jal(\气泡ir扩展器_1_imm_jal ));
  not not_3 (not_3_out, LoadUse);
  or or_2 (EX_isbranch, J, Branch);
  Multiplexer #(.select(1), .width(32), .disabled("Z"), .enable("false")) multiplexer_1 (
    .in0(jAddr), .in1(bAddr), .out(EX_bAddr), .sel(Branch));
  // Probe on \总周期数 
  // Probe on \无条件分支数 
  // Probe on \条件分支成功数 
  // Probe on \预测错误数 
  // Probe on \LoadUse次数 
  \单周期硬布线控制器  \u_单周期硬布线控制器_1  (
    .Funct(\气泡ir扩展器_1_funct ), .OP(\气泡ir扩展器_1_op ), .ALU_OP(\单周期硬布线控制器_1_alu_op ),
    .MemToReg(\单周期硬布线控制器_1_beq [3]), .MemWrite(\单周期硬布线控制器_1_beq [4]), .ALU_SRC(\单周期硬布线控制器_1_beq [9]),
    .RegWrite(\单周期硬布线控制器_1_beq [10]), .ecall(\单周期硬布线控制器_1_beq [11]), .S_type(S), .Jalr(Jalr),
    .Beq(\单周期硬布线控制器_1_beq [1]), .JAL(Jal), .Bne(\单周期硬布线控制器_1_beq [2]), .Lui(Lui), .Lbu(Lbu), .Bge(Bge),
    .rs1(\单周期硬布线控制器_1_rs1 ), .rs2(\单周期硬布线控制器_1_rs2 ), .IR21(ID_IR[21]));  // open: uret, csrrsi, csrrci
  // Probe on IF_PC[11:0]
  // Probe on WB_PC[19:0]
  // RiscV_Probe riscv_probe_5: pin names not known; wires that end beside it: WB_IR
  Multiplexer #(.select(1), .width(5), .disabled("Z"), .enable("false")) multiplexer_2 (
    .in0(\气泡ir扩展器_1_rs1 ), .in1(5'b10001), .out(multiplexer_2_out), .sel(\单周期硬布线控制器_1_beq [11]));
  Multiplexer #(.select(1), .width(5), .disabled("Z"), .enable("false")) multiplexer_3 (
    .in0(\气泡ir扩展器_1_rs2 ), .in1(5'b01010), .out(multiplexer_3_out), .sel(\单周期硬布线控制器_1_beq [11]));
  // Probe on ID_PC[11:0]
  // Probe on EX_PC[11:0]
  \重定向逻辑设计  \u_重定向逻辑设计_1  (
    .rs1_u(\单周期硬布线控制器_1_rs1 ), .bJump(bjump), .rs2_u(\单周期硬布线控制器_1_rs2 ), .J(J), .EX_RegWrite(EX_RegWrite),
    .MEM_RegWrite(MEM_RegWrite), .MemToReg(EX_MemToReg), .rs1(multiplexer_2_out),
    .EX_rd(\动态分支预测id_ex_1_ex_rd ), .MEM_rd(\气泡ex_mem_1_mem_rd ), .rs2(multiplexer_3_out),
    .Jpop(EX_branchtaken), .LoadUse(LoadUse), .fwdb(\重定向逻辑设计_1_fwdb ), .fwda(\重定向逻辑设计_1_fwda ));
  Counter #(.width(16), .max('hffff), .ongoal("wrap"), .trigger("rising"), .behavior("old")) counter_1 (
    .count(halt), .Q(\总周期数 ), .clk(CLK), .clr(RST));  // open: load, D, carry, preset
  // Probe on M_PC[11:0]
  D_Flip_Flop #(.trigger("high"), .Pre_Clr_Positions("LEGACY"), .NegatePresetClear("false"), .enable("true"), .NewFFLayout("false")) d_ff_1 (.Q(d_ff_1_q));  // open: clk, D, Qn, preset, en, reset
  // Probe on 13'h342
  Regifile regifile_1 (
    .Din(RDin), .Clk(CLK), .R1(regifile_1_r1), .R2(regifile_1_r2), .WE(RegWrite), .W_num(WB_rd),
    .R1_num(multiplexer_2_out), .R2_num(multiplexer_3_out));
  // Probe on WB_PC[11:0]
  Comparator #(.width(13), .mode("twosComplement")) comparator_2 (
    .a(CNT_num), .b(13'h342), .eq(comparator_2_eq), .lt(comparator_2_lt));  // open: gt
  Clock #(.highDuration(1), .lowDuration(1)) clock_2 (.out(clock_2_out));
  and and_3 (and_3_out, halt, J);
  nand nand_1 (nand_1_out, d_ff_1_q, comparator_2_eq);
  Counter #(.width(13), .max('h1fff), .ongoal("stay"), .trigger("rising"), .behavior("old")) counter_2 (
    .count(comparator_2_lt), .Q(CNT_num), .clk(clock_2_out));  // open: load, D, carry, clr, preset
  \动态分支预测ID_EX  \u_动态分支预测id_ex_1  (
    .ID_rd(\气泡ir扩展器_1_rd ), .ID_a(regifile_1_r1), .ID_b(regifile_1_r2), .ID_imm(\气泡ir扩展器_1_imm ),
    .ID_imm_B(\气泡ir扩展器_1_imm_b ), .ID_imm_Jal(\气泡ir扩展器_1_imm_jal ), .ID_imm_Lui(\气泡ir扩展器_1_imm_lui ),
    .ID_PC(ID_PC), .ID_IR(ID_IR), .ID_PredictJump(\动态分支预测if_id_1_id_predictjump ),
    .ID_FwdA(\重定向逻辑设计_1_fwda ), .ID_FwdB(\重定向逻辑设计_1_fwdb ),
    .ID_sgn({Lui, Lbu, Jalr, Jal, \单周期硬布线控制器_1_beq [11:9], \单周期硬布线控制器_1_alu_op , \单周期硬布线控制器_1_beq [4:1], Bge}),
    .EX_rd(\动态分支预测id_ex_1_ex_rd ), .EX_a(\动态分支预测id_ex_1_ex_a ), .EX_b(\动态分支预测id_ex_1_ex_b ),
    .EX_imm(\动态分支预测id_ex_1_ex_imm ), .EX_imm_B(\动态分支预测id_ex_1_ex_imm_b ),
    .EX_imm_Jal(\动态分支预测id_ex_1_ex_imm_jal ), .EX_imm_Lui(\动态分支预测id_ex_1_ex_imm_lui ), .EX_PC(EX_PC),
    .EX_IR(EX_IR), .EX_PredictJump(EX_jumpPredict), .EX_FwdA(\动态分支预测id_ex_1_ex_fwda ),
    .EX_FwdB(\动态分支预测id_ex_1_ex_fwdb ),
    .EX_sgn({\动态分支预测id_ex_1_ex_sgn [15:11], EX_RegWrite, \动态分支预测id_ex_1_ex_sgn [9:4], EX_MemToReg, \动态分支预测id_ex_1_ex_sgn [2:0]}),
    .clk(CLK), .rst(or_3_out), .halt(halt));
  Counter #(.width(16), .max('hffff), .ongoal("wrap"), .trigger("rising"), .behavior("old")) counter_3 (
    .count(and_3_out), .Q(\无条件分支数 ), .clk(CLK), .clr(RST));  // open: load, D, carry, preset
  assign CLK = nand_1_out ? clock_2_out : 1'bz;  // Controlled_Buffer controlled_buffer_1
  Multiplexer #(.select(2), .width(32), .disabled("Z"), .enable("false")) multiplexer_4 (
    .in0(\动态分支预测id_ex_1_ex_a ), .in1(RDin), .in2(multiplexer_8_out), .out(multiplexer_4_out),
    .sel(\动态分支预测id_ex_1_ex_fwda ));  // open: in3
  Multiplexer #(.select(2), .width(32), .disabled("Z"), .enable("false")) multiplexer_5 (
    .in0(\动态分支预测id_ex_1_ex_b ), .in1(RDin), .in2(multiplexer_8_out), .out(multiplexer_5_out),
    .sel(\动态分支预测id_ex_1_ex_fwdb ));  // open: in3
  Pull_Resistor #(.pull(1)) pull_resistor_1 (.node(CLK));
  or or_3 (or_3_out, LoadUse, RST, predictError);
  Counter #(.width(16), .max('hffff), .ongoal("wrap"), .trigger("rising"), .behavior("old")) counter_4 (
    .count(and_4_out), .Q(\条件分支成功数 ), .clk(CLK), .clr(RST));  // open: load, D, carry, preset
  and and_4 (and_4_out, halt, bjump);
  Multiplexer #(.select(1), .width(32), .disabled("Z"), .enable("false")) multiplexer_6 (
    .in0(multiplexer_5_out), .in1(\动态分支预测id_ex_1_ex_imm ), .out(multiplexer_6_out),
    .sel(\动态分支预测id_ex_1_ex_sgn [9]));
  Multiplexer #(.select(1), .width(32), .disabled("Z"), .enable("false")) multiplexer_7 (
    .in0(multiplexer_6_out), .in1(32'ha), .out(multiplexer_7_out), .sel(\动态分支预测id_ex_1_ex_sgn [11]));
  ALU alu_1 (
    .X(multiplexer_4_out), .Y(multiplexer_7_out), .AluOP(\动态分支预测id_ex_1_ex_sgn [8:5]), .Equal(alu_1_equal),
    .Result(alu_1_result), .out_4(alu_1_out_4));  // open: Result_2, out_6
  Adder #(.width(32)) adder_3 (.a(EX_PC), .b(\动态分支预测id_ex_1_ex_imm_b ), .out(bAddr));  // open: cin, cout
  or or_4 (Branch, \动态分支预测id_ex_1_ex_sgn [0], \动态分支预测id_ex_1_ex_sgn [1], \动态分支预测id_ex_1_ex_sgn [2]);
  \条件分支逻辑设计  \u_条件分支逻辑设计_1  (
    .Bge(\动态分支预测id_ex_1_ex_sgn [0]), .in_4(alu_1_equal), .Beq(\动态分支预测id_ex_1_ex_sgn [1]), .in_2(alu_1_out_4),
    .Bne(\动态分支预测id_ex_1_ex_sgn [2]), .branchtaken(bjump));
  or or_5 (J, \动态分支预测id_ex_1_ex_sgn [12], \动态分支预测id_ex_1_ex_sgn [13]);
  and and_5 (and_5_out, halt, LoadUse);
  Counter #(.width(16), .max('hffff), .ongoal("wrap"), .trigger("rising"), .behavior("old")) counter_5 (
    .count(and_5_out), .Q(\LoadUse次数 ), .clk(CLK), .clr(RST));  // open: load, D, carry, preset
  \无条件跳转逻辑设计  \u_无条件跳转逻辑设计_1  (
    .JAL(\动态分支预测id_ex_1_ex_sgn [12]), .JALR(\动态分支预测id_ex_1_ex_sgn [13]), .JALR_Addr(alu_1_result),
    .JAL_Addr(\动态分支预测id_ex_1_ex_imm_jal ), .J_Addr(jAddr), .PC(EX_PC));
  Counter #(.width(16), .max('hffff), .ongoal("wrap"), .trigger("rising"), .behavior("old")) counter_6 (
    .count(and_6_out), .Q(\预测错误数 ), .clk(CLK));  // open: load, D, carry, clr, preset
  and and_6 (and_6_out, halt, predictError);
  \气泡EX_MEM  \u_气泡ex_mem_1  (
    .EX_rd(\动态分支预测id_ex_1_ex_rd ), .EX_PC(EX_PC), .EX_IR(EX_IR), .EX_ALU_R(alu_1_result),
    .EX_imm_Lui(\动态分支预测id_ex_1_ex_imm_lui ),
    .EX_sgn({\动态分支预测id_ex_1_ex_sgn [15:11], EX_RegWrite, \动态分支预测id_ex_1_ex_sgn [9:4], EX_MemToReg, \动态分支预测id_ex_1_ex_sgn [2:0]}),
    .MEM_rd(\气泡ex_mem_1_mem_rd ), .MEM_PC(M_PC), .MEM_IR(MEM_IR), .MEM_ALU_R(\气泡ex_mem_1_mem_alu_r ),
    .MEM_imm_Lui(\气泡ex_mem_1_mem_imm_lui ),
    .MEM_sgn({MEM_Lui, \气泡ex_mem_1_mem_sgn [14:11], MEM_RegWrite, \气泡ex_mem_1_mem_sgn [9:5], MemWrite, \气泡ex_mem_1_mem_sgn [3:0]}),
    .rst(RST), .halt(halt), .clk(CLK), .EX_MDin(multiplexer_5_out), .MEM_MDin(MDin), .EX_Equal(alu_1_equal),
    .MEM_Equal(\气泡ex_mem_1_mem_equal ));
  not not_4 (not_4_out, MemWrite);
  RAM #(.addrWidth(10), .dataWidth(32), .bus("separate"), .Select("high")) ram_1 (
    .addr(\气泡ex_mem_1_mem_alu_r [11:2]), .din(MDin), .data(ram_1_data), .str(MemWrite), .clk(CLK),
    .ld(not_4_out));  // open: sel, clr
  assign bit_extender_1_out = {{3{1'b0}}, \气泡ex_mem_1_mem_alu_r [1:0]};  // Bit_Extender bit_extender_1
  Subtractor #(.width(5)) subtractor_1 (.a(5'b11000), .b(minus), .out(subtractor_1_out));  // open: bin, bout
  Multiplexer #(.select(1), .width(32), .disabled("Z"), .enable("false")) multiplexer_8 (
    .in0(\气泡ex_mem_1_mem_alu_r ), .in1(\气泡ex_mem_1_mem_imm_lui ), .out(multiplexer_8_out), .sel(MEM_Lui));
  Shifter #(.width(5), .shift("ll")) shifter_1 (.in(bit_extender_1_out), .\dist (3'b011), .out(minus));
  Shifter #(.width(32), .shift("ll")) shifter_2 (.in(ram_1_data), .\dist (subtractor_1_out), .out(shifter_2_out));
  Shifter #(.width(32), .shift("lr")) shifter_3 (.in(shifter_2_out), .\dist (5'b11000), .out(shifter_3_out));
  Multiplexer #(.select(1), .width(32), .disabled("Z"), .enable("false")) multiplexer_9 (
    .in0(ram_1_data), .in1(shifter_3_out), .out(multiplexer_9_out), .sel(\气泡ex_mem_1_mem_sgn [14]));
  Multiplexer #(.select(1), .width(32), .disabled("Z"), .enable("false")) multiplexer_10 (
    .in0(multiplexer_8_out), .in1(multiplexer_9_out), .out(multiplexer_10_out), .sel(\气泡ex_mem_1_mem_sgn [3]));
  \气泡MEM_WB  \u_气泡mem_wb_1  (
    .MEM_rd(\气泡ex_mem_1_mem_rd ), .MEM_PC(M_PC), .MEM_IR(MEM_IR), .MEM_ALU_MD(multiplexer_10_out),
    .MEM_sgn({MEM_Lui, \气泡ex_mem_1_mem_sgn [14:11], MEM_RegWrite, \气泡ex_mem_1_mem_sgn [9:5], MemWrite, \气泡ex_mem_1_mem_sgn [3:0]}),
    .WB_rd(WB_rd), .WB_PC(WB_PC), .WB_IR(WB_IR), .WB_ALU_MD(\气泡mem_wb_1_wb_alu_md ),
    .WB_sgn({\气泡mem_wb_1_wb_sgn [15:12], Ecall, RegWrite, \气泡mem_wb_1_wb_sgn [9:0]}), .rst(RST), .halt(halt),
    .clk(CLK), .MEM_Equal(\气泡ex_mem_1_mem_equal ), .WB_Equal(Equal), .MEM_LED(MDin), .WB_LED(LedShow));
  not not_5 (not_5_out, Equal);
  Adder #(.width(32)) adder_4 (.a(WB_PC), .b(32'h4), .out(adder_4_out));  // open: cin, cout
  not not_6 (not_6_out, and_7_out);
  and and_7 (and_7_out, Ecall, Equal);
  and and_8 (and_8_out, Ecall, not_5_out);
  or or_6 (or_6_out, \气泡mem_wb_1_wb_sgn [13], \气泡mem_wb_1_wb_sgn [12]);
  Multiplexer #(.select(1), .width(32), .disabled("Z"), .enable("false")) multiplexer_11 (
    .in0(\气泡mem_wb_1_wb_alu_md ), .in1(adder_4_out), .out(RDin), .sel(or_6_out));
  or or_7 (halt, Go, not_6_out);
  Register #(.width(32), .trigger("rising"), .Select("low")) register_1 (
    .D(LedShow), .en(and_8_out), .Q(LedData), .clk(CLK));  // open: clr

  // Other names for the same wires on the sheet: MEM_PC[31:0] = M_PC

  // Notes on the sheet:
  //   中断源
  //   时空图监测，可删除
  //   中断等待指示
  //   数码管输出
  //   指令存储器
  //   contents of rom_1 (hex, n*v repeats v):
  //   100493 100006f 100493 200913 300993 100006f 100493 200913 300993 100006f 100493 200913 300993
  //   100006f 100493 200913 300993 3d0000ef 100413 100493 1f49493 900533 2200893 73 24d493 48463 fedff06f
  //   900533 2200893 73 100493 249493 900533 2200893 73 48463 fedff06f 100493 1f49493 900533 2200893 73
  //   4034d493 900533 2200893 73 4044d493 900533 2200893 73 4044d493 900533 2200893 73 4044d493 900533
  //   2200893 73 4044d493 900533 2200893 73 4044d493 900533 2200893 73 4044d493 900533 2200893 73 4044d493
  //   900533 2200893 73 100413 1f41993 41f9d993 433 c00913 300b13 140413 f47413 800293 100313 499993
  //   89e9b3 1300533 2200893 73 406282b3 fe0294e3 140413 f00f93 1f47433 1c41413 800293 100313 49d993
  //   89e9b3 1300533 2200893 73 406282b3 fe0294e3 1c45413 406b0b33 b0463 f95ff06f 2b3 fff2c293 829293
  //   ff2e293 500533 2200893 73 fff00413 493 84a023 140413 448493 84a023 140413 448493 84a023 140413
  //   448493 84a023 140413 448493 84a023 140413 448493 84a023 140413 448493 84a023 140413 448493 84a023
  //   140413 448493 84a023 140413 448493 84a023 140413 448493 84a023 140413 448493 84a023 140413 448493
  //   84a023 140413 448493 84a023 140413 448493 84a023 140413 448493 84a023 140413 448493 140413 433
  //   3c00493 42983 4aa03 149a2b3 28663 134a023 1442023 ffc48493 fe9412e3 800533 2200893 73 440413 3c00493
  //   fc9416e3 a00893 73 fff00293 7700493 849493 7748493 900533 2200893 73 1000e13 54c4b3 900533 2200893
  //   73 fffe0e13 fe0e16e3 a00893 73 800e13 fedc04b7 fff00413 1045413 84e4b3 900533 2200893 73 ba984b7
  //   900533 73 76544b7 900533 73 32104b7 900533 73 fffe0e13 fa0e1ee3 a00893 73 313 1000e13 8400493 849493
  //   8348493 400913 891913 490913 849493 8248493 849493 8148493 891913 490913 891913 490913 932023
  //   12484b3 430313 fffe0e13 fe0e18e3 2000e13 313 34483 900533 2200893 73 130313 fffe0e13 fe0e14e3 a00893
  //   73 f00493 900533 2200893 73 fff48493 fe04d8e3 a00893 73 413 140413 800533 2200893 73 240413 800533
  //   2200893 73 340413 800533 2200893 73 440413 800533 2200893 73 540413 800533 2200893 73 640413 800533
  //   2200893 73 740413 800533 2200893 73 840413 800533 2200893 2200893 73 8067
  //   判断错误需要清除IF和ID的误取指令，连接reset同步清零
  //   控制位
  //   流水调试日志用
  //   暂停节拍，不能为0
  //   戳工具置1进入计数暂停模式，ctrl+k时钟自动运行到对应节拍暂停
  //   ctrl+k关闭时钟连续运行，将控制位置零，进入单步调试模式调试
  //   数据记录
  //   可计数暂停的时钟源
  //   instruction分配关系
  //   0：Bge指令
  //   1：Beq指令
  //   2：Bne指令
  //   10：RegWrite信号
  //   14：Lbu信号
  //   为方便自动评测，需要输出流水线各段保存的PC值，注意是PC不是PC+4，另外ID段寄存器写入信息，Mem段内存写入信息也要输出
  //   3：MemToReg信号
  //   4：MemWrite信号
  //   11：Ecall信号
  //   15：Lui信号
  //   此处不论是跳转还是数据冲突都需要产生气泡，因此都需要连接reset同步清零
  //   5-8：AluOP信号
  //   9：Alu_src信号
  //   12：Jal信号
  //   13：Jalr信号
  //   数据存储器
  //   Ecall选项
endmodule

module BTB (
  input  [31:0] EX_branchAddr,
  input  [31:0] EX_PC,
  input  EX_IsBranch,
  input  CLK,
  input  [31:0] PC,
  input  EX_BranchTaken,
  output [31:0] JumpAddr,
  output PredictJump
);

  wire AllValid, and_10_out, comparator_1_eq, comparator_2_eq, comparator_3_eq, comparator_4_eq,
       comparator_5_eq, comparator_6_eq, comparator_7_eq, comparator_8_eq, comparator_9_eq, comparator_10_eq,
       comparator_11_eq, comparator_12_eq, comparator_13_eq, comparator_14_eq, comparator_15_eq,
       comparator_16_eq, Er0, Er1, Er2, Er3, Er4, Er5, Er6, Er7, EX_Miss, Hit, not_1_out, not_2_out,
       not_3_out, not_4_out, not_5_out, not_6_out, not_7_out, not_8_out, or_1_out, or_2_out, or_3_out,
       or_4_out, or_5_out, or_6_out, or_7_out, or_8_out, or_9_out, or_10_out, or_11_out, or_12_out,
       or_13_out, or_14_out, or_15_out, or_16_out, or_17_out, or_18_out, or_19_out, or_20_out, or_21_out, r0,
       r1, r2, r3, r4, r5, r6, r7, v0, v1, v2, v3, v4, v5, v6, v7, write0, write1, write2, write3, write4,
       write5, write6, write7;
  wire [1:0] multiplexer_1_out, multiplexer_2_out, multiplexer_3_out, multiplexer_4_out, multiplexer_5_out,
       multiplexer_6_out, multiplexer_7_out, s0, s1, s2, s3, s4, s5, s6, s7, \状态转换_1_new_state ,
       \状态转换_2_new_state , \状态转换_3_new_state , \状态转换_4_new_state , \状态转换_5_new_state , \状态转换_6_new_state ,
       \状态转换_7_new_state , \状态转换_8_new_state ;
  wire [2:0] available, largest, max3_1_max_num, max3_2_max_num, max3_3_max_num, max3_4_max_num,
       max3_5_max_num, max3_6_max_num, multiplexer_8_out;
  wire [15:0] c0, c1, c2, c3, c4, c5, c6, c7, max3_1_max, max3_2_max, max3_3_max, max3_4_max, max3_5_max,
       max3_6_max;
  wire [31:0] register_25_q, register_26_q, register_27_q, register_28_q, register_29_q, register_30_q,
       register_31_q, register_32_q, tag0, tag1, tag2, tag3, tag4, tag5, tag6, tag7;

  Register #(.width(1), .trigger("rising"), .Select("low")) register_1 (
    .D(1'b1), .en(write0), .Q(v0), .clk(CLK));  // open: clr
  Register #(.width(1), .trigger("rising"), .Select("low")) register_2 (
    .D(1'b1), .en(write1), .Q(v1), .clk(CLK));  // open: clr
  Register #(.width(1), .trigger("rising"), .Select("low")) register_3 (
    .D(1'b1), .en(write2), .Q(v2), .clk(CLK));  // open: clr
  Register #(.width(1), .trigger("rising"), .Select("low")) register_4 (
    .D(1'b1), .en(write3), .Q(v3), .clk(CLK));  // open: clr
  Register #(.width(1), .trigger("rising"), .Select("low")) register_5 (
    .D(1'b1), .en(write4), .Q(v4), .clk(CLK));  // open: clr
  Register #(.width(1), .trigger("rising"), .Select("low")) register_6 (
    .D(1'b1), .en(write5), .Q(v5), .clk(CLK));  // open: clr
  Register #(.width(1), .trigger("rising"), .Select("low")) register_7 (
    .D(1'b1), .en(write6), .Q(v6), .clk(CLK));  // open: clr
  Register #(.width(1), .trigger("rising"), .Select("low")) register_8 (
    .D(1'b1), .en(write7), .Q(v7), .clk(CLK));  // open: clr
  Register #(.width(32), .trigger("rising"), .Select("low")) register_9 (
    .D(EX_PC), .en(write0), .Q(tag0), .clk(CLK));  // open: clr
  Register #(.width(32), .trigger("rising"), .Select("low")) register_10 (
    .D(EX_PC), .en(write1), .Q(tag1), .clk(CLK));  // open: clr
  Register #(.width(32), .trigger("rising"), .Select("low")) register_11 (
    .D(EX_PC), .en(write2), .Q(tag2), .clk(CLK));  // open: clr
  Register #(.width(32), .trigger("rising"), .Select("low")) register_12 (
    .D(EX_PC), .en(write3), .Q(tag3), .clk(CLK));  // open: clr
  Register #(.width(32), .trigger("rising"), .Select("low")) register_13 (
    .D(EX_PC), .en(write4), .Q(tag4), .clk(CLK));  // open: clr
  Register #(.width(32), .trigger("rising"), .Select("low")) register_14 (
    .D(EX_PC), .en(write5), .Q(tag5), .clk(CLK));  // open: clr
  Register #(.width(32), .trigger("rising"), .Select("low")) register_15 (
    .D(EX_PC), .en(write6), .Q(tag6), .clk(CLK));  // open: clr
  Register #(.width(32), .trigger("rising"), .Select("low")) register_16 (
    .D(EX_PC), .en(write7), .Q(tag7), .clk(CLK));  // open: clr
  \状态转换  \u_状态转换_1  (.state(s0), .jump(EX_BranchTaken), .write(or_1_out), .new_state(\状态转换_1_new_state ));
  or or_1 (or_1_out, write0, Er0);
  \状态转换  \u_状态转换_2  (.state(s1), .jump(EX_BranchTaken), .write(or_2_out), .new_state(\状态转换_2_new_state ));
  or or_2 (or_2_out, write1, Er1);
  \状态转换  \u_状态转换_3  (.state(s2), .jump(EX_BranchTaken), .write(or_3_out), .new_state(\状态转换_3_new_state ));
  or or_3 (or_3_out, write2, Er2);
  \状态转换  \u_状态转换_4  (.state(s3), .jump(EX_BranchTaken), .write(or_4_out), .new_state(\状态转换_4_new_state ));
  or or_4 (or_4_out, write3, Er3);
  \状态转换  \u_状态转换_5  (.state(s4), .jump(EX_BranchTaken), .write(or_5_out), .new_state(\状态转换_5_new_state ));
  or or_5 (or_5_out, write4, Er4);
  \状态转换  \u_状态转换_6  (.state(s5), .jump(EX_BranchTaken), .write(or_6_out), .new_state(\状态转换_6_new_state ));
  or or_6 (or_6_out, write5, Er5);
  \状态转换  \u_状态转换_7  (.state(s6), .jump(EX_BranchTaken), .write(or_7_out), .new_state(\状态转换_7_new_state ));
  or or_7 (or_7_out, write6, Er6);
  \状态转换  \u_状态转换_8  (.state(s7), .jump(EX_BranchTaken), .write(or_8_out), .new_state(\状态转换_8_new_state ));
  or or_8 (or_8_out, write7, Er7);
  Register #(.width(2), .trigger("rising"), .Select("low")) register_17 (
    .D(\状态转换_1_new_state ), .Q(s0), .clk(CLK));  // open: en, clr
  Register #(.width(2), .trigger("rising"), .Select("low")) register_18 (
    .D(\状态转换_2_new_state ), .Q(s1), .clk(CLK));  // open: en, clr
  Register #(.width(2), .trigger("rising"), .Select("low")) register_19 (
    .D(\状态转换_3_new_state ), .Q(s2), .clk(CLK));  // open: en, clr
  Register #(.width(2), .trigger("rising"), .Select("low")) register_20 (
    .D(\状态转换_4_new_state ), .Q(s3), .clk(CLK));  // open: en, clr
  Register #(.width(2), .trigger("rising"), .Select("low")) register_21 (
    .D(\状态转换_5_new_state ), .Q(s4), .clk(CLK));  // open: en, clr
  Register #(.width(2), .trigger("rising"), .Select("low")) register_22 (
    .D(\状态转换_6_new_state ), .Q(s5), .clk(CLK));  // open: en, clr
  Register #(.width(2), .trigger("rising"), .Select("low")) register_23 (
    .D(\状态转换_7_new_state ), .Q(s6), .clk(CLK));  // open: en, clr
  Register #(.width(2), .trigger("rising"), .Select("low")) register_24 (
    .D(\状态转换_8_new_state ), .Q(s7), .clk(CLK));  // open: en, clr
  Counter #(.width(16), .max('hffff), .ongoal("wrap"), .trigger("rising"), .behavior("new")) counter_1 (
    .load(or_9_out), .D({16{1'b0}}), .Q(c0), .clk(CLK));  // open: count, carry, clr, preset, down
  or or_9 (or_9_out, write0, Er0);
  Counter #(.width(16), .max('hffff), .ongoal("wrap"), .trigger("rising"), .behavior("new")) counter_2 (
    .load(or_10_out), .D({16{1'b0}}), .Q(c1), .clk(CLK));  // open: count, carry, clr, preset, down
  or or_10 (or_10_out, write1, Er1);
  Counter #(.width(16), .max('hffff), .ongoal("wrap"), .trigger("rising"), .behavior("new")) counter_3 (
    .load(or_11_out), .D({16{1'b0}}), .Q(c2), .clk(CLK));  // open: count, carry, clr, preset, down
  or or_11 (or_11_out, write2, Er2);
  Counter #(.width(16), .max('hffff), .ongoal("wrap"), .trigger("rising"), .behavior("new")) counter_4 (
    .load(or_12_out), .D({16{1'b0}}), .Q(c3), .clk(CLK));  // open: count, carry, clr, preset, down
  or or_12 (or_12_out, write3, Er3);
  Counter #(.width(16), .max('hffff), .ongoal("wrap"), .trigger("rising"), .behavior("new")) counter_5 (
    .load(or_13_out), .D({16{1'b0}}), .Q(c4), .clk(CLK));  // open: count, carry, clr, preset, down
  or or_13 (or_13_out, write4, Er4);
  Counter #(.width(16), .max('hffff), .ongoal("wrap"), .trigger("rising"), .behavior("new")) counter_6 (
    .load(or_14_out), .D({16{1'b0}}), .Q(c5), .clk(CLK));  // open: count, carry, clr, preset, down
  or or_14 (or_14_out, write5, Er5);
  Counter #(.width(16), .max('hffff), .ongoal("wrap"), .trigger("rising"), .behavior("new")) counter_7 (
    .load(or_15_out), .D({16{1'b0}}), .Q(c6), .clk(CLK));  // open: count, carry, clr, preset, down
  or or_15 (or_15_out, write6, Er6);
  Counter #(.width(16), .max('hffff), .ongoal("wrap"), .trigger("rising"), .behavior("new")) counter_8 (
    .load(or_16_out), .D({16{1'b0}}), .Q(c7), .clk(CLK));  // open: count, carry, clr, preset, down
  or or_16 (or_16_out, write7, Er7);
  Register #(.width(32), .trigger("rising"), .Select("low")) register_25 (
    .D(EX_branchAddr), .en(write0), .Q(register_25_q), .clk(CLK));  // open: clr
  Register #(.width(32), .trigger("rising"), .Select("low")) register_26 (
    .D(EX_branchAddr), .en(write1), .Q(register_26_q), .clk(CLK));  // open: clr
  Register #(.width(32), .trigger("rising"), .Select("low")) register_27 (
    .D(EX_branchAddr), .en(write2), .Q(register_27_q), .clk(CLK));  // open: clr
  Register #(.width(32), .trigger("rising"), .Select("low")) register_28 (
    .D(EX_branchAddr), .en(write3), .Q(register_28_q), .clk(CLK));  // open: clr
  Register #(.width(32), .trigger("rising"), .Select("low")) register_29 (
    .D(EX_branchAddr), .en(write4), .Q(register_29_q), .clk(CLK));  // open: clr
  Register #(.width(32), .trigger("rising"), .Select("low")) register_30 (
    .D(EX_branchAddr), .en(write5), .Q(register_30_q), .clk(CLK));  // open: clr
  Register #(.width(32), .trigger("rising"), .Select("low")) register_31 (
    .D(EX_branchAddr), .en(write6), .Q(register_31_q), .clk(CLK));  // open: clr
  Register #(.width(32), .trigger("rising"), .Select("low")) register_32 (
    .D(EX_branchAddr), .en(write7), .Q(register_32_q), .clk(CLK));  // open: clr
  assign JumpAddr = r0 ? register_25_q : 32'bz;  // Controlled_Buffer controlled_buffer_1
  assign JumpAddr = r1 ? register_26_q : 32'bz;  // Controlled_Buffer controlled_buffer_2
  assign JumpAddr = r2 ? register_27_q : 32'bz;  // Controlled_Buffer controlled_buffer_3
  assign JumpAddr = r3 ? register_28_q : 32'bz;  // Controlled_Buffer controlled_buffer_4
  assign JumpAddr = r4 ? register_29_q : 32'bz;  // Controlled_Buffer controlled_buffer_5
  assign JumpAddr = r5 ? register_30_q : 32'bz;  // Controlled_Buffer controlled_buffer_6
  assign JumpAddr = r6 ? register_31_q : 32'bz;  // Controlled_Buffer controlled_buffer_7
  assign JumpAddr = r7 ? register_32_q : 32'bz;  // Controlled_Buffer controlled_buffer_8
  MAX3 max3_1 (.Y(c1), .X(c0), .Y_num(3'b001), .X_num(3'b000), .MAX(max3_1_max), .Max_num(max3_1_max_num));
  MAX3 max3_2 (.Y(c3), .X(c2), .Y_num(3'b011), .X_num(3'b010), .MAX(max3_2_max), .Max_num(max3_2_max_num));
  MAX3 max3_3 (.Y(c5), .X(c4), .Y_num(3'b101), .X_num(3'b100), .MAX(max3_3_max), .Max_num(max3_3_max_num));
  MAX3 max3_4 (.Y(c7), .X(c6), .Y_num(3'b111), .X_num(3'b110), .MAX(max3_4_max), .Max_num(max3_4_max_num));
  Multiplexer #(.select(1), .width(2), .disabled("Z"), .enable("false")) multiplexer_1 (
    .in0(s0), .in1(s1), .out(multiplexer_1_out), .sel(r1));
  Multiplexer #(.select(1), .width(2), .disabled("Z"), .enable("false")) multiplexer_2 (
    .in0(s2), .in1(s3), .out(multiplexer_2_out), .sel(r3));
  Multiplexer #(.select(1), .width(2), .disabled("Z"), .enable("false")) multiplexer_3 (
    .in0(s4), .in1(s5), .out(multiplexer_3_out), .sel(r4));
  Multiplexer #(.select(1), .width(2), .disabled("Z"), .enable("false")) multiplexer_4 (
    .in0(s6), .in1(s7), .out(multiplexer_4_out), .sel(r7));
  MAX3 max3_5 (
    .Y(max3_2_max), .X(max3_1_max), .Y_num(max3_2_max_num), .X_num(max3_1_max_num), .MAX(max3_5_max),
    .Max_num(max3_5_max_num));
  MAX3 max3_6 (
    .Y(max3_4_max), .X(max3_3_max), .Y_num(max3_4_max_num), .X_num(max3_3_max_num), .MAX(max3_6_max),
    .Max_num(max3_6_max_num));
  or or_17 (or_17_out, r2, r3);
  or or_18 (or_18_out, r6, r7);
  Comparator #(.width(32), .mode("twosComplement")) comparator_1 (
    .a(tag0), .b(EX_PC), .eq(comparator_1_eq));  // open: gt, lt
  Comparator #(.width(32), .mode("twosComplement")) comparator_2 (
    .a(tag1), .b(EX_PC), .eq(comparator_2_eq));  // open: gt, lt
  Comparator #(.width(32), .mode("twosComplement")) comparator_3 (
    .a(tag2), .b(EX_PC), .eq(comparator_3_eq));  // open: gt, lt
  Comparator #(.width(32), .mode("twosComplement")) comparator_4 (
    .a(tag3), .b(EX_PC), .eq(comparator_4_eq));  // open: gt, lt
  Comparator #(.width(32), .mode("twosComplement")) comparator_5 (
    .a(tag4), .b(EX_PC), .eq(comparator_5_eq));  // open: gt, lt
  Comparator #(.width(32), .mode("twosComplement")) comparator_6 (
    .a(tag5), .b(EX_PC), .eq(comparator_6_eq));  // open: gt, lt
  Comparator #(.width(32), .mode("twosComplement")) comparator_7 (
    .a(tag6), .b(EX_PC), .eq(comparator_7_eq));  // open: gt, lt
  Comparator #(.width(32), .mode("twosComplement")) comparator_8 (
    .a(tag7), .b(EX_PC), .eq(comparator_8_eq));  // open: gt, lt
  Multiplexer #(.select(1), .width(2), .disabled("Z"), .enable("false")) multiplexer_5 (
    .in0(multiplexer_1_out), .in1(multiplexer_2_out), .out(multiplexer_5_out), .sel(or_17_out));
  or or_19 (or_19_out, or_18_out, or_20_out);
  Multiplexer #(.select(1), .width(2), .disabled("Z"), .enable("false")) multiplexer_6 (
    .in0(multiplexer_3_out), .in1(multiplexer_4_out), .out(multiplexer_6_out), .sel(or_18_out));
  MAX3 max3_7 (
    .Y(max3_6_max), .X(max3_5_max), .Y_num(max3_6_max_num), .X_num(max3_5_max_num), .Max_num(largest));  // open: MAX
  Multiplexer #(.select(1), .width(2), .disabled("Z"), .enable("false")) multiplexer_7 (
    .in0(multiplexer_5_out), .in1(multiplexer_6_out), .out(multiplexer_7_out), .sel(or_19_out));
  or or_20 (or_20_out, r4, r5);
  and and_1 (Er0, v0, comparator_1_eq);
  and and_2 (Er1, v1, comparator_2_eq);
  and and_3 (Er2, v2, comparator_3_eq);
  and and_4 (Er3, v3, comparator_4_eq);
  and and_5 (Er4, v4, comparator_5_eq);
  and and_6 (Er5, v5, comparator_6_eq);
  and and_7 (Er6, v6, comparator_7_eq);
  and and_8 (Er7, v7, comparator_8_eq);
  and and_9 (PredictJump, multiplexer_7_out[1], Hit);
  or or_21 (or_21_out, Er0, Er1, Er2, Er3, Er4, Er5, Er6, Er7);
  not not_1 (not_1_out, v0);
  not not_2 (not_2_out, v1);
  not not_3 (not_3_out, v2);
  not not_4 (not_4_out, v3);
  not not_5 (not_5_out, v4);
  not not_6 (not_6_out, v5);
  not not_7 (not_7_out, v6);
  not not_8 (not_8_out, v7);
  not not_9 (EX_Miss, or_21_out);
  Priority_Encoder #(.select(3), .disabled("Z")) priority_encoder_1 (
    .in0(not_1_out), .in1(not_2_out), .in2(not_3_out), .in3(not_4_out), .in4(not_5_out), .in5(not_6_out),
    .in6(not_7_out), .in7(not_8_out), .out(available), .en_out(AllValid), .en_in(1'b1));  // open: gs
  Comparator #(.width(32), .mode("twosComplement")) comparator_9 (
    .a(tag0), .b(PC), .eq(comparator_9_eq));  // open: gt, lt
  Comparator #(.width(32), .mode("twosComplement")) comparator_10 (
    .a(tag1), .b(PC), .eq(comparator_10_eq));  // open: gt, lt
  Comparator #(.width(32), .mode("twosComplement")) comparator_11 (
    .a(tag2), .b(PC), .eq(comparator_11_eq));  // open: gt, lt
  Comparator #(.width(32), .mode("twosComplement")) comparator_12 (
    .a(tag3), .b(PC), .eq(comparator_12_eq));  // open: gt, lt
  Comparator #(.width(32), .mode("twosComplement")) comparator_13 (
    .a(tag4), .b(PC), .eq(comparator_13_eq));  // open: gt, lt
  Comparator #(.width(32), .mode("twosComplement")) comparator_14 (
    .a(tag5), .b(PC), .eq(comparator_14_eq));  // open: gt, lt
  Comparator #(.width(32), .mode("twosComplement")) comparator_15 (
    .a(tag6), .b(PC), .eq(comparator_15_eq));  // open: gt, lt
  Comparator #(.width(32), .mode("twosComplement")) comparator_16 (
    .a(tag7), .b(PC), .eq(comparator_16_eq));  // open: gt, lt
  Multiplexer #(.select(1), .width(3), .disabled("Z"), .enable("false")) multiplexer_8 (
    .in0(available), .in1(largest), .out(multiplexer_8_out), .sel(AllValid));
  and and_10 (and_10_out, EX_IsBranch, EX_Miss);
  and and_11 (r0, v0, comparator_9_eq);
  and and_12 (r1, v1, comparator_10_eq);
  and and_13 (r2, v2, comparator_11_eq);
  and and_14 (r3, v3, comparator_12_eq);
  and and_15 (r4, v4, comparator_13_eq);
  and and_16 (r5, v5, comparator_14_eq);
  and and_17 (r6, v6, comparator_15_eq);
  and and_18 (r7, v7, comparator_16_eq);
  Demultiplexer #(.select(3), .width(1), .tristate("false"), .disabled("Z"), .enable("false")) demultiplexer_1 (
    .out0(write0), .out1(write1), .out2(write2), .out3(write3), .out4(write4), .out5(write5), .out6(write6),
    .out7(write7), .in(and_10_out), .sel(multiplexer_8_out));
  or or_22 (Hit, r0, r1, r2, r3, r4, r5, r6, r7);

  // Other names for the same wires on the sheet: Blk[31:0] = EX_branchAddr; isBranch = EX_IsBranch;
  //   Jump = PredictJump; DataOut[31:0] = JumpAddr; SlotData[31:0] = JumpAddr; taken = EX_BranchTaken

  // Notes on the sheet:
  //   如果每一行都是valid，就需要将count最大的进行替换，利用Max3找出替换的行
  //   如果还有空位，就按照优先级顺序放置，没有空位AllValid信号位1，指示要替换
endmodule

// IF/ID
module \动态分支预测IF_ID  (
  input  IF_PredictJump,
  input  [31:0] IF_PC,
  input  [31:0] IF_IR,
  input  clk,
  input  halt,
  input  rst,
  output ID_PredictJump,
  output [31:0] ID_PC,
  output [31:0] ID_IR
);

  wire multiplexer_1_out;
  wire [31:0] multiplexer_2_out, multiplexer_3_out;

  Multiplexer #(.select(1), .width(1), .disabled("Z"), .enable("false")) multiplexer_1 (
    .in0(IF_PredictJump), .in1(1'b0), .out(multiplexer_1_out), .sel(rst));
  Multiplexer #(.select(1), .width(32), .disabled("Z"), .enable("false")) multiplexer_2 (
    .in0(IF_PC), .in1({32{1'b0}}), .out(multiplexer_2_out), .sel(rst));
  Multiplexer #(.select(1), .width(32), .disabled("Z"), .enable("false")) multiplexer_3 (
    .in0(IF_IR), .in1({32{1'b0}}), .out(multiplexer_3_out), .sel(rst));
  Register #(.width(1), .trigger("rising"), .Select("low")) PC (
    .D(multiplexer_1_out), .en(halt), .Q(ID_PredictJump), .clk(clk));  // open: clr
  Register #(.width(32), .trigger("rising"), .Select("low")) PC_2 (
    .D(multiplexer_2_out), .en(halt), .Q(ID_PC), .clk(clk));  // open: clr
  Register #(.width(32), .trigger("rising"), .Select("low")) IR (
    .D(multiplexer_3_out), .en(halt), .Q(ID_IR), .clk(clk));  // open: clr
endmodule
// ID/EX
module \动态分支预测ID_EX  (
  input  [4:0] ID_rd,
  input  [31:0] ID_a,
  input  [31:0] ID_b,
  input  [31:0] ID_imm,
  input  [31:0] ID_imm_B,
  input  [31:0] ID_imm_Jal,
  input  [31:0] ID_imm_Lui,
  input  [31:0] ID_PC,
  input  [31:0] ID_IR,
  input  ID_PredictJump,
  input  [1:0] ID_FwdA,
  input  [1:0] ID_FwdB,
  input  [15:0] ID_sgn,
  input  clk,
  input  rst,
  input  halt,
  output [4:0] EX_rd,
  output [31:0] EX_a,
  output [31:0] EX_b,
  output [31:0] EX_imm,
  output [31:0] EX_imm_B,
  output [31:0] EX_imm_Jal,
  output [31:0] EX_imm_Lui,
  output [31:0] EX_PC,
  output [31:0] EX_IR,
  output EX_PredictJump,
  output [1:0] EX_FwdA,
  output [1:0] EX_FwdB,
  output [15:0] EX_sgn
);

  wire multiplexer_10_out;
  wire [1:0] multiplexer_11_out, multiplexer_12_out;
  wire [4:0] multiplexer_1_out;
  wire [15:0] multiplexer_13_out;
  wire [31:0] multiplexer_2_out, multiplexer_3_out, multiplexer_4_out, multiplexer_5_out, multiplexer_6_out,
       multiplexer_7_out, multiplexer_8_out, multiplexer_9_out;

  Multiplexer #(.select(1), .width(5), .disabled("Z"), .enable("false")) multiplexer_1 (
    .in0(ID_rd), .in1({5{1'b0}}), .out(multiplexer_1_out), .sel(rst));
  Multiplexer #(.select(1), .width(32), .disabled("Z"), .enable("false")) multiplexer_2 (
    .in0(ID_a), .in1({32{1'b0}}), .out(multiplexer_2_out), .sel(rst));
  Multiplexer #(.select(1), .width(32), .disabled("Z"), .enable("false")) multiplexer_3 (
    .in0(ID_b), .in1({32{1'b0}}), .out(multiplexer_3_out), .sel(rst));
  Multiplexer #(.select(1), .width(32), .disabled("Z"), .enable("false")) multiplexer_4 (
    .in0(ID_imm), .in1({32{1'b0}}), .out(multiplexer_4_out), .sel(rst));
  Multiplexer #(.select(1), .width(32), .disabled("Z"), .enable("false")) multiplexer_5 (
    .in0(ID_imm_B), .in1({32{1'b0}}), .out(multiplexer_5_out), .sel(rst));
  Multiplexer #(.select(1), .width(32), .disabled("Z"), .enable("false")) multiplexer_6 (
    .in0(ID_imm_Jal), .in1({32{1'b0}}), .out(multiplexer_6_out), .sel(rst));
  Multiplexer #(.select(1), .width(32), .disabled("Z"), .enable("false")) multiplexer_7 (
    .in0(ID_imm_Lui), .in1({32{1'b0}}), .out(multiplexer_7_out), .sel(rst));
  Multiplexer #(.select(1), .width(32), .disabled("Z"), .enable("false")) multiplexer_8 (
    .in0(ID_PC), .in1({32{1'b0}}), .out(multiplexer_8_out), .sel(rst));
  Multiplexer #(.select(1), .width(32), .disabled("Z"), .enable("false")) multiplexer_9 (
    .in0(ID_IR), .in1({32{1'b0}}), .out(multiplexer_9_out), .sel(rst));
  Multiplexer #(.select(1), .width(1), .disabled("Z"), .enable("false")) multiplexer_10 (
    .in0(ID_PredictJump), .in1(1'b0), .out(multiplexer_10_out), .sel(rst));
  Multiplexer #(.select(1), .width(2), .disabled("Z"), .enable("false")) multiplexer_11 (
    .in0(ID_FwdA), .in1(2'b00), .out(multiplexer_11_out), .sel(rst));
  Multiplexer #(.select(1), .width(2), .disabled("Z"), .enable("false")) multiplexer_12 (
    .in0(ID_FwdB), .in1(2'b00), .out(multiplexer_12_out), .sel(rst));
  Multiplexer #(.select(1), .width(16), .disabled("Z"), .enable("false")) multiplexer_13 (
    .in0(ID_sgn), .in1({16{1'b0}}), .out(multiplexer_13_out), .sel(rst));
  Register #(.width(5), .trigger("rising"), .Select("low")) register_1 (
    .D(multiplexer_1_out), .en(halt), .Q(EX_rd), .clk(clk));  // open: clr
  Register #(.width(32), .trigger("rising"), .Select("low")) register_2 (
    .D(multiplexer_2_out), .en(halt), .Q(EX_a), .clk(clk));  // open: clr
  Register #(.width(32), .trigger("rising"), .Select("low")) register_3 (
    .D(multiplexer_3_out), .en(halt), .Q(EX_b), .clk(clk));  // open: clr
  Register #(.width(32), .trigger("rising"), .Select("low")) register_4 (
    .D(multiplexer_4_out), .en(halt), .Q(EX_imm), .clk(clk));  // open: clr
  Register #(.width(32), .trigger("rising"), .Select("low")) register_5 (
    .D(multiplexer_5_out), .en(halt), .Q(EX_imm_B), .clk(clk));  // open: clr
  Register #(.width(32), .trigger("rising"), .Select("low")) register_6 (
    .D(multiplexer_6_out), .en(halt), .Q(EX_imm_Jal), .clk(clk));  // open: clr
  Register #(.width(32), .trigger("rising"), .Select("low")) register_7 (
    .D(multiplexer_7_out), .en(halt), .Q(EX_imm_Lui), .clk(clk));  // open: clr
  Register #(.width(32), .trigger("rising"), .Select("low")) register_8 (
    .D(multiplexer_8_out), .en(halt), .Q(EX_PC), .clk(clk));  // open: clr
  Register #(.width(32), .trigger("rising"), .Select("low")) register_9 (
    .D(multiplexer_9_out), .en(halt), .Q(EX_IR), .clk(clk));  // open: clr
  Register #(.width(1), .trigger("rising"), .Select("low")) register_10 (
    .D(multiplexer_10_out), .en(halt), .Q(EX_PredictJump), .clk(clk));  // open: clr
  Register #(.width(2), .trigger("rising"), .Select("low")) register_11 (
    .D(multiplexer_11_out), .en(halt), .Q(EX_FwdA), .clk(clk));  // open: clr
  Register #(.width(2), .trigger("rising"), .Select("low")) register_12 (
    .D(multiplexer_12_out), .en(halt), .Q(EX_FwdB), .clk(clk));  // open: clr
  Register #(.width(16), .trigger("rising"), .Select("low")) register_13 (
    .D(multiplexer_13_out), .en(halt), .Q(EX_sgn), .clk(clk));  // open: clr
endmodule

// NEW PC
module \动态分支预测PC计算  (
  input  predict,
  input  predictError,
  input  [31:0] PC_4,
  input  [31:0] JumpAddr,
  input  EX_bjump,
  input  [31:0] EX_PC___4,
  input  [31:0] EX_BranchAddr,
  output [31:0] new_PC
);

  wire [31:0] multiplexer_1_out, multiplexer_2_out;

  Multiplexer #(.select(1), .width(32), .disabled("Z"), .enable("false")) multiplexer_1 (
    .in0(PC_4), .in1(JumpAddr), .out(multiplexer_1_out), .sel(predict));
  Multiplexer #(.select(1), .width(32), .disabled("Z"), .enable("false")) multiplexer_2 (
    .in0(EX_PC___4), .in1(EX_BranchAddr), .out(multiplexer_2_out), .sel(EX_bjump));
  Multiplexer #(.select(1), .width(32), .disabled("Z"), .enable("false")) multiplexer_3 (
    .in0(multiplexer_1_out), .in1(multiplexer_2_out), .out(new_PC), .sel(predictError));
endmodule

// Max3
module MAX3 (
  input  [15:0] Y,
  input  [15:0] X,
  input  [2:0] Y_num,
  input  [2:0] X_num,
  output [15:0] MAX,
  output [2:0] Max_num
);

  wire comparator_1_eq, comparator_1_gt, or_1_out;

  Multiplexer #(.select(1), .width(16), .disabled("Z"), .enable("false")) multiplexer_1 (
    .in0(Y), .in1(X), .out(MAX), .sel(or_1_out));
  Comparator #(.width(16), .mode("unsigned")) comparator_1 (
    .a(X), .b(Y), .gt(comparator_1_gt), .eq(comparator_1_eq));  // open: lt
  or or_1 (or_1_out, comparator_1_gt, comparator_1_eq);
  Multiplexer #(.select(1), .width(3), .disabled("Z"), .enable("false")) multiplexer_2 (
    .in0(Y_num), .in1(X_num), .out(Max_num), .sel(or_1_out));

  // Notes on the sheet:
  //   输出两个输入中的较大值，并输出较大值的3位编号
endmodule

module \状态转换  (
  input  [1:0] state,
  input  write,
  input  jump,
  output [1:0] new_state
);

  wire and_1_out, and_2_out, and_3_out, and_4_out, not_1_out, not_2_out, not_3_out, not_4_out, not_5_out;
  wire [1:0] or_2_out;

  not not_1 (not_1_out, state[0]);
  not not_2 (not_2_out, state[1]);
  not not_3 (not_3_out, state[0]);
  not not_4 (not_4_out, state[0]);
  not not_5 (not_5_out, jump);
  and and_1 (and_1_out, state[0], jump);
  and and_2 (and_2_out, state[1], not_1_out);
  and and_3 (and_3_out, not_2_out, not_3_out, jump);
  and and_4 (and_4_out, state[1], not_4_out, not_5_out);
  or or_1 (or_2_out[1], and_1_out, and_2_out);
  or or_2 (or_2_out[0], and_3_out, and_4_out);
  Multiplexer #(.select(1), .width(2), .disabled("Z"), .enable("false")) multiplexer_1 (
    .in0(state), .in1(or_2_out), .out(new_state), .sel(write));
endmodule

module \流水线中断  (
  output RegWrite,
  output MemWrite,
  output [31:0] IF_PC,
  output [31:0] ID_PC,
  output [31:0] EX_PC,
  output [31:0] M_PC,
  output [31:0] WB_PC,
  output [31:0] RDin,
  output [31:0] MDin,
  output [31:0] LedData
);

  wire alu_1_equal, alu_1_out_4, and_1_out, and_3_out, and_4_out, and_5_out, and_6_out, and_11_out,
       and_12_out, and_13_out, and_14_out, and_15_out, and_16_out, Bge, bjump, Branch, btb_1_predictjump,
       CLK, clock_1_out, clock_2_out, comparator_1_eq, comparator_2_eq, comparator_3_eq, comparator_4_eq,
       comparator_5_eq, comparator_6_eq, comparator_7_eq, comparator_7_lt, d_ff_1_q, d_ff_2_q, d_ff_3_q,
       d_ff_4_q, decoder_1_out1, decoder_1_out2, decoder_1_out3, Ecall, Equal, EX_branchtaken, EX_isbranch,
       EX_jumpPredict, EX_MemToReg, EX_RegWrite, EX_Uret, F_LoadUse, F_predictError, Go, halt, ID_Uret, IE,
       IF_Uret, INT, IR1_q, IR2_q, IR3_q, IRA, IRB, IRC, ISIR, J, Jal, Jalr, Lbu, LoadUse, Lui, MEM_Lui,
       MEM_RegWrite, nand_1_out, not_1_out, not_3_out, not_5_out, not_6_out, not_7_out, or_1_out, or_5_out,
       or_6_out, or_7_out, or_8_out, or_10_out, or_13_out, or_14_out, predictError, register_2_q,
       register_4_q, RST, rst1, rst2, rst3, S, W1, W2, W3, \动态分支预测if_id_1_id_predictjump , \单周期硬布线控制器_1_rs1 ,
       \单周期硬布线控制器_1_rs2 , \气泡ex_mem_1_mem_equal ;
  wire [1:0] cause_q, priority_encoder_1_out, \流水线中断id_ex_1_ex_fwda , \流水线中断id_ex_1_ex_fwdb ,
       \重定向逻辑设计_1_fwda , \重定向逻辑设计_1_fwdb ;
  wire [3:0] \单周期硬布线控制器_1_alu_op ;
  wire [4:0] bit_extender_1_out, minus, multiplexer_5_out, multiplexer_7_out, subtractor_1_out, WB_rd,
       \气泡ex_mem_1_mem_rd , \气泡ir扩展器_1_funct , \气泡ir扩展器_1_op , \气泡ir扩展器_1_rd , \气泡ir扩展器_1_rs1 ,
       \气泡ir扩展器_1_rs2 , \流水线中断id_ex_1_ex_rd ;
  wire [11:1] \单周期硬布线控制器_1_beq ;
  wire [12:0] CNT_num;
  wire [14:0] \气泡ex_mem_1_mem_sgn ;
  wire [15:0] \LoadUse次数 , \总周期数 , \无条件分支数 , \条件分支成功数 , \气泡mem_wb_1_wb_sgn , \流水线中断id_ex_1_ex_sgn , \预测错误数 ;
  wire [31:0] adder_1_out, adder_2_out, adder_3_out, adder_5_out, alu_1_result, bAddr, BreakPoint, EX_bAddr,
       EX_IR, F_EX_bAddr, ID_IR, IF_IR, INTPC, jAddr, jumpAddr, LedShow, MEM_IR, multiplexer_1_out,
       multiplexer_2_out, multiplexer_8_out, multiplexer_9_out, multiplexer_10_out, multiplexer_11_out,
       multiplexer_12_out, multiplexer_14_out, multiplexer_15_out, multiplexer_16_out, PC_q, ram_1_data,
       regifile_1_r1, regifile_1_r2, RETPC, shifter_2_out, shifter_3_out, WB_IR, \动态分支预测pc计算_1_new_pc ,
       \气泡ex_mem_1_mem_alu_r , \气泡ex_mem_1_mem_imm_lui , \气泡ir扩展器_1_imm , \气泡ir扩展器_1_imm_b ,
       \气泡ir扩展器_1_imm_jal , \气泡ir扩展器_1_imm_lui , \气泡mem_wb_1_wb_alu_md , \流水线中断id_ex_1_ex_a ,
       \流水线中断id_ex_1_ex_b , \流水线中断id_ex_1_ex_imm , \流水线中断id_ex_1_ex_imm_b , \流水线中断id_ex_1_ex_imm_jal ,
       \流水线中断id_ex_1_ex_imm_lui ;

  Button \u_总复位  (.out(RST));
  Button _1 ();  // open: out
  Button _2 ();  // open: out
  Button _3 ();  // open: out
  // Probe on \总周期数 
  // Probe on \总周期数 
  Button \u_继续运行  (.out(Go));
  LED #(.active("true")) led_1 (.in(W1));
  LED #(.active("true")) led_2 (.in(W2));
  LED #(.active("true")) led_3 (.in(W3));
  Hex_Digit_Display hex_digit_display_1 (.value(LedData[31:28]));  // open: dp
  // Probe on IF_PC[19:0]
  // RiscV_Probe riscv_probe_1: pin names not known; wires that end beside it: IRA, IRB, IRC, IF_IR
  Adder #(.width(32)) adder_1 (.a(INTPC), .b(32'h4), .out(adder_1_out));  // open: cin, cout
  Hex_Digit_Display hex_digit_display_2 (.value(LedData[27:24]));  // open: dp
  Hex_Digit_Display hex_digit_display_3 (.value(LedData[23:20]));  // open: dp
  // Probe on ID_PC[19:0]
  // RiscV_Probe riscv_probe_2: pin names not known; wires that end beside it: ID_IR
  Comparator #(.width(16), .mode("twosComplement")) comparator_1 (
    .a(16'h2d2), .b(\总周期数 ), .eq(comparator_1_eq));  // open: gt, lt
  or or_1 (or_1_out, comparator_1_eq, comparator_2_eq);
  Comparator #(.width(16), .mode("twosComplement")) comparator_2 (
    .a(\总周期数 ), .b(16'h13), .eq(comparator_2_eq));  // open: gt, lt
  Comparator #(.width(16), .mode("twosComplement")) comparator_3 (
    .a(\总周期数 ), .b(16'h19), .eq(comparator_3_eq));  // open: gt, lt
  Comparator #(.width(16), .mode("twosComplement")) comparator_4 (
    .a(\总周期数 ), .b(16'h28), .eq(comparator_4_eq));  // open: gt, lt
  Multiplexer #(.select(1), .width(32), .disabled("Z"), .enable("false")) multiplexer_1 (
    .in0(\动态分支预测pc计算_1_new_pc ), .in1(adder_1_out), .out(multiplexer_1_out), .sel(INT));
  Multiplexer #(.select(1), .width(32), .disabled("Z"), .enable("false")) multiplexer_2 (
    .in0(multiplexer_1_out), .in1(RETPC), .out(multiplexer_2_out), .sel(IF_Uret));
  Hex_Digit_Display hex_digit_display_4 (.value(LedData[19:16]));  // open: dp
  Hex_Digit_Display hex_digit_display_5 (.value(LedData[15:12]));  // open: dp
  Pull_Resistor #(.pull(0)) pull_resistor_1 (.node(IRA));
  assign IRA = or_1_out ? ~CLK : 1'bz;  // Controlled_Inverter controlled_inverter_1
  Pull_Resistor #(.pull(0)) pull_resistor_2 (.node(IRB));
  assign IRB = comparator_3_eq ? ~CLK : 1'bz;  // Controlled_Inverter controlled_inverter_2
  Pull_Resistor #(.pull(0)) pull_resistor_3 (.node(IRC));
  assign IRC = comparator_4_eq ? ~CLK : 1'bz;  // Controlled_Inverter controlled_inverter_3
  not not_1 (not_1_out, LoadUse);
  and and_1 (and_1_out, halt, not_1_out);
  Register #(.width(32), .trigger("rising"), .Select("low")) PC (
    .D(multiplexer_2_out), .en(and_1_out), .Q(PC_q), .clk(CLK), .clr(RST));
  Hex_Digit_Display hex_digit_display_6 (.value(LedData[7:4]));  // open: dp
  Hex_Digit_Display hex_digit_display_7 (.value(LedData[11:8]));  // open: dp
  Clock #(.highDuration(1), .lowDuration(1)) clock_1 (.out(clock_1_out));
  // Probe on EX_PC[19:0]
  // RiscV_Probe riscv_probe_3: pin names not known; wires that end beside it: EX_IR, clock_1_out, CLK
  Multiplexer #(.select(1), .width(32), .disabled("Z"), .enable("false")) multiplexer_3 (
    .in0(PC_q), .in1(INTPC), .out(IF_PC), .sel(INT));
  Comparator #(.width(1), .mode("twosComplement")) comparator_5 (
    .a(EX_jumpPredict), .b(EX_branchtaken), .eq(comparator_5_eq));  // open: gt, lt
  Hex_Digit_Display hex_digit_display_8 (.value(LedData[3:0]));  // open: dp
  \动态分支预测PC计算  \u_动态分支预测pc计算_1  (
    .PC_4(adder_3_out), .JumpAddr(jumpAddr), .EX_PC___4(adder_2_out), .EX_BranchAddr(EX_bAddr),
    .new_PC(\动态分支预测pc计算_1_new_pc ), .predict(btb_1_predictjump), .EX_bjump(EX_branchtaken),
    .predictError(predictError));
  BTB btb_1 (
    .EX_branchAddr(EX_bAddr), .EX_PC(EX_PC), .CLK(CLK), .JumpAddr(jumpAddr), .PC(IF_PC),
    .EX_BranchTaken(EX_branchtaken), .PredictJump(btb_1_predictjump), .EX_IsBranch(EX_isbranch));
  not not_2 (predictError, comparator_5_eq);
  // Probe on \总周期数 
  // Probe on M_PC[19:0]
  // RiscV_Probe riscv_probe_4: pin names not known; wires that end beside it: MEM_IR
  D_Flip_Flop #(.trigger("rising"), .Pre_Clr_Positions("LEGACY"), .NegatePresetClear("false"), .enable("true"), .NewFFLayout("false")) d_ff_1 (
    .clk(IRA), .D(1'b1), .Q(d_ff_1_q), .reset(IR1_q));  // open: Qn, preset, en
  or or_2 (W1, IR1_q, d_ff_1_q);
  D_Flip_Flop #(.trigger("rising"), .Pre_Clr_Positions("LEGACY"), .NegatePresetClear("false"), .enable("true"), .NewFFLayout("false")) d_ff_2 (
    .clk(IRB), .D(1'b1), .Q(d_ff_2_q), .reset(IR2_q));  // open: Qn, preset, en
  or or_3 (W2, IR2_q, d_ff_2_q);
  D_Flip_Flop #(.trigger("rising"), .Pre_Clr_Positions("LEGACY"), .NegatePresetClear("false"), .enable("true"), .NewFFLayout("false")) d_ff_3 (
    .clk(IRC), .D(1'b1), .Q(d_ff_3_q), .reset(IR3_q));  // open: Qn, preset, en
  or or_4 (W3, IR3_q, d_ff_3_q);
  and and_2 (IF_Uret, IF_IR[21], comparator_6_eq);
  Comparator #(.width(5), .mode("twosComplement")) comparator_6 (
    .a(IF_IR[6:2]), .b(5'b11100), .eq(comparator_6_eq));  // open: gt, lt
  Adder #(.width(32)) adder_2 (.a(EX_PC), .b(32'h4), .out(adder_2_out));  // open: cin, cout
  // Probe on \总周期数 
  // Probe on \无条件分支数 
  // Probe on \条件分支成功数 
  // Probe on \预测错误数 
  // Probe on \LoadUse次数 
  ROM #(.addrWidth(10), .dataWidth(32), .Select("high")) rom_1 (.addr(IF_PC[11:2]), .data(IF_IR));
  Adder #(.width(32)) adder_3 (.a(IF_PC), .b(32'h4), .out(adder_3_out));  // open: cin, cout
  // Probe on IF_PC[11:0]
  // Probe on WB_PC[19:0]
  // RiscV_Probe riscv_probe_5: pin names not known; wires that end beside it: WB_IR
  or or_5 (or_5_out, d_ff_1_q, IR1_q);
  and and_3 (and_3_out, or_5_out, ~rst1);  // AND_Gate
  or or_6 (or_6_out, d_ff_2_q, IR2_q);
  and and_4 (and_4_out, or_6_out, ~rst2);  // AND_Gate
  or or_7 (or_7_out, d_ff_3_q, IR3_q);
  and and_5 (and_5_out, or_7_out, ~rst3);  // AND_Gate
  \动态分支预测IF_ID  \u_动态分支预测if_id_1  (
    .IF_PredictJump(btb_1_predictjump), .IF_PC(IF_PC), .IF_IR(IF_IR), .clk(CLK), .halt(and_6_out),
    .ID_PredictJump(\动态分支预测if_id_1_id_predictjump ), .ID_PC(ID_PC), .ID_IR(ID_IR), .rst(or_8_out));
  or or_8 (or_8_out, predictError, RST);
  and and_6 (and_6_out, not_3_out, halt);
  Multiplexer #(.select(1), .width(32), .disabled("Z"), .enable("false")) multiplexer_4 (
    .in0(jAddr), .in1(bAddr), .out(EX_bAddr), .sel(Branch));
  // Probe on ID_PC[11:0]
  // Probe on EX_PC[11:0]
  D_Flip_Flop #(.trigger("rising"), .Pre_Clr_Positions("LEGACY"), .NegatePresetClear("false"), .enable("true"), .NewFFLayout("false")) IR1 (
    .clk(CLK), .D(and_3_out), .Q(IR1_q));  // open: Qn, preset, en, reset
  D_Flip_Flop #(.trigger("rising"), .Pre_Clr_Positions("LEGACY"), .NegatePresetClear("false"), .enable("true"), .NewFFLayout("false")) IR2 (
    .clk(CLK), .D(and_4_out), .Q(IR2_q));  // open: Qn, preset, en, reset
  D_Flip_Flop #(.trigger("rising"), .Pre_Clr_Positions("LEGACY"), .NegatePresetClear("false"), .enable("true"), .NewFFLayout("false")) IR3 (
    .clk(CLK), .D(and_5_out), .Q(IR3_q));  // open: Qn, preset, en, reset
  not not_3 (not_3_out, LoadUse);
  or or_9 (EX_isbranch, J, Branch);
  Register #(.width(32), .trigger("rising"), .Select("low")) register_1 (
    .D(EX_bAddr), .Q(F_EX_bAddr), .clk(CLK));  // open: en, clr
  // Probe on M_PC[11:0]
  D_Flip_Flop #(.trigger("high"), .Pre_Clr_Positions("LEGACY"), .NegatePresetClear("false"), .enable("true"), .NewFFLayout("false")) d_ff_4 (.Q(d_ff_4_q));  // open: clk, D, Qn, preset, en, reset
  // Probe on 13'h304
  \气泡IR扩展器  \u_气泡ir扩展器_1  (
    .IR(ID_IR), .s(S), .OP(\气泡ir扩展器_1_op ), .Funct(\气泡ir扩展器_1_funct ), .rs1(\气泡ir扩展器_1_rs1 ),
    .rs2(\气泡ir扩展器_1_rs2 ), .rd(\气泡ir扩展器_1_rd ), .imm(\气泡ir扩展器_1_imm ), .imm_b(\气泡ir扩展器_1_imm_b ),
    .imm_lui(\气泡ir扩展器_1_imm_lui ), .imm_jal(\气泡ir扩展器_1_imm_jal ));
  // Probe on WB_PC[11:0]
  Comparator #(.width(13), .mode("twosComplement")) comparator_7 (
    .a(CNT_num), .b(13'h304), .eq(comparator_7_eq), .lt(comparator_7_lt));  // open: gt
  Clock #(.highDuration(1), .lowDuration(1)) clock_2 (.out(clock_2_out));
  Priority_Encoder #(.select(2), .disabled("Z")) priority_encoder_1 (
    .in0(1'b0), .in1(IR1_q), .in2(IR2_q), .in3(IR3_q), .out(priority_encoder_1_out), .gs(ISIR));  // open: en_out, en_in
  Register #(.width(1), .trigger("rising"), .Select("low")) register_2 (
    .D(IE), .Q(register_2_q), .clk(CLK));  // open: en, clr
  \单周期硬布线控制器  \u_单周期硬布线控制器_1  (
    .Funct(\气泡ir扩展器_1_funct ), .OP(\气泡ir扩展器_1_op ), .ALU_OP(\单周期硬布线控制器_1_alu_op ),
    .MemToReg(\单周期硬布线控制器_1_beq [3]), .MemWrite(\单周期硬布线控制器_1_beq [4]), .ALU_SRC(\单周期硬布线控制器_1_beq [9]),
    .RegWrite(\单周期硬布线控制器_1_beq [10]), .ecall(\单周期硬布线控制器_1_beq [11]), .S_type(S), .Jalr(Jalr),
    .Beq(\单周期硬布线控制器_1_beq [1]), .JAL(Jal), .Bne(\单周期硬布线控制器_1_beq [2]), .Lui(Lui), .Lbu(Lbu), .Bge(Bge),
    .rs1(\单周期硬布线控制器_1_rs1 ), .rs2(\单周期硬布线控制器_1_rs2 ), .uret(ID_Uret), .IR21(ID_IR[21]));  // open: csrrsi, csrrci
  Multiplexer #(.select(1), .width(5), .disabled("Z"), .enable("false")) multiplexer_5 (
    .in0(\气泡ir扩展器_1_rs1 ), .in1(5'b10001), .out(multiplexer_5_out), .sel(\单周期硬布线控制器_1_beq [11]));
  nand nand_1 (nand_1_out, d_ff_4_q, comparator_7_eq);
  Counter #(.width(13), .max('h1fff), .ongoal("stay"), .trigger("rising"), .behavior("old")) counter_1 (
    .count(comparator_7_lt), .Q(CNT_num), .clk(clock_2_out));  // open: load, D, carry, clr, preset
  Register #(.width(2), .trigger("rising"), .Select("low")) cause (
    .D(priority_encoder_1_out), .Q(cause_q), .clk(INT));  // open: en, clr
  Multiplexer #(.select(2), .width(32), .disabled("Z"), .enable("false")) multiplexer_6 (
    .in1(32'h30ac), .in2(32'h3150), .in3(32'h31f4), .out(INTPC), .sel(priority_encoder_1_out));  // open: in0
  and and_7 (INT, ISIR, register_2_q);
  Multiplexer #(.select(1), .width(5), .disabled("Z"), .enable("false")) multiplexer_7 (
    .in0(\气泡ir扩展器_1_rs2 ), .in1(5'b01010), .out(multiplexer_7_out), .sel(\单周期硬布线控制器_1_beq [11]));
  Register #(.width(1), .trigger("rising"), .Select("low")) register_3 (
    .D(predictError), .Q(F_predictError), .clk(CLK));  // open: en, clr
  assign CLK = nand_1_out ? clock_2_out : 1'bz;  // Controlled_Buffer controlled_buffer_1
  Decoder #(.select(2), .tristate("false"), .disabled("Z"), .enable("false")) decoder_1 (
    .out1(decoder_1_out1), .out2(decoder_1_out2), .out3(decoder_1_out3), .sel(cause_q));  // open: out0
  \重定向逻辑设计  \u_重定向逻辑设计_1  (
    .rs1_u(\单周期硬布线控制器_1_rs1 ), .bJump(bjump), .rs2_u(\单周期硬布线控制器_1_rs2 ), .J(J), .EX_RegWrite(EX_RegWrite),
    .MEM_RegWrite(MEM_RegWrite), .MemToReg(EX_MemToReg), .rs1(multiplexer_5_out),
    .EX_rd(\流水线中断id_ex_1_ex_rd ), .MEM_rd(\气泡ex_mem_1_mem_rd ), .rs2(multiplexer_7_out),
    .Jpop(EX_branchtaken), .LoadUse(LoadUse), .fwdb(\重定向逻辑设计_1_fwdb ), .fwda(\重定向逻辑设计_1_fwda ));
  Pull_Resistor #(.pull(1)) pull_resistor_4 (.node(CLK));
  and and_8 (rst1, IF_Uret, decoder_1_out1);
  and and_9 (rst2, IF_Uret, decoder_1_out2);
  and and_10 (rst3, decoder_1_out3, IF_Uret);
  Register #(.width(32), .trigger("falling"), .Select("low")) EPC (
    .D(BreakPoint), .en(INT), .Q(RETPC), .clk(CLK));  // open: clr
  Register #(.width(1), .trigger("rising"), .Select("low")) register_4 (
    .D(1'b0), .en(EX_Uret), .Q(register_4_q), .clk(CLK), .preset(INT));  // open: clr, cs
  not not_4 (IE, register_4_q);
  Regifile regifile_1 (
    .Din(RDin), .Clk(CLK), .R1(regifile_1_r1), .R2(regifile_1_r2), .WE(RegWrite), .W_num(WB_rd),
    .R1_num(multiplexer_5_out), .R2_num(multiplexer_7_out));
  \流水线中断ID_EX  \u_流水线中断id_ex_1  (
    .ID_rd(\气泡ir扩展器_1_rd ), .ID_a(regifile_1_r1), .ID_b(regifile_1_r2), .ID_imm(\气泡ir扩展器_1_imm ),
    .ID_imm_B(\气泡ir扩展器_1_imm_b ), .ID_imm_Jal(\气泡ir扩展器_1_imm_jal ), .ID_imm_Lui(\气泡ir扩展器_1_imm_lui ),
    .ID_PC(ID_PC), .ID_IR(ID_IR), .ID_Uret(ID_Uret), .ID_PredictJump(\动态分支预测if_id_1_id_predictjump ),
    .ID_FwdA(\重定向逻辑设计_1_fwda ), .ID_FwdB(\重定向逻辑设计_1_fwdb ),
    .ID_sgn({Lui, Lbu, Jalr, Jal, \单周期硬布线控制器_1_beq [11:9], \单周期硬布线控制器_1_alu_op , \单周期硬布线控制器_1_beq [4:1], Bge}),
    .EX_rd(\流水线中断id_ex_1_ex_rd ), .EX_a(\流水线中断id_ex_1_ex_a ), .EX_b(\流水线中断id_ex_1_ex_b ),
    .EX_imm(\流水线中断id_ex_1_ex_imm ), .EX_imm_B(\流水线中断id_ex_1_ex_imm_b ),
    .EX_imm_Jal(\流水线中断id_ex_1_ex_imm_jal ), .EX_imm_Lui(\流水线中断id_ex_1_ex_imm_lui ), .EX_PC(EX_PC),
    .EX_IR(EX_IR), .EX_Uret(EX_Uret), .EX_PredictJump(EX_jumpPredict), .EX_FwdA(\流水线中断id_ex_1_ex_fwda ),
    .EX_FwdB(\流水线中断id_ex_1_ex_fwdb ),
    .EX_sgn({\流水线中断id_ex_1_ex_sgn [15:11], EX_RegWrite, \流水线中断id_ex_1_ex_sgn [9:4], EX_MemToReg, \流水线中断id_ex_1_ex_sgn [2:0]}),
    .clk(CLK), .rst(or_10_out), .halt(halt));
  Register #(.width(1), .trigger("rising"), .Select("low")) register_5 (
    .D(LoadUse), .Q(F_LoadUse), .clk(CLK));  // open: en, clr
  Multiplexer #(.select(2), .width(32), .disabled("Z"), .enable("false")) multiplexer_8 (
    .in0(\流水线中断id_ex_1_ex_a ), .in1(RDin), .in2(multiplexer_14_out), .out(multiplexer_8_out),
    .sel(\流水线中断id_ex_1_ex_fwda ));  // open: in3
  Multiplexer #(.select(2), .width(32), .disabled("Z"), .enable("false")) multiplexer_9 (
    .in0(\流水线中断id_ex_1_ex_b ), .in1(RDin), .in2(multiplexer_14_out), .out(multiplexer_9_out),
    .sel(\流水线中断id_ex_1_ex_fwdb ));  // open: in3
  or or_10 (or_10_out, LoadUse, RST, predictError, INT);
  Multiplexer #(.select(1), .width(32), .disabled("Z"), .enable("false")) multiplexer_10 (
    .in0(multiplexer_9_out), .in1(\流水线中断id_ex_1_ex_imm ), .out(multiplexer_10_out),
    .sel(\流水线中断id_ex_1_ex_sgn [9]));
  Counter #(.width(16), .max('hffff), .ongoal("wrap"), .trigger("rising"), .behavior("old")) counter_2 (
    .count(halt), .Q(\总周期数 ), .clk(CLK), .clr(RST));  // open: load, D, carry, preset
  Multiplexer #(.select(1), .width(32), .disabled("Z"), .enable("false")) multiplexer_11 (
    .in0(multiplexer_10_out), .in1(32'ha), .out(multiplexer_11_out), .sel(\流水线中断id_ex_1_ex_sgn [11]));
  Multiplexer #(.select(1), .width(32), .disabled("Z"), .enable("false")) multiplexer_12 (
    .in0(EX_PC), .in1(F_EX_bAddr), .out(multiplexer_12_out), .sel(F_predictError));
  or or_11 (Branch, \流水线中断id_ex_1_ex_sgn [0], \流水线中断id_ex_1_ex_sgn [1], \流水线中断id_ex_1_ex_sgn [2]);
  \条件分支逻辑设计  \u_条件分支逻辑设计_1  (
    .Bge(\流水线中断id_ex_1_ex_sgn [0]), .in_4(alu_1_equal), .Beq(\流水线中断id_ex_1_ex_sgn [1]), .in_2(alu_1_out_4),
    .Bne(\流水线中断id_ex_1_ex_sgn [2]), .branchtaken(bjump));
  ALU alu_1 (
    .X(multiplexer_8_out), .Y(multiplexer_11_out), .AluOP(\流水线中断id_ex_1_ex_sgn [8:5]), .Equal(alu_1_equal),
    .Result(alu_1_result), .out_4(alu_1_out_4));  // open: Result_2, out_6
  Adder #(.width(32)) adder_4 (.a(EX_PC), .b(\流水线中断id_ex_1_ex_imm_b ), .out(bAddr));  // open: cin, cout
  Counter #(.width(16), .max('hffff), .ongoal("wrap"), .trigger("rising"), .behavior("old")) counter_3 (
    .count(and_11_out), .Q(\无条件分支数 ), .clk(CLK), .clr(RST));  // open: load, D, carry, preset
  and and_11 (and_11_out, halt, J);
  Multiplexer #(.select(1), .width(32), .disabled("Z"), .enable("false")) multiplexer_13 (
    .in0(multiplexer_12_out), .in1(ID_PC), .out(BreakPoint), .sel(F_LoadUse));
  or or_12 (J, \流水线中断id_ex_1_ex_sgn [12], \流水线中断id_ex_1_ex_sgn [13]);
  \无条件跳转逻辑设计  \u_无条件跳转逻辑设计_1  (
    .JAL(\流水线中断id_ex_1_ex_sgn [12]), .JALR(\流水线中断id_ex_1_ex_sgn [13]), .JALR_Addr(alu_1_result),
    .JAL_Addr(\流水线中断id_ex_1_ex_imm_jal ), .J_Addr(jAddr), .PC(EX_PC));
  and and_12 (and_12_out, halt, bjump);
  Counter #(.width(16), .max('hffff), .ongoal("wrap"), .trigger("rising"), .behavior("old")) counter_4 (
    .count(and_12_out), .Q(\条件分支成功数 ), .clk(CLK), .clr(RST));  // open: load, D, carry, preset
  \气泡EX_MEM  \u_气泡ex_mem_1  (
    .EX_rd(\流水线中断id_ex_1_ex_rd ), .EX_PC(EX_PC), .EX_IR(EX_IR), .EX_ALU_R(alu_1_result),
    .EX_imm_Lui(\流水线中断id_ex_1_ex_imm_lui ),
    .EX_sgn({\流水线中断id_ex_1_ex_sgn [15:11], EX_RegWrite, \流水线中断id_ex_1_ex_sgn [9:4], EX_MemToReg, \流水线中断id_ex_1_ex_sgn [2:0]}),
    .MEM_rd(\气泡ex_mem_1_mem_rd ), .MEM_PC(M_PC), .MEM_IR(MEM_IR), .MEM_ALU_R(\气泡ex_mem_1_mem_alu_r ),
    .MEM_imm_Lui(\气泡ex_mem_1_mem_imm_lui ),
    .MEM_sgn({MEM_Lui, \气泡ex_mem_1_mem_sgn [14:11], MEM_RegWrite, \气泡ex_mem_1_mem_sgn [9:5], MemWrite, \气泡ex_mem_1_mem_sgn [3:0]}),
    .rst(or_13_out), .halt(halt), .clk(CLK), .EX_MDin(multiplexer_9_out), .MEM_MDin(MDin),
    .EX_Equal(alu_1_equal), .MEM_Equal(\气泡ex_mem_1_mem_equal ));
  or or_13 (or_13_out, INT, RST);
  and and_13 (and_13_out, halt, LoadUse);
  not not_5 (not_5_out, MemWrite);
  Counter #(.width(16), .max('hffff), .ongoal("wrap"), .trigger("rising"), .behavior("old")) counter_5 (
    .count(and_13_out), .Q(\LoadUse次数 ), .clk(CLK), .clr(RST));  // open: load, D, carry, preset
  RAM #(.addrWidth(10), .dataWidth(32), .bus("separate"), .Select("high")) ram_1 (
    .addr(\气泡ex_mem_1_mem_alu_r [11:2]), .din(MDin), .data(ram_1_data), .str(MemWrite), .clk(CLK),
    .ld(not_5_out));  // open: sel, clr
  assign bit_extender_1_out = {{3{1'b0}}, \气泡ex_mem_1_mem_alu_r [1:0]};  // Bit_Extender bit_extender_1
  Subtractor #(.width(5)) subtractor_1 (.a(5'b11000), .b(minus), .out(subtractor_1_out));  // open: bin, bout
  Multiplexer #(.select(1), .width(32), .disabled("Z"), .enable("false")) multiplexer_14 (
    .in0(\气泡ex_mem_1_mem_alu_r ), .in1(\气泡ex_mem_1_mem_imm_lui ), .out(multiplexer_14_out), .sel(MEM_Lui));
  and and_14 (and_14_out, halt, predictError);
  Shifter #(.width(5), .shift("ll")) shifter_1 (.in(bit_extender_1_out), .\dist (3'b011), .out(minus));
  Shifter #(.width(32), .shift("ll")) shifter_2 (.in(ram_1_data), .\dist (subtractor_1_out), .out(shifter_2_out));
  Shifter #(.width(32), .shift("lr")) shifter_3 (.in(shifter_2_out), .\dist (5'b11000), .out(shifter_3_out));
  Counter #(.width(16), .max('hffff), .ongoal("wrap"), .trigger("rising"), .behavior("old")) counter_6 (
    .count(and_14_out), .Q(\预测错误数 ), .clk(CLK));  // open: load, D, carry, clr, preset
  Multiplexer #(.select(1), .width(32), .disabled("Z"), .enable("false")) multiplexer_15 (
    .in0(ram_1_data), .in1(shifter_3_out), .out(multiplexer_15_out), .sel(\气泡ex_mem_1_mem_sgn [14]));
  Multiplexer #(.select(1), .width(32), .disabled("Z"), .enable("false")) multiplexer_16 (
    .in0(multiplexer_14_out), .in1(multiplexer_15_out), .out(multiplexer_16_out),
    .sel(\气泡ex_mem_1_mem_sgn [3]));
  \气泡MEM_WB  \u_气泡mem_wb_1  (
    .MEM_rd(\气泡ex_mem_1_mem_rd ), .MEM_PC(M_PC), .MEM_IR(MEM_IR), .MEM_ALU_MD(multiplexer_16_out),
    .MEM_sgn({MEM_Lui, \气泡ex_mem_1_mem_sgn [14:11], MEM_RegWrite, \气泡ex_mem_1_mem_sgn [9:5], MemWrite, \气泡ex_mem_1_mem_sgn [3:0]}),
    .WB_rd(WB_rd), .WB_PC(WB_PC), .WB_IR(WB_IR), .WB_ALU_MD(\气泡mem_wb_1_wb_alu_md ),
    .WB_sgn({\气泡mem_wb_1_wb_sgn [15:12], Ecall, RegWrite, \气泡mem_wb_1_wb_sgn [9:0]}), .rst(RST), .halt(halt),
    .clk(CLK), .MEM_Equal(\气泡ex_mem_1_mem_equal ), .WB_Equal(Equal), .MEM_LED(MDin), .WB_LED(LedShow));
  and and_15 (and_15_out, Ecall, Equal);
  and and_16 (and_16_out, Ecall, not_6_out);
  not not_6 (not_6_out, Equal);
  Adder #(.width(32)) adder_5 (.a(WB_PC), .b(32'h4), .out(adder_5_out));  // open: cin, cout
  not not_7 (not_7_out, and_15_out);
  or or_14 (or_14_out, \气泡mem_wb_1_wb_sgn [13], \气泡mem_wb_1_wb_sgn [12]);
  Multiplexer #(.select(1), .width(32), .disabled("Z"), .enable("false")) multiplexer_17 (
    .in0(\气泡mem_wb_1_wb_alu_md ), .in1(adder_5_out), .out(RDin), .sel(or_14_out));
  or or_15 (halt, Go, not_7_out);
  Register #(.width(32), .trigger("rising"), .Select("low")) register_6 (
    .D(LedShow), .en(and_16_out), .Q(LedData), .clk(CLK));  // open: clr

  // Other names for the same wires on the sheet: MEM_PC[31:0] = M_PC

  // Notes on the sheet:
  //   中断源
  //   时空图监测，可删除
  //   中断等待指示
  //   单级中断测试信号模拟器
  //   数码管输出
  //   指令存储器
  //   contents of rom_1 (hex, n*v repeats v):
  //   7d000113 100413 1f41993 41f9d993 433 c00913 800b13 140413 f47413 800293 100313 499993 89e9b3 1300533
  //   2200893 73 406282b3 fe0294e3 140413 f00f93 1f47433 1c41413 800293 100313 49d993 89e9b3 1300533
  //   2200893 73 406282b3 fe0294e3 1c45413 406b0b33 b0463 f95ff06f 2b3 fff2c293 1029293 fff2e293 500533
  //   2200893 73 f5dff06f 1112023 410113 a12023 410113 812023 410113 1312023 410113 1412023 410113 1512023
  //   410113 1612023 410113 100b13 300a13 100a93 1600433 441413 14469b3 1300533 2200893 73 fe0416e3
  //   415a0a33 fe0a10e3 ffc10113 12b03 ffc10113 12a83 ffc10113 12a03 ffc10113 12983 ffc10113 12403
  //   ffc10113 12503 ffc10113 12883 200073 1112023 410113 a12023 410113 812023 410113 1312023 410113
  //   1412023 410113 1512023 410113 1612023 410113 200b13 300a13 100a93 1600433 441413 14469b3 1300533
  //   2200893 73 fe0416e3 415a0a33 fe0a10e3 ffc10113 12b03 ffc10113 12a83 ffc10113 12a03 ffc10113 12983
  //   ffc10113 12403 ffc10113 12503 ffc10113 12883 200073 1112023 410113 a12023 410113 812023 410113
  //   1312023 410113 1412023 410113 1512023 410113 1612023 410113 300b13 300a13 100a93 1600433 441413
  //   14469b3 1300533 2200893 73 fe0416e3 415a0a33 fe0a10e3 ffc10113 12b03 ffc10113 12a83 ffc10113 12a03
  //   ffc10113 12983 ffc10113 12403 ffc10113 12503 ffc10113 12883 200073
  //   控制位
  //   Reset 
  //   Reset 
  //   Reset 
  //   流水调试日志用
  //   暂停节拍，不能为0
  //   戳工具置1进入计数暂停模式，ctrl+k时钟自动运行到对应节拍暂停
  //   ctrl+k关闭时钟连续运行，将控制位置零，进入单步调试模式调试
  //   判断错误需要清除IF和ID的误取指令，连接reset同步清零
  //   可计数暂停的时钟源
  //   instruction分配关系
  //   0：Bge指令
  //   1：Beq指令
  //   2：Bne指令
  //   10：RegWrite信号
  //   14：Lbu信号
  //   为方便自动评测，需要输出流水线各段保存的PC值，注意是PC不是PC+4，另外ID段寄存器写入信息，Mem段内存写入信息也要输出
  //   3：MemToReg信号
  //   4：MemWrite信号
  //   11：Ecall信号
  //   15：Lui信号
  //   5-8：AluOP信号
  //   9：Alu_src信号
  //   12：Jal信号
  //   13：Jalr信号
  //   此处不论是跳转还是数据冲突都需要产生气泡，因此都需要连接reset同步清零
  //   数据记录
  //   数据存储器
  //   Ecall选项
endmodule

// ID/EX
module \流水线中断ID_EX  (
  input  [4:0] ID_rd,
  input  [31:0] ID_a,
  input  [31:0] ID_b,
  input  [31:0] ID_imm,
  input  [31:0] ID_imm_B,
  input  [31:0] ID_imm_Jal,
  input  [31:0] ID_imm_Lui,
  input  [31:0] ID_PC,
  input  [31:0] ID_IR,
  input  ID_Uret,
  input  ID_PredictJump,
  input  [1:0] ID_FwdA,
  input  [1:0] ID_FwdB,
  input  [15:0] ID_sgn,
  input  clk,
  input  rst,
  input  halt,
  output [4:0] EX_rd,
  output [31:0] EX_a,
  output [31:0] EX_b,
  output [31:0] EX_imm,
  output [31:0] EX_imm_B,
  output [31:0] EX_imm_Jal,
  output [31:0] EX_imm_Lui,
  output [31:0] EX_PC,
  output [31:0] EX_IR,
  output EX_Uret,
  output EX_PredictJump,
  output [1:0] EX_FwdA,
  output [1:0] EX_FwdB,
  output [15:0] EX_sgn
);

  wire multiplexer_10_out, multiplexer_11_out;
  wire [1:0] multiplexer_12_out, multiplexer_13_out;
  wire [4:0] multiplexer_1_out;
  wire [15:0] multiplexer_14_out;
  wire [31:0] multiplexer_2_out, multiplexer_3_out, multiplexer_4_out, multiplexer_5_out, multiplexer_6_out,
       multiplexer_7_out, multiplexer_8_out, multiplexer_9_out;

  Multiplexer #(.select(1), .width(5), .disabled("Z"), .enable("false")) multiplexer_1 (
    .in0(ID_rd), .in1({5{1'b0}}), .out(multiplexer_1_out), .sel(rst));
  Multiplexer #(.select(1), .width(32), .disabled("Z"), .enable("false")) multiplexer_2 (
    .in0(ID_a), .in1({32{1'b0}}), .out(multiplexer_2_out), .sel(rst));
  Multiplexer #(.select(1), .width(32), .disabled("Z"), .enable("false")) multiplexer_3 (
    .in0(ID_b), .in1({32{1'b0}}), .out(multiplexer_3_out), .sel(rst));
  Multiplexer #(.select(1), .width(32), .disabled("Z"), .enable("false")) multiplexer_4 (
    .in0(ID_imm), .in1({32{1'b0}}), .out(multiplexer_4_out), .sel(rst));
  Multiplexer #(.select(1), .width(32), .disabled("Z"), .enable("false")) multiplexer_5 (
    .in0(ID_imm_B), .in1({32{1'b0}}), .out(multiplexer_5_out), .sel(rst));
  Multiplexer #(.select(1), .width(32), .disabled("Z"), .enable("false")) multiplexer_6 (
    .in0(ID_imm_Jal), .in1({32{1'b0}}), .out(multiplexer_6_out), .sel(rst));
  Multiplexer #(.select(1), .width(32), .disabled("Z"), .enable("false")) multiplexer_7 (
    .in0(ID_imm_Lui), .in1({32{1'b0}}), .out(multiplexer_7_out), .sel(rst));
  Multiplexer #(.select(1), .width(32), .disabled("Z"), .enable("false")) multiplexer_8 (
    .in0(ID_PC), .in1({32{1'b0}}), .out(multiplexer_8_out), .sel(rst));
  Multiplexer #(.select(1), .width(32), .disabled("Z"), .enable("false")) multiplexer_9 (
    .in0(ID_IR), .in1({32{1'b0}}), .out(multiplexer_9_out), .sel(rst));
  Multiplexer #(.select(1), .width(1), .disabled("Z"), .enable("false")) multiplexer_10 (
    .in0(ID_Uret), .in1(1'b0), .out(multiplexer_10_out), .sel(rst));
  Multiplexer #(.select(1), .width(1), .disabled("Z"), .enable("false")) multiplexer_11 (
    .in0(ID_PredictJump), .in1(1'b0), .out(multiplexer_11_out), .sel(rst));
  Multiplexer #(.select(1), .width(2), .disabled("Z"), .enable("false")) multiplexer_12 (
    .in0(ID_FwdA), .in1(2'b00), .out(multiplexer_12_out), .sel(rst));
  Multiplexer #(.select(1), .width(2), .disabled("Z"), .enable("false")) multiplexer_13 (
    .in0(ID_FwdB), .in1(2'b00), .out(multiplexer_13_out), .sel(rst));
  Multiplexer #(.select(1), .width(16), .disabled("Z"), .enable("false")) multiplexer_14 (
    .in0(ID_sgn), .in1({16{1'b0}}), .out(multiplexer_14_out), .sel(rst));
  Register #(.width(5), .trigger("rising"), .Select("low")) register_1 (
    .D(multiplexer_1_out), .en(halt), .Q(EX_rd), .clk(clk));  // open: clr
  Register #(.width(32), .trigger("rising"), .Select("low")) register_2 (
    .D(multiplexer_2_out), .en(halt), .Q(EX_a), .clk(clk));  // open: clr
  Register #(.width(32), .trigger("rising"), .Select("low")) register_3 (
    .D(multiplexer_3_out), .en(halt), .Q(EX_b), .clk(clk));  // open: clr
  Register #(.width(32), .trigger("rising"), .Select("low")) register_4 (
    .D(multiplexer_4_out), .en(halt), .Q(EX_imm), .clk(clk));  // open: clr
  Register #(.width(32), .trigger("rising"), .Select("low")) register_5 (
    .D(multiplexer_5_out), .en(halt), .Q(EX_imm_B), .clk(clk));  // open: clr
  Register #(.width(32), .trigger("rising"), .Select("low")) register_6 (
    .D(multiplexer_6_out), .en(halt), .Q(EX_imm_Jal), .clk(clk));  // open: clr
  Register #(.width(32), .trigger("rising"), .Select("low")) register_7 (
    .D(multiplexer_7_out), .en(halt), .Q(EX_imm_Lui), .clk(clk));  // open: clr
  Register #(.width(32), .trigger("rising"), .Select("low")) register_8 (
    .D(multiplexer_8_out), .en(halt), .Q(EX_PC), .clk(clk));  // open: clr
  Register #(.width(32), .trigger("rising"), .Select("low")) register_9 (
    .D(multiplexer_9_out), .en(halt), .Q(EX_IR), .clk(clk));  // open: clr
  Register #(.width(1), .trigger("rising"), .Select("low")) register_10 (
    .D(multiplexer_10_out), .en(halt), .Q(EX_Uret), .clk(clk));  // open: clr
  Register #(.width(1), .trigger("rising"), .Select("low")) register_11 (
    .D(multiplexer_11_out), .en(halt), .Q(EX_PredictJump), .clk(clk));  // open: clr
  Register #(.width(2), .trigger("rising"), .Select("low")) register_12 (
    .D(multiplexer_12_out), .en(halt), .Q(EX_FwdA), .clk(clk));  // open: clr
  Register #(.width(2), .trigger("rising"), .Select("low")) register_13 (
    .D(multiplexer_13_out), .en(halt), .Q(EX_FwdB), .clk(clk));  // open: clr
  Register #(.width(16), .trigger("rising"), .Select("low")) register_14 (
    .D(multiplexer_14_out), .en(halt), .Q(EX_sgn), .clk(clk));  // open: clr
endmodule
